// Logisim project cpu24.circ as structural Verilog: 27 circuits, main circuit ◇单周期MIPS
module \单周期MIPS  (
  input  IR1,
  input  IR2,
  input  IR3,
  output RegWrite,
  output MemWrite,
  output [31:0] PC,
  output [31:0] IR,
  output [31:0] RDin,
  output [31:0] MDin,
  output [31:0] LedData
);

  wire AluSrcB, Beq, Blez, Bne, CLK, clock_2_out, comparator_1_eq, comparator_1_lt, d_ff_1_q, Equal, Go,
       HalfW, IR1_t, IR2_t, IR3_t, IRA, IRB, IRC, JAL, JMP, JR, Less, MemToReg, nand_1_out, Pause, RegDst,
       SignedExt, Syscall, Vshamt, W1, W2, W3;
  wire [3:0] AluOP;
  wire [4:0] multiplexer_2_out, \reg选择逻辑_1_r1_num , \reg选择逻辑_1_r2_num , \reg选择逻辑_1_shamt , \reg选择逻辑_1_w_num ;
  wire [12:0] CNT_num;
  wire [15:0] \总周期数 ;
  wire [31:0] adder_1_out, adder_2_out, bit_extender_1_out, bit_extender_2_out, mips_alu_1_result,
       mips_mem_1_memreaddata, multiplexer_1_out, multiplexer_3_out, multiplexer_4_out, \pc更新逻辑_1_pc_next ,
       R1;

  Clock #(.highDuration(1), .lowDuration(1)) clock_1 ();  // open: out
  Button _1 (.out(IRA));
  Button _2 (.out(IRB));
  Button _3 (.out(IRC));
  Button \u_继续运行  (.out(Go));
  LED #(.active("true")) led_1 (.in(W1));
  LED #(.active("true")) led_2 (.in(W2));
  LED #(.active("true")) led_3 (.in(W3));
  \PC更新逻辑  \pc更新逻辑_1  (
    .Equal(Equal), .Beq(Beq), .Bne(Bne), .JAL(JAL), .JMP(JMP), .JR(JR), .BAddr(adder_2_out),
    .PC_4(adder_1_out), .JAddr({PC[31:28], IR[25:0], 2'b00}), .JRAddr(R1), .PC_Next(\pc更新逻辑_1_pc_next ),
    .Blez(Blez), .Less(Less));  // open: Branched, BranchSig
  Hex_Digit_Display hex_digit_display_1 (.value(LedData[31:28]));  // open: dp
  Register #(.width(32), .trigger("rising"), .Select("low")) u_PC (
    .D(\pc更新逻辑_1_pc_next ), .Q(PC), .clk(CLK));  // open: en, clr
  D_Flip_Flop #(.trigger("high"), .Pre_Clr_Positions("LEGACY"), .NegatePresetClear("false"), .enable("true"), .NewFFLayout("false")) d_ff_1 (
    .Q(d_ff_1_q), .preset(Pause), .reset(Go));  // open: clk, D, Qn, en
  Hex_Digit_Display hex_digit_display_2 (.value(LedData[23:20]));  // open: dp
  Hex_Digit_Display hex_digit_display_3 (.value(LedData[27:24]));  // open: dp
  Adder #(.width(32)) adder_1 (.a(PC), .b(32'h4), .out(adder_1_out));  // open: cin, cout
  // Probe on 13'hc
  Hex_Digit_Display hex_digit_display_4 (.value(LedData[19:16]));  // open: dp
  Hex_Digit_Display hex_digit_display_5 (.value(LedData[15:12]));  // open: dp
  Comparator #(.width(13), .mode("twosComplement")) comparator_1 (
    .a(CNT_num), .b(13'hc), .eq(comparator_1_eq), .lt(comparator_1_lt));  // open: gt
  Clock #(.highDuration(1), .lowDuration(1)) clock_2 (.out(clock_2_out));
  Hex_Digit_Display hex_digit_display_6 (.value(LedData[11:8]));  // open: dp
  Hex_Digit_Display hex_digit_display_7 (.value(LedData[7:4]));  // open: dp
  // Probe on \总周期数 
  // Mips_Probe mips_probe_1: pin names not known; wires that end beside it: IR
  ROM #(.addrWidth(10), .dataWidth(32), .Select("low")) rom_1 (.addr(PC[11:2]), .data(IR));
  nand nand_1 (nand_1_out, d_ff_1_q, comparator_1_eq);
  Counter #(.width(13), .max('h1fff), .ongoal("stay"), .trigger("rising"), .behavior("old")) counter_1 (
    .count(comparator_1_lt), .Q(CNT_num), .clk(clock_2_out));  // open: load, D, carry, clr, preset
  Hex_Digit_Display hex_digit_display_8 (.value(LedData[3:0]));  // open: dp
  assign CLK = nand_1_out ? clock_2_out : 1'bz;  // Controlled_Buffer controlled_buffer_1
  Pull_Resistor #(.pull(1)) pull_resistor_1 (.node(CLK));
  \Reg选择逻辑  \reg选择逻辑_1  (
    ._21_25(IR[25:21]), .Syscall(Syscall), .RegDst(RegDst), ._16_20(IR[20:16]), ._11_15(IR[15:11]),
    .JAL(JAL), .PC_4(adder_1_out), .WriteBack_Data(multiplexer_4_out), ._6_10(IR[10:6]),
    .R1_num(\reg选择逻辑_1_r1_num ), .R2_num(\reg选择逻辑_1_r2_num ), .W_num(\reg选择逻辑_1_w_num ), .RDin(RDin),
    .Shamt(\reg选择逻辑_1_shamt ));
  assign bit_extender_1_out = {{16{1'b0}}, IR[15:0]};  // Bit_Extender bit_extender_1
  assign bit_extender_2_out = {{16{IR[15]}}, IR[15:0]};  // Bit_Extender bit_extender_2
  or or_1 (IR1_t, IR1, IRA);
  Multiplexer #(.select(1), .width(32), .disabled("Z"), .enable("false")) multiplexer_1 (
    .in0(bit_extender_1_out), .in1(bit_extender_2_out), .out(multiplexer_1_out), .sel(SignedExt));
  or or_2 (IR2_t, IR2, IRB);
  MIPS_Regifile mips_regifile_1 (
    .Din(RDin), .Clk(CLK), .R1(R1), .R2(MDin), .WE(RegWrite), .W_num(\reg选择逻辑_1_w_num ),
    .R1_num(\reg选择逻辑_1_r1_num ), .R2_num(\reg选择逻辑_1_r2_num ));
  Multiplexer #(.select(1), .width(5), .disabled("Z"), .enable("false")) multiplexer_2 (
    .in0(\reg选择逻辑_1_shamt ), .in1(R1[4:0]), .out(multiplexer_2_out), .sel(Vshamt));
  Adder #(.width(32)) adder_2 (
    .a(adder_1_out), .b({bit_extender_2_out[29:0], 2'b00}), .out(adder_2_out));  // open: cin, cout
  Counter #(.width(16), .max('hffff), .ongoal("wrap"), .trigger("rising"), .behavior("new")) counter_2 (
    .Q(\总周期数 ), .clk(CLK));  // open: load, D, count, carry, clr, preset, down
  Multiplexer #(.select(1), .width(32), .disabled("Z"), .enable("false")) multiplexer_3 (
    .in0(MDin), .in1(multiplexer_1_out), .out(multiplexer_3_out), .sel(AluSrcB));
  or or_3 (IR3_t, IR3, IRC);
  MIPS_ALU mips_alu_1 (
    .X(R1), .Y(multiplexer_3_out), .AluOP(AluOP), .Equal(Equal), .Result(mips_alu_1_result),
    .shamt(multiplexer_2_out), .Less(Less));  // open: Result_2
  MIPS_MEM mips_mem_1 (
    .AluResult(mips_alu_1_result), .HalfW(HalfW), .WriteData(MDin), .MemWrite(MemWrite), .CLK(CLK),
    .MemReadData(mips_mem_1_memreaddata));
  Multiplexer #(.select(1), .width(32), .disabled("Z"), .enable("false")) multiplexer_4 (
    .in0(mips_alu_1_result), .in1(mips_mem_1_memreaddata), .out(multiplexer_4_out), .sel(MemToReg));
  \单周期硬布线控制器  \u_单周期硬布线控制器_1  (
    .Func(IR[5:0]), .OP(IR[31:26]), .ALU_OP(AluOP), .MemToReg(MemToReg), .MemWrite(MemWrite),
    .ALU_SRC(AluSrcB), .RegWrite(RegWrite), .SysCALL(Syscall), .SignedExt(SignedExt), .RegDst(RegDst),
    .JR(JR), .JMP(JMP), .Beq(Beq), .JAL(JAL), .Bne(Bne), .Vshamt(Vshamt), .BLEZ(Blez), .HalfW(HalfW));
  \Syscall处理  \syscall处理_1  (.Syscall(Syscall), .CLK(CLK), .R2(MDin), .R1(R1), .Pause(Pause), .LedData(LedData));

  // Other names for the same wires on the sheet: Func[5:0] = IR[5:0]; OP[5:0] = IR[31:26]; R2[31:0] = MDin

  // Notes on the sheet:
  //   中断源
  //   中断等待指示
  //   总复位信号应将除ROM以外所有存储组件全部清零
  //   控制位
  //   暂停节拍，不能为0
  //   用这个时钟源需要去掉电路中的其他时钟源
  //   数码管输出
  //   指令存储器
  //   戳工具置1进入计数暂停模式，ctrl+k时钟自动运行到对应节拍暂停
  //   ctrl+k关闭时钟连续运行，将控制位置零，进入单步调试模式调试
  //   数码管输出应该用寄存器锁存，否则显示数据只能一闪而过
  //   指令字
  //   contents of rom_1 (hex, n*v repeats v):
  //   20110001 8000005 20110001 20120002 20130003 8000009 20110001 20120002 20130003 800000d 20110001
  //   20120002 20130003 8000011 20110001 20120002 20130003 c0000f2 20100001 20110001 118fc0 112020
  //   20020022 c 118882 12200001 8000015 112020 20020022 c 20110001 118880 112020 20020022 c 12200001
  //   800001f 20110001 118fc0 112020 20020022 c 1188c3 112020 20020022 c 118903 112020 20020022 c 118903
  //   112020 20020022 c 118903 112020 20020022 c 118903 112020 20020022 c 118903 112020 20020022 c 118903
  //   112020 20020022 c 118903 112020 20020022 c 20100001 109fc0 139fc3 8021 2012000c 24160003 26100001
  //   3210000f 20080008 20090001 139900 2709825 132020 20020022 c 1094022 1500fff9 22100001 2018000f
  //   2188024 108700 20080008 20090001 139902 2709825 132021 20020022 c 1094022 1500fff9 108702 2c9b022
  //   12c00001 8000050 4020 1084027 84400 3508ffff 82021 20020022 c 2010ffff 20110000 ae300000 22100001
  //   22310004 ae300000 22100001 22310004 ae300000 22100001 22310004 ae300000 22100001 22310004 ae300000
  //   22100001 22310004 ae300000 22100001 22310004 ae300000 22100001 22310004 ae300000 22100001 22310004
  //   ae300000 22100001 22310004 ae300000 22100001 22310004 ae300000 22100001 22310004 ae300000 22100001
  //   22310004 ae300000 22100001 22310004 ae300000 22100001 22310004 ae300000 22100001 22310004 ae300000
  //   22100001 22310004 22100001 8020 2011003c 8e130000 8e340000 274402a 11000002 ae330000 ae140000
  //   2231fffc 1611fff8 102020 20020022 c 22100004 2011003c 1611fff2 20020032 c 20080001 20090003 20110876
  //   112020 20020022 c 200b0008 1118804 1318804 112020 20020022 c 216bffff 1560fff9 2002000a c 2008ffff
  //   20090000 20111997 112020 20020022 c 2288820 2e291949 1120fffa 2002000a c 20090000 200b0020 20110001
  //   20120001 a5310000 112020 20020022 c 2328820 21290002 216bffff 1560fff8 200b0010 20090000 8d310000
  //   112020 20020022 c 21290004 216bffff 1560fff9 2002000a c 2011fff1 112020 20020022 c 22310001 1a20fffb
  //   2002000a c 20100000 22100001 102020 20020022 c 22100002 102020 20020022 c 22100003 102020 20020022 c
  //   22100004 102020 20020022 c 22100005 102020 20020022 c 22100006 102020 20020022 c 22100007 102020
  //   20020022 c 22100008 102020 20020022 20020022 c 3e00008
  //   可计数暂停的时钟源
  //   为方便自动评测，需要输出PC，IR，寄存器堆写如数据RDin
  //   RAM写使能MemWrite、RAM写入数据MDin等信号
endmodule

// 单周期硬布线控制器
module \单周期硬布线控制器  (
  input  [5:0] OP,
  input  [5:0] Func,
  output [3:0] ALU_OP,
  output MemToReg,
  output MemWrite,
  output ALU_SRC,
  output RegWrite,
  output SysCALL,
  output SignedExt,
  output RegDst,
  output Beq,
  output Bne,
  output JR,
  output JMP,
  output JAL,
  output Vshamt,
  output BLEZ,
  output HalfW
);

  \运算控制器自动生成  \u_运算控制器自动生成_1  (
    .OP0(OP[0]), .OP1(OP[1]), .OP2(OP[2]), .OP3(OP[3]), .OP4(OP[4]), .OP5(OP[5]), .F0(Func[0]), .F1(Func[1]),
    .F2(Func[2]), .F3(Func[3]), .F4(Func[4]), .F5(Func[5]), .S0(ALU_OP[0]), .S1(ALU_OP[1]), .S2(ALU_OP[2]),
    .S3(ALU_OP[3]));
  \控制信号自动生成  \u_控制信号自动生成_1  (
    .OP0(OP[0]), .MemToReg(MemToReg), .OP1(OP[1]), .OP2(OP[2]), .MemWrite(MemWrite), .OP3(OP[3]),
    .OP4(OP[4]), .OP5(OP[5]), .F0(Func[0]), .F1(Func[1]), .ALU_SRC(ALU_SRC), .F2(Func[2]), .F3(Func[3]),
    .F4(Func[4]), .F5(Func[5]), .RegWrite(RegWrite), .SysCALL(SysCALL), .SignedExt(SignedExt),
    .RegDst(RegDst), .BEQ(Beq), .BNE(Bne), .JR(JR), .JUMP(JMP), .JAL(JAL), .Vshamt(Vshamt), .BLEZ(BLEZ),
    .HalfW(HalfW));

  // Other names for the same wires on the sheet: OP_CODE[5:0] = OP

  // Notes on the sheet:
  //   运算器控制器，根据指令生成运算器功能选择信号
  //   控制信号生成，产生数据通路需要的其他控制信号
endmodule

// 运算器控制器
module \运算控制器自动生成  (
  input  OP0,
  input  OP1,
  input  OP2,
  input  OP3,
  input  OP4,
  input  OP5,
  input  F0,
  input  F1,
  input  F2,
  input  F3,
  input  F4,
  input  F5,
  output S0,
  output S1,
  output S2,
  output S3
);

  wire and_1_out, and_2_out, and_3_out, and_4_out, and_5_out, and_6_out, and_7_out, and_8_out, and_9_out,
       and_10_out, and_11_out, and_12_out, and_13_out, and_14_out, and_15_out, and_16_out, and_17_out,
       and_18_out, and_19_out, and_20_out, and_21_out, and_22_out, and_23_out, and_24_out, and_25_out,
       and_26_out, and_27_out, and_28_out, and_29_out, and_30_out, and_31_out, and_32_out, and_33_out,
       and_34_out, and_35_out, and_36_out, and_37_out, and_38_out, not_1_out, not_2_out, not_3_out,
       not_4_out, not_5_out, not_6_out, not_7_out, not_8_out, not_9_out, not_10_out, not_11_out, not_12_out,
       not_13_out, not_14_out, not_15_out, not_16_out, not_17_out, not_18_out, not_19_out, not_20_out,
       not_21_out, not_22_out, not_23_out, not_24_out, not_25_out, not_26_out, not_27_out, not_28_out,
       not_29_out, not_30_out, not_31_out, not_32_out, not_33_out, not_34_out, not_35_out, not_36_out,
       not_37_out, not_38_out, not_39_out, not_40_out, not_41_out, not_42_out, not_43_out, not_44_out,
       not_45_out, not_46_out, not_47_out, not_48_out, not_49_out, not_50_out, not_51_out, not_52_out,
       not_53_out, not_54_out, not_55_out, not_56_out, not_57_out, not_58_out, not_59_out, not_60_out,
       not_61_out, not_62_out, not_63_out, not_64_out, not_65_out, not_66_out, not_67_out, not_68_out,
       not_69_out, not_70_out, not_71_out, not_72_out, not_73_out, not_74_out, not_75_out, not_76_out,
       not_77_out, not_78_out, not_79_out, not_80_out, not_81_out, not_82_out, not_83_out, not_84_out,
       not_85_out, not_86_out, not_87_out, not_88_out, not_89_out, not_90_out, not_91_out, not_92_out,
       not_93_out, not_94_out, not_95_out, not_96_out, not_97_out, not_98_out, not_99_out, not_100_out,
       not_101_out, not_102_out, not_103_out, not_104_out, not_105_out, not_106_out, not_107_out,
       not_108_out, not_109_out, not_110_out, not_111_out, not_112_out, not_113_out, not_114_out,
       not_115_out, not_116_out, not_117_out, not_118_out, not_119_out, not_120_out, not_121_out,
       not_122_out, not_123_out, not_124_out, not_125_out, not_126_out, not_127_out, not_128_out,
       not_129_out, not_130_out, not_131_out, not_132_out, not_133_out, not_134_out, not_135_out,
       not_136_out, not_137_out, not_138_out, not_139_out, not_140_out, not_141_out, not_142_out,
       not_143_out, not_144_out, not_145_out, not_146_out, not_147_out, not_148_out, not_149_out,
       not_150_out, not_151_out, not_152_out, not_153_out, not_154_out, not_155_out, not_156_out,
       not_157_out, not_158_out, not_159_out, not_160_out, not_161_out, not_162_out, not_163_out,
       not_164_out, not_165_out, not_166_out, not_167_out, not_168_out, not_169_out, not_170_out,
       not_171_out, not_172_out, not_173_out, not_174_out, not_175_out, not_176_out, not_177_out,
       not_178_out, not_179_out, not_180_out, not_181_out, not_182_out, not_183_out, not_184_out,
       not_185_out, not_186_out, not_187_out, not_188_out, not_189_out, not_190_out, not_191_out,
       not_192_out, not_193_out, not_194_out, not_195_out, not_196_out, not_197_out, not_198_out,
       not_199_out, not_200_out, not_201_out, not_202_out, not_203_out, not_204_out, not_205_out,
       not_206_out, not_207_out, not_208_out, not_209_out, not_210_out, not_211_out, not_212_out,
       not_213_out, not_214_out, not_215_out, not_216_out, not_217_out, not_218_out, not_219_out,
       not_220_out, not_221_out, not_222_out, not_223_out, not_224_out, not_225_out, not_226_out,
       not_227_out, not_228_out, not_229_out, not_230_out, not_231_out, not_232_out, not_233_out,
       not_234_out, not_235_out, not_236_out, not_237_out, not_238_out, not_239_out, not_240_out,
       not_241_out, not_242_out, not_243_out, not_244_out, not_245_out, not_246_out, not_247_out, not_248_out;

  not not_1 (not_1_out, OP5);
  not not_2 (not_2_out, OP4);
  not not_3 (not_3_out, OP3);
  not not_4 (not_4_out, OP2);
  not not_5 (not_5_out, OP1);
  not not_6 (not_6_out, OP0);
  not not_7 (not_7_out, F5);
  not not_8 (not_8_out, F4);
  not not_9 (not_9_out, F3);
  not not_10 (not_10_out, F2);
  not not_11 (not_11_out, OP5);
  not not_12 (not_12_out, OP4);
  not not_13 (not_13_out, OP3);
  not not_14 (not_14_out, OP2);
  not not_15 (not_15_out, OP1);
  not not_16 (not_16_out, OP0);
  not not_17 (not_17_out, F4);
  not not_18 (not_18_out, F3);
  not not_19 (not_19_out, F2);
  not not_20 (not_20_out, F1);
  not not_21 (not_21_out, F0);
  not not_22 (not_22_out, OP5);
  not not_23 (not_23_out, OP4);
  not not_24 (not_24_out, OP3);
  not not_25 (not_25_out, OP2);
  not not_26 (not_26_out, OP1);
  not not_27 (not_27_out, OP0);
  not not_28 (not_28_out, F4);
  not not_29 (not_29_out, F3);
  not not_30 (not_30_out, F2);
  not not_31 (not_31_out, F1);
  not not_32 (not_32_out, OP5);
  not not_33 (not_33_out, OP4);
  not not_34 (not_34_out, OP3);
  not not_35 (not_35_out, OP2);
  not not_36 (not_36_out, OP1);
  not not_37 (not_37_out, OP0);
  not not_38 (not_38_out, F4);
  not not_39 (not_39_out, F3);
  not not_40 (not_40_out, F1);
  not not_41 (not_41_out, F0);
  not not_42 (not_42_out, OP5);
  not not_43 (not_43_out, OP4);
  not not_44 (not_44_out, OP3);
  not not_45 (not_45_out, OP2);
  not not_46 (not_46_out, OP1);
  not not_47 (not_47_out, OP0);
  not not_48 (not_48_out, F4);
  not not_49 (not_49_out, F2);
  not not_50 (not_50_out, F0);
  not not_51 (not_51_out, OP5);
  not not_52 (not_52_out, OP4);
  not not_53 (not_53_out, OP2);
  not not_54 (not_54_out, OP1);
  not not_55 (not_55_out, OP0);
  not not_56 (not_56_out, OP5);
  not not_57 (not_57_out, OP4);
  not not_58 (not_58_out, OP1);
  not not_59 (not_59_out, OP0);
  not not_60 (not_60_out, OP5);
  not not_61 (not_61_out, OP4);
  not not_62 (not_62_out, OP2);
  not not_63 (not_63_out, OP1);
  not not_64 (not_64_out, OP5);
  not not_65 (not_65_out, OP4);
  not not_66 (not_66_out, OP2);
  not not_67 (not_67_out, OP0);
  not not_68 (not_68_out, OP4);
  not not_69 (not_69_out, OP3);
  not not_70 (not_70_out, OP2);
  not not_71 (not_71_out, OP4);
  not not_72 (not_72_out, OP2);
  not not_73 (not_73_out, OP4);
  not not_74 (not_74_out, OP2);
  not not_75 (not_75_out, OP1);
  not not_76 (not_76_out, OP5);
  not not_77 (not_77_out, OP4);
  not not_78 (not_78_out, OP3);
  not not_79 (not_79_out, OP2);
  not not_80 (not_80_out, OP1);
  not not_81 (not_81_out, OP0);
  not not_82 (not_82_out, F5);
  not not_83 (not_83_out, F4);
  not not_84 (not_84_out, F3);
  not not_85 (not_85_out, F2);
  not not_86 (not_86_out, F0);
  not not_87 (not_87_out, OP5);
  not not_88 (not_88_out, OP4);
  not not_89 (not_89_out, OP3);
  not not_90 (not_90_out, OP2);
  not not_91 (not_91_out, OP1);
  not not_92 (not_92_out, OP0);
  not not_93 (not_93_out, F4);
  not not_94 (not_94_out, F3);
  not not_95 (not_95_out, F2);
  not not_96 (not_96_out, F0);
  not not_97 (not_97_out, OP5);
  not not_98 (not_98_out, OP4);
  not not_99 (not_99_out, OP3);
  not not_100 (not_100_out, OP2);
  not not_101 (not_101_out, OP1);
  not not_102 (not_102_out, OP0);
  not not_103 (not_103_out, F4);
  not not_104 (not_104_out, F3);
  not not_105 (not_105_out, F1);
  not not_106 (not_106_out, F0);
  not not_107 (not_107_out, OP5);
  not not_108 (not_108_out, OP4);
  not not_109 (not_109_out, OP3);
  not not_110 (not_110_out, OP2);
  not not_111 (not_111_out, OP1);
  not not_112 (not_112_out, OP0);
  not not_113 (not_113_out, F4);
  not not_114 (not_114_out, F3);
  not not_115 (not_115_out, OP5);
  not not_116 (not_116_out, OP4);
  not not_117 (not_117_out, OP3);
  not not_118 (not_118_out, OP2);
  not not_119 (not_119_out, OP1);
  not not_120 (not_120_out, OP0);
  not not_121 (not_121_out, F4);
  not not_122 (not_122_out, F2);
  not not_123 (not_123_out, F0);
  not not_124 (not_124_out, OP5);
  not not_125 (not_125_out, OP4);
  not not_126 (not_126_out, OP1);
  not not_127 (not_127_out, OP0);
  not not_128 (not_128_out, OP5);
  not not_129 (not_129_out, OP4);
  not not_130 (not_130_out, OP2);
  not not_131 (not_131_out, OP0);
  not not_132 (not_132_out, OP5);
  not not_133 (not_133_out, OP4);
  not not_134 (not_134_out, OP3);
  not not_135 (not_135_out, OP2);
  not not_136 (not_136_out, OP1);
  not not_137 (not_137_out, OP0);
  not not_138 (not_138_out, F4);
  not not_139 (not_139_out, F3);
  not not_140 (not_140_out, F2);
  not not_141 (not_141_out, F1);
  not not_142 (not_142_out, F0);
  not not_143 (not_143_out, OP5);
  not not_144 (not_144_out, OP4);
  not not_145 (not_145_out, OP3);
  not not_146 (not_146_out, OP2);
  not not_147 (not_147_out, OP1);
  not not_148 (not_148_out, OP0);
  not not_149 (not_149_out, F4);
  not not_150 (not_150_out, F3);
  not not_151 (not_151_out, F2);
  not not_152 (not_152_out, F1);
  not not_153 (not_153_out, OP5);
  not not_154 (not_154_out, OP4);
  not not_155 (not_155_out, OP3);
  not not_156 (not_156_out, OP2);
  not not_157 (not_157_out, OP1);
  not not_158 (not_158_out, OP0);
  not not_159 (not_159_out, F4);
  not not_160 (not_160_out, F3);
  not not_161 (not_161_out, F2);
  not not_162 (not_162_out, F0);
  not not_163 (not_163_out, OP5);
  not not_164 (not_164_out, OP4);
  not not_165 (not_165_out, OP3);
  not not_166 (not_166_out, OP2);
  not not_167 (not_167_out, OP1);
  not not_168 (not_168_out, OP0);
  not not_169 (not_169_out, F4);
  not not_170 (not_170_out, F3);
  not not_171 (not_171_out, F1);
  not not_172 (not_172_out, F0);
  not not_173 (not_173_out, OP5);
  not not_174 (not_174_out, OP4);
  not not_175 (not_175_out, OP3);
  not not_176 (not_176_out, OP2);
  not not_177 (not_177_out, OP1);
  not not_178 (not_178_out, OP0);
  not not_179 (not_179_out, F4);
  not not_180 (not_180_out, F2);
  not not_181 (not_181_out, OP5);
  not not_182 (not_182_out, OP4);
  not not_183 (not_183_out, OP2);
  not not_184 (not_184_out, OP1);
  not not_185 (not_185_out, OP0);
  not not_186 (not_186_out, OP5);
  not not_187 (not_187_out, OP4);
  not not_188 (not_188_out, OP1);
  not not_189 (not_189_out, OP0);
  not not_190 (not_190_out, OP5);
  not not_191 (not_191_out, OP4);
  not not_192 (not_192_out, OP2);
  not not_193 (not_193_out, OP1);
  not not_194 (not_194_out, OP4);
  not not_195 (not_195_out, OP3);
  not not_196 (not_196_out, OP2);
  not not_197 (not_197_out, OP4);
  not not_198 (not_198_out, OP2);
  not not_199 (not_199_out, OP5);
  not not_200 (not_200_out, OP4);
  not not_201 (not_201_out, OP2);
  not not_202 (not_202_out, OP4);
  not not_203 (not_203_out, OP2);
  not not_204 (not_204_out, OP1);
  not not_205 (not_205_out, OP5);
  not not_206 (not_206_out, OP4);
  not not_207 (not_207_out, OP3);
  not not_208 (not_208_out, OP2);
  not not_209 (not_209_out, OP1);
  not not_210 (not_210_out, OP0);
  not not_211 (not_211_out, F4);
  not not_212 (not_212_out, F3);
  not not_213 (not_213_out, F1);
  not not_214 (not_214_out, OP5);
  not not_215 (not_215_out, OP4);
  not not_216 (not_216_out, OP3);
  not not_217 (not_217_out, OP2);
  not not_218 (not_218_out, OP1);
  not not_219 (not_219_out, OP0);
  not not_220 (not_220_out, F4);
  not not_221 (not_221_out, F3);
  not not_222 (not_222_out, OP5);
  not not_223 (not_223_out, OP4);
  not not_224 (not_224_out, OP3);
  not not_225 (not_225_out, OP2);
  not not_226 (not_226_out, OP1);
  not not_227 (not_227_out, OP0);
  not not_228 (not_228_out, F4);
  not not_229 (not_229_out, F2);
  not not_230 (not_230_out, F0);
  not not_231 (not_231_out, OP5);
  not not_232 (not_232_out, OP4);
  not not_233 (not_233_out, OP3);
  not not_234 (not_234_out, OP2);
  not not_235 (not_235_out, OP1);
  not not_236 (not_236_out, OP0);
  not not_237 (not_237_out, F4);
  not not_238 (not_238_out, F2);
  not not_239 (not_239_out, OP5);
  not not_240 (not_240_out, OP4);
  not not_241 (not_241_out, OP2);
  not not_242 (not_242_out, OP0);
  not not_243 (not_243_out, OP5);
  not not_244 (not_244_out, OP4);
  not not_245 (not_245_out, OP1);
  not not_246 (not_246_out, OP5);
  not not_247 (not_247_out, OP4);
  not not_248 (not_248_out, OP2);
  and and_1 (and_1_out, not_1_out, not_2_out, not_3_out, not_4_out, not_5_out, not_6_out, not_7_out, not_8_out, not_9_out, not_10_out, F1, F0);
  and and_2 (and_2_out, not_11_out, not_12_out, not_13_out, not_14_out, not_15_out, not_16_out, F5, not_17_out, not_18_out, not_19_out, not_20_out, not_21_out);
  and and_3 (and_3_out, not_22_out, not_23_out, not_24_out, not_25_out, not_26_out, not_27_out, F5, not_28_out, not_29_out, not_30_out, not_31_out, F0);
  and and_4 (and_4_out, not_32_out, not_33_out, not_34_out, not_35_out, not_36_out, not_37_out, F5, not_38_out, not_39_out, F2, not_40_out, not_41_out);
  and and_5 (and_5_out, not_42_out, not_43_out, not_44_out, not_45_out, not_46_out, not_47_out, F5, not_48_out, F3, not_49_out, F1, not_50_out);
  and and_6 (and_6_out, not_51_out, not_52_out, OP3, not_53_out, not_54_out, not_55_out);
  and and_7 (and_7_out, not_56_out, not_57_out, OP3, OP2, not_58_out, not_59_out);
  and and_8 (and_8_out, not_60_out, not_61_out, OP3, not_62_out, not_63_out, OP0);
  and and_9 (and_9_out, not_64_out, not_65_out, OP3, not_66_out, OP1, not_67_out);
  and and_10 (and_10_out, OP5, not_68_out, not_69_out, not_70_out, OP1, OP0);
  and and_11 (and_11_out, OP5, not_71_out, OP3, not_72_out, OP1, OP0);
  and and_12 (and_12_out, OP5, not_73_out, OP3, not_74_out, not_75_out, OP0);
  and and_13 (and_13_out, not_76_out, not_77_out, not_78_out, not_79_out, not_80_out, not_81_out, not_82_out, not_83_out, not_84_out, not_85_out, F1, not_86_out);
  and and_14 (and_14_out, not_87_out, not_88_out, not_89_out, not_90_out, not_91_out, not_92_out, F5, not_93_out, not_94_out, not_95_out, F1, not_96_out);
  and and_15 (and_15_out, not_97_out, not_98_out, not_99_out, not_100_out, not_101_out, not_102_out, F5, not_103_out, not_104_out, F2, not_105_out, not_106_out);
  and and_16 (and_16_out, not_107_out, not_108_out, not_109_out, not_110_out, not_111_out, not_112_out, F5, not_113_out, not_114_out, F2, F1, F0);
  and and_17 (and_17_out, not_115_out, not_116_out, not_117_out, not_118_out, not_119_out, not_120_out, F5, not_121_out, F3, not_122_out, F1, not_123_out);
  and and_18 (and_18_out, not_124_out, not_125_out, OP3, OP2, not_126_out, not_127_out);
  and and_19 (and_19_out, not_128_out, not_129_out, OP3, not_130_out, OP1, not_131_out);
  and and_20 (and_20_out, not_132_out, not_133_out, not_134_out, not_135_out, not_136_out, not_137_out, F5, not_138_out, not_139_out, not_140_out, not_141_out, not_142_out);
  and and_21 (and_21_out, not_143_out, not_144_out, not_145_out, not_146_out, not_147_out, not_148_out, F5, not_149_out, not_150_out, not_151_out, not_152_out, F0);
  and and_22 (and_22_out, not_153_out, not_154_out, not_155_out, not_156_out, not_157_out, not_158_out, F5, not_159_out, not_160_out, not_161_out, F1, not_162_out);
  and and_23 (and_23_out, not_163_out, not_164_out, not_165_out, not_166_out, not_167_out, not_168_out, F5, not_169_out, not_170_out, F2, not_171_out, not_172_out);
  and and_24 (and_24_out, not_173_out, not_174_out, not_175_out, not_176_out, not_177_out, not_178_out, F5, not_179_out, F3, not_180_out, F1, F0);
  and and_25 (and_25_out, not_181_out, not_182_out, OP3, not_183_out, not_184_out, not_185_out);
  and and_26 (and_26_out, not_186_out, not_187_out, OP3, OP2, not_188_out, not_189_out);
  and and_27 (and_27_out, not_190_out, not_191_out, OP3, not_192_out, not_193_out, OP0);
  and and_28 (and_28_out, OP5, not_194_out, not_195_out, not_196_out, OP1, OP0);
  and and_29 (and_29_out, OP5, not_197_out, OP3, not_198_out, OP1, OP0);
  and and_30 (and_30_out, not_199_out, not_200_out, OP3, not_201_out, OP1, OP0);
  and and_31 (and_31_out, OP5, not_202_out, OP3, not_203_out, not_204_out, OP0);
  and and_32 (and_32_out, not_205_out, not_206_out, not_207_out, not_208_out, not_209_out, not_210_out, F5, not_211_out, not_212_out, F2, not_213_out, F0);
  and and_33 (and_33_out, not_214_out, not_215_out, not_216_out, not_217_out, not_218_out, not_219_out, F5, not_220_out, not_221_out, F2, F1, F0);
  and and_34 (and_34_out, not_222_out, not_223_out, not_224_out, not_225_out, not_226_out, not_227_out, F5, not_228_out, F3, not_229_out, F1, not_230_out);
  and and_35 (and_35_out, not_231_out, not_232_out, not_233_out, not_234_out, not_235_out, not_236_out, F5, not_237_out, F3, not_238_out, F1, F0);
  and and_36 (and_36_out, not_239_out, not_240_out, OP3, not_241_out, OP1, not_242_out);
  and and_37 (and_37_out, not_243_out, not_244_out, OP3, OP2, not_245_out, OP0);
  and and_38 (and_38_out, not_246_out, not_247_out, OP3, not_248_out, OP1, OP0);
  or or_1 (S1, and_13_out, and_14_out, and_15_out, and_16_out, and_17_out, and_18_out, and_19_out);
  or or_2 (S3, and_32_out, and_33_out, and_34_out, and_35_out, and_36_out, and_37_out, and_38_out);
  or or_3 (S0, and_1_out, and_2_out, and_3_out, and_4_out, and_5_out, and_6_out, and_7_out, and_8_out, and_9_out, and_10_out, and_11_out, and_12_out);
  or or_4 (S2, and_20_out, and_21_out, and_22_out, and_23_out, and_24_out, and_25_out, and_26_out, and_27_out, and_28_out, and_29_out, and_30_out, and_31_out);
endmodule

// 控制信号生成
module \控制信号自动生成  (
  input  OP0,
  input  OP1,
  input  OP2,
  input  OP3,
  input  OP4,
  input  OP5,
  input  F0,
  input  F1,
  input  F2,
  input  F3,
  input  F4,
  input  F5,
  output MemToReg,
  output MemWrite,
  output ALU_SRC,
  output RegWrite,
  output SysCALL,
  output SignedExt,
  output RegDst,
  output BEQ,
  output BNE,
  output JR,
  output JUMP,
  output JAL,
  output Vshamt,
  output BLEZ,
  output HalfW
);

  wire and_3_out, and_4_out, and_5_out, and_6_out, and_7_out, and_8_out, and_9_out, and_10_out, and_11_out,
       and_12_out, and_13_out, and_14_out, and_15_out, and_17_out, and_18_out, and_19_out, and_20_out,
       and_21_out, and_22_out, and_23_out, and_24_out, and_25_out, and_26_out, and_27_out, and_28_out,
       not_1_out, not_2_out, not_3_out, not_4_out, not_5_out, not_6_out, not_7_out, not_8_out, not_9_out,
       not_10_out, not_11_out, not_12_out, not_13_out, not_14_out, not_15_out, not_16_out, not_17_out,
       not_18_out, not_19_out, not_20_out, not_21_out, not_22_out, not_23_out, not_24_out, not_25_out,
       not_26_out, not_27_out, not_28_out, not_29_out, not_30_out, not_31_out, not_32_out, not_33_out,
       not_34_out, not_35_out, not_36_out, not_37_out, not_38_out, not_39_out, not_40_out, not_41_out,
       not_42_out, not_43_out, not_44_out, not_45_out, not_46_out, not_47_out, not_48_out, not_49_out,
       not_50_out, not_51_out, not_52_out, not_53_out, not_54_out, not_55_out, not_56_out, not_57_out,
       not_58_out, not_59_out, not_60_out, not_61_out, not_62_out, not_63_out, not_64_out, not_65_out,
       not_66_out, not_67_out, not_68_out, not_69_out, not_70_out, not_71_out, not_72_out, not_73_out,
       not_74_out, not_75_out, not_76_out, not_77_out, not_78_out, not_79_out, not_80_out, not_81_out,
       not_82_out, not_83_out, not_84_out, not_85_out, not_86_out, not_87_out, not_88_out, not_89_out,
       not_90_out, not_91_out, not_92_out, not_93_out, not_94_out, not_95_out, not_96_out, not_97_out,
       not_98_out, not_99_out, not_100_out, not_101_out, not_102_out, not_103_out, not_104_out, not_105_out,
       not_106_out, not_107_out, not_108_out, not_109_out, not_110_out, not_111_out, not_112_out,
       not_113_out, not_114_out, not_115_out, not_116_out, not_117_out, not_118_out, not_119_out,
       not_120_out, not_121_out, not_122_out, not_123_out, not_124_out, not_125_out, not_126_out,
       not_127_out, not_128_out, not_129_out, not_130_out, not_131_out, not_132_out, not_133_out,
       not_134_out, not_135_out, not_136_out, not_137_out, not_138_out, not_139_out, not_140_out,
       not_141_out, not_142_out, not_143_out, not_144_out, not_145_out, not_146_out, not_147_out,
       not_148_out, not_149_out, not_150_out, not_151_out, not_152_out, not_153_out, not_154_out,
       not_155_out, not_156_out, not_157_out, not_158_out, not_159_out, not_160_out, not_161_out,
       not_162_out, not_163_out, not_164_out, not_165_out, not_166_out, not_167_out, not_168_out,
       not_169_out, not_170_out, not_171_out, not_172_out, not_173_out, not_174_out, not_175_out,
       not_176_out, not_177_out, not_178_out, not_179_out, not_180_out, not_181_out, not_182_out,
       not_183_out, not_184_out, not_185_out, not_186_out, not_187_out, not_188_out, not_189_out,
       not_190_out, not_191_out, not_192_out, not_193_out, not_194_out, not_195_out, not_196_out,
       not_197_out, not_198_out, not_199_out, not_200_out, not_201_out, not_202_out, not_203_out;

  not not_1 (not_1_out, OP2);
  not not_2 (not_2_out, OP3);
  not not_3 (not_3_out, OP4);
  not not_4 (not_4_out, OP2);
  not not_5 (not_5_out, OP4);
  not not_6 (not_6_out, OP1);
  not not_7 (not_7_out, OP4);
  not not_8 (not_8_out, OP5);
  not not_9 (not_9_out, OP2);
  not not_10 (not_10_out, OP4);
  not not_11 (not_11_out, OP5);
  not not_12 (not_12_out, OP2);
  not not_13 (not_13_out, OP4);
  not not_14 (not_14_out, OP2);
  not not_15 (not_15_out, OP4);
  not not_16 (not_16_out, OP0);
  not not_17 (not_17_out, OP1);
  not not_18 (not_18_out, OP2);
  not not_19 (not_19_out, OP4);
  not not_20 (not_20_out, OP5);
  not not_21 (not_21_out, F0);
  not not_22 (not_22_out, F1);
  not not_23 (not_23_out, F3);
  not not_24 (not_24_out, F4);
  not not_25 (not_25_out, OP0);
  not not_26 (not_26_out, OP1);
  not not_27 (not_27_out, OP2);
  not not_28 (not_28_out, OP4);
  not not_29 (not_29_out, OP5);
  not not_30 (not_30_out, F0);
  not not_31 (not_31_out, F2);
  not not_32 (not_32_out, F3);
  not not_33 (not_33_out, F4);
  not not_34 (not_34_out, OP0);
  not not_35 (not_35_out, OP1);
  not not_36 (not_36_out, OP2);
  not not_37 (not_37_out, OP4);
  not not_38 (not_38_out, OP5);
  not not_39 (not_39_out, F1);
  not not_40 (not_40_out, F3);
  not not_41 (not_41_out, F4);
  not not_42 (not_42_out, OP0);
  not not_43 (not_43_out, OP1);
  not not_44 (not_44_out, OP2);
  not not_45 (not_45_out, OP4);
  not not_46 (not_46_out, OP5);
  not not_47 (not_47_out, F2);
  not not_48 (not_48_out, F3);
  not not_49 (not_49_out, F4);
  not not_50 (not_50_out, F5);
  not not_51 (not_51_out, OP0);
  not not_52 (not_52_out, OP1);
  not not_53 (not_53_out, OP2);
  not not_54 (not_54_out, OP4);
  not not_55 (not_55_out, OP5);
  not not_56 (not_56_out, F2);
  not not_57 (not_57_out, F4);
  not not_58 (not_58_out, OP0);
  not not_59 (not_59_out, OP1);
  not not_60 (not_60_out, OP2);
  not not_61 (not_61_out, OP4);
  not not_62 (not_62_out, OP5);
  not not_63 (not_63_out, F3);
  not not_64 (not_64_out, F4);
  not not_65 (not_65_out, OP1);
  not not_66 (not_66_out, OP4);
  not not_67 (not_67_out, OP5);
  not not_68 (not_68_out, OP2);
  not not_69 (not_69_out, OP4);
  not not_70 (not_70_out, OP5);
  not not_71 (not_71_out, OP2);
  not not_72 (not_72_out, OP3);
  not not_73 (not_73_out, OP4);
  not not_74 (not_74_out, OP0);
  not not_75 (not_75_out, OP1);
  not not_76 (not_76_out, OP2);
  not not_77 (not_77_out, OP3);
  not not_78 (not_78_out, OP4);
  not not_79 (not_79_out, OP5);
  not not_80 (not_80_out, F0);
  not not_81 (not_81_out, F1);
  not not_82 (not_82_out, F4);
  not not_83 (not_83_out, F5);
  not not_84 (not_84_out, OP0);
  not not_85 (not_85_out, OP1);
  not not_86 (not_86_out, OP4);
  not not_87 (not_87_out, OP5);
  not not_88 (not_88_out, OP0);
  not not_89 (not_89_out, OP3);
  not not_90 (not_90_out, OP4);
  not not_91 (not_91_out, OP5);
  not not_92 (not_92_out, OP1);
  not not_93 (not_93_out, OP4);
  not not_94 (not_94_out, OP5);
  not not_95 (not_95_out, OP2);
  not not_96 (not_96_out, OP4);
  not not_97 (not_97_out, OP5);
  not not_98 (not_98_out, OP2);
  not not_99 (not_99_out, OP4);
  not not_100 (not_100_out, OP2);
  not not_101 (not_101_out, OP4);
  not not_102 (not_102_out, OP0);
  not not_103 (not_103_out, OP1);
  not not_104 (not_104_out, OP2);
  not not_105 (not_105_out, OP3);
  not not_106 (not_106_out, OP4);
  not not_107 (not_107_out, OP5);
  not not_108 (not_108_out, F0);
  not not_109 (not_109_out, F1);
  not not_110 (not_110_out, F3);
  not not_111 (not_111_out, F4);
  not not_112 (not_112_out, OP0);
  not not_113 (not_113_out, OP1);
  not not_114 (not_114_out, OP2);
  not not_115 (not_115_out, OP3);
  not not_116 (not_116_out, OP4);
  not not_117 (not_117_out, OP5);
  not not_118 (not_118_out, F0);
  not not_119 (not_119_out, F2);
  not not_120 (not_120_out, F3);
  not not_121 (not_121_out, F4);
  not not_122 (not_122_out, OP0);
  not not_123 (not_123_out, OP1);
  not not_124 (not_124_out, OP2);
  not not_125 (not_125_out, OP3);
  not not_126 (not_126_out, OP4);
  not not_127 (not_127_out, OP5);
  not not_128 (not_128_out, F1);
  not not_129 (not_129_out, F3);
  not not_130 (not_130_out, F4);
  not not_131 (not_131_out, OP0);
  not not_132 (not_132_out, OP1);
  not not_133 (not_133_out, OP2);
  not not_134 (not_134_out, OP3);
  not not_135 (not_135_out, OP4);
  not not_136 (not_136_out, OP5);
  not not_137 (not_137_out, F2);
  not not_138 (not_138_out, F3);
  not not_139 (not_139_out, F4);
  not not_140 (not_140_out, F5);
  not not_141 (not_141_out, OP0);
  not not_142 (not_142_out, OP1);
  not not_143 (not_143_out, OP2);
  not not_144 (not_144_out, OP3);
  not not_145 (not_145_out, OP4);
  not not_146 (not_146_out, OP5);
  not not_147 (not_147_out, F2);
  not not_148 (not_148_out, F4);
  not not_149 (not_149_out, OP0);
  not not_150 (not_150_out, OP1);
  not not_151 (not_151_out, OP2);
  not not_152 (not_152_out, OP3);
  not not_153 (not_153_out, OP4);
  not not_154 (not_154_out, OP5);
  not not_155 (not_155_out, F3);
  not not_156 (not_156_out, F4);
  not not_157 (not_157_out, OP0);
  not not_158 (not_158_out, OP1);
  not not_159 (not_159_out, OP3);
  not not_160 (not_160_out, OP4);
  not not_161 (not_161_out, OP5);
  not not_162 (not_162_out, OP1);
  not not_163 (not_163_out, OP3);
  not not_164 (not_164_out, OP4);
  not not_165 (not_165_out, OP5);
  not not_166 (not_166_out, OP0);
  not not_167 (not_167_out, OP1);
  not not_168 (not_168_out, OP2);
  not not_169 (not_169_out, OP3);
  not not_170 (not_170_out, OP4);
  not not_171 (not_171_out, OP5);
  not not_172 (not_172_out, F0);
  not not_173 (not_173_out, F1);
  not not_174 (not_174_out, F2);
  not not_175 (not_175_out, F4);
  not not_176 (not_176_out, F5);
  not not_177 (not_177_out, OP0);
  not not_178 (not_178_out, OP2);
  not not_179 (not_179_out, OP3);
  not not_180 (not_180_out, OP4);
  not not_181 (not_181_out, OP5);
  not not_182 (not_182_out, OP2);
  not not_183 (not_183_out, OP3);
  not not_184 (not_184_out, OP4);
  not not_185 (not_185_out, OP5);
  not not_186 (not_186_out, OP0);
  not not_187 (not_187_out, OP1);
  not not_188 (not_188_out, OP2);
  not not_189 (not_189_out, OP3);
  not not_190 (not_190_out, OP4);
  not not_191 (not_191_out, OP5);
  not not_192 (not_192_out, F0);
  not not_193 (not_193_out, F1);
  not not_194 (not_194_out, F3);
  not not_195 (not_195_out, F4);
  not not_196 (not_196_out, F5);
  not not_197 (not_197_out, OP0);
  not not_198 (not_198_out, OP3);
  not not_199 (not_199_out, OP4);
  not not_200 (not_200_out, OP5);
  not not_201 (not_201_out, OP1);
  not not_202 (not_202_out, OP2);
  not not_203 (not_203_out, OP4);
  and and_1 (MemToReg, OP0, OP1, not_1_out, not_2_out, not_3_out, OP5);
  and and_2 (MemWrite, OP0, not_4_out, OP3, not_5_out, OP5);
  and and_3 (and_3_out, not_6_out, OP3, not_7_out, not_8_out);
  and and_4 (and_4_out, not_9_out, OP3, not_10_out, not_11_out);
  and and_5 (and_5_out, OP0, not_12_out, OP3, not_13_out);
  and and_6 (and_6_out, OP0, OP1, not_14_out, not_15_out, OP5);
  and and_7 (and_7_out, not_16_out, not_17_out, not_18_out, not_19_out, not_20_out, not_21_out, not_22_out, not_23_out, not_24_out);
  and and_8 (and_8_out, not_25_out, not_26_out, not_27_out, not_28_out, not_29_out, not_30_out, not_31_out, not_32_out, not_33_out);
  and and_9 (and_9_out, not_34_out, not_35_out, not_36_out, not_37_out, not_38_out, not_39_out, not_40_out, not_41_out, F5);
  and and_10 (and_10_out, not_42_out, not_43_out, not_44_out, not_45_out, not_46_out, F1, not_47_out, not_48_out, not_49_out, not_50_out);
  and and_11 (and_11_out, not_51_out, not_52_out, not_53_out, not_54_out, not_55_out, F1, not_56_out, F3, not_57_out, F5);
  and and_12 (and_12_out, not_58_out, not_59_out, not_60_out, not_61_out, not_62_out, F0, F2, not_63_out, not_64_out, F5);
  and and_13 (and_13_out, not_65_out, OP3, not_66_out, not_67_out);
  and and_14 (and_14_out, not_68_out, OP3, not_69_out, not_70_out);
  and and_15 (and_15_out, OP0, OP1, not_71_out, not_72_out, not_73_out);
  and and_16 (SysCALL, not_74_out, not_75_out, not_76_out, not_77_out, not_78_out, not_79_out, not_80_out, not_81_out, F2, F3, not_82_out, not_83_out);
  and and_17 (and_17_out, not_84_out, not_85_out, OP3, not_86_out, not_87_out);
  and and_18 (and_18_out, not_88_out, OP2, not_89_out, not_90_out, not_91_out);
  and and_19 (and_19_out, not_92_out, OP2, not_93_out, not_94_out);
  and and_20 (and_20_out, OP1, not_95_out, OP3, not_96_out, not_97_out);
  and and_21 (and_21_out, OP0, not_98_out, OP3, not_99_out, OP5);
  and and_22 (and_22_out, OP0, OP1, not_100_out, not_101_out, OP5);
  and and_23 (and_23_out, not_102_out, not_103_out, not_104_out, not_105_out, not_106_out, not_107_out, not_108_out, not_109_out, not_110_out, not_111_out);
  and and_24 (and_24_out, not_112_out, not_113_out, not_114_out, not_115_out, not_116_out, not_117_out, not_118_out, not_119_out, not_120_out, not_121_out);
  and and_25 (and_25_out, not_122_out, not_123_out, not_124_out, not_125_out, not_126_out, not_127_out, not_128_out, not_129_out, not_130_out, F5);
  and and_26 (and_26_out, not_131_out, not_132_out, not_133_out, not_134_out, not_135_out, not_136_out, F1, not_137_out, not_138_out, not_139_out, not_140_out);
  and and_27 (and_27_out, not_141_out, not_142_out, not_143_out, not_144_out, not_145_out, not_146_out, F1, not_147_out, F3, not_148_out, F5);
  and and_28 (and_28_out, not_149_out, not_150_out, not_151_out, not_152_out, not_153_out, not_154_out, F0, F2, not_155_out, not_156_out, F5);
  and and_29 (BEQ, not_157_out, not_158_out, OP2, not_159_out, not_160_out, not_161_out);
  and and_30 (BNE, OP0, not_162_out, OP2, not_163_out, not_164_out, not_165_out);
  and and_31 (JR, not_166_out, not_167_out, not_168_out, not_169_out, not_170_out, not_171_out, not_172_out, not_173_out, not_174_out, F3, not_175_out, not_176_out);
  and and_32 (JUMP, not_177_out, OP1, not_178_out, not_179_out, not_180_out, not_181_out);
  and and_33 (JAL, OP0, OP1, not_182_out, not_183_out, not_184_out, not_185_out);
  and and_34 (Vshamt, not_186_out, not_187_out, not_188_out, not_189_out, not_190_out, not_191_out, not_192_out, not_193_out, F2, not_194_out, not_195_out, not_196_out);
  and and_35 (BLEZ, not_197_out, OP1, OP2, not_198_out, not_199_out, not_200_out);
  and and_36 (HalfW, OP0, not_201_out, not_202_out, OP3, not_203_out, OP5);
  or or_1 (ALU_SRC, and_3_out, and_4_out, and_5_out, and_6_out);
  or or_2 (RegWrite, and_7_out, and_8_out, and_9_out, and_10_out, and_11_out, and_12_out, and_13_out, and_14_out, and_15_out);
  or or_3 (SignedExt, and_17_out, and_18_out, and_19_out, and_20_out, and_21_out, and_22_out);
  or or_4 (RegDst, and_23_out, and_24_out, and_25_out, and_26_out, and_27_out, and_28_out);
endmodule

// ALU
module MIPS_ALU (
  input  [4:0] shamt,
  input  [31:0] X,
  input  [31:0] Y,
  input  [3:0] AluOP,
  output Equal,
  output [31:0] Result,
  output [31:0] Result_2,
  output Less
);

  wire [0:0] comparator_1_lt, comparator_2_lt;
  wire [31:0] adder_1_out, AND_out, divider_1_out, divider_1_rem, multiplier_1_cout, multiplier_1_out,
       NOR_out, OR_out, shifter_1_out, shifter_2_out, shifter_3_out, subtractor_1_out, XOR_out;

  assign AND_out = X & Y;  // AND_Gate AND, 32 bits wide
  assign OR_out = X | Y;  // OR_Gate OR, 32 bits wide
  Shifter #(.width(32), .shift("ll")) shifter_1 (.in(Y), .\dist (shamt), .out(shifter_1_out));
  Shifter #(.width(32), .shift("ar")) shifter_2 (.in(Y), .\dist (shamt), .out(shifter_2_out));
  Shifter #(.width(32), .shift("lr")) shifter_3 (.in(Y), .\dist (shamt), .out(shifter_3_out));
  Multiplier #(.width(32)) multiplier_1 (.a(X), .b(Y), .out(multiplier_1_out), .cout(multiplier_1_cout));  // open: cin
  Divider #(.width(32)) divider_1 (.a(X), .b(Y), .out(divider_1_out), .rem(divider_1_rem));  // open: upper
  Adder #(.width(32)) adder_1 (.a(X), .b(Y), .out(adder_1_out));  // open: cin, cout
  Subtractor #(.width(32)) subtractor_1 (.a(X), .b(Y), .out(subtractor_1_out));  // open: bin, bout
  assign XOR_out = X ^ Y;  // XOR_Gate XOR, 32 bits wide
  assign NOR_out = ~(X | Y);  // NOR_Gate NOR, 32 bits wide
  Comparator #(.width(32), .mode("twosComplement")) comparator_1 (
    .a(X), .b(Y), .eq(Equal), .lt(comparator_1_lt[0]));  // open: gt
  Comparator #(.width(32), .mode("unsigned")) comparator_2 (.a(X), .b(Y), .lt(comparator_2_lt[0]));  // open: gt, eq
  Comparator #(.width(32), .mode("twosComplement")) comparator_3 (.a(X), .b(Y), .lt(Less));  // open: gt, eq
  Multiplexer #(.select(4), .width(32), .disabled(0), .enable("false")) multiplexer_1 (
    .in0(shifter_1_out), .in1(shifter_2_out), .in2(shifter_3_out), .in3(multiplier_1_out),
    .in4(divider_1_out), .in5(adder_1_out), .in6(subtractor_1_out), .in7(AND_out), .in8(OR_out),
    .in9(XOR_out), .in10(NOR_out), .in11({{31{1'b0}}, comparator_1_lt[0]}),
    .in12({{31{1'b0}}, comparator_2_lt[0]}), .in13({32{1'b0}}), .in14({32{1'b0}}), .in15({32{1'b0}}),
    .out(Result), .sel(AluOP));
  Multiplexer #(.select(4), .width(32), .disabled(0), .enable("false")) multiplexer_2 (
    .in0({32{1'b0}}), .in1({32{1'b0}}), .in2({32{1'b0}}), .in3(multiplier_1_cout), .in4(divider_1_rem),
    .in5({32{1'b0}}), .in6({32{1'b0}}), .in7({32{1'b0}}), .in8({32{1'b0}}), .in9({32{1'b0}}),
    .in10({32{1'b0}}), .in11({32{1'b0}}), .in12({32{1'b0}}), .in13({32{1'b0}}), .in14({32{1'b0}}),
    .in15({32{1'b0}}), .out(Result_2), .sel(AluOP));

  // Other names for the same wires on the sheet: Result2[31:0] = Result_2; S[3:0] = AluOP

  // Notes on the sheet:
  //   不要改变此引脚区域内容，也不要改变ALU封装形式
  //   输入引脚
  //   输出引脚
endmodule

module MIPS_Regifile (
  input  [31:0] Din,
  input  Clk,
  input  WE,
  input  [4:0] R1_num,
  input  [4:0] W_num,
  input  [4:0] R2_num,
  output [31:0] R1,
  output [31:0] R2
);

  // RegisterFile registerfile_1: pin names not known; wires that end beside it: Din, Clk, WE, W_num, R1_num, R2_num, R1, R2
endmodule

module \理想流水线  (
  output RegWrite,
  output MemWrite,
  output [31:0] IF_PC,
  output [31:0] ID_PC,
  output [31:0] EX_PC,
  output [31:0] M_PC,
  output [31:0] WB_PC,
  output [31:0] RDin,
  output [31:0] MDin,
  output [31:0] LedData
);

  wire Beq, Blez, Bne, CLK, clock_1_out, clock_2_out, comparator_1_eq, comparator_1_lt, d_ff_1_q, Equal,
       ex_mem_1_halfw_out, ex_mem_1_jal_out, ex_mem_1_memtoreg_out, ex_mem_1_regwrite_out,
       ex_mem_1_syscall_out, Go, id_ex_1_alusrcb_out, id_ex_1_halfw_out, id_ex_1_memtoreg_out,
       id_ex_1_memwrite_out, id_ex_1_regwrite_out, id_ex_1_syscall_out, IR1, IR2, IR3, JAL, JAL_WB, JMP, JR,
       Less, mem_wb_1_p10, nand_1_out, Pause, RegDst, RST, SignedExt, Syscall, Vshamt, W1, W2, W3;
  wire [3:0] id_ex_1_aluop_out, \单周期硬布线控制器_1_alu_op ;
  wire [4:0] ex_mem_1_w__out, id_ex_1_shamt_out, id_ex_1_w__out, mem_wb_1_p14, multiplexer_2_out,
       \reg选择逻辑_1_r1_num , \reg选择逻辑_1_r2_num , \reg选择逻辑_1_shamt , \reg选择逻辑_1_w_num ;
  wire [5:0] Func, OP, \单周期硬布线控制器_1_jr ;
  wire [8:0] \单周期硬布线控制器_1_memtoreg ;
  wire [12:0] CNT_num;
  wire [15:0] \LoadUse次数 , \总周期数 , \插入气泡数 , \无条件分支数 , \条件分支成功数 ;
  wire [27:8] if_id_1_instr_out;
  wire [31:0] adder_1_out, adder_2_out, bit_extender_1_out, bit_extender_2_out, EX_IR,
       ex_mem_1_aluresult_out, ex_mem_1_r1_out, id_ex_1_extdata_out, id_ex_1_pc_4_out, id_ex_1_r2_out, ID_IR,
       if_id_1_pc_4_out, IF_IR, IR, MEM_IR, mem_wb_1_p12, mem_wb_1_p13, mips_alu_1_result,
       mips_mem_1_memreaddata, mips_regifile_1_r1, mips_regifile_1_r2, multiplexer_1_out, multiplexer_3_out,
       multiplexer_4_out, \pc更新逻辑_1_pc_next , R1, WB_IR;

  Button \u_总复位  (.out(RST));
  Button _1 (.out(IR1));
  Button _2 (.out(IR2));
  Button _3 (.out(IR3));
  // Probe on \总周期数 
  // Probe on \总周期数 
  Button \u_继续运行  (.out(Go));
  LED #(.active("true")) led_1 (.in(W1));
  LED #(.active("true")) led_2 (.in(W2));
  LED #(.active("true")) led_3 (.in(W3));
  \PC更新逻辑  \pc更新逻辑_1  (
    .Equal(Equal), .Beq(Beq), .Bne(Bne), .JAL(JAL), .JMP(JMP), .JR(JR), .BAddr(adder_2_out),
    .PC_4(adder_1_out), .JAddr({ID_PC[31:28], if_id_1_instr_out, Func, 2'b00}), .JRAddr(R1),
    .PC_Next(\pc更新逻辑_1_pc_next ), .Blez(Blez), .Less(Less));  // open: Branched, BranchSig
  Hex_Digit_Display hex_digit_display_1 (.value(LedData[31:28]));  // open: dp
  // Probe on IF_PC[19:0]
  // Mips_Probe mips_probe_1: pin names not known; wires that end beside it: IF_IR
  D_Flip_Flop #(.trigger("high"), .Pre_Clr_Positions("LEGACY"), .NegatePresetClear("false"), .enable("true"), .NewFFLayout("false")) d_ff_1 (
    .Q(d_ff_1_q), .preset(Pause), .reset(Go));  // open: clk, D, Qn, en
  // Probe on 13'hc
  Hex_Digit_Display hex_digit_display_2 (.value(LedData[23:20]));  // open: dp
  Hex_Digit_Display hex_digit_display_3 (.value(LedData[27:24]));  // open: dp
  // Probe on ID_PC[19:0]
  // Mips_Probe mips_probe_2: pin names not known; wires that end beside it: ID_IR
  Register #(.width(32), .trigger("rising"), .Select("low")) PC (
    .D(\pc更新逻辑_1_pc_next ), .Q(IF_PC), .clk(CLK));  // open: en, clr
  Comparator #(.width(13), .mode("twosComplement")) comparator_1 (
    .a(CNT_num), .b(13'hc), .eq(comparator_1_eq), .lt(comparator_1_lt));  // open: gt
  Clock #(.highDuration(1), .lowDuration(1)) clock_1 (.out(clock_1_out));
  Hex_Digit_Display hex_digit_display_4 (.value(LedData[19:16]));  // open: dp
  Hex_Digit_Display hex_digit_display_5 (.value(LedData[15:12]));  // open: dp
  Adder #(.width(32)) adder_1 (.a(IF_PC), .b(32'h4), .out(adder_1_out));  // open: cin, cout
  nand nand_1 (nand_1_out, d_ff_1_q, comparator_1_eq);
  Counter #(.width(13), .max('h1fff), .ongoal("stay"), .trigger("rising"), .behavior("old")) counter_1 (
    .count(comparator_1_lt), .Q(CNT_num), .clk(clock_1_out));  // open: load, D, carry, clr, preset
  Hex_Digit_Display hex_digit_display_6 (.value(LedData[7:4]));  // open: dp
  Hex_Digit_Display hex_digit_display_7 (.value(LedData[11:8]));  // open: dp
  Clock #(.highDuration(1), .lowDuration(1)) clock_2 (.out(clock_2_out));
  // Probe on EX_PC[19:0]
  // Mips_Probe mips_probe_3: pin names not known; wires that end beside it: clock_2_out, EX_IR, CLK
  ROM #(.addrWidth(10), .dataWidth(32), .Select("low")) rom_1 (.addr(IF_PC[11:2]), .data(IR));
  Hex_Digit_Display hex_digit_display_8 (.value(LedData[3:0]));  // open: dp
  // Mips_Probe mips_probe_4: pin names not known; wires that end beside it: IR
  assign CLK = nand_1_out ? clock_1_out : 1'bz;  // Controlled_Buffer controlled_buffer_1
  Pull_Resistor #(.pull(1)) pull_resistor_1 (.node(CLK));
  // Probe on \总周期数 
  // Probe on M_PC[19:0]
  // Mips_Probe mips_probe_5: pin names not known; wires that end beside it: MEM_IR
  IF_ID if_id_1 (
    .CLK(CLK), .Instr(IR), .Instr_Out({OP, if_id_1_instr_out, Func}), .PC_4(adder_1_out),
    .PC_4_Out(if_id_1_pc_4_out), .PC(IF_PC), .PC_Out(ID_PC), .CLR(1'b0));  // open: Stall, Eff, PredictJump, PredictJump_Out
  // Probe on \总周期数 
  // Probe on \无条件分支数 
  // Probe on \条件分支成功数 
  // Probe on \插入气泡数 
  // Probe on \LoadUse次数 
  Counter #(.width(16), .max('hffff), .ongoal("wrap"), .trigger("rising"), .behavior("new")) counter_2 (
    .Q(\总周期数 ), .clk(CLK));  // open: load, D, count, carry, clr, preset, down
  // Probe on IF_PC[11:0]
  // Probe on WB_PC[19:0]
  // Mips_Probe mips_probe_6: pin names not known; wires that end beside it: WB_IR
  \单周期硬布线控制器  \u_单周期硬布线控制器_1  (
    .Func(Func), .OP(OP), .ALU_OP(\单周期硬布线控制器_1_alu_op ), .MemToReg(\单周期硬布线控制器_1_memtoreg [0]),
    .MemWrite(\单周期硬布线控制器_1_memtoreg [2]), .ALU_SRC(\单周期硬布线控制器_1_memtoreg [8]),
    .RegWrite(\单周期硬布线控制器_1_memtoreg [1]), .SysCALL(Syscall), .SignedExt(SignedExt), .RegDst(RegDst),
    .JR(\单周期硬布线控制器_1_jr [0]), .JMP(JMP), .Beq(\单周期硬布线控制器_1_jr [4]), .JAL(\单周期硬布线控制器_1_jr [2]),
    .Bne(\单周期硬布线控制器_1_jr [5]), .Vshamt(Vshamt), .BLEZ(\单周期硬布线控制器_1_jr [3]), .HalfW(\单周期硬布线控制器_1_memtoreg [3]));
  // Probe on ID_PC[11:0]
  // Probe on EX_PC[11:0]
  \Reg选择逻辑  \reg选择逻辑_1  (
    ._21_25(if_id_1_instr_out[27:23]), .Syscall(Syscall), .RegDst(RegDst), ._16_20(if_id_1_instr_out[22:18]),
    ._11_15(if_id_1_instr_out[17:13]), .JAL(JAL_WB), .PC_4(if_id_1_pc_4_out),
    .WriteBack_Data(multiplexer_4_out), ._6_10(if_id_1_instr_out[12:8]), .R1_num(\reg选择逻辑_1_r1_num ),
    .R2_num(\reg选择逻辑_1_r2_num ), .W_num(\reg选择逻辑_1_w_num ), .RDin(RDin), .Shamt(\reg选择逻辑_1_shamt ));
  assign bit_extender_1_out = {{16{1'b0}}, {if_id_1_instr_out[17:8], Func}};  // Bit_Extender bit_extender_1
  assign bit_extender_2_out = {{16{if_id_1_instr_out[17]}}, {if_id_1_instr_out[17:8], Func}};  // Bit_Extender bit_extender_2
  // Probe on M_PC[11:0]
  Multiplexer #(.select(1), .width(32), .disabled("Z"), .enable("false")) multiplexer_1 (
    .in0(bit_extender_1_out), .in1(bit_extender_2_out), .out(multiplexer_1_out), .sel(SignedExt));
  // Probe on WB_PC[11:0]
  MIPS_Regifile mips_regifile_1 (
    .Din(RDin), .Clk(CLK), .R1(mips_regifile_1_r1), .R2(mips_regifile_1_r2), .WE(RegWrite),
    .W_num(mem_wb_1_p14), .R1_num(\reg选择逻辑_1_r1_num ), .R2_num(\reg选择逻辑_1_r2_num ));
  Multiplexer #(.select(1), .width(5), .disabled("Z"), .enable("false")) multiplexer_2 (
    .in0(\reg选择逻辑_1_shamt ), .in1(R1[4:0]), .out(multiplexer_2_out), .sel(Vshamt));
  ID_EX id_ex_1 (
    .JR(\单周期硬布线控制器_1_jr [0]), .JMP(JMP), .JAL(\单周期硬布线控制器_1_jr [2]), .BLEZ(\单周期硬布线控制器_1_jr [3]),
    .BEQ(\单周期硬布线控制器_1_jr [4]), .BNE(\单周期硬布线控制器_1_jr [5]), .MemToReg(\单周期硬布线控制器_1_memtoreg [0]),
    .Shamt(multiplexer_2_out), .R1(mips_regifile_1_r1), .R2(mips_regifile_1_r2), .JR_Out(JR), .JAL_Out(JAL),
    .BLEZ_Out(Blez), .BEQ_Out(Beq), .BNE_Out(Bne), .MemToReg_Out(id_ex_1_memtoreg_out),
    .Shamt_Out(id_ex_1_shamt_out), .R1_Out(R1), .R2_Out(id_ex_1_r2_out), .CLK(CLK),
    .AluOp(\单周期硬布线控制器_1_alu_op ), .AluOp_Out(id_ex_1_aluop_out), .ExtData(multiplexer_1_out),
    .W_num(\reg选择逻辑_1_w_num ), .RegWrite(\单周期硬布线控制器_1_memtoreg [1]), .RegWrite_Out(id_ex_1_regwrite_out),
    .MemWrite_Out(id_ex_1_memwrite_out), .HalfW_Out(id_ex_1_halfw_out), .AluSrcB_Out(id_ex_1_alusrcb_out),
    .Syscall_Out(id_ex_1_syscall_out), .MemWrite(\单周期硬布线控制器_1_memtoreg [2]),
    .HalfW(\单周期硬布线控制器_1_memtoreg [3]), .AluSrcB(\单周期硬布线控制器_1_memtoreg [8]), .Syscall(Syscall),
    .ExtData_Out(id_ex_1_extdata_out), .W__Out(id_ex_1_w__out), .PC(ID_PC), .PC_Out(EX_PC), .CLR(1'b0),
    .PC_4(if_id_1_pc_4_out), .PC_4_Out(id_ex_1_pc_4_out));  // open: JMP_Out, JAddr, JAddr_Out, Eff_in, Eff, R1_Forward, R1_Forward_Out, Instr, Instr_out, R2_Forward, R2_Forward_Out, PredictJump, PredictJump_Out
  Multiplexer #(.select(1), .width(32), .disabled("Z"), .enable("false")) multiplexer_3 (
    .in0(id_ex_1_r2_out), .in1(id_ex_1_extdata_out), .out(multiplexer_3_out), .sel(id_ex_1_alusrcb_out));
  MIPS_ALU mips_alu_1 (
    .X(R1), .Y(multiplexer_3_out), .AluOP(id_ex_1_aluop_out), .Equal(Equal), .Result(mips_alu_1_result),
    .shamt(id_ex_1_shamt_out), .Less(Less));  // open: Result_2
  Adder #(.width(32)) adder_2 (
    .a(id_ex_1_pc_4_out), .b({id_ex_1_extdata_out[29:0], 2'b00}), .out(adder_2_out));  // open: cin, cout
  EX_MEM ex_mem_1 (
    .MemToReg(id_ex_1_memtoreg_out), .RegWrite(id_ex_1_regwrite_out), .MemWrite(id_ex_1_memwrite_out),
    .HalfW(id_ex_1_halfw_out), .AluResult(mips_alu_1_result), .R2(id_ex_1_r2_out), .W_num(id_ex_1_w__out),
    .CLK(CLK), .MemToReg_Out(ex_mem_1_memtoreg_out), .RegWrite_Out(ex_mem_1_regwrite_out),
    .MemWrite_Out(MemWrite), .HalfW_Out(ex_mem_1_halfw_out), .AluResult_Out(ex_mem_1_aluresult_out),
    .R2_Out(MDin), .W__Out(ex_mem_1_w__out), .PC(EX_PC), .PC_Out(M_PC), .R1(R1), .R1_Out(ex_mem_1_r1_out),
    .Syscall(id_ex_1_syscall_out), .Syscall_Out(ex_mem_1_syscall_out), .CLR(1'b0), .JAL(JAL),
    .JAL_Out(ex_mem_1_jal_out));  // open: PC_4, PC_4_Out, Eff_in, Eff, Instr, Instr_out
  \Syscall处理  \syscall处理_1  (
    .Syscall(ex_mem_1_syscall_out), .CLK(CLK), .R2(MDin), .R1(ex_mem_1_r1_out), .Pause(Pause),
    .LedData(LedData));
  MIPS_MEM mips_mem_1 (
    .AluResult(ex_mem_1_aluresult_out), .HalfW(ex_mem_1_halfw_out), .WriteData(MDin), .MemWrite(MemWrite),
    .CLK(CLK), .MemReadData(mips_mem_1_memreaddata));
  // MEM_WB mem_wb_1: pin names not known; wires that end beside it: ex_mem_1_jal_out, ex_mem_1_memtoreg_out, ex_mem_1_regwrite_out, ex_mem_1_aluresult_out, mips_mem_1_memreaddata, ex_mem_1_w__out, M_PC, CLK, JAL_WB, mem_wb_1_p10, RegWrite, mem_wb_1_p12, mem_wb_1_p13, mem_wb_1_p14, WB_PC
  Multiplexer #(.select(1), .width(32), .disabled("Z"), .enable("false")) multiplexer_4 (
    .in0(mem_wb_1_p12), .in1(mem_wb_1_p13), .out(multiplexer_4_out), .sel(mem_wb_1_p10));

  // Other names for the same wires on the sheet: MEM_PC[31:0] = M_PC

  // Notes on the sheet:
  //   中断源
  //   时空图监测，可删除
  //   中断等待指示
  //   控制位
  //   戳工具置1进入计数暂停模式，ctrl+k时钟自动运行到对应节拍暂停
  //   ctrl+k关闭时钟连续运行，将控制位置零，进入单步调试模式调试
  //   用这个时钟源需要去掉电路中的其他时钟源
  //   数码管输出
  //   指令存储器
  //   contents of rom_1 (hex, n*v repeats v):
  //   20100000 20110000 20120000 20130000 36100000 36310001 36520002 36730003 ae100000 ae110004 ae120008
  //   ae13000c 2002000a 20110000 20120000 20130000 c
  //   可计数暂停的时钟源
  //   指令字
  //   JR
  //   JMP
  //   JAL
  //   BLEZ
  //   BEQ
  //   BNE
  //   MemToReg
  //   RegWrite
  //   MemWrite
  //   HalfW
  //   AluOp
  //   AluSrcB
  //   流水调试日志用
  //   为方便自动评测，需要输出流水线各段保存的PC值，注意是PC不是PC+4，另外ID段寄存器写入信息，Mem段内存写入信息也要输出
endmodule

module \气泡流水线  (
  output RegWrite,
  output MemWrite,
  output [31:0] IF_PC,
  output [31:0] ID_PC,
  output [31:0] EX_PC,
  output [31:0] M_PC,
  output [31:0] WB_PC,
  output [31:0] RDin,
  output [31:0] MDin,
  output [31:0] LedData
);

  wire Beq, Blez, Bne, CLK, clock_1_out, clock_2_out, comparator_1_eq, comparator_1_lt, d_ff_1_q, Equal,
       ex_mem_1_halfw_out, ex_mem_1_jal_out, ex_mem_1_memtoreg_out, ex_mem_1_regwrite_out,
       ex_mem_1_syscall_out, Go, id_ex_1_alusrcb_out, id_ex_1_eff, id_ex_1_halfw_out, id_ex_1_memtoreg_out,
       id_ex_1_memwrite_out, id_ex_1_regwrite_out, id_ex_1_syscall_out, if_id_1_eff, IR1, IR2, IR3, JAL,
       JAL_WB, JMP, JR, Less, mem_wb_1_memtoreg_out, MemEff, nand_1_out, not_1_out, not_2_out, or_1_out,
       or_2_out, Pause, \pc更新逻辑_1_branched , RegDst, RST, SignedExt, Syscall, Vshamt, W1, W2, W3,
       \气泡流水冲突处理_1_stall_pc_id , \气泡流水冲突处理_2_stall_pc_id ;
  wire [3:0] id_ex_1_aluop_out, \单周期硬布线控制器_1_alu_op ;
  wire [4:0] ex_mem_1_w__out, id_ex_1_shamt_out, id_ex_1_w__out, mem_wb_1_w__out, multiplexer_3_out,
       \reg选择逻辑_1_r1_num , \reg选择逻辑_1_r2_num , \reg选择逻辑_1_shamt , \reg选择逻辑_1_w_num ;
  wire [5:0] Func, \单周期硬布线控制器_1_jr ;
  wire [8:0] \单周期硬布线控制器_1_memtoreg ;
  wire [12:0] CNT_num;
  wire [15:0] \LoadUse次数 , \总周期数 , \插入气泡数 , \无条件分支数 , \条件分支成功数 ;
  wire [31:0] adder_1_out, adder_2_out, bit_extender_1_out, bit_extender_2_out, EX_IR,
       ex_mem_1_aluresult_out, ex_mem_1_pc_4_out, ex_mem_1_r1_out, id_ex_1_extdata_out, id_ex_1_jaddr_out,
       id_ex_1_pc_4_out, id_ex_1_r2_out, if_id_1_pc_4_out, IF_IR, MEM_IR, mem_wb_1_aluresult_out,
       mem_wb_1_pc_4_out, mem_wb_1_r2_out, mips_alu_1_result, mips_mem_1_memreaddata, mips_regifile_1_r1,
       mips_regifile_1_r2, multiplexer_1_out, multiplexer_4_out, multiplexer_5_out, \pc更新逻辑_1_pc_next , R1,
       WB_IR;
  wire [31:6] ID_IR;

  Button \u_总复位  (.out(RST));
  Button _1 (.out(IR1));
  Button _2 (.out(IR2));
  Button _3 (.out(IR3));
  // Probe on \总周期数 
  // Probe on \总周期数 
  Button \u_继续运行  (.out(Go));
  LED #(.active("true")) led_1 (.in(W1));
  LED #(.active("true")) led_2 (.in(W2));
  LED #(.active("true")) led_3 (.in(W3));
  \PC更新逻辑  \pc更新逻辑_1  (
    .Equal(Equal), .Beq(Beq), .Bne(Bne), .JAL(JAL), .JMP(JMP), .JR(JR), .BAddr(adder_2_out),
    .PC_4(adder_1_out), .JAddr(id_ex_1_jaddr_out), .JRAddr(R1), .PC_Next(\pc更新逻辑_1_pc_next ), .Blez(Blez),
    .Less(Less), .Branched(\pc更新逻辑_1_branched ));  // open: BranchSig
  Hex_Digit_Display hex_digit_display_1 (.value(LedData[31:28]));  // open: dp
  // Probe on IF_PC[19:0]
  // Mips_Probe mips_probe_1: pin names not known; wires that end beside it: IF_IR
  D_Flip_Flop #(.trigger("high"), .Pre_Clr_Positions("LEGACY"), .NegatePresetClear("false"), .enable("true"), .NewFFLayout("false")) d_ff_1 (
    .Q(d_ff_1_q), .preset(Pause), .reset(Go));  // open: clk, D, Qn, en
  // Probe on 13'h624
  Hex_Digit_Display hex_digit_display_2 (.value(LedData[23:20]));  // open: dp
  Hex_Digit_Display hex_digit_display_3 (.value(LedData[27:24]));  // open: dp
  // Probe on ID_PC[19:0]
  // Mips_Probe mips_probe_2: pin names not known; wires that end beside it: {ID_IR, Func}
  Register #(.width(32), .trigger("rising"), .Select("low")) PC (
    .D(\pc更新逻辑_1_pc_next ), .en(not_2_out), .Q(IF_PC), .clk(CLK));  // open: clr
  Comparator #(.width(13), .mode("twosComplement")) comparator_1 (
    .a(CNT_num), .b(13'h624), .eq(comparator_1_eq), .lt(comparator_1_lt));  // open: gt
  Clock #(.highDuration(1), .lowDuration(1)) clock_1 (.out(clock_1_out));
  Hex_Digit_Display hex_digit_display_4 (.value(LedData[19:16]));  // open: dp
  Hex_Digit_Display hex_digit_display_5 (.value(LedData[15:12]));  // open: dp
  Adder #(.width(32)) adder_1 (.a(IF_PC), .b(32'h4), .out(adder_1_out));  // open: cin, cout
  nand nand_1 (nand_1_out, d_ff_1_q, comparator_1_eq);
  Counter #(.width(13), .max('h1fff), .ongoal("stay"), .trigger("rising"), .behavior("old")) counter_1 (
    .count(comparator_1_lt), .Q(CNT_num), .clk(clock_1_out));  // open: load, D, carry, clr, preset
  Hex_Digit_Display hex_digit_display_6 (.value(LedData[7:4]));  // open: dp
  Hex_Digit_Display hex_digit_display_7 (.value(LedData[11:8]));  // open: dp
  Clock #(.highDuration(1), .lowDuration(1)) clock_2 (.out(clock_2_out));
  // Probe on EX_PC[19:0]
  // Mips_Probe mips_probe_3: pin names not known; wires that end beside it: clock_2_out, EX_IR, CLK
  ROM #(.addrWidth(10), .dataWidth(32), .Select("low")) rom_1 (.addr(IF_PC[11:2]), .data(IF_IR));
  Hex_Digit_Display hex_digit_display_8 (.value(LedData[3:0]));  // open: dp
  // Mips_Probe mips_probe_4: pin names not known; wires that end beside it: IF_IR
  assign CLK = nand_1_out ? clock_1_out : 1'bz;  // Controlled_Buffer controlled_buffer_1
  Pull_Resistor #(.pull(1)) pull_resistor_1 (.node(CLK));
  // Probe on \总周期数 
  // Probe on M_PC[19:0]
  // Mips_Probe mips_probe_5: pin names not known; wires that end beside it: MEM_IR
  IF_ID if_id_1 (
    .CLK(CLK), .Instr(IF_IR), .Instr_Out({ID_IR, Func}), .PC_4(adder_1_out), .PC_4_Out(if_id_1_pc_4_out),
    .PC(IF_PC), .PC_Out(ID_PC), .CLR(\pc更新逻辑_1_branched ), .Stall(not_2_out), .Eff(if_id_1_eff));  // open: PredictJump, PredictJump_Out
  // Probe on \总周期数 
  // Probe on \无条件分支数 
  // Probe on \条件分支成功数 
  // Probe on \插入气泡数 
  // Probe on \LoadUse次数 
  Counter #(.width(16), .max('hffff), .ongoal("wrap"), .trigger("rising"), .behavior("new")) counter_2 (
    .Q(\总周期数 ), .clk(CLK));  // open: load, D, count, carry, clr, preset, down
  // Probe on IF_PC[11:0]
  // Probe on WB_PC[19:0]
  // Mips_Probe mips_probe_6: pin names not known; wires that end beside it: WB_IR
  \单周期硬布线控制器  \u_单周期硬布线控制器_1  (
    .Func(Func), .OP(ID_IR[31:26]), .ALU_OP(\单周期硬布线控制器_1_alu_op ), .MemToReg(\单周期硬布线控制器_1_memtoreg [0]),
    .MemWrite(\单周期硬布线控制器_1_memtoreg [2]), .ALU_SRC(\单周期硬布线控制器_1_memtoreg [8]),
    .RegWrite(\单周期硬布线控制器_1_memtoreg [1]), .SysCALL(Syscall), .SignedExt(SignedExt), .RegDst(RegDst),
    .JR(\单周期硬布线控制器_1_jr [0]), .JMP(\单周期硬布线控制器_1_jr [1]), .Beq(\单周期硬布线控制器_1_jr [4]),
    .JAL(\单周期硬布线控制器_1_jr [2]), .Bne(\单周期硬布线控制器_1_jr [5]), .Vshamt(Vshamt), .BLEZ(\单周期硬布线控制器_1_jr [3]),
    .HalfW(\单周期硬布线控制器_1_memtoreg [3]));
  // Probe on ID_PC[11:0]
  // Probe on EX_PC[11:0]
  \Reg选择逻辑  \reg选择逻辑_1  (
    ._21_25(ID_IR[25:21]), .Syscall(Syscall), .RegDst(RegDst), ._16_20(ID_IR[20:16]), ._11_15(ID_IR[15:11]),
    .JAL(\单周期硬布线控制器_1_jr [2]), ._6_10(ID_IR[10:6]), .R1_num(\reg选择逻辑_1_r1_num ), .R2_num(\reg选择逻辑_1_r2_num ),
    .W_num(\reg选择逻辑_1_w_num ), .Shamt(\reg选择逻辑_1_shamt ));  // open: PC_4, WriteBack_Data, RDin
  assign bit_extender_1_out = {{16{1'b0}}, {ID_IR[15:6], Func}};  // Bit_Extender bit_extender_1
  assign bit_extender_2_out = {{16{ID_IR[15]}}, {ID_IR[15:6], Func}};  // Bit_Extender bit_extender_2
  // Probe on M_PC[11:0]
  Multiplexer #(.select(1), .width(32), .disabled("Z"), .enable("false")) multiplexer_1 (
    .in0(bit_extender_1_out), .in1(bit_extender_2_out), .out(multiplexer_1_out), .sel(SignedExt));
  Multiplexer #(.select(1), .width(32), .disabled("Z"), .enable("false")) multiplexer_2 (
    .in0(multiplexer_5_out), .in1(mem_wb_1_pc_4_out), .out(RDin), .sel(JAL_WB));
  // Probe on WB_PC[11:0]
  not not_1 (not_1_out, CLK);
  MIPS_Regifile mips_regifile_1 (
    .Din(RDin), .Clk(not_1_out), .R1(mips_regifile_1_r1), .R2(mips_regifile_1_r2), .WE(RegWrite),
    .W_num(mem_wb_1_w__out), .R1_num(\reg选择逻辑_1_r1_num ), .R2_num(\reg选择逻辑_1_r2_num ));
  Multiplexer #(.select(1), .width(5), .disabled("Z"), .enable("false")) multiplexer_3 (
    .in0(\reg选择逻辑_1_shamt ), .in1(mips_regifile_1_r1[4:0]), .out(multiplexer_3_out), .sel(Vshamt));
  not not_2 (not_2_out, or_2_out);
  or or_1 (or_1_out, \pc更新逻辑_1_branched , or_2_out);
  ID_EX id_ex_1 (
    .JR(\单周期硬布线控制器_1_jr [0]), .JMP(\单周期硬布线控制器_1_jr [1]), .JAL(\单周期硬布线控制器_1_jr [2]),
    .BLEZ(\单周期硬布线控制器_1_jr [3]), .BEQ(\单周期硬布线控制器_1_jr [4]), .BNE(\单周期硬布线控制器_1_jr [5]),
    .MemToReg(\单周期硬布线控制器_1_memtoreg [0]), .Shamt(multiplexer_3_out), .R1(mips_regifile_1_r1),
    .R2(mips_regifile_1_r2), .JR_Out(JR), .JMP_Out(JMP), .JAL_Out(JAL), .BLEZ_Out(Blez), .BEQ_Out(Beq),
    .BNE_Out(Bne), .MemToReg_Out(id_ex_1_memtoreg_out), .Shamt_Out(id_ex_1_shamt_out), .R1_Out(R1),
    .R2_Out(id_ex_1_r2_out), .CLK(CLK), .AluOp(\单周期硬布线控制器_1_alu_op ), .AluOp_Out(id_ex_1_aluop_out),
    .ExtData(multiplexer_1_out), .W_num(\reg选择逻辑_1_w_num ), .RegWrite(\单周期硬布线控制器_1_memtoreg [1]),
    .RegWrite_Out(id_ex_1_regwrite_out), .MemWrite_Out(id_ex_1_memwrite_out), .HalfW_Out(id_ex_1_halfw_out),
    .AluSrcB_Out(id_ex_1_alusrcb_out), .Syscall_Out(id_ex_1_syscall_out),
    .MemWrite(\单周期硬布线控制器_1_memtoreg [2]), .HalfW(\单周期硬布线控制器_1_memtoreg [3]),
    .AluSrcB(\单周期硬布线控制器_1_memtoreg [8]), .Syscall(Syscall), .ExtData_Out(id_ex_1_extdata_out),
    .W__Out(id_ex_1_w__out), .PC(ID_PC), .PC_Out(EX_PC), .CLR(or_1_out),
    .JAddr({ID_PC[31:28], ID_IR[25:6], Func, 2'b00}), .JAddr_Out(id_ex_1_jaddr_out), .PC_4(if_id_1_pc_4_out),
    .PC_4_Out(id_ex_1_pc_4_out), .Eff_in(if_id_1_eff), .Eff(id_ex_1_eff), .Instr({ID_IR, Func}),
    .Instr_out(EX_IR));  // open: R1_Forward, R1_Forward_Out, R2_Forward, R2_Forward_Out, PredictJump, PredictJump_Out
  or or_2 (or_2_out, \气泡流水冲突处理_2_stall_pc_id , \气泡流水冲突处理_1_stall_pc_id );
  \气泡流水冲突处理  \u_气泡流水冲突处理_1  (
    .R1_num(\reg选择逻辑_1_r1_num ), .W_num(id_ex_1_w__out), .R2_num(\reg选择逻辑_1_r2_num ),
    .CLR(\pc更新逻辑_1_branched ), .RegWrite(id_ex_1_regwrite_out), .Stall_PC_ID(\气泡流水冲突处理_1_stall_pc_id ),
    .AluSrc(\单周期硬布线控制器_1_memtoreg [8]));  // open: R1_CF, R2_CF
  Multiplexer #(.select(1), .width(32), .disabled("Z"), .enable("false")) multiplexer_4 (
    .in0(id_ex_1_r2_out), .in1(id_ex_1_extdata_out), .out(multiplexer_4_out), .sel(id_ex_1_alusrcb_out));
  \气泡流水冲突处理  \u_气泡流水冲突处理_2  (
    .R1_num(\reg选择逻辑_1_r1_num ), .W_num(ex_mem_1_w__out), .R2_num(\reg选择逻辑_1_r2_num ),
    .CLR(\pc更新逻辑_1_branched ), .RegWrite(ex_mem_1_regwrite_out), .Stall_PC_ID(\气泡流水冲突处理_2_stall_pc_id ),
    .AluSrc(\单周期硬布线控制器_1_memtoreg [8]));  // open: R1_CF, R2_CF
  MIPS_ALU mips_alu_1 (
    .X(R1), .Y(multiplexer_4_out), .AluOP(id_ex_1_aluop_out), .Equal(Equal), .Result(mips_alu_1_result),
    .shamt(id_ex_1_shamt_out), .Less(Less));  // open: Result_2
  Adder #(.width(32)) adder_2 (
    .a(id_ex_1_pc_4_out), .b({id_ex_1_extdata_out[29:0], 2'b00}), .out(adder_2_out));  // open: cin, cout
  EX_MEM ex_mem_1 (
    .MemToReg(id_ex_1_memtoreg_out), .RegWrite(id_ex_1_regwrite_out), .MemWrite(id_ex_1_memwrite_out),
    .HalfW(id_ex_1_halfw_out), .AluResult(mips_alu_1_result), .R2(id_ex_1_r2_out), .W_num(id_ex_1_w__out),
    .CLK(CLK), .MemToReg_Out(ex_mem_1_memtoreg_out), .RegWrite_Out(ex_mem_1_regwrite_out),
    .MemWrite_Out(MemWrite), .HalfW_Out(ex_mem_1_halfw_out), .AluResult_Out(ex_mem_1_aluresult_out),
    .R2_Out(MDin), .W__Out(ex_mem_1_w__out), .PC(EX_PC), .PC_Out(M_PC), .R1(R1), .R1_Out(ex_mem_1_r1_out),
    .Syscall(id_ex_1_syscall_out), .Syscall_Out(ex_mem_1_syscall_out), .CLR(1'b0), .JAL(JAL),
    .JAL_Out(ex_mem_1_jal_out), .PC_4(id_ex_1_pc_4_out), .PC_4_Out(ex_mem_1_pc_4_out), .Eff_in(id_ex_1_eff),
    .Eff(MemEff), .Instr(EX_IR), .Instr_out(MEM_IR));
  \Syscall处理  \syscall处理_1  (
    .Syscall(ex_mem_1_syscall_out), .CLK(CLK), .R2(MDin), .R1(ex_mem_1_r1_out), .Pause(Pause),
    .LedData(LedData));
  MIPS_MEM mips_mem_1 (
    .AluResult(ex_mem_1_aluresult_out), .HalfW(ex_mem_1_halfw_out), .WriteData(MDin), .MemWrite(MemWrite),
    .CLK(CLK), .MemReadData(mips_mem_1_memreaddata));
  MEM_WB mem_wb_1 (
    .MemToReg(ex_mem_1_memtoreg_out), .RegWrite(ex_mem_1_regwrite_out), .AluResult(ex_mem_1_aluresult_out),
    .R2(mips_mem_1_memreaddata), .W_num(ex_mem_1_w__out), .CLK(CLK), .MemToReg_Out(mem_wb_1_memtoreg_out),
    .RegWrite_Out(RegWrite), .AluResult_Out(mem_wb_1_aluresult_out), .R2_Out(mem_wb_1_r2_out),
    .W__Out(mem_wb_1_w__out), .PC(M_PC), .PC_Out(WB_PC), .JAL(ex_mem_1_jal_out), .JAL_Out(JAL_WB),
    .PC_4(ex_mem_1_pc_4_out), .PC_4_Out(mem_wb_1_pc_4_out), .Eff_in(MemEff), .Instr(MEM_IR), .Instr_out(WB_IR));  // open: Eff
  Multiplexer #(.select(1), .width(32), .disabled("Z"), .enable("false")) multiplexer_5 (
    .in0(mem_wb_1_aluresult_out), .in1(mem_wb_1_r2_out), .out(multiplexer_5_out), .sel(mem_wb_1_memtoreg_out));

  // Other names for the same wires on the sheet: ID_IR[5:0] = Func; OP[5:0] = ID_IR[31:26]; IR[31:0] = IF_IR;
  //   MEM_PC[31:0] = M_PC

  // Notes on the sheet:
  //   中断源
  //   时空图监测，可删除
  //   中断等待指示
  //   控制位
  //   戳工具置1进入计数暂停模式，ctrl+k时钟自动运行到对应节拍暂停
  //   ctrl+k关闭时钟连续运行，将控制位置零，进入单步调试模式调试
  //   用这个时钟源需要去掉电路中的其他时钟源
  //   数码管输出
  //   指令存储器
  //   contents of rom_1 (hex, n*v repeats v):
  //   20110001 8000c05 20110001 20120002 20130003 8000c09 20110001 20120002 20130003 8000c0d 20110001
  //   20120002 20130003 8000c11 20110001 20120002 20130003 c000cb8 20100001 20110001 118fc0 112020
  //   20020022 c 118882 12200001 8000c15 112020 20020022 c 20110001 118880 112020 20020022 c 12200001
  //   8000c1f 20110001 118fc0 112020 20020022 c 1188c3 112020 20020022 c 118903 112020 20020022 c 118903
  //   112020 20020022 c 118903 112020 20020022 c 118903 112020 20020022 c 118903 112020 20020022 c 118903
  //   112020 20020022 c 118903 112020 20020022 c 20100001 109fc0 139fc3 8021 2012000c 24160003 26100001
  //   3210000f 20080008 20090001 139900 2709825 132020 20020022 c 1094022 1500fff9 22100001 2018000f
  //   2188024 108700 20080008 20090001 139902 2709825 132021 20020022 c 1094022 1500fff9 108702 2c9b022
  //   12c00001 8000c50 4020 1084027 84400 3508ffff 82021 20020022 c 2010ffff 20110000 ae300000 22100001
  //   22310004 ae300000 22100001 22310004 ae300000 22100001 22310004 ae300000 22100001 22310004 ae300000
  //   22100001 22310004 ae300000 22100001 22310004 ae300000 22100001 22310004 ae300000 22100001 22310004
  //   ae300000 22100001 22310004 ae300000 22100001 22310004 ae300000 22100001 22310004 ae300000 22100001
  //   22310004 ae300000 22100001 22310004 ae300000 22100001 22310004 ae300000 22100001 22310004 ae300000
  //   22100001 22310004 22100001 8020 2011003c 8e130000 8e340000 274402a 11000002 ae330000 ae140000
  //   2231fffc 1611fff8 102020 20020022 c 22100004 2011003c 1611fff2 20020032 c 20100000 22100001 102020
  //   20020022 c 22100002 102020 20020022 c 22100003 102020 20020022 c 22100004 102020 20020022 c 22100005
  //   102020 20020022 c 22100006 102020 20020022 c 22100007 102020 20020022 c 22100008 102020 20020022
  //   20020022 c 3e00008
  //   可计数暂停的时钟源
  //   指令字
  //   IF/ID
  //   JR
  //   JMP
  //   JAL
  //   BLEZ
  //   BEQ
  //   BNE
  //   MemToReg
  //   RegWrite
  //   MemWrite
  //   HalfW
  //   AluOp
  //   AluSrcB
  //   流水调试日志用
  //   为方便自动评测，需要输出流水线各段保存的PC值，注意是PC不是PC+4，另外ID段寄存器写入信息，Mem段内存写入信息也要输出
endmodule

module \重定向流水线  (
  output RegWrite,
  output MemWrite,
  output [31:0] IF_PC,
  output [31:0] ID_PC,
  output [31:0] EX_PC,
  output [31:0] M_PC,
  output [31:0] WB_PC,
  output [31:0] RDin,
  output [31:0] MDin,
  output [31:0] LedData
);

  wire Beq, Blez, Bne, CLK, clock_1_out, clock_2_out, comparator_1_eq, comparator_1_lt, d_ff_1_q, Equal,
       ex_mem_1_halfw_out, ex_mem_1_jal_out, ex_mem_1_memtoreg_out, ex_mem_1_regwrite_out,
       ex_mem_1_syscall_out, Go, id_ex_1_alusrcb_out, id_ex_1_eff, id_ex_1_halfw_out, id_ex_1_memtoreg_out,
       id_ex_1_memwrite_out, id_ex_1_regwrite_out, id_ex_1_syscall_out, if_id_1_eff, IR1, IR2, IR3, JAL,
       JAL_WB, JMP, JR, Less, mem_wb_1_memtoreg_out, MemEff, nand_1_out, not_1_out, not_2_out, or_1_out,
       Pause, \pc更新逻辑_1_branched , RegDst, RST, SignedExt, Syscall, Vshamt, W1, W2, W3,
       \重定向数据旁路控制信号生成_1_stall ;
  wire [1:0] id_ex_1_r1_forward_out, id_ex_1_r2_forward_out, \重定向数据旁路控制信号生成_1_r1_forward ,
       \重定向数据旁路控制信号生成_1_r2_forward ;
  wire [3:0] id_ex_1_aluop_out, \单周期硬布线控制器_1_alu_op ;
  wire [4:0] ex_mem_1_w__out, id_ex_1_shamt_out, id_ex_1_w__out, mem_wb_1_w__out, multiplexer_3_out,
       \reg选择逻辑_1_r1_num , \reg选择逻辑_1_r2_num , \reg选择逻辑_1_shamt , \reg选择逻辑_1_w_num ;
  wire [5:0] Func, \单周期硬布线控制器_1_jr ;
  wire [8:0] \单周期硬布线控制器_1_memtoreg ;
  wire [12:0] CNT_num;
  wire [15:0] \LoadUse次数 , \总周期数 , \插入气泡数 , \无条件分支数 , \条件分支成功数 ;
  wire [31:0] adder_1_out, adder_2_out, bit_extender_1_out, bit_extender_2_out, EX_IR,
       ex_mem_1_aluresult_out, ex_mem_1_pc_4_out, ex_mem_1_r1_out, id_ex_1_extdata_out, id_ex_1_jaddr_out,
       id_ex_1_pc_4_out, id_ex_1_r1_out, id_ex_1_r2_out, if_id_1_pc_4_out, IF_IR, MEM_IR,
       mem_wb_1_aluresult_out, mem_wb_1_pc_4_out, mem_wb_1_r2_out, mips_alu_1_result, mips_mem_1_memreaddata,
       mips_regifile_1_r1, mips_regifile_1_r2, multiplexer_1_out, multiplexer_5_out, multiplexer_6_out,
       multiplexer_7_out, \pc更新逻辑_1_pc_next , R1, WB_IR;
  wire [31:6] ID_IR;

  Button \u_总复位  (.out(RST));
  Button _1 (.out(IR1));
  Button _2 (.out(IR2));
  Button _3 (.out(IR3));
  // Probe on \总周期数 
  // Probe on \总周期数 
  Button \u_继续运行  (.out(Go));
  LED #(.active("true")) led_1 (.in(W1));
  LED #(.active("true")) led_2 (.in(W2));
  LED #(.active("true")) led_3 (.in(W3));
  \PC更新逻辑  \pc更新逻辑_1  (
    .Equal(Equal), .Beq(Beq), .Bne(Bne), .JAL(JAL), .JMP(JMP), .JR(JR), .BAddr(adder_2_out),
    .PC_4(adder_1_out), .JAddr(id_ex_1_jaddr_out), .JRAddr(R1), .PC_Next(\pc更新逻辑_1_pc_next ), .Blez(Blez),
    .Less(Less), .Branched(\pc更新逻辑_1_branched ));  // open: BranchSig
  Hex_Digit_Display hex_digit_display_1 (.value(LedData[31:28]));  // open: dp
  // Probe on IF_PC[19:0]
  // Mips_Probe mips_probe_1: pin names not known; wires that end beside it: IF_IR
  D_Flip_Flop #(.trigger("high"), .Pre_Clr_Positions("LEGACY"), .NegatePresetClear("false"), .enable("true"), .NewFFLayout("false")) d_ff_1 (
    .Q(d_ff_1_q), .preset(Pause), .reset(Go));  // open: clk, D, Qn, en
  // Probe on 13'h8f6
  Hex_Digit_Display hex_digit_display_2 (.value(LedData[27:24]));  // open: dp
  Hex_Digit_Display hex_digit_display_3 (.value(LedData[23:20]));  // open: dp
  // Probe on ID_PC[19:0]
  // Mips_Probe mips_probe_2: pin names not known; wires that end beside it: {ID_IR, Func}
  Register #(.width(32), .trigger("rising"), .Select("low")) PC (
    .D(\pc更新逻辑_1_pc_next ), .en(not_1_out), .Q(IF_PC), .clk(CLK));  // open: clr
  Comparator #(.width(13), .mode("twosComplement")) comparator_1 (
    .a(CNT_num), .b(13'h8f6), .eq(comparator_1_eq), .lt(comparator_1_lt));  // open: gt
  Clock #(.highDuration(1), .lowDuration(1)) clock_1 (.out(clock_1_out));
  Hex_Digit_Display hex_digit_display_4 (.value(LedData[19:16]));  // open: dp
  Hex_Digit_Display hex_digit_display_5 (.value(LedData[15:12]));  // open: dp
  Adder #(.width(32)) adder_1 (.a(IF_PC), .b(32'h4), .out(adder_1_out));  // open: cin, cout
  nand nand_1 (nand_1_out, d_ff_1_q, comparator_1_eq);
  Counter #(.width(13), .max('h1fff), .ongoal("stay"), .trigger("rising"), .behavior("old")) counter_1 (
    .count(comparator_1_lt), .Q(CNT_num), .clk(clock_1_out));  // open: load, D, carry, clr, preset
  Hex_Digit_Display hex_digit_display_6 (.value(LedData[7:4]));  // open: dp
  Hex_Digit_Display hex_digit_display_7 (.value(LedData[11:8]));  // open: dp
  Clock #(.highDuration(1), .lowDuration(1)) clock_2 (.out(clock_2_out));
  // Probe on EX_PC[19:0]
  // Mips_Probe mips_probe_3: pin names not known; wires that end beside it: clock_2_out, EX_IR, CLK
  ROM #(.addrWidth(10), .dataWidth(32), .Select("low")) rom_1 (.addr(IF_PC[11:2]), .data(IF_IR));
  Hex_Digit_Display hex_digit_display_8 (.value(LedData[3:0]));  // open: dp
  // Mips_Probe mips_probe_4: pin names not known; wires that end beside it: IF_IR
  assign CLK = nand_1_out ? clock_1_out : 1'bz;  // Controlled_Buffer controlled_buffer_1
  Pull_Resistor #(.pull(1)) pull_resistor_1 (.node(CLK));
  // Probe on \总周期数 
  // Probe on M_PC[19:0]
  // Mips_Probe mips_probe_5: pin names not known; wires that end beside it: MEM_IR
  not not_1 (not_1_out, \重定向数据旁路控制信号生成_1_stall );
  IF_ID if_id_1 (
    .CLK(CLK), .Instr(IF_IR), .Instr_Out({ID_IR, Func}), .PC_4(adder_1_out), .PC_4_Out(if_id_1_pc_4_out),
    .PC(IF_PC), .PC_Out(ID_PC), .CLR(\pc更新逻辑_1_branched ), .Stall(not_1_out), .Eff(if_id_1_eff));  // open: PredictJump, PredictJump_Out
  // Probe on \总周期数 
  // Probe on \无条件分支数 
  // Probe on \条件分支成功数 
  // Probe on \插入气泡数 
  // Probe on \LoadUse次数 
  Counter #(.width(16), .max('hffff), .ongoal("wrap"), .trigger("rising"), .behavior("new")) counter_2 (
    .Q(\总周期数 ), .clk(CLK));  // open: load, D, count, carry, clr, preset, down
  // Probe on IF_PC[11:0]
  // Probe on WB_PC[19:0]
  // Mips_Probe mips_probe_6: pin names not known; wires that end beside it: WB_IR
  \单周期硬布线控制器  \u_单周期硬布线控制器_1  (
    .Func(Func), .OP(ID_IR[31:26]), .ALU_OP(\单周期硬布线控制器_1_alu_op ), .MemToReg(\单周期硬布线控制器_1_memtoreg [0]),
    .MemWrite(\单周期硬布线控制器_1_memtoreg [2]), .ALU_SRC(\单周期硬布线控制器_1_memtoreg [8]),
    .RegWrite(\单周期硬布线控制器_1_memtoreg [1]), .SysCALL(Syscall), .SignedExt(SignedExt), .RegDst(RegDst),
    .JR(\单周期硬布线控制器_1_jr [0]), .JMP(\单周期硬布线控制器_1_jr [1]), .Beq(\单周期硬布线控制器_1_jr [4]),
    .JAL(\单周期硬布线控制器_1_jr [2]), .Bne(\单周期硬布线控制器_1_jr [5]), .Vshamt(Vshamt), .BLEZ(\单周期硬布线控制器_1_jr [3]),
    .HalfW(\单周期硬布线控制器_1_memtoreg [3]));
  // Probe on ID_PC[11:0]
  // Probe on EX_PC[11:0]
  \Reg选择逻辑  \reg选择逻辑_1  (
    ._21_25(ID_IR[25:21]), .Syscall(Syscall), .RegDst(RegDst), ._16_20(ID_IR[20:16]), ._11_15(ID_IR[15:11]),
    .JAL(\单周期硬布线控制器_1_jr [2]), ._6_10(ID_IR[10:6]), .R1_num(\reg选择逻辑_1_r1_num ), .R2_num(\reg选择逻辑_1_r2_num ),
    .W_num(\reg选择逻辑_1_w_num ), .Shamt(\reg选择逻辑_1_shamt ));  // open: PC_4, WriteBack_Data, RDin
  assign bit_extender_1_out = {{16{1'b0}}, {ID_IR[15:6], Func}};  // Bit_Extender bit_extender_1
  assign bit_extender_2_out = {{16{ID_IR[15]}}, {ID_IR[15:6], Func}};  // Bit_Extender bit_extender_2
  // Probe on M_PC[11:0]
  Multiplexer #(.select(1), .width(32), .disabled("Z"), .enable("false")) multiplexer_1 (
    .in0(bit_extender_1_out), .in1(bit_extender_2_out), .out(multiplexer_1_out), .sel(SignedExt));
  Multiplexer #(.select(1), .width(32), .disabled("Z"), .enable("false")) multiplexer_2 (
    .in0(multiplexer_7_out), .in1(mem_wb_1_pc_4_out), .out(RDin), .sel(JAL_WB));
  // Probe on WB_PC[11:0]
  not not_2 (not_2_out, CLK);
  MIPS_Regifile mips_regifile_1 (
    .Din(RDin), .Clk(not_2_out), .R1(mips_regifile_1_r1), .R2(mips_regifile_1_r2), .WE(RegWrite),
    .W_num(mem_wb_1_w__out), .R1_num(\reg选择逻辑_1_r1_num ), .R2_num(\reg选择逻辑_1_r2_num ));
  Multiplexer #(.select(1), .width(5), .disabled("Z"), .enable("false")) multiplexer_3 (
    .in0(\reg选择逻辑_1_shamt ), .in1(mips_regifile_1_r1[4:0]), .out(multiplexer_3_out), .sel(Vshamt));
  or or_1 (or_1_out, \pc更新逻辑_1_branched , \重定向数据旁路控制信号生成_1_stall );
  ID_EX id_ex_1 (
    .JR(\单周期硬布线控制器_1_jr [0]), .JMP(\单周期硬布线控制器_1_jr [1]), .JAL(\单周期硬布线控制器_1_jr [2]),
    .BLEZ(\单周期硬布线控制器_1_jr [3]), .BEQ(\单周期硬布线控制器_1_jr [4]), .BNE(\单周期硬布线控制器_1_jr [5]),
    .MemToReg(\单周期硬布线控制器_1_memtoreg [0]), .Shamt(multiplexer_3_out), .R1(mips_regifile_1_r1),
    .R2(mips_regifile_1_r2), .JR_Out(JR), .JMP_Out(JMP), .JAL_Out(JAL), .BLEZ_Out(Blez), .BEQ_Out(Beq),
    .BNE_Out(Bne), .MemToReg_Out(id_ex_1_memtoreg_out), .Shamt_Out(id_ex_1_shamt_out),
    .R1_Out(id_ex_1_r1_out), .R2_Out(id_ex_1_r2_out), .CLK(CLK), .AluOp(\单周期硬布线控制器_1_alu_op ),
    .AluOp_Out(id_ex_1_aluop_out), .ExtData(multiplexer_1_out), .W_num(\reg选择逻辑_1_w_num ),
    .RegWrite(\单周期硬布线控制器_1_memtoreg [1]), .RegWrite_Out(id_ex_1_regwrite_out),
    .MemWrite_Out(id_ex_1_memwrite_out), .HalfW_Out(id_ex_1_halfw_out), .AluSrcB_Out(id_ex_1_alusrcb_out),
    .Syscall_Out(id_ex_1_syscall_out), .MemWrite(\单周期硬布线控制器_1_memtoreg [2]),
    .HalfW(\单周期硬布线控制器_1_memtoreg [3]), .AluSrcB(\单周期硬布线控制器_1_memtoreg [8]), .Syscall(Syscall),
    .ExtData_Out(id_ex_1_extdata_out), .W__Out(id_ex_1_w__out), .PC(ID_PC), .PC_Out(EX_PC), .CLR(or_1_out),
    .JAddr({ID_PC[31:28], ID_IR[25:6], Func, 2'b00}), .JAddr_Out(id_ex_1_jaddr_out), .PC_4(if_id_1_pc_4_out),
    .PC_4_Out(id_ex_1_pc_4_out), .Eff_in(if_id_1_eff), .Eff(id_ex_1_eff),
    .R1_Forward(\重定向数据旁路控制信号生成_1_r1_forward ), .R1_Forward_Out(id_ex_1_r1_forward_out),
    .Instr({ID_IR, Func}), .Instr_out(EX_IR), .R2_Forward(\重定向数据旁路控制信号生成_1_r2_forward ),
    .R2_Forward_Out(id_ex_1_r2_forward_out));  // open: PredictJump, PredictJump_Out
  Multiplexer #(.select(2), .width(32), .disabled("Z"), .enable("false")) multiplexer_4 (
    .in0(id_ex_1_r1_out), .in1(mem_wb_1_aluresult_out), .in2(mem_wb_1_r2_out), .in3(ex_mem_1_aluresult_out),
    .out(R1), .sel(id_ex_1_r1_forward_out));
  Multiplexer #(.select(2), .width(32), .disabled("Z"), .enable("false")) multiplexer_5 (
    .in0(id_ex_1_r2_out), .in1(mem_wb_1_aluresult_out), .in2(mem_wb_1_r2_out), .in3(ex_mem_1_aluresult_out),
    .out(multiplexer_5_out), .sel(id_ex_1_r2_forward_out));
  Adder #(.width(32)) adder_2 (
    .a(id_ex_1_pc_4_out), .b({id_ex_1_extdata_out[29:0], 2'b00}), .out(adder_2_out));  // open: cin, cout
  \重定向数据旁路控制信号生成  \u_重定向数据旁路控制信号生成_1  (
    .ID_AluSrc(\单周期硬布线控制器_1_memtoreg [8]), .BranchCLR(\pc更新逻辑_1_branched ), .ID_R1_num(\reg选择逻辑_1_r1_num ),
    .ID_R2_num(\reg选择逻辑_1_r2_num ), .EX_W_num(id_ex_1_w__out), .MEM_W_num(ex_mem_1_w__out),
    .EX_RegWrite(id_ex_1_regwrite_out), .MEM_RegWrite(ex_mem_1_regwrite_out),
    .MEM_MemToReg(ex_mem_1_memtoreg_out), .R1_Forward(\重定向数据旁路控制信号生成_1_r1_forward ),
    .R2_Forward(\重定向数据旁路控制信号生成_1_r2_forward ), .ID_IR({ID_IR, Func}), .EX_IR(EX_IR),
    .Stall(\重定向数据旁路控制信号生成_1_stall ));
  Multiplexer #(.select(1), .width(32), .disabled("Z"), .enable("false")) multiplexer_6 (
    .in0(multiplexer_5_out), .in1(id_ex_1_extdata_out), .out(multiplexer_6_out), .sel(id_ex_1_alusrcb_out));
  MIPS_ALU mips_alu_1 (
    .X(R1), .Y(multiplexer_6_out), .AluOP(id_ex_1_aluop_out), .Equal(Equal), .Result(mips_alu_1_result),
    .shamt(id_ex_1_shamt_out), .Less(Less));  // open: Result_2
  EX_MEM ex_mem_1 (
    .MemToReg(id_ex_1_memtoreg_out), .RegWrite(id_ex_1_regwrite_out), .MemWrite(id_ex_1_memwrite_out),
    .HalfW(id_ex_1_halfw_out), .AluResult(mips_alu_1_result), .R2(multiplexer_5_out), .W_num(id_ex_1_w__out),
    .CLK(CLK), .MemToReg_Out(ex_mem_1_memtoreg_out), .RegWrite_Out(ex_mem_1_regwrite_out),
    .MemWrite_Out(MemWrite), .HalfW_Out(ex_mem_1_halfw_out), .AluResult_Out(ex_mem_1_aluresult_out),
    .R2_Out(MDin), .W__Out(ex_mem_1_w__out), .PC(EX_PC), .PC_Out(M_PC), .R1(R1), .R1_Out(ex_mem_1_r1_out),
    .Syscall(id_ex_1_syscall_out), .Syscall_Out(ex_mem_1_syscall_out), .CLR(1'b0), .JAL(JAL),
    .JAL_Out(ex_mem_1_jal_out), .PC_4(id_ex_1_pc_4_out), .PC_4_Out(ex_mem_1_pc_4_out), .Eff_in(id_ex_1_eff),
    .Eff(MemEff), .Instr(EX_IR), .Instr_out(MEM_IR));
  \Syscall处理  \syscall处理_1  (
    .Syscall(ex_mem_1_syscall_out), .CLK(CLK), .R2(MDin), .R1(ex_mem_1_r1_out), .Pause(Pause),
    .LedData(LedData));
  MIPS_MEM mips_mem_1 (
    .AluResult(ex_mem_1_aluresult_out), .HalfW(ex_mem_1_halfw_out), .WriteData(MDin), .MemWrite(MemWrite),
    .CLK(CLK), .MemReadData(mips_mem_1_memreaddata));
  Multiplexer #(.select(1), .width(32), .disabled("Z"), .enable("false")) multiplexer_7 (
    .in0(mem_wb_1_aluresult_out), .in1(mem_wb_1_r2_out), .out(multiplexer_7_out), .sel(mem_wb_1_memtoreg_out));
  MEM_WB mem_wb_1 (
    .MemToReg(ex_mem_1_memtoreg_out), .RegWrite(ex_mem_1_regwrite_out), .AluResult(ex_mem_1_aluresult_out),
    .R2(mips_mem_1_memreaddata), .W_num(ex_mem_1_w__out), .CLK(CLK), .MemToReg_Out(mem_wb_1_memtoreg_out),
    .RegWrite_Out(RegWrite), .AluResult_Out(mem_wb_1_aluresult_out), .R2_Out(mem_wb_1_r2_out),
    .W__Out(mem_wb_1_w__out), .PC(M_PC), .PC_Out(WB_PC), .JAL(ex_mem_1_jal_out), .JAL_Out(JAL_WB),
    .PC_4(ex_mem_1_pc_4_out), .PC_4_Out(mem_wb_1_pc_4_out), .Eff_in(MemEff), .Instr(MEM_IR), .Instr_out(WB_IR));  // open: Eff

  // Other names for the same wires on the sheet: ID_IR[5:0] = Func; OP[5:0] = ID_IR[31:26]; IR[31:0] = IF_IR;
  //   MEM_PC[31:0] = M_PC

  // Notes on the sheet:
  //   中断源
  //   时空图监测，可删除
  //   中断等待指示
  //   控制位
  //   戳工具置1进入计数暂停模式，ctrl+k时钟自动运行到对应节拍暂停
  //   ctrl+k关闭时钟连续运行，将控制位置零，进入单步调试模式调试
  //   用这个时钟源需要去掉电路中的其他时钟源
  //   数码管输出
  //   指令存储器
  //   contents of rom_1 (hex, n*v repeats v):
  //   20110001 8000c05 20110001 20120002 20130003 8000c09 20110001 20120002 20130003 8000c0d 20110001
  //   20120002 20130003 8000c11 20110001 20120002 20130003 c000cb8 20100001 20110001 118fc0 112020
  //   20020022 c 118882 12200001 8000c15 112020 20020022 c 20110001 118880 112020 20020022 c 12200001
  //   8000c1f 20110001 118fc0 112020 20020022 c 1188c3 112020 20020022 c 118903 112020 20020022 c 118903
  //   112020 20020022 c 118903 112020 20020022 c 118903 112020 20020022 c 118903 112020 20020022 c 118903
  //   112020 20020022 c 118903 112020 20020022 c 20100001 109fc0 139fc3 8021 2012000c 24160003 26100001
  //   3210000f 20080008 20090001 139900 2709825 132020 20020022 c 1094022 1500fff9 22100001 2018000f
  //   2188024 108700 20080008 20090001 139902 2709825 132021 20020022 c 1094022 1500fff9 108702 2c9b022
  //   12c00001 8000c50 4020 1084027 84400 3508ffff 82021 20020022 c 2010ffff 20110000 ae300000 22100001
  //   22310004 ae300000 22100001 22310004 ae300000 22100001 22310004 ae300000 22100001 22310004 ae300000
  //   22100001 22310004 ae300000 22100001 22310004 ae300000 22100001 22310004 ae300000 22100001 22310004
  //   ae300000 22100001 22310004 ae300000 22100001 22310004 ae300000 22100001 22310004 ae300000 22100001
  //   22310004 ae300000 22100001 22310004 ae300000 22100001 22310004 ae300000 22100001 22310004 ae300000
  //   22100001 22310004 22100001 8020 2011003c 8e130000 8e340000 274402a 11000002 ae330000 ae140000
  //   2231fffc 1611fff8 102020 20020022 c 22100004 2011003c 1611fff2 20020032 c 20100000 22100001 102020
  //   20020022 c 22100002 102020 20020022 c 22100003 102020 20020022 c 22100004 102020 20020022 c 22100005
  //   102020 20020022 c 22100006 102020 20020022 c 22100007 102020 20020022 c 22100008 102020 20020022
  //   20020022 c 3e00008
  //   可计数暂停的时钟源
  //   指令字
  //   IF/ID
  //   JR
  //   JMP
  //   JAL
  //   BLEZ
  //   BEQ
  //   BNE
  //   MemToReg
  //   RegWrite
  //   MemWrite
  //   HalfW
  //   AluOp
  //   AluSrcB
  //   流水调试日志用
  //   为方便自动评测，需要输出流水线各段保存的PC值，注意是PC不是PC+4，另外ID段寄存器写入信息，Mem段内存写入信息也要输出
endmodule
module \重定向流水线_动态分支预测  (
  output RegWrite,
  output MemWrite,
  output [31:0] IF_PC,
  output [31:0] ID_PC,
  output [31:0] EX_PC,
  output [31:0] M_PC,
  output [31:0] WB_PC,
  output [31:0] RDin,
  output [31:0] MDin,
  output [31:0] LedData
);

  wire and_1_out, Beq, Blez, Bne, CLK, clock_1_out, clock_2_out, comparator_1_eq, comparator_1_lt, d_ff_1_q,
       Equal, EX_Branched, EX_BranchSig, ex_mem_1_halfw_out, ex_mem_1_jal_out, ex_mem_1_memtoreg_out,
       ex_mem_1_regwrite_out, ex_mem_1_syscall_out, EX_PredictJump, Go, id_ex_1_alusrcb_out, id_ex_1_eff,
       id_ex_1_halfw_out, id_ex_1_memtoreg_out, id_ex_1_memwrite_out, id_ex_1_regwrite_out,
       id_ex_1_syscall_out, if_id_1_eff, if_id_1_predictjump_out, IR1, IR2, IR3, JAL, JAL_WB, JMP, JR, Less,
       mem_wb_1_memtoreg_out, MemEff, nand_1_out, not_1_out, not_2_out, or_1_out, Pause, RegDst, RST,
       SignedExt, Syscall, Vshamt, W1, W2, W3, xor_1_out, \分支预测缓冲器_1_predictjump , \重定向数据旁路控制信号生成_1_stall ;
  wire [1:0] id_ex_1_r1_forward_out, id_ex_1_r2_forward_out, \重定向数据旁路控制信号生成_1_r1_forward ,
       \重定向数据旁路控制信号生成_1_r2_forward ;
  wire [3:0] id_ex_1_aluop_out, \单周期硬布线控制器_1_alu_op ;
  wire [4:0] ex_mem_1_w__out, id_ex_1_shamt_out, id_ex_1_w__out, mem_wb_1_w__out, mips_regifile_1_r1,
       multiplexer_6_out, \reg选择逻辑_1_r1_num , \reg选择逻辑_1_r2_num , \reg选择逻辑_1_shamt , \reg选择逻辑_1_w_num ;
  wire [5:0] Func, \单周期硬布线控制器_1_jr ;
  wire [8:0] \单周期硬布线控制器_1_memtoreg ;
  wire [12:0] CNT_num;
  wire [15:0] \LoadUse次数 , \总周期数 , \插入气泡数 , \无条件分支数 , \条件分支成功数 ;
  wire [31:0] adder_1_out, adder_2_out, bit_extender_1_out, bit_extender_2_out, EX_IR,
       ex_mem_1_aluresult_out, ex_mem_1_pc_4_out, ex_mem_1_r1_out, EX_PC_4, id_ex_1_extdata_out,
       id_ex_1_jaddr_out, id_ex_1_r1_out, id_ex_1_r2_out, if_id_1_pc_4_out, IF_IR, MEM_IR,
       mem_wb_1_aluresult_out, mem_wb_1_pc_4_out, mem_wb_1_r2_out, mips_alu_1_result, mips_mem_1_memreaddata,
       mips_regifile_1_r2, multiplexer_1_out, multiplexer_2_out, multiplexer_3_out, multiplexer_5_out,
       multiplexer_8_out, multiplexer_9_out, multiplexer_10_out, \pc更新逻辑_1_pc_next , R1, WB_IR,
       \分支预测缓冲器_1_jumpaddr ;
  wire [31:5] mips_regifile_1_r1_2;
  wire [31:6] ID_IR;

  Button \u_总复位  (.out(RST));
  Button _1 (.out(IR1));
  Button _2 (.out(IR2));
  Button _3 (.out(IR3));
  // Probe on \总周期数 
  // Probe on \总周期数 
  Button \u_继续运行  (.out(Go));
  LED #(.active("true")) led_1 (.in(W1));
  LED #(.active("true")) led_2 (.in(W2));
  LED #(.active("true")) led_3 (.in(W3));
  Hex_Digit_Display hex_digit_display_1 (.value(LedData[31:28]));  // open: dp
  // Probe on IF_PC[19:0]
  // Mips_Probe mips_probe_1: pin names not known; wires that end beside it: IF_IR
  D_Flip_Flop #(.trigger("high"), .Pre_Clr_Positions("LEGACY"), .NegatePresetClear("false"), .enable("true"), .NewFFLayout("false")) d_ff_1 (
    .Q(d_ff_1_q), .preset(Pause), .reset(Go));  // open: clk, D, Qn, en
  // Probe on 13'h12f
  Hex_Digit_Display hex_digit_display_2 (.value(LedData[23:20]));  // open: dp
  Hex_Digit_Display hex_digit_display_3 (.value(LedData[27:24]));  // open: dp
  \PC更新逻辑  \pc更新逻辑_1  (
    .Equal(Equal), .Beq(Beq), .Bne(Bne), .JAL(JAL), .JMP(JMP), .JR(JR), .BAddr(adder_2_out),
    .PC_4(adder_1_out), .JAddr(id_ex_1_jaddr_out), .JRAddr(R1), .PC_Next(\pc更新逻辑_1_pc_next ), .Blez(Blez),
    .Less(Less), .Branched(EX_Branched), .BranchSig(EX_BranchSig));
  Comparator #(.width(13), .mode("twosComplement")) comparator_1 (
    .a(CNT_num), .b(13'h12f), .eq(comparator_1_eq), .lt(comparator_1_lt));  // open: gt
  Clock #(.highDuration(1), .lowDuration(1)) clock_1 (.out(clock_1_out));
  Hex_Digit_Display hex_digit_display_4 (.value(LedData[15:12]));  // open: dp
  Hex_Digit_Display hex_digit_display_5 (.value(LedData[19:16]));  // open: dp
  // Probe on ID_PC[19:0]
  // Mips_Probe mips_probe_2: pin names not known; wires that end beside it: {ID_IR, Func}
  nand nand_1 (nand_1_out, d_ff_1_q, comparator_1_eq);
  Counter #(.width(13), .max('h1fff), .ongoal("stay"), .trigger("rising"), .behavior("old")) counter_1 (
    .count(comparator_1_lt), .Q(CNT_num), .clk(clock_1_out));  // open: load, D, carry, clr, preset
  Hex_Digit_Display hex_digit_display_6 (.value(LedData[7:4]));  // open: dp
  Hex_Digit_Display hex_digit_display_7 (.value(LedData[11:8]));  // open: dp
  Clock #(.highDuration(1), .lowDuration(1)) clock_2 (.out(clock_2_out));
  // Mips_Probe mips_probe_3: pin names not known; wires that end beside it: clock_2_out, CLK, EX_IR
  xor xor_1 (xor_1_out, EX_PredictJump, EX_Branched);
  and and_1 (and_1_out, xor_1_out, EX_BranchSig);
  Multiplexer #(.select(1), .width(32), .disabled("Z"), .enable("false")) multiplexer_1 (
    .in0(EX_PC_4), .in1(\pc更新逻辑_1_pc_next ), .out(multiplexer_1_out), .sel(EX_Branched));
  Hex_Digit_Display hex_digit_display_8 (.value(LedData[3:0]));  // open: dp
  // Probe on EX_PC[19:0]
  Register #(.width(32), .trigger("rising"), .Select("low")) PC (
    .D(multiplexer_2_out), .en(not_1_out), .Q(IF_PC), .clk(CLK));  // open: clr
  Multiplexer #(.select(1), .width(32), .disabled("Z"), .enable("false")) multiplexer_2 (
    .in0(multiplexer_3_out), .in1(multiplexer_1_out), .out(multiplexer_2_out), .sel(and_1_out));
  Multiplexer #(.select(1), .width(32), .disabled("Z"), .enable("false")) multiplexer_3 (
    .in0(adder_1_out), .in1(\分支预测缓冲器_1_jumpaddr ), .out(multiplexer_3_out), .sel(\分支预测缓冲器_1_predictjump ));
  assign CLK = nand_1_out ? clock_1_out : 1'bz;  // Controlled_Buffer controlled_buffer_1
  Pull_Resistor #(.pull(1)) pull_resistor_1 (.node(CLK));
  // Probe on \总周期数 
  // Probe on M_PC[19:0]
  // Mips_Probe mips_probe_4: pin names not known; wires that end beside it: MEM_IR
  // Probe on \总周期数 
  // Probe on \无条件分支数 
  // Probe on \条件分支成功数 
  // Probe on \插入气泡数 
  // Probe on \LoadUse次数 
  Adder #(.width(32)) adder_1 (.a(IF_PC), .b(32'h4), .out(adder_1_out));  // open: cin, cout
  Counter #(.width(16), .max('hffff), .ongoal("wrap"), .trigger("rising"), .behavior("new")) counter_2 (
    .Q(\总周期数 ), .clk(CLK));  // open: load, D, count, carry, clr, preset, down
  // Probe on IF_PC[11:0]
  // Probe on WB_PC[19:0]
  // Mips_Probe mips_probe_5: pin names not known; wires that end beside it: WB_IR
  // Mips_Probe mips_probe_6: pin names not known; wires that end beside it: IF_IR
  ROM #(.addrWidth(10), .dataWidth(32), .Select("low")) rom_1 (.addr(IF_PC[11:2]), .data(IF_IR));
  \分支预测缓冲器  \u_分支预测缓冲器_1  (
    .BranchSig(EX_BranchSig), .EX_PC(EX_PC), .IF_PC(IF_PC), .BranchAddr(\pc更新逻辑_1_pc_next ),
    .Branched(EX_Branched), .PredictJump(\分支预测缓冲器_1_predictjump ), .JumpAddr(\分支预测缓冲器_1_jumpaddr ), .CLK(CLK));
  // Probe on ID_PC[11:0]
  // Probe on EX_PC[11:0]
  // Probe on M_PC[11:0]
  not not_1 (not_1_out, \重定向数据旁路控制信号生成_1_stall );
  IF_ID if_id_1 (
    .CLK(CLK), .Instr(IF_IR), .Instr_Out({ID_IR, Func}), .PC_4(adder_1_out), .PC_4_Out(if_id_1_pc_4_out),
    .PC(IF_PC), .PC_Out(ID_PC), .CLR(and_1_out), .Stall(not_1_out), .Eff(if_id_1_eff),
    .PredictJump(\分支预测缓冲器_1_predictjump ), .PredictJump_Out(if_id_1_predictjump_out));
  // Probe on WB_PC[11:0]
  \单周期硬布线控制器  \u_单周期硬布线控制器_1  (
    .Func(Func), .OP(ID_IR[31:26]), .ALU_OP(\单周期硬布线控制器_1_alu_op ), .MemToReg(\单周期硬布线控制器_1_memtoreg [0]),
    .MemWrite(\单周期硬布线控制器_1_memtoreg [2]), .ALU_SRC(\单周期硬布线控制器_1_memtoreg [8]),
    .RegWrite(\单周期硬布线控制器_1_memtoreg [1]), .SysCALL(Syscall), .SignedExt(SignedExt), .RegDst(RegDst),
    .JR(\单周期硬布线控制器_1_jr [0]), .JMP(\单周期硬布线控制器_1_jr [1]), .Beq(\单周期硬布线控制器_1_jr [4]),
    .JAL(\单周期硬布线控制器_1_jr [2]), .Bne(\单周期硬布线控制器_1_jr [5]), .Vshamt(Vshamt), .BLEZ(\单周期硬布线控制器_1_jr [3]),
    .HalfW(\单周期硬布线控制器_1_memtoreg [3]));
  \Reg选择逻辑  \reg选择逻辑_1  (
    ._21_25(ID_IR[25:21]), .Syscall(Syscall), .RegDst(RegDst), ._16_20(ID_IR[20:16]), ._11_15(ID_IR[15:11]),
    .JAL(\单周期硬布线控制器_1_jr [2]), ._6_10(ID_IR[10:6]), .R1_num(\reg选择逻辑_1_r1_num ), .R2_num(\reg选择逻辑_1_r2_num ),
    .W_num(\reg选择逻辑_1_w_num ), .Shamt(\reg选择逻辑_1_shamt ));  // open: PC_4, WriteBack_Data, RDin
  assign bit_extender_1_out = {{16{1'b0}}, {ID_IR[15:6], Func}};  // Bit_Extender bit_extender_1
  assign bit_extender_2_out = {{16{ID_IR[15]}}, {ID_IR[15:6], Func}};  // Bit_Extender bit_extender_2
  Multiplexer #(.select(1), .width(32), .disabled("Z"), .enable("false")) multiplexer_4 (
    .in0(multiplexer_10_out), .in1(mem_wb_1_pc_4_out), .out(RDin), .sel(JAL_WB));
  not not_2 (not_2_out, CLK);
  Multiplexer #(.select(1), .width(32), .disabled("Z"), .enable("false")) multiplexer_5 (
    .in0(bit_extender_1_out), .in1(bit_extender_2_out), .out(multiplexer_5_out), .sel(SignedExt));
  MIPS_Regifile mips_regifile_1 (
    .Din(RDin), .Clk(not_2_out), .R1({mips_regifile_1_r1_2, mips_regifile_1_r1}), .R2(mips_regifile_1_r2),
    .WE(RegWrite), .W_num(mem_wb_1_w__out), .R1_num(\reg选择逻辑_1_r1_num ), .R2_num(\reg选择逻辑_1_r2_num ));
  Multiplexer #(.select(1), .width(5), .disabled("Z"), .enable("false")) multiplexer_6 (
    .in0(\reg选择逻辑_1_shamt ), .in1(mips_regifile_1_r1), .out(multiplexer_6_out), .sel(Vshamt));
  or or_1 (or_1_out, and_1_out, \重定向数据旁路控制信号生成_1_stall );
  ID_EX id_ex_1 (
    .JR(\单周期硬布线控制器_1_jr [0]), .JMP(\单周期硬布线控制器_1_jr [1]), .JAL(\单周期硬布线控制器_1_jr [2]),
    .BLEZ(\单周期硬布线控制器_1_jr [3]), .BEQ(\单周期硬布线控制器_1_jr [4]), .BNE(\单周期硬布线控制器_1_jr [5]),
    .MemToReg(\单周期硬布线控制器_1_memtoreg [0]), .Shamt(multiplexer_6_out),
    .R1({mips_regifile_1_r1_2, mips_regifile_1_r1}), .R2(mips_regifile_1_r2), .JR_Out(JR), .JMP_Out(JMP),
    .JAL_Out(JAL), .BLEZ_Out(Blez), .BEQ_Out(Beq), .BNE_Out(Bne), .MemToReg_Out(id_ex_1_memtoreg_out),
    .Shamt_Out(id_ex_1_shamt_out), .R1_Out(id_ex_1_r1_out), .R2_Out(id_ex_1_r2_out), .CLK(CLK),
    .AluOp(\单周期硬布线控制器_1_alu_op ), .AluOp_Out(id_ex_1_aluop_out), .ExtData(multiplexer_5_out),
    .W_num(\reg选择逻辑_1_w_num ), .RegWrite(\单周期硬布线控制器_1_memtoreg [1]), .RegWrite_Out(id_ex_1_regwrite_out),
    .MemWrite_Out(id_ex_1_memwrite_out), .HalfW_Out(id_ex_1_halfw_out), .AluSrcB_Out(id_ex_1_alusrcb_out),
    .Syscall_Out(id_ex_1_syscall_out), .MemWrite(\单周期硬布线控制器_1_memtoreg [2]),
    .HalfW(\单周期硬布线控制器_1_memtoreg [3]), .AluSrcB(\单周期硬布线控制器_1_memtoreg [8]), .Syscall(Syscall),
    .ExtData_Out(id_ex_1_extdata_out), .W__Out(id_ex_1_w__out), .PC(ID_PC), .PC_Out(EX_PC), .CLR(or_1_out),
    .JAddr({ID_PC[31:28], ID_IR[25:6], Func, 2'b00}), .JAddr_Out(id_ex_1_jaddr_out), .PC_4(if_id_1_pc_4_out),
    .PC_4_Out(EX_PC_4), .Eff_in(if_id_1_eff), .Eff(id_ex_1_eff), .R1_Forward(\重定向数据旁路控制信号生成_1_r1_forward ),
    .R1_Forward_Out(id_ex_1_r1_forward_out), .Instr({ID_IR, Func}), .Instr_out(EX_IR),
    .R2_Forward(\重定向数据旁路控制信号生成_1_r2_forward ), .R2_Forward_Out(id_ex_1_r2_forward_out),
    .PredictJump(if_id_1_predictjump_out), .PredictJump_Out(EX_PredictJump));
  Multiplexer #(.select(2), .width(32), .disabled("Z"), .enable("false")) multiplexer_7 (
    .in0(id_ex_1_r1_out), .in1(mem_wb_1_aluresult_out), .in2(mem_wb_1_r2_out), .in3(ex_mem_1_aluresult_out),
    .out(R1), .sel(id_ex_1_r1_forward_out));
  Multiplexer #(.select(2), .width(32), .disabled("Z"), .enable("false")) multiplexer_8 (
    .in0(id_ex_1_r2_out), .in1(mem_wb_1_aluresult_out), .in2(mem_wb_1_r2_out), .in3(ex_mem_1_aluresult_out),
    .out(multiplexer_8_out), .sel(id_ex_1_r2_forward_out));
  \重定向数据旁路控制信号生成  \u_重定向数据旁路控制信号生成_1  (
    .ID_AluSrc(\单周期硬布线控制器_1_memtoreg [8]), .BranchCLR(and_1_out), .ID_R1_num(\reg选择逻辑_1_r1_num ),
    .ID_R2_num(\reg选择逻辑_1_r2_num ), .EX_W_num(id_ex_1_w__out), .MEM_W_num(ex_mem_1_w__out),
    .EX_RegWrite(id_ex_1_regwrite_out), .MEM_RegWrite(ex_mem_1_regwrite_out),
    .MEM_MemToReg(ex_mem_1_memtoreg_out), .R1_Forward(\重定向数据旁路控制信号生成_1_r1_forward ),
    .R2_Forward(\重定向数据旁路控制信号生成_1_r2_forward ), .ID_IR({ID_IR, Func}), .EX_IR(EX_IR),
    .Stall(\重定向数据旁路控制信号生成_1_stall ));
  Multiplexer #(.select(1), .width(32), .disabled("Z"), .enable("false")) multiplexer_9 (
    .in0(multiplexer_8_out), .in1(id_ex_1_extdata_out), .out(multiplexer_9_out), .sel(id_ex_1_alusrcb_out));
  Adder #(.width(32)) adder_2 (
    .a(EX_PC_4), .b({id_ex_1_extdata_out[29:0], 2'b00}), .out(adder_2_out));  // open: cin, cout
  MIPS_ALU mips_alu_1 (
    .X(R1), .Y(multiplexer_9_out), .AluOP(id_ex_1_aluop_out), .Equal(Equal), .Result(mips_alu_1_result),
    .shamt(id_ex_1_shamt_out), .Less(Less));  // open: Result_2
  EX_MEM ex_mem_1 (
    .MemToReg(id_ex_1_memtoreg_out), .RegWrite(id_ex_1_regwrite_out), .MemWrite(id_ex_1_memwrite_out),
    .HalfW(id_ex_1_halfw_out), .AluResult(mips_alu_1_result), .R2(multiplexer_8_out), .W_num(id_ex_1_w__out),
    .CLK(CLK), .MemToReg_Out(ex_mem_1_memtoreg_out), .RegWrite_Out(ex_mem_1_regwrite_out),
    .MemWrite_Out(MemWrite), .HalfW_Out(ex_mem_1_halfw_out), .AluResult_Out(ex_mem_1_aluresult_out),
    .R2_Out(MDin), .W__Out(ex_mem_1_w__out), .PC(EX_PC), .PC_Out(M_PC), .R1(R1), .R1_Out(ex_mem_1_r1_out),
    .Syscall(id_ex_1_syscall_out), .Syscall_Out(ex_mem_1_syscall_out), .CLR(1'b0), .JAL(JAL),
    .JAL_Out(ex_mem_1_jal_out), .PC_4(EX_PC_4), .PC_4_Out(ex_mem_1_pc_4_out), .Eff_in(id_ex_1_eff),
    .Eff(MemEff), .Instr(EX_IR), .Instr_out(MEM_IR));
  \Syscall处理  \syscall处理_1  (
    .Syscall(ex_mem_1_syscall_out), .CLK(CLK), .R2(MDin), .R1(ex_mem_1_r1_out), .Pause(Pause),
    .LedData(LedData));
  MIPS_MEM mips_mem_1 (
    .AluResult(ex_mem_1_aluresult_out), .HalfW(ex_mem_1_halfw_out), .WriteData(MDin), .MemWrite(MemWrite),
    .CLK(CLK), .MemReadData(mips_mem_1_memreaddata));
  MEM_WB mem_wb_1 (
    .MemToReg(ex_mem_1_memtoreg_out), .RegWrite(ex_mem_1_regwrite_out), .AluResult(ex_mem_1_aluresult_out),
    .R2(mips_mem_1_memreaddata), .W_num(ex_mem_1_w__out), .CLK(CLK), .MemToReg_Out(mem_wb_1_memtoreg_out),
    .RegWrite_Out(RegWrite), .AluResult_Out(mem_wb_1_aluresult_out), .R2_Out(mem_wb_1_r2_out),
    .W__Out(mem_wb_1_w__out), .PC(M_PC), .PC_Out(WB_PC), .JAL(ex_mem_1_jal_out), .JAL_Out(JAL_WB),
    .PC_4(ex_mem_1_pc_4_out), .PC_4_Out(mem_wb_1_pc_4_out), .Eff_in(MemEff), .Instr(MEM_IR), .Instr_out(WB_IR));  // open: Eff
  Multiplexer #(.select(1), .width(32), .disabled("Z"), .enable("false")) multiplexer_10 (
    .in0(mem_wb_1_aluresult_out), .in1(mem_wb_1_r2_out), .out(multiplexer_10_out), .sel(mem_wb_1_memtoreg_out));

  // Other names for the same wires on the sheet: ID_IR[5:0] = Func; OP[5:0] = ID_IR[31:26]; IR[31:0] = IF_IR;
  //   MEM_PC[31:0] = M_PC

  // Notes on the sheet:
  //   中断源
  //   中断等待指示
  //   控制位
  //   戳工具置1进入计数暂停模式，ctrl+k时钟自动运行到对应节拍暂停
  //   ctrl+k关闭时钟连续运行，将控制位置零，进入单步调试模式调试
  //   用这个时钟源需要去掉电路中的其他时钟源
  //   数码管输出
  //   可计数暂停的时钟源
  //   指令存储器
  //   contents of rom_1 (hex, n*v repeats v):
  //   20110001 8000005 20110001 20120002 20130003 8000009 20110001 20120002 20130003 800000d 20110001
  //   20120002 20130003 8000011 20110001 20120002 20130003 c0000f2 20100001 20110001 118fc0 112020
  //   20020022 c 118882 12200001 8000015 112020 20020022 c 20110001 118880 112020 20020022 c 12200001
  //   800001f 20110001 118fc0 112020 20020022 c 1188c3 112020 20020022 c 118903 112020 20020022 c 118903
  //   112020 20020022 c 118903 112020 20020022 c 118903 112020 20020022 c 118903 112020 20020022 c 118903
  //   112020 20020022 c 118903 112020 20020022 c 20100001 109fc0 139fc3 8021 2012000c 24160003 26100001
  //   3210000f 20080008 20090001 139900 2709825 132020 20020022 c 1094022 1500fff9 22100001 2018000f
  //   2188024 108700 20080008 20090001 139902 2709825 132021 20020022 c 1094022 1500fff9 108702 2c9b022
  //   12c00001 8000050 4020 1084027 84400 3508ffff 82021 20020022 c 2010ffff 20110000 ae300000 22100001
  //   22310004 ae300000 22100001 22310004 ae300000 22100001 22310004 ae300000 22100001 22310004 ae300000
  //   22100001 22310004 ae300000 22100001 22310004 ae300000 22100001 22310004 ae300000 22100001 22310004
  //   ae300000 22100001 22310004 ae300000 22100001 22310004 ae300000 22100001 22310004 ae300000 22100001
  //   22310004 ae300000 22100001 22310004 ae300000 22100001 22310004 ae300000 22100001 22310004 ae300000
  //   22100001 22310004 22100001 8020 2011003c 8e130000 8e340000 274402a 11000002 ae330000 ae140000
  //   2231fffc 1611fff8 102020 20020022 c 22100004 2011003c 1611fff2 20020032 c 20080001 20090003 20110876
  //   112020 20020022 c 200b0008 1118804 1318804 112020 20020022 c 216bffff 1560fff9 2002000a c 2008ffff
  //   20090000 20111997 112020 20020022 c 2288820 2e291949 1120fffa 2002000a c 20090000 200b0020 20110001
  //   20120001 a5310000 112020 20020022 c 2328820 21290002 216bffff 1560fff8 200b0010 20090000 8d310000
  //   112020 20020022 c 21290004 216bffff 1560fff9 2002000a c 2011fff1 112020 20020022 c 22310001 1a20fffb
  //   2002000a c 20100000 22100001 102020 20020022 c 22100002 102020 20020022 c 22100003 102020 20020022 c
  //   22100004 102020 20020022 c 22100005 102020 20020022 c 22100006 102020 20020022 c 22100007 102020
  //   20020022 c 22100008 102020 20020022 20020022 c 3e00008
  //   IF/ID
  //   指令字
  //   流水调试日志用
  //   JR
  //   JMP
  //   JAL
  //   BLEZ
  //   BEQ
  //   BNE
  //   MemToReg
  //   RegWrite
  //   MemWrite
  //   HalfW
  //   AluOp
  //   AluSrcB
  //   为方便自动评测，需要输出流水线各段保存的PC值，注意是PC不是PC+4，另外ID段寄存器写入信息，Mem段内存写入信息也要输出
endmodule

module \中断按键参考电路  (
  input  \同步清零信号 ,
  output \与中断屏蔽位与 
);

  wire \_1号中断_out , and_1_out, clock_1_out, d_ff_1_q, or_1_out, or_2_out;

  Clock #(.highDuration(1), .lowDuration(1)) clock_1 (.out(clock_1_out));
  Button \_1号中断  (.out(\_1号中断_out ));
  or or_1 (or_1_out, \与中断屏蔽位与 , d_ff_1_q);
  LED #(.active("true")) \_1号中断等待指示灯  (.in(or_1_out));
  D_Flip_Flop #(.trigger("rising"), .Pre_Clr_Positions("LEGACY"), .NegatePresetClear("false"), .enable("true"), .NewFFLayout("false")) d_ff_1 (
    .clk(\_1号中断_out ), .D(1'b1), .Q(d_ff_1_q), .reset(\与中断屏蔽位与 ));  // open: Qn, preset, en
  or or_2 (or_2_out, d_ff_1_q, \与中断屏蔽位与 );
  and and_1 (and_1_out, or_2_out, ~\同步清零信号 );  // AND_Gate
  D_Flip_Flop #(.trigger("rising"), .Pre_Clr_Positions("LEGACY"), .NegatePresetClear("false"), .enable("true"), .NewFFLayout("false")) IR1 (
    .clk(clock_1_out), .D(and_1_out), .Q(\与中断屏蔽位与 ));  // open: Qn, preset, en, reset

  // Notes on the sheet:
  //   中断信号采样参考电路
  //   Reset 
endmodule

module \单周期MIPS_单级中断  (
  input  IR1,
  input  IR2,
  input  IR3,
  output RegWrite,
  output MemWrite,
  output [31:0] PC,
  output [31:0] IR,
  output [31:0] RDin,
  output [31:0] MDin,
  output [31:0] LedData
);

  wire AluSrcB, and_1_out, and_2_out, and_3_out, and_4_out, Beq, Blez, Bne, CLK, clock_2_out,
       comparator_1_eq, comparator_1_lt, comparator_4_eq, comparator_5_eq, comparator_6_eq, comparator_7_eq,
       d_ff_1_q, d_ff_2_q, d_ff_3_q, d_ff_4_q, d_ff_5_q, d_ff_6_q, d_ff_7_q, decoder_1_out0, decoder_1_out1,
       decoder_1_out2, Equal, ERET, Go, HalfW, IE, IE_p2, INIT, IR1_t, IR2_t, IR3_t, IRA, IRB, IRC, IRQ, JAL,
       JMP, JR, Less, MemToReg, nand_1_out, not_1_out, or_1_out, or_5_out, or_6_out, or_7_out, or_9_out,
       or_12_out, Pause, priority_encoder_1_gs, RegDst, SignedExt, Syscall, Vshamt, W1, W2, W3;
  wire [1:0] IRQ_Exe, priority_encoder_1_out;
  wire [3:0] AluOP;
  wire [4:0] multiplexer_1_out, \reg选择逻辑_1_r1_num , \reg选择逻辑_1_r2_num , \reg选择逻辑_1_shamt , \reg选择逻辑_1_w_num ;
  wire [12:0] CNT_num;
  wire [15:0] \总周期数 ;
  wire [31:0] adder_1_out, adder_2_out, bit_extender_1_out, bit_extender_2_out, controlled_buffer_1_out, EPC,
       IRQ_Entry, mips_alu_1_result, mips_mem_1_memreaddata, multiplexer_2_out, multiplexer_3_out,
       multiplexer_5_out, PC_Next, R1;

  Clock #(.highDuration(1), .lowDuration(1)) clock_1 ();  // open: out
  Button _1 ();  // open: out
  Button _2 ();  // open: out
  Button _3 ();  // open: out
  Button \u_继续运行  (.out(Go));
  LED #(.active("true")) led_1 (.in(W1));
  LED #(.active("true")) led_2 (.in(W2));
  LED #(.active("true")) led_3 (.in(W3));
  Hex_Digit_Display hex_digit_display_1 (.value(LedData[31:28]));  // open: dp
  and and_1 (and_1_out, ~ERET, IRQ);  // AND_Gate
  or or_1 (or_1_out, ERET, IRQ);
  \PC更新逻辑  \pc更新逻辑_1  (
    .Equal(Equal), .Beq(Beq), .Bne(Bne), .JAL(JAL), .JMP(JMP), .JR(JR), .BAddr(adder_2_out),
    .PC_4(adder_1_out), .JAddr({PC[31:28], IR[25:0], 2'b00}), .JRAddr(R1), .PC_Next(PC_Next), .Blez(Blez),
    .Less(Less));  // open: Branched, BranchSig
  Decoder #(.select(2), .tristate("false"), .disabled(0), .enable("true")) decoder_1 (
    .out0(decoder_1_out0), .out1(decoder_1_out1), .out2(decoder_1_out2), .sel(IRQ_Exe), .en(ERET));  // open: out3
  Hex_Digit_Display hex_digit_display_2 (.value(LedData[23:20]));  // open: dp
  Hex_Digit_Display hex_digit_display_3 (.value(LedData[27:24]));  // open: dp
  assign controlled_buffer_1_out = ERET ? EPC : 32'bz;  // Controlled_Buffer controlled_buffer_1
  assign controlled_buffer_1_out = and_1_out ? IRQ_Entry : 32'bz;  // Controlled_Buffer controlled_buffer_2
  assign controlled_buffer_1_out = ~or_1_out ? PC_Next : 32'bz;  // Controlled_Buffer controlled_buffer_3
  D_Flip_Flop #(.trigger("high"), .Pre_Clr_Positions("LEGACY"), .NegatePresetClear("false"), .enable("true"), .NewFFLayout("false")) d_ff_1 (
    .Q(d_ff_1_q), .preset(Pause), .reset(Go));  // open: clk, D, Qn, en
  // Probe on 13'hc
  or or_2 (W1, d_ff_5_q, d_ff_2_q);
  or or_3 (W2, d_ff_6_q, d_ff_3_q);
  or or_4 (W3, d_ff_7_q, d_ff_4_q);
  Hex_Digit_Display hex_digit_display_4 (.value(LedData[19:16]));  // open: dp
  Hex_Digit_Display hex_digit_display_5 (.value(LedData[15:12]));  // open: dp
  Register #(.width(32), .trigger("rising"), .Select("low")) u_PC (
    .D(controlled_buffer_1_out), .Q(PC), .clk(CLK));  // open: en, clr
  Comparator #(.width(13), .mode("twosComplement")) comparator_1 (
    .a(CNT_num), .b(13'hc), .eq(comparator_1_eq), .lt(comparator_1_lt));  // open: gt
  Clock #(.highDuration(1), .lowDuration(1)) clock_2 (.out(clock_2_out));
  D_Flip_Flop #(.trigger("rising"), .Pre_Clr_Positions("LEGACY"), .NegatePresetClear("false"), .enable("true"), .NewFFLayout("false")) d_ff_2 (
    .clk(IR1_t), .D(1'b1), .Q(d_ff_2_q), .reset(d_ff_5_q));  // open: Qn, preset, en
  D_Flip_Flop #(.trigger("rising"), .Pre_Clr_Positions("LEGACY"), .NegatePresetClear("false"), .enable("true"), .NewFFLayout("false")) d_ff_3 (
    .clk(IR2_t), .D(1'b1), .Q(d_ff_3_q), .reset(d_ff_6_q));  // open: Qn, preset, en
  D_Flip_Flop #(.trigger("rising"), .Pre_Clr_Positions("LEGACY"), .NegatePresetClear("false"), .enable("true"), .NewFFLayout("false")) d_ff_4 (
    .clk(IR3_t), .D(1'b1), .Q(d_ff_4_q), .reset(d_ff_7_q));  // open: Qn, preset, en
  Hex_Digit_Display hex_digit_display_6 (.value(LedData[7:4]));  // open: dp
  Hex_Digit_Display hex_digit_display_7 (.value(LedData[11:8]));  // open: dp
  // Probe on \总周期数 
  Adder #(.width(32)) adder_1 (.a(PC), .b(32'h4), .out(adder_1_out));  // open: cin, cout
  nand nand_1 (nand_1_out, d_ff_1_q, comparator_1_eq);
  Counter #(.width(13), .max('h1fff), .ongoal("stay"), .trigger("rising"), .behavior("old")) counter_1 (
    .count(comparator_1_lt), .Q(CNT_num), .clk(clock_2_out));  // open: load, D, carry, clr, preset
  or or_5 (or_5_out, d_ff_2_q, d_ff_5_q);
  or or_6 (or_6_out, d_ff_3_q, d_ff_6_q);
  or or_7 (or_7_out, d_ff_4_q, d_ff_7_q);
  Hex_Digit_Display hex_digit_display_8 (.value(LedData[3:0]));  // open: dp
  // Mips_Probe mips_probe_1: pin names not known; wires that end beside it: IR
  ROM #(.addrWidth(10), .dataWidth(32), .Select("low")) rom_1 (.addr(PC[11:2]), .data(IR));
  assign CLK = nand_1_out ? clock_2_out : 1'bz;  // Controlled_Buffer controlled_buffer_4
  and and_2 (and_2_out, or_5_out, ~decoder_1_out0);  // AND_Gate
  and and_3 (and_3_out, or_6_out, ~decoder_1_out1);  // AND_Gate
  and and_4 (and_4_out, or_7_out, ~decoder_1_out2);  // AND_Gate
  Pull_Resistor #(.pull(1)) pull_resistor_1 (.node(CLK));
  D_Flip_Flop #(.trigger("rising"), .Pre_Clr_Positions("LEGACY"), .NegatePresetClear("false"), .enable("true"), .NewFFLayout("false")) d_ff_5 (
    .clk(CLK), .D(and_2_out), .Q(d_ff_5_q));  // open: Qn, preset, en, reset
  D_Flip_Flop #(.trigger("rising"), .Pre_Clr_Positions("LEGACY"), .NegatePresetClear("false"), .enable("true"), .NewFFLayout("false")) d_ff_6 (
    .clk(CLK), .D(and_3_out), .Q(d_ff_6_q));  // open: Qn, preset, en, reset
  D_Flip_Flop #(.trigger("rising"), .Pre_Clr_Positions("LEGACY"), .NegatePresetClear("false"), .enable("true"), .NewFFLayout("false")) d_ff_7 (
    .clk(CLK), .D(and_4_out), .Q(d_ff_7_q));  // open: Qn, preset, en, reset
  or or_8 (IR1_t, IR1, IRA);
  assign bit_extender_1_out = {{16{1'b0}}, IR[15:0]};  // Bit_Extender bit_extender_1
  assign bit_extender_2_out = {{16{IR[15]}}, IR[15:0]};  // Bit_Extender bit_extender_2
  or or_9 (or_9_out, ERET, INIT);
  or or_10 (IR2_t, IR2, IRB);
  \Reg选择逻辑  \reg选择逻辑_1  (
    ._21_25(IR[25:21]), .Syscall(Syscall), .RegDst(RegDst), ._16_20(IR[20:16]), ._11_15(IR[15:11]),
    .JAL(JAL), .PC_4(adder_1_out), .WriteBack_Data(multiplexer_5_out), ._6_10(IR[10:6]),
    .R1_num(\reg选择逻辑_1_r1_num ), .R2_num(\reg选择逻辑_1_r2_num ), .W_num(\reg选择逻辑_1_w_num ), .RDin(RDin),
    .Shamt(\reg选择逻辑_1_shamt ));
  Counter #(.width(16), .max('hffff), .ongoal("stay"), .trigger("rising"), .behavior("old")) counter_2 (
    .Q(\总周期数 ), .clk(CLK));  // open: load, D, count, carry, clr, preset
  Priority_Encoder #(.select(2), .disabled("Z")) priority_encoder_1 (
    .in0(d_ff_5_q), .in1(d_ff_6_q), .in2(d_ff_7_q), .in3(1'b0), .out(priority_encoder_1_out),
    .gs(priority_encoder_1_gs));  // open: en_out, en_in
  // D_Flip_Flop #(.trigger("latch"), .Pre_Clr_Positions("LEGACY"), .NegatePresetClear("false"), .enable("false"), .NewFFLayout("false")) IE: pin names not known; wires that end beside it: or_9_out, IE_p2, IE
  Comparator #(.width(16), .mode("twosComplement")) comparator_2 (
    .a({16{1'b0}}), .b(\总周期数 ), .eq(INIT));  // open: gt, lt
  MIPS_Regifile mips_regifile_1 (
    .Din(RDin), .Clk(CLK), .R1(R1), .R2(MDin), .WE(RegWrite), .W_num(\reg选择逻辑_1_w_num ),
    .R1_num(\reg选择逻辑_1_r1_num ), .R2_num(\reg选择逻辑_1_r2_num ));
  Multiplexer #(.select(1), .width(5), .disabled("Z"), .enable("false")) multiplexer_1 (
    .in0(\reg选择逻辑_1_shamt ), .in1(R1[4:0]), .out(multiplexer_1_out), .sel(Vshamt));
  Adder #(.width(32)) adder_2 (
    .a(adder_1_out), .b({bit_extender_2_out[29:0], 2'b00}), .out(adder_2_out));  // open: cin, cout
  Multiplexer #(.select(1), .width(32), .disabled("Z"), .enable("false")) multiplexer_2 (
    .in0(bit_extender_1_out), .in1(bit_extender_2_out), .out(multiplexer_2_out), .sel(SignedExt));
  and and_5 (IRQ, priority_encoder_1_gs, IE);
  not not_1 (not_1_out, ERET);
  Comparator #(.width(32), .mode("twosComplement")) comparator_3 (.a(IR), .b(32'h42000018), .eq(ERET));  // open: gt, lt
  or or_11 (IR3_t, IR3, IRC);
  Multiplexer #(.select(1), .width(32), .disabled("Z"), .enable("false")) multiplexer_3 (
    .in0(MDin), .in1(multiplexer_2_out), .out(multiplexer_3_out), .sel(AluSrcB));
  Multiplexer #(.select(2), .width(32), .disabled("Z"), .enable("false")) multiplexer_4 (
    .in0(32'h30ac), .in1(32'h3150), .in2(32'h31f4), .out(IRQ_Entry), .sel(priority_encoder_1_out));  // open: in3
  D_Flip_Flop #(.trigger("rising"), .Pre_Clr_Positions("LEGACY"), .NegatePresetClear("false"), .enable("true"), .NewFFLayout("false")) d_ff_8 (
    .clk(CLK), .D(IRQ), .Q(IE_p2), .en(not_1_out));  // open: Qn, preset, reset
  MIPS_ALU mips_alu_1 (
    .X(R1), .Y(multiplexer_3_out), .AluOP(AluOP), .Equal(Equal), .Result(mips_alu_1_result),
    .shamt(multiplexer_1_out), .Less(Less));  // open: Result_2
  Register #(.width(2), .trigger("rising"), .Select("low")) register_1 (
    .D(priority_encoder_1_out), .Q(IRQ_Exe), .clk(IE_p2), .preset(INIT));  // open: en, clr, cs
  Register #(.width(32), .trigger("rising"), .Select("low")) u_EPC (
    .D(PC_Next), .Q(EPC), .clk(IE_p2));  // open: en, clr
  MIPS_MEM mips_mem_1 (
    .AluResult(mips_alu_1_result), .HalfW(HalfW), .WriteData(MDin), .MemWrite(MemWrite), .CLK(CLK),
    .MemReadData(mips_mem_1_memreaddata));
  Multiplexer #(.select(1), .width(32), .disabled("Z"), .enable("false")) multiplexer_5 (
    .in0(mips_alu_1_result), .in1(mips_mem_1_memreaddata), .out(multiplexer_5_out), .sel(MemToReg));
  Comparator #(.width(16), .mode("twosComplement")) comparator_4 (
    .a(16'h23b), .b(\总周期数 ), .eq(comparator_4_eq));  // open: gt, lt
  Comparator #(.width(16), .mode("twosComplement")) comparator_5 (
    .a(\总周期数 ), .b(16'h1), .eq(comparator_5_eq));  // open: gt, lt
  Comparator #(.width(16), .mode("twosComplement")) comparator_6 (
    .a(\总周期数 ), .b(16'h4), .eq(comparator_6_eq));  // open: gt, lt
  Comparator #(.width(16), .mode("twosComplement")) comparator_7 (
    .a(\总周期数 ), .b(16'h7), .eq(comparator_7_eq));  // open: gt, lt
  or or_12 (or_12_out, comparator_4_eq, comparator_5_eq);
  Pull_Resistor #(.pull(0)) pull_resistor_2 (.node(IRA));
  assign IRA = or_12_out ? ~CLK : 1'bz;  // Controlled_Inverter controlled_inverter_1
  Pull_Resistor #(.pull(0)) pull_resistor_3 (.node(IRB));
  assign IRB = comparator_6_eq ? ~CLK : 1'bz;  // Controlled_Inverter controlled_inverter_2
  Pull_Resistor #(.pull(0)) pull_resistor_4 (.node(IRC));
  assign IRC = comparator_7_eq ? ~CLK : 1'bz;  // Controlled_Inverter controlled_inverter_3
  \单周期硬布线控制器  \u_单周期硬布线控制器_1  (
    .Func(IR[5:0]), .OP(IR[31:26]), .ALU_OP(AluOP), .MemToReg(MemToReg), .MemWrite(MemWrite),
    .ALU_SRC(AluSrcB), .RegWrite(RegWrite), .SysCALL(Syscall), .SignedExt(SignedExt), .RegDst(RegDst),
    .JR(JR), .JMP(JMP), .Beq(Beq), .JAL(JAL), .Bne(Bne), .Vshamt(Vshamt), .BLEZ(Blez), .HalfW(HalfW));
  \Syscall处理  \syscall处理_1  (.Syscall(Syscall), .CLK(CLK), .R2(MDin), .R1(R1), .Pause(Pause), .LedData(LedData));

  // Other names for the same wires on the sheet: Func[5:0] = IR[5:0]; OP[5:0] = IR[31:26]; R2[31:0] = MDin

  // Notes on the sheet:
  //   中断源
  //   中断等待指示
  //   总复位信号应将除ROM以外所有存储组件全部清零
  //   控制位
  //   暂停节拍，不能为0
  //   用这个时钟源需要去掉电路中的其他时钟源
  //   数码管输出
  //   戳工具置1进入计数暂停模式，ctrl+k时钟自动运行到对应节拍暂停
  //   ctrl+k关闭时钟连续运行，将控制位置零，进入单步调试模式调试
  //   数码管输出应该用寄存器锁存，否则显示数据只能一闪而过
  //   指令存储器
  //   指令字
  //   contents of rom_1 (hex, n*v repeats v):
  //   201d07d0 20100001 109fc0 139fc3 8021 2012000c 24160008 26100001 3210000f 20080008 20090001 139900
  //   2709825 132020 20020022 c 1094022 1500fff9 22100001 2018000f 2188024 108700 20080008 20090001 139902
  //   2709825 132021 20020022 c 1094022 1500fff9 108702 2c9b022 12c00001 8000c07 4020 1084027 84400
  //   3508ffff 82021 20020022 c 8000c01 afa20000 23bd0004 afa40000 23bd0004 afb00000 23bd0004 afb30000
  //   23bd0004 afb40000 23bd0004 afb50000 23bd0004 afb60000 23bd0004 20160001 20140003 20150001 168020
  //   108100 2149825 132020 20020022 c 1600fffa 295a022 1680fff7 23bdfffc 8fb60000 23bdfffc 8fb50000
  //   23bdfffc 8fb40000 23bdfffc 8fb30000 23bdfffc 8fb00000 23bdfffc 8fa40000 23bdfffc 8fa20000 42000018
  //   afa20000 23bd0004 afa40000 23bd0004 afb00000 23bd0004 afb30000 23bd0004 afb40000 23bd0004 afb50000
  //   23bd0004 afb60000 23bd0004 20160002 20140003 20150001 168020 108100 2149825 132020 20020022 c
  //   1600fffa 295a022 1680fff7 23bdfffc 8fb60000 23bdfffc 8fb50000 23bdfffc 8fb40000 23bdfffc 8fb30000
  //   23bdfffc 8fb00000 23bdfffc 8fa40000 23bdfffc 8fa20000 42000018 afa20000 23bd0004 afa40000 23bd0004
  //   afb00000 23bd0004 afb30000 23bd0004 afb40000 23bd0004 afb50000 23bd0004 afb60000 23bd0004 20160003
  //   20140003 20150001 168020 108100 2149825 132020 20020022 c 1600fffa 295a022 1680fff7 23bdfffc
  //   8fb60000 23bdfffc 8fb50000 23bdfffc 8fb40000 23bdfffc 8fb30000 23bdfffc 8fb00000 23bdfffc 8fa40000
  //   23bdfffc 8fa20000 42000018
  //   可计数暂停的时钟源
  //   为方便自动评测，需要输出PC，IR，寄存器堆写如数据RDin
  //   RAM写使能MemWrite、RAM写入数据MDin等信号
  //   单级中断测试信号模拟器
endmodule

module \单周期MIPS_多级中断  (
  input  IR1,
  input  IR2,
  input  IR3,
  output RegWrite,
  output MemWrite,
  output [31:0] PC,
  output [31:0] IR,
  output [31:0] RDin,
  output [31:0] MDin,
  output [31:0] LedData
);

  wire AluSrcB, and_1_out, and_2_out, and_3_out, and_4_out, and_5_out, and_6_out, and_7_out, and_9_out, Beq,
       Blez, Bne, CLK, clock_2_out, comparator_2_eq, comparator_3_eq, comparator_4_eq, comparator_5_eq,
       comparator_7_eq, comparator_8_eq, comparator_9_eq, comparator_10_eq, comparator_11_eq,
       comparator_12_eq, comparator_12_lt, d_ff_1_q, d_ff_2_q, d_ff_3_q, d_ff_4_q, d_ff_5_qn, d_ff_6_q,
       d_ff_7_qn, d_ff_8_q, d_ff_9_qn, d_ff_10_q, d_ff_11_q, decoder_1_out0, decoder_1_out1, decoder_1_out2,
       Equal, ERET, Go, HalfW, IE, INIT, IR1_t, IR2_t, IR3_t, IRA, IRB, IRC, IRQ, JAL, JMP, JR, Less,
       MemToReg, MFC, MTC, nand_1_out, not_1_out, not_2_out, not_3_out, not_4_out, not_5_out, not_6_out,
       or_1_out, or_5_out, or_6_out, or_7_out, or_9_out, or_10_out, or_12_out, or_13_out, or_15_out,
       or_16_out, Pause, priority_encoder_1_gs, RegDst, SignedExt, Syscall, Vshamt, W1, W2, W3;
  wire [1:0] controlled_buffer_4_out, IRQ_Exe, IRQ_TODO, ram_1_data;
  wire [2:0] multiplexer_1_out;
  wire [3:0] AluOP;
  wire [4:0] multiplexer_2_out, \reg选择逻辑_1_r1_num , \reg选择逻辑_1_r2_num , \reg选择逻辑_1_shamt , \reg选择逻辑_1_w_num ;
  wire [12:0] CNT_num;
  wire [15:0] adder_3_out, controlled_buffer_6_out, controlled_buffer_8_out, register_2_q, subtractor_1_out,
       \总周期数 ;
  wire [31:0] adder_1_out, adder_2_out, bit_extender_1_out, bit_extender_2_out, controlled_buffer_1_out, EPC,
       IRQ_Entry, mips_alu_1_result, mips_mem_1_memreaddata, multiplexer_3_out, multiplexer_5_out,
       multiplexer_6_out, PC_Next, R1;

  Clock #(.highDuration(1), .lowDuration(1)) clock_1 ();  // open: out
  Button _1 ();  // open: out
  Button _2 ();  // open: out
  Button _3 ();  // open: out
  Button \u_继续运行  (.out(Go));
  LED #(.active("true")) led_1 (.in(W1));
  LED #(.active("true")) led_2 (.in(W2));
  LED #(.active("true")) led_3 (.in(W3));
  Decoder #(.select(2), .tristate("false"), .disabled(0), .enable("true")) decoder_1 (
    .out0(decoder_1_out0), .out1(decoder_1_out1), .out2(decoder_1_out2), .sel(IRQ_Exe), .en(ERET));  // open: out3
  Multiplexer #(.select(2), .width(3), .disabled("Z"), .enable("false")) multiplexer_1 (
    .in0(3'b001), .in1(3'b011), .in2(3'b111), .in3(3'b000), .out(multiplexer_1_out), .sel(IRQ_Exe));
  Hex_Digit_Display hex_digit_display_1 (.value(LedData[31:28]));  // open: dp
  and and_1 (and_1_out, ~ERET, IRQ);  // AND_Gate
  or or_1 (or_1_out, ERET, IRQ);
  \PC更新逻辑  \pc更新逻辑_1  (
    .Equal(Equal), .Beq(Beq), .Bne(Bne), .JAL(JAL), .JMP(JMP), .JR(JR), .BAddr(adder_2_out),
    .PC_4(adder_1_out), .JAddr({PC[31:28], IR[25:0], 2'b00}), .JRAddr(R1), .PC_Next(PC_Next), .Blez(Blez),
    .Less(Less));  // open: Branched, BranchSig
  or or_2 (W1, d_ff_4_q, d_ff_1_q);
  or or_3 (W2, d_ff_6_q, d_ff_2_q);
  or or_4 (W3, d_ff_8_q, d_ff_3_q);
  Hex_Digit_Display hex_digit_display_2 (.value(LedData[27:24]));  // open: dp
  Hex_Digit_Display hex_digit_display_3 (.value(LedData[23:20]));  // open: dp
  assign controlled_buffer_1_out = ERET ? EPC : 32'bz;  // Controlled_Buffer controlled_buffer_1
  assign controlled_buffer_1_out = and_1_out ? IRQ_Entry : 32'bz;  // Controlled_Buffer controlled_buffer_2
  assign controlled_buffer_1_out = ~or_1_out ? PC_Next : 32'bz;  // Controlled_Buffer controlled_buffer_3
  D_Flip_Flop #(.trigger("rising"), .Pre_Clr_Positions("LEGACY"), .NegatePresetClear("false"), .enable("true"), .NewFFLayout("false")) d_ff_1 (
    .clk(IR1_t), .D(1'b1), .Q(d_ff_1_q), .reset(d_ff_4_q));  // open: Qn, preset, en
  D_Flip_Flop #(.trigger("rising"), .Pre_Clr_Positions("LEGACY"), .NegatePresetClear("false"), .enable("true"), .NewFFLayout("false")) d_ff_2 (
    .clk(IR2_t), .D(1'b1), .Q(d_ff_2_q), .reset(d_ff_6_q));  // open: Qn, preset, en
  D_Flip_Flop #(.trigger("rising"), .Pre_Clr_Positions("LEGACY"), .NegatePresetClear("false"), .enable("true"), .NewFFLayout("false")) d_ff_3 (
    .clk(IR3_t), .D(1'b1), .Q(d_ff_3_q), .reset(d_ff_8_q));  // open: Qn, preset, en
  Hex_Digit_Display hex_digit_display_4 (.value(LedData[15:12]));  // open: dp
  Hex_Digit_Display hex_digit_display_5 (.value(LedData[19:16]));  // open: dp
  Register #(.width(32), .trigger("rising"), .Select("low")) u_PC (
    .D(controlled_buffer_1_out), .Q(PC), .clk(CLK));  // open: en, clr
  or or_5 (or_5_out, d_ff_1_q, d_ff_4_q);
  or or_6 (or_6_out, d_ff_2_q, d_ff_6_q);
  or or_7 (or_7_out, d_ff_3_q, d_ff_8_q);
  Hex_Digit_Display hex_digit_display_6 (.value(LedData[7:4]));  // open: dp
  Hex_Digit_Display hex_digit_display_7 (.value(LedData[11:8]));  // open: dp
  // Probe on \总周期数 
  Adder #(.width(32)) adder_1 (.a(PC), .b(32'h4), .out(adder_1_out));  // open: cin, cout
  and and_2 (and_2_out, or_5_out, ~decoder_1_out0);  // AND_Gate
  not not_1 (not_1_out, multiplexer_1_out[0]);
  and and_3 (and_3_out, or_6_out, ~decoder_1_out1);  // AND_Gate
  and and_4 (and_4_out, or_7_out, ~decoder_1_out2);  // AND_Gate
  not not_2 (not_2_out, multiplexer_1_out[2]);
  Hex_Digit_Display hex_digit_display_8 (.value(LedData[3:0]));  // open: dp
  // Mips_Probe mips_probe_1: pin names not known; wires that end beside it: IR
  ROM #(.addrWidth(10), .dataWidth(32), .Select("low")) rom_1 (.addr(PC[11:2]), .data(IR));
  D_Flip_Flop #(.trigger("rising"), .Pre_Clr_Positions("LEGACY"), .NegatePresetClear("false"), .enable("false"), .NewFFLayout("false")) d_ff_4 (
    .clk(CLK), .D(and_2_out), .Q(d_ff_4_q));  // open: Qn, preset, reset
  D_Flip_Flop #(.trigger("rising"), .Pre_Clr_Positions("LEGACY"), .NegatePresetClear("false"), .enable("false"), .NewFFLayout("false")) d_ff_5 (
    .clk(CLK), .Qn(d_ff_5_qn), .preset(multiplexer_1_out[0]), .reset(not_1_out));  // open: D, Q
  and and_5 (and_5_out, d_ff_4_q, d_ff_5_qn);
  D_Flip_Flop #(.trigger("rising"), .Pre_Clr_Positions("LEGACY"), .NegatePresetClear("false"), .enable("true"), .NewFFLayout("false")) d_ff_6 (
    .clk(CLK), .D(and_3_out), .Q(d_ff_6_q));  // open: Qn, preset, en, reset
  D_Flip_Flop #(.trigger("rising"), .Pre_Clr_Positions("LEGACY"), .NegatePresetClear("false"), .enable("false"), .NewFFLayout("false")) d_ff_7 (
    .clk(CLK), .Qn(d_ff_7_qn), .preset(multiplexer_1_out[1]), .reset(not_3_out));  // open: D, Q
  and and_6 (and_6_out, d_ff_6_q, d_ff_7_qn);
  not not_3 (not_3_out, multiplexer_1_out[1]);
  D_Flip_Flop #(.trigger("rising"), .Pre_Clr_Positions("LEGACY"), .NegatePresetClear("false"), .enable("false"), .NewFFLayout("false")) d_ff_8 (
    .clk(CLK), .D(and_4_out), .Q(d_ff_8_q));  // open: Qn, preset, reset
  D_Flip_Flop #(.trigger("rising"), .Pre_Clr_Positions("LEGACY"), .NegatePresetClear("false"), .enable("false"), .NewFFLayout("false")) d_ff_9 (
    .clk(CLK), .Qn(d_ff_9_qn), .preset(multiplexer_1_out[2]), .reset(not_2_out));  // open: D, Q
  and and_7 (and_7_out, d_ff_8_q, d_ff_9_qn);
  or or_8 (IR1_t, IR1, IRA);
  assign bit_extender_1_out = {{16{1'b0}}, IR[15:0]};  // Bit_Extender bit_extender_1
  assign bit_extender_2_out = {{16{IR[15]}}, IR[15:0]};  // Bit_Extender bit_extender_2
  Priority_Encoder #(.select(2), .disabled("Z")) priority_encoder_1 (
    .in0(and_5_out), .in1(and_6_out), .in2(and_7_out), .in3(1'b0), .out(IRQ_TODO), .gs(priority_encoder_1_gs));  // open: en_out, en_in
  D_Flip_Flop #(.trigger("rising"), .Pre_Clr_Positions("LEGACY"), .NegatePresetClear("false"), .enable("true"), .NewFFLayout("false")) u_IE (
    .clk(CLK), .D(MFC), .Q(IE), .preset(or_9_out), .en(or_10_out), .reset(d_ff_10_q));  // open: Qn
  or or_9 (or_9_out, ERET, INIT);
  or or_10 (or_10_out, MTC, ERET, MFC, IRQ);
  Comparator #(.width(16), .mode("twosComplement")) comparator_1 (
    .a({16{1'b0}}), .b(\总周期数 ), .eq(INIT));  // open: gt, lt
  or or_11 (IR2_t, IR2, IRB);
  \Reg选择逻辑  \reg选择逻辑_1  (
    ._21_25(IR[25:21]), .Syscall(Syscall), .RegDst(RegDst), ._16_20(IR[20:16]), ._11_15(IR[15:11]),
    .JAL(JAL), .PC_4(adder_1_out), .WriteBack_Data(multiplexer_6_out), ._6_10(IR[10:6]),
    .R1_num(\reg选择逻辑_1_r1_num ), .R2_num(\reg选择逻辑_1_r2_num ), .W_num(\reg选择逻辑_1_w_num ), .RDin(RDin),
    .Shamt(\reg选择逻辑_1_shamt ));
  and and_8 (IRQ, priority_encoder_1_gs, IE);
  Comparator #(.width(8), .mode("twosComplement")) comparator_2 (
    .a({8{1'b0}}), .b(IR[10:3]), .eq(comparator_2_eq));  // open: gt, lt
  Comparator #(.width(6), .mode("twosComplement")) comparator_3 (
    .a(6'b010000), .b(IR[31:26]), .eq(comparator_3_eq));  // open: gt, lt
  Comparator #(.width(5), .mode("twosComplement")) comparator_4 (
    .a({5{1'b0}}), .b(IR[25:21]), .eq(comparator_4_eq));  // open: gt, lt
  Comparator #(.width(5), .mode("twosComplement")) comparator_5 (
    .a(5'b00100), .b(IR[25:21]), .eq(comparator_5_eq));  // open: gt, lt
  MIPS_Regifile mips_regifile_1 (
    .Din(RDin), .Clk(CLK), .R1(R1), .R2(MDin), .WE(RegWrite), .W_num(\reg选择逻辑_1_w_num ),
    .R1_num(\reg选择逻辑_1_r1_num ), .R2_num(\reg选择逻辑_1_r2_num ));
  Multiplexer #(.select(1), .width(5), .disabled("Z"), .enable("false")) multiplexer_2 (
    .in0(\reg选择逻辑_1_shamt ), .in1(R1[4:0]), .out(multiplexer_2_out), .sel(Vshamt));
  Adder #(.width(32)) adder_2 (
    .a(adder_1_out), .b({bit_extender_2_out[29:0], 2'b00}), .out(adder_2_out));  // open: cin, cout
  Multiplexer #(.select(1), .width(32), .disabled("Z"), .enable("false")) multiplexer_3 (
    .in0(bit_extender_1_out), .in1(bit_extender_2_out), .out(multiplexer_3_out), .sel(SignedExt));
  assign controlled_buffer_4_out = ERET ? ram_1_data : 2'bz;  // Controlled_Buffer controlled_buffer_4
  or or_12 (or_12_out, IRQ, ERET);
  assign controlled_buffer_4_out = IRQ ? IRQ_TODO : 2'bz;  // Controlled_Buffer controlled_buffer_5
  Multiplexer #(.select(2), .width(32), .disabled("Z"), .enable("false")) multiplexer_4 (
    .in0(32'h30ac), .in1(32'h3158), .in2(32'h3204), .out(IRQ_Entry), .sel(controlled_buffer_4_out));  // open: in3
  D_Flip_Flop #(.trigger("rising"), .Pre_Clr_Positions("LEGACY"), .NegatePresetClear("false"), .enable("true"), .NewFFLayout("false")) d_ff_10 (
    .clk(CLK), .D(or_13_out), .Q(d_ff_10_q), .en(not_4_out));  // open: Qn, preset, reset
  or or_13 (or_13_out, IRQ, MTC);
  not not_4 (not_4_out, ERET);
  and and_9 (and_9_out, comparator_2_eq, comparator_3_eq);
  or or_14 (IR3_t, IR3, IRC);
  Multiplexer #(.select(1), .width(32), .disabled("Z"), .enable("false")) multiplexer_5 (
    .in0(MDin), .in1(multiplexer_3_out), .out(multiplexer_5_out), .sel(AluSrcB));
  Register #(.width(2), .trigger("rising"), .Select("low")) register_1 (
    .D(controlled_buffer_4_out), .en(or_12_out), .Q(IRQ_Exe), .clk(CLK), .preset(INIT));  // open: clr, cs
  and and_10 (MFC, and_9_out, comparator_4_eq);
  and and_11 (MTC, and_9_out, comparator_5_eq);
  Comparator #(.width(32), .mode("twosComplement")) comparator_6 (.a(IR), .b(32'h42000018), .eq(ERET));  // open: gt, lt
  MIPS_ALU mips_alu_1 (
    .X(R1), .Y(multiplexer_5_out), .AluOP(AluOP), .Equal(Equal), .Result(mips_alu_1_result),
    .shamt(multiplexer_2_out), .Less(Less));  // open: Result_2
  Adder #(.width(16)) adder_3 (.a(controlled_buffer_8_out), .b(16'h1), .out(adder_3_out));  // open: cin, cout
  Subtractor #(.width(16)) subtractor_1 (.a(register_2_q), .b(16'h1), .out(subtractor_1_out));  // open: bin, bout
  assign controlled_buffer_6_out = IRQ ? adder_3_out : 16'bz;  // Controlled_Buffer controlled_buffer_6
  assign controlled_buffer_6_out = ERET ? subtractor_1_out : 16'bz;  // Controlled_Buffer controlled_buffer_7
  assign controlled_buffer_8_out = ~ERET ? register_2_q : 16'bz;  // Controlled_Buffer controlled_buffer_8
  Register #(.width(16), .trigger("rising"), .Select("low")) register_2 (
    .D(controlled_buffer_6_out), .Q(register_2_q), .clk(CLK));  // open: en, clr
  assign controlled_buffer_8_out = ERET ? controlled_buffer_6_out : 16'bz;  // Controlled_Buffer controlled_buffer_9
  MIPS_MEM mips_mem_1 (
    .AluResult(mips_alu_1_result), .HalfW(HalfW), .WriteData(MDin), .MemWrite(MemWrite), .CLK(CLK),
    .MemReadData(mips_mem_1_memreaddata));
  not not_5 (not_5_out, IRQ);
  not not_6 (not_6_out, IRQ);
  RAM #(.addrWidth(16), .dataWidth(2), .bus("separate"), .Select("low")) ram_1 (
    .addr(controlled_buffer_8_out), .din(IRQ_Exe), .data(ram_1_data), .str(IRQ), .clk(CLK), .ld(not_5_out));  // open: sel, clr
  RAM #(.addrWidth(16), .dataWidth(32), .bus("separate"), .Select("low")) ram_2 (
    .addr(controlled_buffer_8_out), .din(PC_Next), .data(EPC), .str(IRQ), .clk(CLK), .ld(not_6_out));  // open: sel, clr
  Multiplexer #(.select(1), .width(32), .disabled("Z"), .enable("false")) multiplexer_6 (
    .in0(mips_alu_1_result), .in1(mips_mem_1_memreaddata), .out(multiplexer_6_out), .sel(MemToReg));
  D_Flip_Flop #(.trigger("high"), .Pre_Clr_Positions("LEGACY"), .NegatePresetClear("false"), .enable("true"), .NewFFLayout("false")) d_ff_11 (
    .Q(d_ff_11_q), .preset(Pause), .reset(Go));  // open: clk, D, Qn, en
  // Probe on 13'hc
  Comparator #(.width(16), .mode("twosComplement")) comparator_7 (
    .a(16'h258), .b(\总周期数 ), .eq(comparator_7_eq));  // open: gt, lt
  Comparator #(.width(16), .mode("twosComplement")) comparator_8 (
    .a(\总周期数 ), .b(16'h1), .eq(comparator_8_eq));  // open: gt, lt
  Comparator #(.width(16), .mode("twosComplement")) comparator_9 (
    .a(\总周期数 ), .b(16'h4), .eq(comparator_9_eq));  // open: gt, lt
  Comparator #(.width(16), .mode("twosComplement")) comparator_10 (
    .a(\总周期数 ), .b(16'h7), .eq(comparator_10_eq));  // open: gt, lt
  Comparator #(.width(16), .mode("twosComplement")) comparator_11 (
    .a(\总周期数 ), .b(16'h241), .eq(comparator_11_eq));  // open: gt, lt
  Clock #(.highDuration(1), .lowDuration(1)) clock_2 (.out(clock_2_out));
  \单周期硬布线控制器  \u_单周期硬布线控制器_1  (
    .Func(IR[5:0]), .OP(IR[31:26]), .ALU_OP(AluOP), .MemToReg(MemToReg), .MemWrite(MemWrite),
    .ALU_SRC(AluSrcB), .RegWrite(RegWrite), .SysCALL(Syscall), .SignedExt(SignedExt), .RegDst(RegDst),
    .JR(JR), .JMP(JMP), .Beq(Beq), .JAL(JAL), .Bne(Bne), .Vshamt(Vshamt), .BLEZ(Blez), .HalfW(HalfW));
  \Syscall处理  \syscall处理_1  (.Syscall(Syscall), .CLK(CLK), .R2(MDin), .R1(R1), .Pause(Pause), .LedData(LedData));
  or or_15 (or_15_out, comparator_7_eq, comparator_8_eq);
  assign IRA = or_15_out ? ~CLK : 1'bz;  // Controlled_Inverter controlled_inverter_1
  assign IRB = comparator_9_eq ? ~CLK : 1'bz;  // Controlled_Inverter controlled_inverter_2
  or or_16 (or_16_out, comparator_10_eq, comparator_11_eq);
  assign IRC = or_16_out ? ~CLK : 1'bz;  // Controlled_Inverter controlled_inverter_3
  Comparator #(.width(13), .mode("twosComplement")) comparator_12 (
    .a(CNT_num), .b(13'hc), .eq(comparator_12_eq), .lt(comparator_12_lt));  // open: gt
  Pull_Resistor #(.pull(0)) pull_resistor_1 (.node(IRA));
  Pull_Resistor #(.pull(0)) pull_resistor_2 (.node(IRB));
  Pull_Resistor #(.pull(0)) pull_resistor_3 (.node(IRC));
  nand nand_1 (nand_1_out, d_ff_11_q, comparator_12_eq);
  Counter #(.width(13), .max('h1fff), .ongoal("stay"), .trigger("rising"), .behavior("old")) counter_1 (
    .count(comparator_12_lt), .Q(CNT_num), .clk(clock_2_out));  // open: load, D, carry, clr, preset
  assign CLK = nand_1_out ? clock_2_out : 1'bz;  // Controlled_Buffer controlled_buffer_10
  Pull_Resistor #(.pull(1)) pull_resistor_4 (.node(CLK));
  Counter #(.width(16), .max('hffff), .ongoal("stay"), .trigger("rising"), .behavior("old")) counter_2 (
    .Q(\总周期数 ), .clk(CLK));  // open: load, D, count, carry, clr, preset

  // Other names for the same wires on the sheet: Func[5:0] = IR[5:0]; OP[5:0] = IR[31:26]; R2[31:0] = MDin

  // Notes on the sheet:
  //   中断源
  //   中断等待指示
  //   总复位信号应将除ROM以外所有存储组件全部清零
  //   数码管输出
  //   数码管输出应该用寄存器锁存，否则显示数据只能一闪而过
  //   指令存储器
  //   指令字
  //   contents of rom_1 (hex, n*v repeats v):
  //   201d07d0 20100001 109fc0 139fc3 8021 2012000c 24160008 26100001 3210000f 20080008 20090001 139900
  //   2709825 132020 20020022 c 1094022 1500fff9 22100001 2018000f 2188024 108700 20080008 20090001 139902
  //   2709825 132021 20020022 c 1094022 1500fff9 108702 2c9b022 12c00001 8000c07 4020 1084027 84400
  //   3508ffff 82021 20020022 c 8000c01 afa20000 23bd0004 afa40000 23bd0004 afb00000 23bd0004 afb30000
  //   23bd0004 afb40000 23bd0004 afb50000 23bd0004 afb60000 23bd0004 40000000 20160001 20140003 20150001
  //   168020 108100 2149825 132020 20020022 c 1600fffa 295a022 1680fff7 40800000 23bdfffc 8fb60000
  //   23bdfffc 8fb50000 23bdfffc 8fb40000 23bdfffc 8fb30000 23bdfffc 8fb00000 23bdfffc 8fa40000 23bdfffc
  //   8fa20000 42000018 afa20000 23bd0004 afa40000 23bd0004 afb00000 23bd0004 afb30000 23bd0004 afb40000
  //   23bd0004 afb50000 23bd0004 afb60000 23bd0004 40000000 20160002 20140003 20150001 168020 108100
  //   2149825 132020 20020022 c 1600fffa 295a022 1680fff7 40800000 23bdfffc 8fb60000 23bdfffc 8fb50000
  //   23bdfffc 8fb40000 23bdfffc 8fb30000 23bdfffc 8fb00000 23bdfffc 8fa40000 23bdfffc 8fa20000 42000018
  //   afa20000 23bd0004 afa40000 23bd0004 afb00000 23bd0004 afb30000 23bd0004 afb40000 23bd0004 afb50000
  //   23bd0004 afb60000 23bd0004 40000000 20160003 20140003 20150001 168020 108100 2149825 132020 20020022
  //   c 1600fffa 295a022 1680fff7 40800000 23bdfffc 8fb60000 23bdfffc 8fb50000 23bdfffc 8fb40000 23bdfffc
  //   8fb30000 23bdfffc 8fb00000 23bdfffc 8fa40000 23bdfffc 8fa20000 42000018
  //   为方便自动评测，需要输出PC，IR，寄存器堆写如数据RDin
  //   RAM写使能MemWrite、RAM写入数据MDin等信号
  //   控制位
  //   暂停节拍，不能为0
  //   多级中断测试信号模拟器
  //   戳工具置1进入计数暂停模式，ctrl+k时钟自动运行到对应节拍暂停
  //   ctrl+k关闭时钟连续运行，将控制位置零，进入单步调试模式调试
  //   用这个时钟源需要去掉电路中的其他时钟源
  //   可计数暂停的时钟源
endmodule

module \封装正确性测试  (
);

  wire IR1, IR2, IR3, MemW, RegW;
  wire [31:0] EX_PC, ID_PC, IF_PC, IR, LED, MDin, MDinr, MEM_PC, PC, RDin, RDinr, WB_PC;

  \单周期MIPS  \u_单周期mips_1  (
    .RegWrite(RegW), .MemWrite(MemW), .PC(PC), .IR(IR), .RDin(RDin), .MDin(MDin), .LedData(LED));  // open: IR1, IR2, IR3
  \气泡流水线  \u_气泡流水线_1  (
    .RegWrite(RegW), .MemWrite(MemW), .IF_PC(IF_PC), .ID_PC(ID_PC), .EX_PC(EX_PC), .M_PC(MEM_PC),
    .WB_PC(WB_PC), .RDin(RDinr), .MDin(MDinr), .LedData(LED));
  \单周期MIPS_单级中断  \u_单周期mips_单级中断_1  (
    .IR1(IR1), .IR2(IR2), .IR3(IR3), .RegWrite(RegW), .MemWrite(MemW), .PC(PC), .IR(IR), .RDin(RDin),
    .MDin(MDin), .LedData(LED));
  \理想流水线  \u_理想流水线_1  (
    .RegWrite(RegW), .MemWrite(MemW), .IF_PC(IF_PC), .ID_PC(ID_PC), .EX_PC(EX_PC), .M_PC(MEM_PC),
    .WB_PC(WB_PC), .RDin(RDinr), .MDin(MDinr), .LedData(LED));
  \重定向流水线  \u_重定向流水线_1  (
    .RegWrite(RegW), .MemWrite(MemW), .IF_PC(IF_PC), .ID_PC(ID_PC), .EX_PC(EX_PC), .M_PC(MEM_PC),
    .WB_PC(WB_PC), .RDin(RDinr), .MDin(MDinr), .LedData(LED));
  \单周期MIPS_多级中断  \u_单周期mips_多级中断_1  (
    .IR1(IR1), .IR2(IR2), .IR3(IR3), .RegWrite(RegW), .MemWrite(MemW), .PC(PC), .IR(IR), .RDin(RDin),
    .MDin(MDin), .LedData(LED));

  // Notes on the sheet:
  //   单周期封装测试
  //   气泡流水封装测试
  //   单周期+单级中断封装测试
  //   请检查上面封装有无位宽不匹配，引脚标签是否和连接的标签相对应，否则无法在educoder平台上正确测试
  //   理想流水封装测试
  //   重定向流水封装测试
  //   单周期+多级中断封装测试
endmodule

module \Syscall处理  (
  input  Syscall,
  input  CLK,
  input  [31:0] R2,
  input  [31:0] R1,
  output Pause,
  output [31:0] LedData
);

  wire and_1_out, and_2_out, comparator_1_eq;

  Comparator #(.width(32), .mode("twosComplement")) comparator_1 (
    .a(R1), .b(32'h22), .eq(comparator_1_eq));  // open: gt, lt
  and and_1 (and_1_out, Syscall, ~comparator_1_eq);  // AND_Gate
  and and_2 (and_2_out, Syscall, comparator_1_eq);
  Register #(.width(1), .trigger("rising"), .Select("low")) register_1 (
    .D(and_1_out), .Q(Pause), .clk(CLK));  // open: en, clr
  Register #(.width(32), .trigger("rising"), .Select("low")) register_2 (
    .D(R2), .en(and_2_out), .Q(LedData), .clk(CLK));  // open: clr
endmodule

module \Reg选择逻辑  (
  input  [4:0] _21_25,
  input  Syscall,
  input  RegDst,
  input  [4:0] _16_20,
  input  [4:0] _11_15,
  input  JAL,
  input  [31:0] WriteBack_Data,
  input  [31:0] PC_4,
  input  [4:0] _6_10,
  output [4:0] R1_num,
  output [4:0] R2_num,
  output [4:0] W_num,
  output [31:0] RDin,
  output [4:0] Shamt
);

  wire [4:0] multiplexer_1_out;

  Multiplexer #(.select(1), .width(5), .disabled("Z"), .enable("false")) multiplexer_1 (
    .in0(_16_20), .in1(_11_15), .out(multiplexer_1_out), .sel(RegDst));
  Multiplexer #(.select(1), .width(5), .disabled("Z"), .enable("false")) multiplexer_2 (
    .in0(_21_25), .in1(5'b00010), .out(R1_num), .sel(Syscall));
  Multiplexer #(.select(1), .width(5), .disabled("Z"), .enable("false")) multiplexer_3 (
    .in0(_16_20), .in1(5'b00100), .out(R2_num), .sel(Syscall));
  Multiplexer #(.select(1), .width(5), .disabled("Z"), .enable("false")) multiplexer_4 (
    .in0(multiplexer_1_out), .in1({5{1'b1}}), .out(W_num), .sel(JAL));
  Multiplexer #(.select(1), .width(32), .disabled("Z"), .enable("false")) multiplexer_5 (
    .in0(WriteBack_Data), .in1(PC_4), .out(RDin), .sel(JAL));

  assign Shamt = _6_10;
endmodule

module \PC更新逻辑  (
  input  Blez,
  input  Less,
  input  Equal,
  input  Beq,
  input  Bne,
  input  JAL,
  input  JMP,
  input  JR,
  input  [31:0] BAddr,
  input  [31:0] PC_4,
  input  [31:0] JAddr,
  input  [31:0] JRAddr,
  output BranchSig,
  output Branched,
  output [31:0] PC_Next
);

  wire and_1_out, and_2_out, and_3_out, nor_1_out, or_1_out, or_2_out, or_4_out;

  or or_1 (or_1_out, Less, Equal);
  and and_1 (and_1_out, Equal, Beq);
  and and_2 (and_2_out, ~Equal, Bne);  // AND_Gate
  or or_2 (or_2_out, JAL, JMP);
  or or_3 (BranchSig, Blez, Beq, Bne, JAL, JMP, JR);
  and and_3 (and_3_out, Blez, or_1_out);
  or or_4 (or_4_out, and_3_out, and_1_out, and_2_out);
  nor nor_1 (nor_1_out, and_3_out, and_1_out, and_2_out, JR, or_2_out);
  assign PC_Next = or_4_out ? BAddr : 32'bz;  // Controlled_Buffer controlled_buffer_1
  assign PC_Next = nor_1_out ? PC_4 : 32'bz;  // Controlled_Buffer controlled_buffer_2
  assign PC_Next = or_2_out ? JAddr : 32'bz;  // Controlled_Buffer controlled_buffer_3
  assign PC_Next = JR ? JRAddr : 32'bz;  // Controlled_Buffer controlled_buffer_4
  or or_5 (Branched, or_4_out, or_2_out, JR);
endmodule

module IF_ID (
  input  [31:0] Instr,
  input  PredictJump,
  input  [31:0] PC,
  input  [31:0] PC_4,
  input  CLK,
  input  CLR,
  input  Stall,
  output [31:0] Instr_Out,
  output PredictJump_Out,
  output [31:0] PC_Out,
  output [31:0] PC_4_Out,
  output Eff
);

  wire multiplexer_2_out, multiplexer_5_out;
  wire [31:0] multiplexer_1_out, multiplexer_3_out, multiplexer_4_out;

  Multiplexer #(.select(1), .width(32), .disabled("Z"), .enable("false")) multiplexer_1 (
    .in0(Instr), .in1({32{1'b0}}), .out(multiplexer_1_out), .sel(CLR));
  Multiplexer #(.select(1), .width(1), .disabled("Z"), .enable("false")) multiplexer_2 (
    .in0(PredictJump), .in1(1'b0), .out(multiplexer_2_out), .sel(CLR));
  Multiplexer #(.select(1), .width(32), .disabled("Z"), .enable("false")) multiplexer_3 (
    .in0(PC), .in1({32{1'b0}}), .out(multiplexer_3_out), .sel(CLR));
  Multiplexer #(.select(1), .width(32), .disabled("Z"), .enable("false")) multiplexer_4 (
    .in0(PC_4), .in1({32{1'b0}}), .out(multiplexer_4_out), .sel(CLR));
  Multiplexer #(.select(1), .width(1), .disabled("Z"), .enable("false")) multiplexer_5 (
    .in0(1'b1), .in1(1'b0), .out(multiplexer_5_out), .sel(CLR));
  Register #(.width(32), .trigger("rising"), .Select("low")) register_1 (
    .D(multiplexer_1_out), .en(Stall), .Q(Instr_Out), .clk(CLK));  // open: clr
  Register #(.width(1), .trigger("rising"), .Select("low")) register_2 (
    .D(multiplexer_2_out), .en(Stall), .Q(PredictJump_Out), .clk(CLK));  // open: clr
  Register #(.width(32), .trigger("rising"), .Select("low")) register_3 (
    .D(multiplexer_3_out), .en(Stall), .Q(PC_Out), .clk(CLK));  // open: clr
  Register #(.width(32), .trigger("rising"), .Select("low")) register_4 (
    .D(multiplexer_4_out), .en(Stall), .Q(PC_4_Out), .clk(CLK));  // open: clr
  Register #(.width(1), .trigger("rising"), .Select("low")) register_5 (
    .D(multiplexer_5_out), .en(Stall), .Q(Eff), .clk(CLK));  // open: clr
endmodule

module ID_EX (
  input  JR,
  input  JMP,
  input  JAL,
  input  BLEZ,
  input  BEQ,
  input  BNE,
  input  MemToReg,
  input  RegWrite,
  input  MemWrite,
  input  HalfW,
  input  AluSrcB,
  input  Syscall,
  input  [4:0] Shamt,
  input  [31:0] R1,
  input  [1:0] R1_Forward,
  input  [1:0] R2_Forward,
  input  [31:0] R2,
  input  [3:0] AluOp,
  input  [31:0] ExtData,
  input  [4:0] W_num,
  input  PredictJump,
  input  [31:0] PC,
  input  [31:0] Instr,
  input  [31:0] PC_4,
  input  [31:0] JAddr,
  input  Eff_in,
  input  CLR,
  input  CLK,
  output JR_Out,
  output JMP_Out,
  output JAL_Out,
  output BLEZ_Out,
  output BEQ_Out,
  output BNE_Out,
  output MemToReg_Out,
  output RegWrite_Out,
  output MemWrite_Out,
  output HalfW_Out,
  output AluSrcB_Out,
  output Syscall_Out,
  output [4:0] Shamt_Out,
  output [31:0] R1_Out,
  output [1:0] R1_Forward_Out,
  output [1:0] R2_Forward_Out,
  output [31:0] R2_Out,
  output [3:0] AluOp_Out,
  output [31:0] ExtData_Out,
  output [4:0] W__Out,
  output PredictJump_Out,
  output [31:0] PC_Out,
  output [31:0] Instr_out,
  output [31:0] PC_4_Out,
  output [31:0] JAddr_Out,
  output Eff
);

  wire multiplexer_10_out, multiplexer_15_out;
  wire [1:0] multiplexer_4_out, multiplexer_5_out;
  wire [3:0] multiplexer_7_out;
  wire [4:0] multiplexer_2_out, multiplexer_9_out;
  wire [11:0] multiplexer_1_out;
  wire [31:0] multiplexer_3_out, multiplexer_6_out, multiplexer_8_out, multiplexer_11_out,
       multiplexer_12_out, multiplexer_13_out, multiplexer_14_out;

  Multiplexer #(.select(1), .width(12), .disabled("Z"), .enable("false")) multiplexer_1 (
    .in0({Syscall, AluSrcB, HalfW, MemWrite, RegWrite, MemToReg, BNE, BEQ, BLEZ, JAL, JMP, JR}),
    .in1({12{1'b0}}), .out(multiplexer_1_out), .sel(CLR));
  Multiplexer #(.select(1), .width(5), .disabled("Z"), .enable("false")) multiplexer_2 (
    .in0(Shamt), .in1({5{1'b0}}), .out(multiplexer_2_out), .sel(CLR));
  Multiplexer #(.select(1), .width(32), .disabled("Z"), .enable("false")) multiplexer_3 (
    .in0(R1), .in1({32{1'b0}}), .out(multiplexer_3_out), .sel(CLR));
  Multiplexer #(.select(1), .width(2), .disabled("Z"), .enable("false")) multiplexer_4 (
    .in0(R1_Forward), .in1(2'b00), .out(multiplexer_4_out), .sel(CLR));
  Multiplexer #(.select(1), .width(2), .disabled("Z"), .enable("false")) multiplexer_5 (
    .in0(R2_Forward), .in1(2'b00), .out(multiplexer_5_out), .sel(CLR));
  Multiplexer #(.select(1), .width(32), .disabled("Z"), .enable("false")) multiplexer_6 (
    .in0(R2), .in1({32{1'b0}}), .out(multiplexer_6_out), .sel(CLR));
  Multiplexer #(.select(1), .width(4), .disabled("Z"), .enable("false")) multiplexer_7 (
    .in0(AluOp), .in1(4'b0000), .out(multiplexer_7_out), .sel(CLR));
  Multiplexer #(.select(1), .width(32), .disabled("Z"), .enable("false")) multiplexer_8 (
    .in0(ExtData), .in1({32{1'b0}}), .out(multiplexer_8_out), .sel(CLR));
  Multiplexer #(.select(1), .width(5), .disabled("Z"), .enable("false")) multiplexer_9 (
    .in0(W_num), .in1({5{1'b0}}), .out(multiplexer_9_out), .sel(CLR));
  Multiplexer #(.select(1), .width(1), .disabled("Z"), .enable("false")) multiplexer_10 (
    .in0(PredictJump), .in1(1'b0), .out(multiplexer_10_out), .sel(CLR));
  Multiplexer #(.select(1), .width(32), .disabled("Z"), .enable("false")) multiplexer_11 (
    .in0(PC), .in1({32{1'b0}}), .out(multiplexer_11_out), .sel(CLR));
  Multiplexer #(.select(1), .width(32), .disabled("Z"), .enable("false")) multiplexer_12 (
    .in0(Instr), .in1({32{1'b0}}), .out(multiplexer_12_out), .sel(CLR));
  Multiplexer #(.select(1), .width(32), .disabled("Z"), .enable("false")) multiplexer_13 (
    .in0(PC_4), .in1({32{1'b0}}), .out(multiplexer_13_out), .sel(CLR));
  Multiplexer #(.select(1), .width(32), .disabled("Z"), .enable("false")) multiplexer_14 (
    .in0(JAddr), .in1({32{1'b0}}), .out(multiplexer_14_out), .sel(CLR));
  Multiplexer #(.select(1), .width(1), .disabled("Z"), .enable("false")) multiplexer_15 (
    .in0(Eff_in), .in1(1'b0), .out(multiplexer_15_out), .sel(CLR));
  Register #(.width(12), .trigger("rising"), .Select("low")) register_1 (
    .D(multiplexer_1_out),
    .Q({Syscall_Out, AluSrcB_Out, HalfW_Out, MemWrite_Out, RegWrite_Out, MemToReg_Out, BNE_Out, BEQ_Out, BLEZ_Out, JAL_Out, JMP_Out, JR_Out}),
    .clk(CLK));  // open: en, clr
  Register #(.width(5), .trigger("rising"), .Select("low")) register_2 (
    .D(multiplexer_2_out), .Q(Shamt_Out), .clk(CLK));  // open: en, clr
  Register #(.width(32), .trigger("rising"), .Select("low")) register_3 (
    .D(multiplexer_3_out), .Q(R1_Out), .clk(CLK));  // open: en, clr
  Register #(.width(2), .trigger("rising"), .Select("low")) register_4 (
    .D(multiplexer_4_out), .Q(R1_Forward_Out), .clk(CLK));  // open: en, clr
  Register #(.width(2), .trigger("rising"), .Select("low")) register_5 (
    .D(multiplexer_5_out), .Q(R2_Forward_Out), .clk(CLK));  // open: en, clr
  Register #(.width(32), .trigger("rising"), .Select("low")) register_6 (
    .D(multiplexer_6_out), .Q(R2_Out), .clk(CLK));  // open: en, clr
  Register #(.width(4), .trigger("rising"), .Select("low")) register_7 (
    .D(multiplexer_7_out), .Q(AluOp_Out), .clk(CLK));  // open: en, clr
  Register #(.width(32), .trigger("rising"), .Select("low")) register_8 (
    .D(multiplexer_8_out), .Q(ExtData_Out), .clk(CLK));  // open: en, clr
  Register #(.width(5), .trigger("rising"), .Select("low")) register_9 (
    .D(multiplexer_9_out), .Q(W__Out), .clk(CLK));  // open: en, clr
  Register #(.width(1), .trigger("rising"), .Select("low")) register_10 (
    .D(multiplexer_10_out), .Q(PredictJump_Out), .clk(CLK));  // open: en, clr
  Register #(.width(32), .trigger("rising"), .Select("low")) register_11 (
    .D(multiplexer_11_out), .Q(PC_Out), .clk(CLK));  // open: en, clr
  Register #(.width(32), .trigger("rising"), .Select("low")) register_12 (
    .D(multiplexer_12_out), .Q(Instr_out), .clk(CLK));  // open: en, clr
  Register #(.width(32), .trigger("rising"), .Select("low")) register_13 (
    .D(multiplexer_13_out), .Q(PC_4_Out), .clk(CLK));  // open: en, clr
  Register #(.width(32), .trigger("rising"), .Select("low")) register_14 (
    .D(multiplexer_14_out), .Q(JAddr_Out), .clk(CLK));  // open: en, clr
  Register #(.width(1), .trigger("rising"), .Select("low")) register_15 (
    .D(multiplexer_15_out), .Q(Eff), .clk(CLK));  // open: en, clr
endmodule

module EX_MEM (
  input  JAL,
  input  MemToReg,
  input  RegWrite,
  input  MemWrite,
  input  HalfW,
  input  Syscall,
  input  [31:0] AluResult,
  input  [31:0] R1,
  input  [31:0] R2,
  input  [31:0] PC,
  input  [31:0] Instr,
  input  [31:0] PC_4,
  input  [4:0] W_num,
  input  Eff_in,
  input  CLR,
  input  CLK,
  output JAL_Out,
  output MemToReg_Out,
  output RegWrite_Out,
  output MemWrite_Out,
  output HalfW_Out,
  output Syscall_Out,
  output [31:0] AluResult_Out,
  output [31:0] R1_Out,
  output [31:0] R2_Out,
  output [31:0] PC_Out,
  output [31:0] Instr_out,
  output [31:0] PC_4_Out,
  output [4:0] W__Out,
  output Eff
);

  wire multiplexer_9_out;
  wire [4:0] multiplexer_8_out;
  wire [5:0] multiplexer_1_out;
  wire [31:0] multiplexer_2_out, multiplexer_3_out, multiplexer_4_out, multiplexer_5_out, multiplexer_6_out,
       multiplexer_7_out;

  Multiplexer #(.select(1), .width(6), .disabled("Z"), .enable("false")) multiplexer_1 (
    .in0({Syscall, HalfW, MemWrite, RegWrite, MemToReg, JAL}), .in1({6{1'b0}}), .out(multiplexer_1_out),
    .sel(CLR));
  Multiplexer #(.select(1), .width(32), .disabled("Z"), .enable("false")) multiplexer_2 (
    .in0(AluResult), .in1({32{1'b0}}), .out(multiplexer_2_out), .sel(CLR));
  Multiplexer #(.select(1), .width(32), .disabled("Z"), .enable("false")) multiplexer_3 (
    .in0(R1), .in1({32{1'b0}}), .out(multiplexer_3_out), .sel(CLR));
  Multiplexer #(.select(1), .width(32), .disabled("Z"), .enable("false")) multiplexer_4 (
    .in0(R2), .in1({32{1'b0}}), .out(multiplexer_4_out), .sel(CLR));
  Multiplexer #(.select(1), .width(32), .disabled("Z"), .enable("false")) multiplexer_5 (
    .in0(PC), .in1({32{1'b0}}), .out(multiplexer_5_out), .sel(CLR));
  Multiplexer #(.select(1), .width(32), .disabled("Z"), .enable("false")) multiplexer_6 (
    .in0(Instr), .in1({32{1'b0}}), .out(multiplexer_6_out), .sel(CLR));
  Multiplexer #(.select(1), .width(32), .disabled("Z"), .enable("false")) multiplexer_7 (
    .in0(PC_4), .in1({32{1'b0}}), .out(multiplexer_7_out), .sel(CLR));
  Multiplexer #(.select(1), .width(5), .disabled("Z"), .enable("false")) multiplexer_8 (
    .in0(W_num), .in1({5{1'b0}}), .out(multiplexer_8_out), .sel(CLR));
  Multiplexer #(.select(1), .width(1), .disabled("Z"), .enable("false")) multiplexer_9 (
    .in0(Eff_in), .in1(1'b0), .out(multiplexer_9_out), .sel(CLR));
  Register #(.width(6), .trigger("rising"), .Select("low")) register_1 (
    .D(multiplexer_1_out), .Q({Syscall_Out, HalfW_Out, MemWrite_Out, RegWrite_Out, MemToReg_Out, JAL_Out}),
    .clk(CLK));  // open: en, clr
  Register #(.width(32), .trigger("rising"), .Select("low")) register_2 (
    .D(multiplexer_2_out), .Q(AluResult_Out), .clk(CLK));  // open: en, clr
  Register #(.width(32), .trigger("rising"), .Select("low")) register_3 (
    .D(multiplexer_3_out), .Q(R1_Out), .clk(CLK));  // open: en, clr
  Register #(.width(32), .trigger("rising"), .Select("low")) register_4 (
    .D(multiplexer_4_out), .Q(R2_Out), .clk(CLK));  // open: en, clr
  Register #(.width(32), .trigger("rising"), .Select("low")) register_5 (
    .D(multiplexer_5_out), .Q(PC_Out), .clk(CLK));  // open: en, clr
  Register #(.width(32), .trigger("rising"), .Select("low")) register_6 (
    .D(multiplexer_6_out), .Q(Instr_out), .clk(CLK));  // open: en, clr
  Register #(.width(32), .trigger("rising"), .Select("low")) register_7 (
    .D(multiplexer_7_out), .Q(PC_4_Out), .clk(CLK));  // open: en, clr
  Register #(.width(5), .trigger("rising"), .Select("low")) register_8 (
    .D(multiplexer_8_out), .Q(W__Out), .clk(CLK));  // open: en, clr
  Register #(.width(1), .trigger("rising"), .Select("low")) register_9 (
    .D(multiplexer_9_out), .Q(Eff), .clk(CLK));  // open: en, clr
endmodule

module MEM_WB (
  input  JAL,
  input  MemToReg,
  input  RegWrite,
  input  [31:0] AluResult,
  input  [31:0] R2,
  input  [31:0] PC,
  input  [31:0] Instr,
  input  [31:0] PC_4,
  input  [4:0] W_num,
  input  Eff_in,
  input  CLK,
  output JAL_Out,
  output MemToReg_Out,
  output RegWrite_Out,
  output [31:0] AluResult_Out,
  output [31:0] R2_Out,
  output [31:0] PC_Out,
  output [31:0] Instr_out,
  output [31:0] PC_4_Out,
  output [4:0] W__Out,
  output Eff
);

  Register #(.width(3), .trigger("rising"), .Select("low")) register_1 (
    .D({RegWrite, MemToReg, JAL}), .Q({RegWrite_Out, MemToReg_Out, JAL_Out}), .clk(CLK));  // open: en, clr
  Register #(.width(32), .trigger("rising"), .Select("low")) register_2 (
    .D(AluResult), .Q(AluResult_Out), .clk(CLK));  // open: en, clr
  Register #(.width(32), .trigger("rising"), .Select("low")) register_3 (
    .D(R2), .Q(R2_Out), .clk(CLK));  // open: en, clr
  Register #(.width(32), .trigger("rising"), .Select("low")) register_4 (
    .D(PC), .Q(PC_Out), .clk(CLK));  // open: en, clr
  Register #(.width(32), .trigger("rising"), .Select("low")) register_5 (
    .D(Instr), .Q(Instr_out), .clk(CLK));  // open: en, clr
  Register #(.width(32), .trigger("rising"), .Select("low")) register_6 (
    .D(PC_4), .Q(PC_4_Out), .clk(CLK));  // open: en, clr
  Register #(.width(5), .trigger("rising"), .Select("low")) register_7 (
    .D(W_num), .Q(W__Out), .clk(CLK));  // open: en, clr
  Register #(.width(1), .trigger("rising"), .Select("low")) register_8 (
    .D(Eff_in), .Q(Eff), .clk(CLK));  // open: en, clr
endmodule

module MIPS_MEM (
  input  [31:0] AluResult,
  input  HalfW,
  input  [31:0] WriteData,
  input  MemWrite,
  input  CLK,
  output [31:0] MemReadData
);

  wire decoder_1_out0, decoder_1_out1, not_1_out, not_2_out;
  wire [15:0] demultiplexer_1_out0, demultiplexer_1_out1;

  Demultiplexer #(.select(1), .width(16), .tristate("false"), .disabled("Z"), .enable("true")) demultiplexer_1 (
    .out0(demultiplexer_1_out0), .out1(demultiplexer_1_out1), .in(WriteData[15:0]), .sel(AluResult[1]),
    .en(HalfW));
  Decoder #(.select(1), .tristate("false"), .disabled(0), .enable("true")) decoder_1 (
    .out0(decoder_1_out0), .out1(decoder_1_out1), .sel(AluResult[1]), .en(HalfW));
  not not_1 (not_1_out, decoder_1_out0);
  not not_2 (not_2_out, decoder_1_out1);
  assign demultiplexer_1_out0 = ~HalfW ? WriteData[15:0] : 16'bz;  // Controlled_Buffer controlled_buffer_1
  assign demultiplexer_1_out1 = ~HalfW ? WriteData[31:16] : 16'bz;  // Controlled_Buffer controlled_buffer_2
  RAM #(.addrWidth(10), .dataWidth(16), .bus("separate"), .Select("high")) ram_1 (
    .addr(AluResult[11:2]), .din(demultiplexer_1_out0), .data(MemReadData[15:0]), .str(MemWrite),
    .sel(not_2_out), .clk(CLK));  // open: ld, clr
  RAM #(.addrWidth(10), .dataWidth(16), .bus("separate"), .Select("high")) ram_2 (
    .addr(AluResult[11:2]), .din(demultiplexer_1_out1), .data(MemReadData[31:16]), .str(MemWrite),
    .sel(not_1_out), .clk(CLK));  // open: ld, clr
endmodule

module \气泡流水冲突处理  (
  input  [4:0] R1_num,
  input  [4:0] W_num,
  input  [4:0] R2_num,
  input  CLR,
  input  RegWrite,
  input  AluSrc,
  output R1_CF,
  output Stall_PC_ID,
  output R2_CF
);

  wire comparator_1_eq, comparator_2_eq, comparator_3_eq, comparator_4_eq, or_1_out;

  Comparator #(.width(5), .mode("twosComplement")) comparator_1 (
    .a({5{1'b0}}), .b(R1_num), .eq(comparator_1_eq));  // open: gt, lt
  Comparator #(.width(5), .mode("twosComplement")) comparator_2 (
    .a(W_num), .b(R1_num), .eq(comparator_2_eq));  // open: gt, lt
  Comparator #(.width(5), .mode("twosComplement")) comparator_3 (
    .a(W_num), .b(R2_num), .eq(comparator_3_eq));  // open: gt, lt
  Comparator #(.width(5), .mode("twosComplement")) comparator_4 (
    .a(R2_num), .b({5{1'b0}}), .eq(comparator_4_eq));  // open: gt, lt
  and and_1 (R1_CF, ~comparator_1_eq, comparator_2_eq);  // AND_Gate
  or or_1 (or_1_out, R1_CF, R2_CF);
  and and_2 (R2_CF, comparator_3_eq, ~AluSrc, ~comparator_4_eq);  // AND_Gate
  and and_3 (Stall_PC_ID, or_1_out, ~CLR, RegWrite);  // AND_Gate
endmodule

module \重定向数据旁路控制信号生成  (
  input  [31:0] EX_IR,
  input  [31:0] ID_IR,
  input  ID_AluSrc,
  input  BranchCLR,
  input  [4:0] ID_R1_num,
  input  [4:0] ID_R2_num,
  input  [4:0] EX_W_num,
  input  [4:0] MEM_W_num,
  input  EX_RegWrite,
  input  MEM_RegWrite,
  input  MEM_MemToReg,
  output Stall,
  output [1:0] R1_Forward,
  output [1:0] R2_Forward
);

  wire and_1_out, and_2_out, and_4_out, and_5_out, and_6_out, and_7_out, and_8_out, and_9_out, and_10_out,
       and_11_out, comparator_1_eq, comparator_2_eq, comparator_3_eq, comparator_4_eq, comparator_5_eq,
       or_1_out, or_2_out, \气泡流水冲突处理_1_r1_cf , \气泡流水冲突处理_1_r2_cf , \气泡流水冲突处理_1_stall_pc_id ,
       \气泡流水冲突处理_2_r1_cf , \气泡流水冲突处理_2_r2_cf , \气泡流水冲突处理_2_stall_pc_id ;

  Comparator #(.width(6), .mode("twosComplement")) comparator_1 (
    .a(6'b100011), .b(EX_IR[31:26]), .eq(comparator_1_eq));  // open: gt, lt
  Comparator #(.width(5), .mode("twosComplement")) comparator_2 (
    .a(EX_IR[20:16]), .b(ID_IR[25:21]), .eq(comparator_2_eq));  // open: gt, lt
  Comparator #(.width(5), .mode("twosComplement")) comparator_3 (
    .a(EX_IR[20:16]), .b(ID_IR[20:16]), .eq(comparator_3_eq));  // open: gt, lt
  Comparator #(.width(6), .mode("twosComplement")) comparator_4 (
    .a(6'b100011), .b(ID_IR[31:26]), .eq(comparator_4_eq));  // open: gt, lt
  Comparator #(.width(6), .mode("twosComplement")) comparator_5 (
    .a(ID_IR[31:26]), .b(6'b101011), .eq(comparator_5_eq));  // open: gt, lt
  or or_1 (or_1_out, comparator_2_eq, and_1_out);
  and and_1 (and_1_out, comparator_3_eq, ~ID_AluSrc);  // AND_Gate
  or or_2 (or_2_out, comparator_4_eq, comparator_5_eq);
  and and_2 (and_2_out, ~or_2_out, ID_AluSrc);  // AND_Gate
  and and_3 (Stall, comparator_1_eq, or_1_out);
  and and_4 (and_4_out, \气泡流水冲突处理_1_stall_pc_id , \气泡流水冲突处理_1_r2_cf );
  and and_5 (and_5_out, \气泡流水冲突处理_1_r1_cf , \气泡流水冲突处理_1_stall_pc_id );
  \气泡流水冲突处理  \u_气泡流水冲突处理_1  (
    .R1_num(ID_R1_num), .W_num(EX_W_num), .R2_num(ID_R2_num), .CLR(BranchCLR), .RegWrite(EX_RegWrite),
    .Stall_PC_ID(\气泡流水冲突处理_1_stall_pc_id ), .AluSrc(and_2_out), .R1_CF(\气泡流水冲突处理_1_r1_cf ),
    .R2_CF(\气泡流水冲突处理_1_r2_cf ));
  and and_6 (and_6_out, ~MEM_MemToReg, and_8_out);  // AND_Gate
  and and_7 (and_7_out, MEM_MemToReg, and_8_out);
  and and_8 (and_8_out, \气泡流水冲突处理_2_r1_cf , \气泡流水冲突处理_2_stall_pc_id );
  and and_9 (and_9_out, \气泡流水冲突处理_2_stall_pc_id , \气泡流水冲突处理_2_r2_cf );
  \气泡流水冲突处理  \u_气泡流水冲突处理_2  (
    .R1_num(ID_R1_num), .W_num(MEM_W_num), .R2_num(ID_R2_num), .CLR(BranchCLR), .RegWrite(MEM_RegWrite),
    .Stall_PC_ID(\气泡流水冲突处理_2_stall_pc_id ), .AluSrc(and_2_out), .R1_CF(\气泡流水冲突处理_2_r1_cf ),
    .R2_CF(\气泡流水冲突处理_2_r2_cf ));
  Priority_Encoder #(.select(2), .disabled(0)) priority_encoder_1 (
    .in0(1'b1), .in1(and_6_out), .in2(and_7_out), .in3(and_5_out), .out(R1_Forward));  // open: gs, en_out, en_in
  and and_10 (and_10_out, ~MEM_MemToReg, and_9_out);  // AND_Gate
  and and_11 (and_11_out, MEM_MemToReg, and_9_out);
  Priority_Encoder #(.select(2), .disabled(0)) priority_encoder_2 (
    .in0(1'b1), .in1(and_10_out), .in2(and_11_out), .in3(and_4_out), .out(R2_Forward));  // open: gs, en_out, en_in
endmodule

module \分支预测缓冲器  (
  input  BranchSig,
  input  [31:0] EX_PC,
  input  [31:0] IF_PC,
  input  [31:0] BranchAddr,
  input  Branched,
  input  CLK,
  output PredictJump,
  output [31:0] JumpAddr
);

  wire and_1_out, and_2_out, and_3_out, and_4_out, and_5_out, and_6_out, and_7_out, and_8_out, and_9_out,
       and_10_out, and_11_out, and_12_out, and_13_out, and_14_out, and_15_out, and_16_out, and_17_out,
       comparator_1_eq, comparator_2_eq, comparator_3_eq, comparator_4_eq, comparator_5_eq, comparator_6_eq,
       comparator_7_eq, comparator_8_eq, comparator_9_eq, comparator_10_eq, comparator_11_eq,
       comparator_12_eq, comparator_13_eq, comparator_14_eq, comparator_15_eq, comparator_16_eq,
       comparator_17_eq, comparator_18_eq, comparator_19_eq, comparator_20_eq, comparator_21_eq,
       comparator_22_eq, comparator_23_eq, comparator_24_eq, decoder_1_out0, decoder_1_out1, decoder_1_out2,
       decoder_1_out3, decoder_1_out4, decoder_1_out5, decoder_1_out6, decoder_1_out7, decoder_2_out0,
       decoder_2_out1, decoder_2_out2, decoder_2_out3, decoder_2_out4, decoder_2_out5, decoder_2_out6,
       decoder_2_out7, EX_L1, EX_L2, EX_L3, EX_L4, EX_L5, EX_L6, EX_L7, EX_L8, EX_Miss, Hit, L1, L2, L3, L4,
       L5, L6, L7, L8, multiplexer_1_out, multiplexer_2_out, multiplexer_3_out, multiplexer_4_out,
       multiplexer_5_out, multiplexer_6_out, multiplexer_7_out, multiplexer_8_out, not_1_out, not_2_out,
       not_3_out, not_4_out, not_5_out, not_6_out, not_7_out, not_8_out, or_2_out, or_3_out, or_4_out,
       or_5_out, or_6_out, or_7_out, or_8_out, or_9_out, or_10_out, or_11_out, priority_encoder_1_gs, V1, V2,
       V3, V4, V5, V6, V7, V8, \双位预测状态转移逻辑_1_jumppredict , \双位预测状态转移逻辑_2_jumppredict ,
       \双位预测状态转移逻辑_3_jumppredict , \双位预测状态转移逻辑_4_jumppredict , \双位预测状态转移逻辑_5_jumppredict ,
       \双位预测状态转移逻辑_6_jumppredict , \双位预测状态转移逻辑_7_jumppredict , \双位预测状态转移逻辑_8_jumppredict ;
  wire [2:0] max3_1_max_num, max3_2_max_num, max3_3_max_num, max3_4_max_num, max3_5_max_num, max3_6_max_num,
       priority_encoder_1_out, priority_encoder_2_out, ReWriteAddr;
  wire [15:0] counter_1_q, counter_2_q, counter_3_q, counter_4_q, counter_5_q, counter_6_q, counter_7_q,
       counter_8_q, max3_1_max, max3_2_max, max3_3_max, max3_4_max, max3_5_max, max3_6_max,
       multiplexer_9_out, multiplexer_10_out, multiplexer_11_out, multiplexer_12_out, multiplexer_13_out,
       multiplexer_14_out, multiplexer_15_out, multiplexer_16_out;
  wire [31:0] register_9_q, register_10_q, register_11_q, register_12_q, register_13_q, register_14_q,
       register_15_q, register_16_q, register_17_q, register_18_q, register_19_q, register_20_q,
       register_21_q, register_22_q, register_23_q, register_24_q;

  or or_1 (Hit, L1, L2, L3, L4, L5, L6, L7, L8);
  nor nor_1 (EX_Miss, EX_L1, EX_L2, EX_L3, EX_L4, EX_L5, EX_L6, EX_L7, EX_L8);
  not not_1 (not_1_out, V8);
  not not_2 (not_2_out, V7);
  not not_3 (not_3_out, V6);
  not not_4 (not_4_out, V5);
  not not_5 (not_5_out, V4);
  not not_6 (not_6_out, V3);
  not not_7 (not_7_out, V2);
  not not_8 (not_8_out, V1);
  Priority_Encoder #(.select(3), .disabled(0)) priority_encoder_1 (
    .in0(not_1_out), .in1(not_2_out), .in2(not_3_out), .in3(not_4_out), .in4(not_5_out), .in5(not_6_out),
    .in6(not_7_out), .in7(not_8_out), .out(priority_encoder_1_out), .gs(priority_encoder_1_gs), .en_in(1'b1));  // open: en_out
  Decoder #(.select(3), .tristate("false"), .disabled(0), .enable("false")) decoder_1 (
    .out0(decoder_1_out0), .out1(decoder_1_out1), .out2(decoder_1_out2), .out3(decoder_1_out3),
    .out4(decoder_1_out4), .out5(decoder_1_out5), .out6(decoder_1_out6), .out7(decoder_1_out7),
    .sel(ReWriteAddr));
  Decoder #(.select(3), .tristate("false"), .disabled(0), .enable("false")) decoder_2 (
    .out0(decoder_2_out0), .out1(decoder_2_out1), .out2(decoder_2_out2), .out3(decoder_2_out3),
    .out4(decoder_2_out4), .out5(decoder_2_out5), .out6(decoder_2_out6), .out7(decoder_2_out7),
    .sel(priority_encoder_1_out));
  and and_1 (and_1_out, BranchSig, Branched);
  Multiplexer #(.select(1), .width(1), .disabled(0), .enable("false")) multiplexer_1 (
    .in0(decoder_1_out0), .in1(decoder_2_out7), .out(multiplexer_1_out), .sel(priority_encoder_1_gs));
  Multiplexer #(.select(1), .width(1), .disabled(0), .enable("false")) multiplexer_2 (
    .in0(decoder_1_out1), .in1(decoder_2_out6), .out(multiplexer_2_out), .sel(priority_encoder_1_gs));
  Multiplexer #(.select(1), .width(1), .disabled(0), .enable("false")) multiplexer_3 (
    .in0(decoder_1_out2), .in1(decoder_2_out5), .out(multiplexer_3_out), .sel(priority_encoder_1_gs));
  Multiplexer #(.select(1), .width(1), .disabled(0), .enable("false")) multiplexer_4 (
    .in0(decoder_1_out3), .in1(decoder_2_out4), .out(multiplexer_4_out), .sel(priority_encoder_1_gs));
  Multiplexer #(.select(1), .width(1), .disabled(0), .enable("false")) multiplexer_5 (
    .in0(decoder_1_out4), .in1(decoder_2_out3), .out(multiplexer_5_out), .sel(priority_encoder_1_gs));
  Multiplexer #(.select(1), .width(1), .disabled(0), .enable("false")) multiplexer_6 (
    .in0(decoder_1_out5), .in1(decoder_2_out2), .out(multiplexer_6_out), .sel(priority_encoder_1_gs));
  Multiplexer #(.select(1), .width(1), .disabled(0), .enable("false")) multiplexer_7 (
    .in0(decoder_1_out6), .in1(decoder_2_out1), .out(multiplexer_7_out), .sel(priority_encoder_1_gs));
  Multiplexer #(.select(1), .width(1), .disabled(0), .enable("false")) multiplexer_8 (
    .in0(decoder_1_out7), .in1(decoder_2_out0), .out(multiplexer_8_out), .sel(priority_encoder_1_gs));
  and and_2 (and_2_out, EX_Miss, and_1_out, multiplexer_1_out);
  and and_3 (and_3_out, EX_Miss, and_1_out, multiplexer_2_out);
  and and_4 (and_4_out, EX_Miss, and_1_out, multiplexer_3_out);
  and and_5 (and_5_out, EX_Miss, and_1_out, multiplexer_4_out);
  and and_6 (and_6_out, EX_Miss, and_1_out, multiplexer_5_out);
  and and_7 (and_7_out, EX_Miss, and_1_out, multiplexer_6_out);
  and and_8 (and_8_out, EX_Miss, and_1_out, multiplexer_7_out);
  and and_9 (and_9_out, EX_Miss, and_1_out, multiplexer_8_out);
  and and_10 (and_10_out, Hit, L1);
  or or_2 (or_2_out, and_10_out, and_2_out);
  and and_11 (and_11_out, Hit, L2);
  or or_3 (or_3_out, and_11_out, and_3_out);
  and and_12 (and_12_out, Hit, L3);
  or or_4 (or_4_out, and_12_out, and_4_out);
  and and_13 (and_13_out, Hit, L4);
  or or_5 (or_5_out, and_13_out, and_5_out);
  and and_14 (and_14_out, Hit, L5);
  or or_6 (or_6_out, and_14_out, and_6_out);
  and and_15 (and_15_out, Hit, L6);
  or or_7 (or_7_out, and_15_out, and_7_out);
  and and_16 (and_16_out, Hit, L7);
  or or_8 (or_8_out, and_16_out, and_8_out);
  and and_17 (and_17_out, Hit, L8);
  or or_9 (or_9_out, and_17_out, and_9_out);
  Multiplexer #(.select(1), .width(16), .disabled(0), .enable("false")) multiplexer_9 (
    .in0(counter_1_q), .in1({16{1'b0}}), .out(multiplexer_9_out), .sel(or_2_out));
  Counter #(.width(16), .max('hffff), .ongoal("wrap"), .trigger("rising"), .behavior("new")) counter_1 (
    .load(or_2_out), .D(multiplexer_9_out), .Q(counter_1_q), .clk(CLK));  // open: count, carry, clr, preset, down
  Multiplexer #(.select(1), .width(16), .disabled(0), .enable("false")) multiplexer_10 (
    .in0(counter_2_q), .in1({16{1'b0}}), .out(multiplexer_10_out), .sel(or_3_out));
  Counter #(.width(16), .max('hffff), .ongoal("wrap"), .trigger("rising"), .behavior("new")) counter_2 (
    .load(or_3_out), .D(multiplexer_10_out), .Q(counter_2_q), .clk(CLK));  // open: count, carry, clr, preset, down
  Multiplexer #(.select(1), .width(16), .disabled(0), .enable("false")) multiplexer_11 (
    .in0(counter_3_q), .in1({16{1'b0}}), .out(multiplexer_11_out), .sel(or_4_out));
  Counter #(.width(16), .max('hffff), .ongoal("wrap"), .trigger("rising"), .behavior("new")) counter_3 (
    .load(or_4_out), .D(multiplexer_11_out), .Q(counter_3_q), .clk(CLK));  // open: count, carry, clr, preset, down
  Multiplexer #(.select(1), .width(16), .disabled(0), .enable("false")) multiplexer_12 (
    .in0(counter_4_q), .in1({16{1'b0}}), .out(multiplexer_12_out), .sel(or_5_out));
  Counter #(.width(16), .max('hffff), .ongoal("wrap"), .trigger("rising"), .behavior("new")) counter_4 (
    .load(or_5_out), .D(multiplexer_12_out), .Q(counter_4_q), .clk(CLK));  // open: count, carry, clr, preset, down
  Multiplexer #(.select(1), .width(16), .disabled(0), .enable("false")) multiplexer_13 (
    .in0(counter_5_q), .in1({16{1'b0}}), .out(multiplexer_13_out), .sel(or_6_out));
  Counter #(.width(16), .max('hffff), .ongoal("wrap"), .trigger("rising"), .behavior("new")) counter_5 (
    .load(or_6_out), .D(multiplexer_13_out), .Q(counter_5_q), .clk(CLK));  // open: count, carry, clr, preset, down
  Multiplexer #(.select(1), .width(16), .disabled(0), .enable("false")) multiplexer_14 (
    .in0(counter_6_q), .in1({16{1'b0}}), .out(multiplexer_14_out), .sel(or_7_out));
  Counter #(.width(16), .max('hffff), .ongoal("wrap"), .trigger("rising"), .behavior("new")) counter_6 (
    .load(or_7_out), .D(multiplexer_14_out), .Q(counter_6_q), .clk(CLK));  // open: count, carry, clr, preset, down
  Multiplexer #(.select(1), .width(16), .disabled(0), .enable("false")) multiplexer_15 (
    .in0(counter_7_q), .in1({16{1'b0}}), .out(multiplexer_15_out), .sel(or_8_out));
  Counter #(.width(16), .max('hffff), .ongoal("wrap"), .trigger("rising"), .behavior("new")) counter_7 (
    .load(or_8_out), .D(multiplexer_15_out), .Q(counter_7_q), .clk(CLK));  // open: count, carry, clr, preset, down
  Multiplexer #(.select(1), .width(16), .disabled(0), .enable("false")) multiplexer_16 (
    .in0(counter_8_q), .in1({16{1'b0}}), .out(multiplexer_16_out), .sel(or_9_out));
  Counter #(.width(16), .max('hffff), .ongoal("wrap"), .trigger("rising"), .behavior("new")) counter_8 (
    .load(or_9_out), .D(multiplexer_16_out), .Q(counter_8_q), .clk(CLK));  // open: count, carry, clr, preset, down
  MAX3 max3_1 (
    .Y(counter_2_q), .X(counter_1_q), .Y_num(3'b001), .X_num(3'b000), .MAX(max3_1_max),
    .Max_num(max3_1_max_num));
  MAX3 max3_2 (
    .Y(counter_4_q), .X(counter_3_q), .Y_num(3'b011), .X_num(3'b010), .MAX(max3_2_max),
    .Max_num(max3_2_max_num));
  MAX3 max3_3 (
    .Y(counter_6_q), .X(counter_5_q), .Y_num(3'b101), .X_num(3'b100), .MAX(max3_3_max),
    .Max_num(max3_3_max_num));
  MAX3 max3_4 (
    .Y(counter_8_q), .X(counter_7_q), .Y_num(3'b111), .X_num(3'b110), .MAX(max3_4_max),
    .Max_num(max3_4_max_num));
  MAX3 max3_5 (
    .Y(max3_2_max), .X(max3_1_max), .Y_num(max3_2_max_num), .X_num(max3_1_max_num), .MAX(max3_5_max),
    .Max_num(max3_5_max_num));
  MAX3 max3_6 (
    .Y(max3_4_max), .X(max3_3_max), .Y_num(max3_4_max_num), .X_num(max3_3_max_num), .MAX(max3_6_max),
    .Max_num(max3_6_max_num));
  MAX3 max3_7 (
    .Y(max3_6_max), .X(max3_5_max), .Y_num(max3_6_max_num), .X_num(max3_5_max_num), .Max_num(ReWriteAddr));  // open: MAX
  Register #(.width(1), .trigger("rising"), .Select("low")) register_1 (
    .D(and_2_out), .en(and_2_out), .Q(V1), .clk(CLK));  // open: clr
  Register #(.width(1), .trigger("rising"), .Select("low")) register_2 (
    .D(and_3_out), .en(and_3_out), .Q(V2), .clk(CLK));  // open: clr
  Register #(.width(1), .trigger("rising"), .Select("low")) register_3 (
    .D(and_4_out), .en(and_4_out), .Q(V3), .clk(CLK));  // open: clr
  Register #(.width(1), .trigger("rising"), .Select("low")) register_4 (
    .D(and_5_out), .en(and_5_out), .Q(V4), .clk(CLK));  // open: clr
  Register #(.width(1), .trigger("rising"), .Select("low")) register_5 (
    .D(and_6_out), .en(and_6_out), .Q(V5), .clk(CLK));  // open: clr
  Register #(.width(1), .trigger("rising"), .Select("low")) register_6 (
    .D(and_7_out), .en(and_7_out), .Q(V6), .clk(CLK));  // open: clr
  Register #(.width(1), .trigger("rising"), .Select("low")) register_7 (
    .D(and_8_out), .en(and_8_out), .Q(V7), .clk(CLK));  // open: clr
  Register #(.width(1), .trigger("rising"), .Select("low")) register_8 (
    .D(and_9_out), .en(and_9_out), .Q(V8), .clk(CLK));  // open: clr
  Register #(.width(32), .trigger("rising"), .Select("low")) register_9 (
    .D(EX_PC), .en(and_2_out), .Q(register_9_q), .clk(CLK));  // open: clr
  Register #(.width(32), .trigger("rising"), .Select("low")) register_10 (
    .D(EX_PC), .en(and_3_out), .Q(register_10_q), .clk(CLK));  // open: clr
  Register #(.width(32), .trigger("rising"), .Select("low")) register_11 (
    .D(EX_PC), .en(and_4_out), .Q(register_11_q), .clk(CLK));  // open: clr
  Register #(.width(32), .trigger("rising"), .Select("low")) register_12 (
    .D(EX_PC), .en(and_5_out), .Q(register_12_q), .clk(CLK));  // open: clr
  Register #(.width(32), .trigger("rising"), .Select("low")) register_13 (
    .D(EX_PC), .en(and_6_out), .Q(register_13_q), .clk(CLK));  // open: clr
  Register #(.width(32), .trigger("rising"), .Select("low")) register_14 (
    .D(EX_PC), .en(and_7_out), .Q(register_14_q), .clk(CLK));  // open: clr
  Register #(.width(32), .trigger("rising"), .Select("low")) register_15 (
    .D(EX_PC), .en(and_8_out), .Q(register_15_q), .clk(CLK));  // open: clr
  Register #(.width(32), .trigger("rising"), .Select("low")) register_16 (
    .D(EX_PC), .en(and_9_out), .Q(register_16_q), .clk(CLK));  // open: clr
  Comparator #(.width(32), .mode("twosComplement")) comparator_1 (
    .a(register_9_q), .b(IF_PC), .eq(comparator_1_eq));  // open: gt, lt
  Comparator #(.width(32), .mode("twosComplement")) comparator_2 (
    .a(register_10_q), .b(IF_PC), .eq(comparator_2_eq));  // open: gt, lt
  Comparator #(.width(32), .mode("twosComplement")) comparator_3 (
    .a(register_11_q), .b(IF_PC), .eq(comparator_3_eq));  // open: gt, lt
  Comparator #(.width(32), .mode("twosComplement")) comparator_4 (
    .a(register_12_q), .b(IF_PC), .eq(comparator_4_eq));  // open: gt, lt
  Comparator #(.width(32), .mode("twosComplement")) comparator_5 (
    .a(register_13_q), .b(IF_PC), .eq(comparator_5_eq));  // open: gt, lt
  Comparator #(.width(32), .mode("twosComplement")) comparator_6 (
    .a(register_14_q), .b(IF_PC), .eq(comparator_6_eq));  // open: gt, lt
  Comparator #(.width(32), .mode("twosComplement")) comparator_7 (
    .a(register_15_q), .b(IF_PC), .eq(comparator_7_eq));  // open: gt, lt
  Comparator #(.width(32), .mode("twosComplement")) comparator_8 (
    .a(register_16_q), .b(IF_PC), .eq(comparator_8_eq));  // open: gt, lt
  and and_18 (L1, V1, comparator_1_eq);
  and and_19 (L2, V2, comparator_2_eq);
  and and_20 (L3, V3, comparator_3_eq);
  and and_21 (L4, V4, comparator_4_eq);
  and and_22 (L5, V5, comparator_5_eq);
  and and_23 (L6, V6, comparator_6_eq);
  and and_24 (L7, V7, comparator_7_eq);
  and and_25 (L8, V8, comparator_8_eq);
  Comparator #(.width(32), .mode("twosComplement")) comparator_9 (
    .a(EX_PC), .b(register_9_q), .eq(comparator_9_eq));  // open: gt, lt
  Comparator #(.width(32), .mode("twosComplement")) comparator_10 (
    .a(EX_PC), .b(register_10_q), .eq(comparator_10_eq));  // open: gt, lt
  Comparator #(.width(32), .mode("twosComplement")) comparator_11 (
    .a(EX_PC), .b(register_11_q), .eq(comparator_11_eq));  // open: gt, lt
  Comparator #(.width(32), .mode("twosComplement")) comparator_12 (
    .a(EX_PC), .b(register_12_q), .eq(comparator_12_eq));  // open: gt, lt
  Comparator #(.width(32), .mode("twosComplement")) comparator_13 (
    .a(EX_PC), .b(register_13_q), .eq(comparator_13_eq));  // open: gt, lt
  Comparator #(.width(32), .mode("twosComplement")) comparator_14 (
    .a(EX_PC), .b(register_14_q), .eq(comparator_14_eq));  // open: gt, lt
  Comparator #(.width(32), .mode("twosComplement")) comparator_15 (
    .a(EX_PC), .b(register_15_q), .eq(comparator_15_eq));  // open: gt, lt
  Comparator #(.width(32), .mode("twosComplement")) comparator_16 (
    .a(EX_PC), .b(register_16_q), .eq(comparator_16_eq));  // open: gt, lt
  and and_26 (EX_L1, V1, comparator_9_eq);
  and and_27 (EX_L2, V2, comparator_10_eq);
  and and_28 (EX_L3, V3, comparator_11_eq);
  and and_29 (EX_L4, V4, comparator_12_eq);
  and and_30 (EX_L5, V5, comparator_13_eq);
  and and_31 (EX_L6, V6, comparator_14_eq);
  and and_32 (EX_L7, V7, comparator_15_eq);
  and and_33 (EX_L8, V8, comparator_16_eq);
  \双位预测状态转移逻辑  \u_双位预测状态转移逻辑_1  (
    .JumpPredict(\双位预测状态转移逻辑_1_jumppredict ), .Success(comparator_17_eq), .Preset(and_2_out), .CLK(CLK),
    .EX_Hit(EX_L1), .Hit(L1));
  \双位预测状态转移逻辑  \u_双位预测状态转移逻辑_2  (
    .JumpPredict(\双位预测状态转移逻辑_2_jumppredict ), .Success(comparator_18_eq), .Preset(and_3_out), .CLK(CLK),
    .EX_Hit(EX_L2), .Hit(L2));
  \双位预测状态转移逻辑  \u_双位预测状态转移逻辑_3  (
    .JumpPredict(\双位预测状态转移逻辑_3_jumppredict ), .Success(comparator_19_eq), .Preset(and_4_out), .CLK(CLK),
    .EX_Hit(EX_L3), .Hit(L3));
  \双位预测状态转移逻辑  \u_双位预测状态转移逻辑_4  (
    .JumpPredict(\双位预测状态转移逻辑_4_jumppredict ), .Success(comparator_20_eq), .Preset(and_5_out), .CLK(CLK),
    .EX_Hit(EX_L4), .Hit(L4));
  \双位预测状态转移逻辑  \u_双位预测状态转移逻辑_5  (
    .JumpPredict(\双位预测状态转移逻辑_5_jumppredict ), .Success(comparator_21_eq), .Preset(and_6_out), .CLK(CLK),
    .EX_Hit(EX_L5), .Hit(L5));
  \双位预测状态转移逻辑  \u_双位预测状态转移逻辑_6  (
    .JumpPredict(\双位预测状态转移逻辑_6_jumppredict ), .Success(comparator_22_eq), .Preset(and_7_out), .CLK(CLK),
    .EX_Hit(EX_L6), .Hit(L6));
  \双位预测状态转移逻辑  \u_双位预测状态转移逻辑_7  (
    .JumpPredict(\双位预测状态转移逻辑_7_jumppredict ), .Success(comparator_23_eq), .Preset(and_8_out), .CLK(CLK),
    .EX_Hit(EX_L7), .Hit(L7));
  \双位预测状态转移逻辑  \u_双位预测状态转移逻辑_8  (
    .JumpPredict(\双位预测状态转移逻辑_8_jumppredict ), .Success(comparator_24_eq), .Preset(and_9_out), .CLK(CLK),
    .EX_Hit(EX_L8), .Hit(L8));
  or or_10 (or_10_out, \双位预测状态转移逻辑_1_jumppredict , \双位预测状态转移逻辑_2_jumppredict , \双位预测状态转移逻辑_3_jumppredict , \双位预测状态转移逻辑_4_jumppredict );
  or or_11 (or_11_out, \双位预测状态转移逻辑_5_jumppredict , \双位预测状态转移逻辑_6_jumppredict , \双位预测状态转移逻辑_7_jumppredict , \双位预测状态转移逻辑_8_jumppredict );
  or or_12 (PredictJump, or_10_out, or_11_out);
  Register #(.width(32), .trigger("rising"), .Select("low")) register_17 (
    .D(BranchAddr), .en(and_2_out), .Q(register_17_q), .clk(CLK));  // open: clr
  Register #(.width(32), .trigger("rising"), .Select("low")) register_18 (
    .D(BranchAddr), .en(and_3_out), .Q(register_18_q), .clk(CLK));  // open: clr
  Register #(.width(32), .trigger("rising"), .Select("low")) register_19 (
    .D(BranchAddr), .en(and_4_out), .Q(register_19_q), .clk(CLK));  // open: clr
  Register #(.width(32), .trigger("rising"), .Select("low")) register_20 (
    .D(BranchAddr), .en(and_5_out), .Q(register_20_q), .clk(CLK));  // open: clr
  Register #(.width(32), .trigger("rising"), .Select("low")) register_21 (
    .D(BranchAddr), .en(and_6_out), .Q(register_21_q), .clk(CLK));  // open: clr
  Register #(.width(32), .trigger("rising"), .Select("low")) register_22 (
    .D(BranchAddr), .en(and_7_out), .Q(register_22_q), .clk(CLK));  // open: clr
  Register #(.width(32), .trigger("rising"), .Select("low")) register_23 (
    .D(BranchAddr), .en(and_8_out), .Q(register_23_q), .clk(CLK));  // open: clr
  Register #(.width(32), .trigger("rising"), .Select("low")) register_24 (
    .D(BranchAddr), .en(and_9_out), .Q(register_24_q), .clk(CLK));  // open: clr
  Comparator #(.width(32), .mode("twosComplement")) comparator_17 (
    .a(BranchAddr), .b(register_17_q), .eq(comparator_17_eq));  // open: gt, lt
  Comparator #(.width(32), .mode("twosComplement")) comparator_18 (
    .a(BranchAddr), .b(register_18_q), .eq(comparator_18_eq));  // open: gt, lt
  Comparator #(.width(32), .mode("twosComplement")) comparator_19 (
    .a(BranchAddr), .b(register_19_q), .eq(comparator_19_eq));  // open: gt, lt
  Comparator #(.width(32), .mode("twosComplement")) comparator_20 (
    .a(BranchAddr), .b(register_20_q), .eq(comparator_20_eq));  // open: gt, lt
  Comparator #(.width(32), .mode("twosComplement")) comparator_21 (
    .a(BranchAddr), .b(register_21_q), .eq(comparator_21_eq));  // open: gt, lt
  Comparator #(.width(32), .mode("twosComplement")) comparator_22 (
    .a(BranchAddr), .b(register_22_q), .eq(comparator_22_eq));  // open: gt, lt
  Comparator #(.width(32), .mode("twosComplement")) comparator_23 (
    .a(BranchAddr), .b(register_23_q), .eq(comparator_23_eq));  // open: gt, lt
  Comparator #(.width(32), .mode("twosComplement")) comparator_24 (
    .a(BranchAddr), .b(register_24_q), .eq(comparator_24_eq));  // open: gt, lt
  Priority_Encoder #(.select(3), .disabled(0)) priority_encoder_2 (
    .in0(L1), .in1(L2), .in2(L3), .in3(L4), .in4(L5), .in5(L6), .in6(L7), .in7(L8),
    .out(priority_encoder_2_out));  // open: gs, en_out, en_in
  Multiplexer #(.select(3), .width(32), .disabled(0), .enable("false")) multiplexer_17 (
    .in0(register_17_q), .in1(register_18_q), .in2(register_19_q), .in3(register_20_q), .in4(register_21_q),
    .in5(register_22_q), .in6(register_23_q), .in7(register_24_q), .out(JumpAddr),
    .sel(priority_encoder_2_out));
endmodule

module MAX3 (
  input  [15:0] Y,
  input  [15:0] X,
  input  [2:0] Y_num,
  input  [2:0] X_num,
  output [15:0] MAX,
  output [2:0] Max_num
);

  wire comparator_1_eq, comparator_1_gt, or_1_out;

  Multiplexer #(.select(1), .width(16), .disabled("Z"), .enable("false")) multiplexer_1 (
    .in0(Y), .in1(X), .out(MAX), .sel(or_1_out));
  Comparator #(.width(16), .mode("unsigned")) comparator_1 (
    .a(X), .b(Y), .gt(comparator_1_gt), .eq(comparator_1_eq));  // open: lt
  or or_1 (or_1_out, comparator_1_gt, comparator_1_eq);
  Multiplexer #(.select(1), .width(3), .disabled("Z"), .enable("false")) multiplexer_2 (
    .in0(Y_num), .in1(X_num), .out(Max_num), .sel(or_1_out));
endmodule

module \双位预测状态转移逻辑  (
  input  Success,
  input  Preset,
  input  CLK,
  input  EX_Hit,
  input  Hit,
  output JumpPredict
);

  wire and_1_out, and_2_out, and_3_out, and_4_out, and_5_out, not_1_out, not_2_out, not_3_out, not_4_out,
       not_5_out, or_3_out;
  wire [1:0] multiplexer_1_out, or_2_out, register_1_q;

  not not_1 (not_1_out, register_1_q[0]);
  not not_2 (not_2_out, register_1_q[1]);
  not not_3 (not_3_out, register_1_q[0]);
  not not_4 (not_4_out, register_1_q[0]);
  not not_5 (not_5_out, Success);
  and and_1 (and_1_out, register_1_q[0], Success);
  and and_2 (and_2_out, register_1_q[1], not_1_out);
  and and_3 (and_3_out, not_2_out, not_3_out, Success);
  and and_4 (and_4_out, register_1_q[1], not_4_out, not_5_out);
  or or_1 (or_2_out[1], and_1_out, and_2_out);
  or or_2 (or_2_out[0], and_3_out, and_4_out);
  Multiplexer #(.select(1), .width(2), .disabled(0), .enable("false")) multiplexer_1 (
    .in0(or_2_out), .in1(2'b11), .out(multiplexer_1_out), .sel(Preset));
  or or_3 (or_3_out, Preset, EX_Hit);
  Register #(.width(2), .trigger("rising"), .Select("low")) register_1 (
    .D(multiplexer_1_out), .en(or_3_out), .Q(register_1_q), .clk(CLK));  // open: clr
  and and_5 (and_5_out, register_1_q[1], Hit);
  Register #(.width(1), .trigger("high"), .Select("low")) register_2 (
    .D(and_5_out), .en(1'b1), .Q(JumpPredict), .clk(CLK));  // open: clr
endmodule
