// Logisim project cpu24_verilog_tetris_ver04.circ as structural Verilog: 32 circuits, main circuit redirection_pipeline_with_BTB_and_multistage_interruption_support
module sc_MIPS (
  input  IR1,
  input  IR2,
  input  IR3,
  output RegWrite,
  output MemWrite,
  output [31:0] PC,
  output [31:0] IR,
  output [31:0] RDin,
  output [31:0] MDin,
  output [31:0] LedData
);

  wire AluSrcB, Beq, Blez, Bne, CLK, clock_2_out, comparator_1_eq, comparator_1_lt, d_ff_1_q, Equal, Go,
       HalfW, IR1_t, IR2_t, IR3_t, IRA, IRB, IRC, JAL, JMP, JR, Less, MemToReg, nand_1_out, Pause, RegDst,
       SignedExt, Syscall, Vshamt, W1, W2, W3;
  wire [3:0] AluOP;
  wire [4:0] multiplexer_2_out, reg_choose_logic_1_r1adr, reg_choose_logic_1_r2adr, reg_choose_logic_1_shamt,
       reg_choose_logic_1_wadr;
  wire [12:0] CNT;
  wire [15:0] TotalCycles;
  wire [31:0] adder_1_out, adder_2_out, bit_extender_1_out, bit_extender_2_out, mips_alu_1_result,
       mips_mem_1_memreaddata, multiplexer_1_out, multiplexer_3_out, multiplexer_4_out,
       pc_update_logic_1_pc_next, R1;

  Clock #(.highDuration(1), .lowDuration(1)) clock_1 ();  // open: out
  Button _1 (.out(IRA));
  Button _2 (.out(IRB));
  Button _3 (.out(IRC));
  Button \u_继续运行  (.out(Go));
  LED #(.active("true")) IRQ_1 (.in(W1));
  LED #(.active("true")) IRQ_2 (.in(W2));
  LED #(.active("true")) IRQ_3 (.in(W3));
  PC_update_logic pc_update_logic_1 (
    .Equal(Equal), .Beq(Beq), .Bne(Bne), .JAL(JAL), .JMP(JMP), .JR(JR), .BAddr(adder_2_out),
    .PC_plus_four(adder_1_out), .JAddr({PC[31:28], IR[25:0], 2'b00}), .JRAddr(R1),
    .PC_Next(pc_update_logic_1_pc_next), .Blez(Blez), .Less(Less));  // open: Branched, BranchSig
  Hex_Digit_Display hex_digit_display_1 (.value(LedData[31:28]));  // open: dp
  Register #(.width(32), .trigger("rising"), .Select("low")) u_PC (
    .D(pc_update_logic_1_pc_next), .Q(PC), .clk(CLK));  // open: en, clr
  D_Flip_Flop #(.trigger("high"), .Pre_Clr_Positions("LEGACY"), .NegatePresetClear("false"), .enable("true"), .NewFFLayout("false")) d_ff_1 (
    .Q(d_ff_1_q), .preset(Pause), .reset(Go));  // open: clk, D, Qn, en
  Hex_Digit_Display hex_digit_display_2 (.value(LedData[23:20]));  // open: dp
  Hex_Digit_Display hex_digit_display_3 (.value(LedData[27:24]));  // open: dp
  Adder #(.width(32)) adder_1 (.a(PC), .b(32'h4), .out(adder_1_out));  // open: cin, cout
  // Probe on 13'hc
  Hex_Digit_Display hex_digit_display_4 (.value(LedData[19:16]));  // open: dp
  Hex_Digit_Display hex_digit_display_5 (.value(LedData[15:12]));  // open: dp
  Comparator #(.width(13), .mode("twosComplement")) comparator_1 (
    .a(CNT), .b(13'hc), .eq(comparator_1_eq), .lt(comparator_1_lt));  // open: gt
  Clock #(.highDuration(1), .lowDuration(1)) clock_2 (.out(clock_2_out));
  Hex_Digit_Display hex_digit_display_6 (.value(LedData[11:8]));  // open: dp
  Hex_Digit_Display hex_digit_display_7 (.value(LedData[7:4]));  // open: dp
  ROM #(.addrWidth(10), .dataWidth(32), .Select("low")) IR_ROM (.addr(PC[11:2]), .data(IR));
  nand nand_1 (nand_1_out, d_ff_1_q, comparator_1_eq);
  Counter #(.width(13), .max('h1fff), .ongoal("stay"), .trigger("rising"), .behavior("old")) counter_1 (
    .count(comparator_1_lt), .Q(CNT), .clk(clock_2_out));  // open: load, D, carry, clr, preset
  Hex_Digit_Display hex_digit_display_8 (.value(LedData[3:0]));  // open: dp
  // Probe on TotalCycles
  assign CLK = nand_1_out ? clock_2_out : 1'bz;  // Controlled_Buffer controlled_buffer_1
  reg_choose_logic reg_choose_logic_1 (
    ._21_25(IR[25:21]), .Syscall(Syscall), .RegDst(RegDst), ._16_20(IR[20:16]), ._11_15(IR[15:11]),
    .JAL(JAL), .PC_plus_four(adder_1_out), .WriteBack_Data(multiplexer_4_out), ._6_10(IR[10:6]),
    .R1Adr(reg_choose_logic_1_r1adr), .R2Adr(reg_choose_logic_1_r2adr), .WAdr(reg_choose_logic_1_wadr),
    .RDin(RDin), .Shamt(reg_choose_logic_1_shamt));
  assign bit_extender_1_out = {{16{1'b0}}, IR[15:0]};  // Bit_Extender bit_extender_1
  assign bit_extender_2_out = {{16{IR[15]}}, IR[15:0]};  // Bit_Extender bit_extender_2
  or or_1 (IR1_t, IR1, IRA);
  Multiplexer #(.select(1), .width(32), .disabled(0), .enable("false")) multiplexer_1 (
    .in0(bit_extender_1_out), .in1(bit_extender_2_out), .out(multiplexer_1_out), .sel(SignedExt));
  or or_2 (IR2_t, IR2, IRB);
  MIPS_Regifile mips_regifile_1 (
    .Din(RDin), .Clk(CLK), .R1(R1), .R2(MDin), .WE(RegWrite), .WAdr(reg_choose_logic_1_wadr),
    .R1Adr(reg_choose_logic_1_r1adr), .R2Adr(reg_choose_logic_1_r2adr));
  Multiplexer #(.select(1), .width(5), .disabled(0), .enable("false")) multiplexer_2 (
    .in0(reg_choose_logic_1_shamt), .in1(R1[4:0]), .out(multiplexer_2_out), .sel(Vshamt));
  Adder #(.width(32)) adder_2 (
    .a(adder_1_out), .b({bit_extender_2_out[29:0], 2'b00}), .out(adder_2_out));  // open: cin, cout
  Counter #(.width(16), .max('hffff), .ongoal("wrap"), .trigger("rising"), .behavior("new")) counter_2 (
    .Q(TotalCycles), .clk(CLK));  // open: load, D, count, carry, clr, preset, down
  Multiplexer #(.select(1), .width(32), .disabled(0), .enable("false")) multiplexer_3 (
    .in0(MDin), .in1(multiplexer_1_out), .out(multiplexer_3_out), .sel(AluSrcB));
  or or_3 (IR3_t, IR3, IRC);
  MIPS_ALU mips_alu_1 (
    .X(R1), .Y(multiplexer_3_out), .AluOP(AluOP), .Equal(Equal), .Result(mips_alu_1_result),
    .shamt(multiplexer_2_out), .Less(Less));  // open: Result_2
  MIPS_MEM mips_mem_1 (
    .AluResult(mips_alu_1_result), .HalfW(HalfW), .WriteData(MDin), .MemWrite(MemWrite), .CLK(CLK),
    .MemReadData(mips_mem_1_memreaddata));
  Multiplexer #(.select(1), .width(32), .disabled(0), .enable("false")) multiplexer_4 (
    .in0(mips_alu_1_result), .in1(mips_mem_1_memreaddata), .out(multiplexer_4_out), .sel(MemToReg));
  sc_hard_wired_controller sc_hard_wired_controller_1 (
    .Func(IR[5:0]), .OP(IR[31:26]), .ALU_OP(AluOP), .MemToReg(MemToReg), .MemWrite(MemWrite),
    .ALU_SRC(AluSrcB), .RegWrite(RegWrite), .SysCALL(Syscall), .SignedExt(SignedExt), .RegDst(RegDst),
    .JR(JR), .JMP(JMP), .Beq(Beq), .JAL(JAL), .Bne(Bne), .Vshamt(Vshamt), .BLEZ(Blez), .HalfW(HalfW));
  syscall_process syscall_process_1 (
    .Syscall(Syscall), .CLK(CLK), .R2(MDin), .R1(R1), .Pause(Pause), .LedData(LedData));  // open: Get_KB_in, Screen_opt, Cycles, Get_Bitmap, CopyToRAM, FrameFlush

  // Other names for the same wires on the sheet: Func[5:0] = IR[5:0]; OP[5:0] = IR[31:26]; R2[31:0] = MDin

  // Notes on the sheet:
  //   中断源
  //   中断等待指示
  //   总复位信号应将除ROM以外所有存储组件全部清零
  //   控制位
  //   暂停节拍，不能为0
  //   数码管输出
  //   指令存储器
  //   数码管输出应该用寄存器锁存，否则显示数据只能一闪而过
  //   指令字
  //   contents of IR_ROM (hex, n*v repeats v):
  //   20110001 8000005 20110001 20120002 20130003 8000009 20110001 20120002 20130003 800000d 20110001
  //   20120002 20130003 8000011 20110001 20120002 20130003 c0000f2 20100001 20110001 118fc0 112020
  //   20020022 c 118882 12200001 8000015 112020 20020022 c 20110001 118880 112020 20020022 c 12200001
  //   800001f 20110001 118fc0 112020 20020022 c 1188c3 112020 20020022 c 118903 112020 20020022 c 118903
  //   112020 20020022 c 118903 112020 20020022 c 118903 112020 20020022 c 118903 112020 20020022 c 118903
  //   112020 20020022 c 118903 112020 20020022 c 20100001 109fc0 139fc3 8021 2012000c 24160003 26100001
  //   3210000f 20080008 20090001 139900 2709825 132020 20020022 c 1094022 1500fff9 22100001 2018000f
  //   2188024 108700 20080008 20090001 139902 2709825 132021 20020022 c 1094022 1500fff9 108702 2c9b022
  //   12c00001 8000050 4020 1084027 84400 3508ffff 82021 20020022 c 2010ffff 20110000 ae300000 22100001
  //   22310004 ae300000 22100001 22310004 ae300000 22100001 22310004 ae300000 22100001 22310004 ae300000
  //   22100001 22310004 ae300000 22100001 22310004 ae300000 22100001 22310004 ae300000 22100001 22310004
  //   ae300000 22100001 22310004 ae300000 22100001 22310004 ae300000 22100001 22310004 ae300000 22100001
  //   22310004 ae300000 22100001 22310004 ae300000 22100001 22310004 ae300000 22100001 22310004 ae300000
  //   22100001 22310004 22100001 8020 2011003c 8e130000 8e340000 274402a 11000002 ae330000 ae140000
  //   2231fffc 1611fff8 102020 20020022 c 22100004 2011003c 1611fff2 20020032 c 20080001 20090003 20110876
  //   112020 20020022 c 200b0008 1118804 1318804 112020 20020022 c 216bffff 1560fff9 2002000a c 2008ffff
  //   20090000 20111997 112020 20020022 c 2288820 2e291949 1120fffa 2002000a c 20090000 200b0020 20110001
  //   20120001 a5310000 112020 20020022 c 2328820 21290002 216bffff 1560fff8 200b0010 20090000 8d310000
  //   112020 20020022 c 21290004 216bffff 1560fff9 2002000a c 2011fff1 112020 20020022 c 22310001 1a20fffb
  //   2002000a c 20100000 22100001 102020 20020022 c 22100002 102020 20020022 c 22100003 102020 20020022 c
  //   22100004 102020 20020022 c 22100005 102020 20020022 c 22100006 102020 20020022 c 22100007 102020
  //   20020022 c 22100008 102020 20020022 20020022 c 3e00008
  //   可计数暂停的时钟源
  //   为方便自动评测，需要输出PC，IR，寄存器堆写如数据RDin
  //   RAM写使能MemWrite、RAM写入数据MDin等信号
endmodule

module single_stage_interruption_support (
  input  IR1,
  input  IR2,
  input  IR3,
  output RegWrite,
  output MemWrite,
  output [31:0] PC,
  output [31:0] IR,
  output [31:0] RDin,
  output [31:0] MDin,
  output [31:0] LedData
);

  wire AluSrcB, and_1_out, and_2_out, and_3_out, and_4_out, Beq, Blez, Bne, CLK, clock_2_out,
       comparator_1_eq, comparator_1_lt, comparator_4_eq, comparator_5_eq, comparator_6_eq, comparator_7_eq,
       d_ff_1_q, d_ff_2_q, d_ff_3_q, d_ff_4_q, d_ff_5_q, d_ff_6_q, d_ff_7_q, decoder_1_out0, decoder_1_out1,
       decoder_1_out2, Equal, ERET, Go, HalfW, IE, IE_p2, INIT, IR1_t, IR2_t, IR3_t, IRA, IRB, IRC, IRQ, JAL,
       JMP, JR, Less, MemToReg, nand_1_out, not_1_out, or_1_out, or_5_out, or_6_out, or_7_out, or_9_out,
       or_12_out, Pause, priority_encoder_1_gs, RegDst, SignedExt, Syscall, Vshamt, W1, W2, W3;
  wire [1:0] IRQ_Exe, priority_encoder_1_out;
  wire [3:0] AluOP;
  wire [4:0] multiplexer_1_out, reg_choose_logic_1_r1adr, reg_choose_logic_1_r2adr, reg_choose_logic_1_shamt,
       reg_choose_logic_1_wadr;
  wire [12:0] CNT_num;
  wire [15:0] \总周期数 ;
  wire [31:0] adder_1_out, adder_2_out, bit_extender_1_out, bit_extender_2_out, controlled_buffer_1_out, EPC,
       IRQ_Entry, mips_alu_1_result, mips_mem_1_memreaddata, multiplexer_2_out, multiplexer_3_out,
       multiplexer_5_out, PC_Next, R1;

  Clock #(.highDuration(1), .lowDuration(1)) clock_1 ();  // open: out
  Button _1 ();  // open: out
  Button _2 ();  // open: out
  Button _3 ();  // open: out
  Button \u_继续运行  (.out(Go));
  LED #(.active("true")) led_1 (.in(W1));
  LED #(.active("true")) led_2 (.in(W2));
  LED #(.active("true")) led_3 (.in(W3));
  Hex_Digit_Display hex_digit_display_1 (.value(LedData[31:28]));  // open: dp
  and and_1 (and_1_out, ~ERET, IRQ);  // AND_Gate
  or or_1 (or_1_out, ERET, IRQ);
  PC_update_logic pc_update_logic_1 (
    .Equal(Equal), .Beq(Beq), .Bne(Bne), .JAL(JAL), .JMP(JMP), .JR(JR), .BAddr(adder_2_out),
    .PC_plus_four(adder_1_out), .JAddr({PC[31:28], IR[25:0], 2'b00}), .JRAddr(R1), .PC_Next(PC_Next),
    .Blez(Blez), .Less(Less));  // open: Branched, BranchSig
  Decoder #(.select(2), .tristate("false"), .disabled(0), .enable("true")) decoder_1 (
    .out0(decoder_1_out0), .out1(decoder_1_out1), .out2(decoder_1_out2), .sel(IRQ_Exe), .en(ERET));  // open: out3
  Hex_Digit_Display hex_digit_display_2 (.value(LedData[27:24]));  // open: dp
  Hex_Digit_Display hex_digit_display_3 (.value(LedData[23:20]));  // open: dp
  assign controlled_buffer_1_out = ERET ? EPC : 32'bz;  // Controlled_Buffer controlled_buffer_1
  assign controlled_buffer_1_out = and_1_out ? IRQ_Entry : 32'bz;  // Controlled_Buffer controlled_buffer_2
  assign controlled_buffer_1_out = ~or_1_out ? PC_Next : 32'bz;  // Controlled_Buffer controlled_buffer_3
  D_Flip_Flop #(.trigger("high"), .Pre_Clr_Positions("LEGACY"), .NegatePresetClear("false"), .enable("true"), .NewFFLayout("false")) d_ff_1 (
    .Q(d_ff_1_q), .preset(Pause), .reset(Go));  // open: clk, D, Qn, en
  // Probe on 13'hc
  or or_2 (W1, d_ff_5_q, d_ff_2_q);
  or or_3 (W2, d_ff_6_q, d_ff_3_q);
  or or_4 (W3, d_ff_7_q, d_ff_4_q);
  Hex_Digit_Display hex_digit_display_4 (.value(LedData[19:16]));  // open: dp
  Hex_Digit_Display hex_digit_display_5 (.value(LedData[15:12]));  // open: dp
  Register #(.width(32), .trigger("rising"), .Select("low")) u_PC (
    .D(controlled_buffer_1_out), .Q(PC), .clk(CLK));  // open: en, clr
  Comparator #(.width(13), .mode("twosComplement")) comparator_1 (
    .a(CNT_num), .b(13'hc), .eq(comparator_1_eq), .lt(comparator_1_lt));  // open: gt
  Clock #(.highDuration(1), .lowDuration(1)) clock_2 (.out(clock_2_out));
  D_Flip_Flop #(.trigger("rising"), .Pre_Clr_Positions("LEGACY"), .NegatePresetClear("false"), .enable("true"), .NewFFLayout("false")) d_ff_2 (
    .clk(IR1_t), .D(1'b1), .Q(d_ff_2_q), .reset(d_ff_5_q));  // open: Qn, preset, en
  D_Flip_Flop #(.trigger("rising"), .Pre_Clr_Positions("LEGACY"), .NegatePresetClear("false"), .enable("true"), .NewFFLayout("false")) d_ff_3 (
    .clk(IR2_t), .D(1'b1), .Q(d_ff_3_q), .reset(d_ff_6_q));  // open: Qn, preset, en
  D_Flip_Flop #(.trigger("rising"), .Pre_Clr_Positions("LEGACY"), .NegatePresetClear("false"), .enable("true"), .NewFFLayout("false")) d_ff_4 (
    .clk(IR3_t), .D(1'b1), .Q(d_ff_4_q), .reset(d_ff_7_q));  // open: Qn, preset, en
  Hex_Digit_Display hex_digit_display_6 (.value(LedData[11:8]));  // open: dp
  Hex_Digit_Display hex_digit_display_7 (.value(LedData[7:4]));  // open: dp
  // Probe on \总周期数 
  Adder #(.width(32)) adder_1 (.a(PC), .b(32'h4), .out(adder_1_out));  // open: cin, cout
  nand nand_1 (nand_1_out, d_ff_1_q, comparator_1_eq);
  Counter #(.width(13), .max('h1fff), .ongoal("stay"), .trigger("rising"), .behavior("old")) counter_1 (
    .count(comparator_1_lt), .Q(CNT_num), .clk(clock_2_out));  // open: load, D, carry, clr, preset
  or or_5 (or_5_out, d_ff_2_q, d_ff_5_q);
  or or_6 (or_6_out, d_ff_3_q, d_ff_6_q);
  or or_7 (or_7_out, d_ff_4_q, d_ff_7_q);
  Hex_Digit_Display hex_digit_display_8 (.value(LedData[3:0]));  // open: dp
  // Mips_Probe mips_probe_1: pin names not known; wires that end beside it: IR
  ROM #(.addrWidth(10), .dataWidth(32), .Select("low")) rom_1 (.addr(PC[11:2]), .data(IR));
  assign CLK = nand_1_out ? clock_2_out : 1'bz;  // Controlled_Buffer controlled_buffer_4
  and and_2 (and_2_out, or_5_out, ~decoder_1_out0);  // AND_Gate
  and and_3 (and_3_out, or_6_out, ~decoder_1_out1);  // AND_Gate
  and and_4 (and_4_out, or_7_out, ~decoder_1_out2);  // AND_Gate
  Pull_Resistor #(.pull(1)) pull_resistor_1 (.node(CLK));
  D_Flip_Flop #(.trigger("rising"), .Pre_Clr_Positions("LEGACY"), .NegatePresetClear("false"), .enable("true"), .NewFFLayout("false")) d_ff_5 (
    .clk(CLK), .D(and_2_out), .Q(d_ff_5_q));  // open: Qn, preset, en, reset
  D_Flip_Flop #(.trigger("rising"), .Pre_Clr_Positions("LEGACY"), .NegatePresetClear("false"), .enable("true"), .NewFFLayout("false")) d_ff_6 (
    .clk(CLK), .D(and_3_out), .Q(d_ff_6_q));  // open: Qn, preset, en, reset
  D_Flip_Flop #(.trigger("rising"), .Pre_Clr_Positions("LEGACY"), .NegatePresetClear("false"), .enable("true"), .NewFFLayout("false")) d_ff_7 (
    .clk(CLK), .D(and_4_out), .Q(d_ff_7_q));  // open: Qn, preset, en, reset
  or or_8 (IR1_t, IR1, IRA);
  assign bit_extender_1_out = {{16{1'b0}}, IR[15:0]};  // Bit_Extender bit_extender_1
  assign bit_extender_2_out = {{16{IR[15]}}, IR[15:0]};  // Bit_Extender bit_extender_2
  or or_9 (or_9_out, ERET, INIT);
  or or_10 (IR2_t, IR2, IRB);
  reg_choose_logic reg_choose_logic_1 (
    ._21_25(IR[25:21]), .Syscall(Syscall), .RegDst(RegDst), ._16_20(IR[20:16]), ._11_15(IR[15:11]),
    .JAL(JAL), .PC_plus_four(adder_1_out), .WriteBack_Data(multiplexer_5_out), ._6_10(IR[10:6]),
    .R1Adr(reg_choose_logic_1_r1adr), .R2Adr(reg_choose_logic_1_r2adr), .WAdr(reg_choose_logic_1_wadr),
    .RDin(RDin), .Shamt(reg_choose_logic_1_shamt));
  Counter #(.width(16), .max('hffff), .ongoal("stay"), .trigger("rising"), .behavior("old")) counter_2 (
    .Q(\总周期数 ), .clk(CLK));  // open: load, D, count, carry, clr, preset
  Priority_Encoder #(.select(2), .disabled("Z")) priority_encoder_1 (
    .in0(d_ff_5_q), .in1(d_ff_6_q), .in2(d_ff_7_q), .in3(1'b0), .out(priority_encoder_1_out),
    .gs(priority_encoder_1_gs));  // open: en_out, en_in
  // D_Flip_Flop #(.trigger("latch"), .Pre_Clr_Positions("LEGACY"), .NegatePresetClear("false"), .enable("false"), .NewFFLayout("false")) IE: pin names not known; wires that end beside it: or_9_out, IE_p2, IE
  Comparator #(.width(16), .mode("twosComplement")) comparator_2 (
    .a({16{1'b0}}), .b(\总周期数 ), .eq(INIT));  // open: gt, lt
  MIPS_Regifile mips_regifile_1 (
    .Din(RDin), .Clk(CLK), .R1(R1), .R2(MDin), .WE(RegWrite), .WAdr(reg_choose_logic_1_wadr),
    .R1Adr(reg_choose_logic_1_r1adr), .R2Adr(reg_choose_logic_1_r2adr));
  Multiplexer #(.select(1), .width(5), .disabled("Z"), .enable("false")) multiplexer_1 (
    .in0(reg_choose_logic_1_shamt), .in1(R1[4:0]), .out(multiplexer_1_out), .sel(Vshamt));
  Adder #(.width(32)) adder_2 (
    .a(adder_1_out), .b({bit_extender_2_out[29:0], 2'b00}), .out(adder_2_out));  // open: cin, cout
  Multiplexer #(.select(1), .width(32), .disabled("Z"), .enable("false")) multiplexer_2 (
    .in0(bit_extender_1_out), .in1(bit_extender_2_out), .out(multiplexer_2_out), .sel(SignedExt));
  and and_5 (IRQ, priority_encoder_1_gs, IE);
  not not_1 (not_1_out, ERET);
  Comparator #(.width(32), .mode("twosComplement")) comparator_3 (.a(IR), .b(32'h42000018), .eq(ERET));  // open: gt, lt
  or or_11 (IR3_t, IR3, IRC);
  Multiplexer #(.select(1), .width(32), .disabled("Z"), .enable("false")) multiplexer_3 (
    .in0(MDin), .in1(multiplexer_2_out), .out(multiplexer_3_out), .sel(AluSrcB));
  Multiplexer #(.select(2), .width(32), .disabled("Z"), .enable("false")) multiplexer_4 (
    .in0(32'h30ac), .in1(32'h3150), .in2(32'h31f4), .out(IRQ_Entry), .sel(priority_encoder_1_out));  // open: in3
  D_Flip_Flop #(.trigger("rising"), .Pre_Clr_Positions("LEGACY"), .NegatePresetClear("false"), .enable("true"), .NewFFLayout("false")) d_ff_8 (
    .clk(CLK), .D(IRQ), .Q(IE_p2), .en(not_1_out));  // open: Qn, preset, reset
  MIPS_ALU mips_alu_1 (
    .X(R1), .Y(multiplexer_3_out), .AluOP(AluOP), .Equal(Equal), .Result(mips_alu_1_result),
    .shamt(multiplexer_1_out), .Less(Less));  // open: Result_2
  Register #(.width(2), .trigger("rising"), .Select("low")) register_1 (
    .D(priority_encoder_1_out), .Q(IRQ_Exe), .clk(IE_p2), .preset(INIT));  // open: en, clr, cs
  Register #(.width(32), .trigger("rising"), .Select("low")) u_EPC (
    .D(PC_Next), .Q(EPC), .clk(IE_p2));  // open: en, clr
  MIPS_MEM mips_mem_1 (
    .AluResult(mips_alu_1_result), .HalfW(HalfW), .WriteData(MDin), .MemWrite(MemWrite), .CLK(CLK),
    .MemReadData(mips_mem_1_memreaddata));
  Multiplexer #(.select(1), .width(32), .disabled("Z"), .enable("false")) multiplexer_5 (
    .in0(mips_alu_1_result), .in1(mips_mem_1_memreaddata), .out(multiplexer_5_out), .sel(MemToReg));
  Comparator #(.width(16), .mode("twosComplement")) comparator_4 (
    .a(16'h23b), .b(\总周期数 ), .eq(comparator_4_eq));  // open: gt, lt
  Comparator #(.width(16), .mode("twosComplement")) comparator_5 (
    .a(\总周期数 ), .b(16'h1), .eq(comparator_5_eq));  // open: gt, lt
  Comparator #(.width(16), .mode("twosComplement")) comparator_6 (
    .a(\总周期数 ), .b(16'h4), .eq(comparator_6_eq));  // open: gt, lt
  Comparator #(.width(16), .mode("twosComplement")) comparator_7 (
    .a(\总周期数 ), .b(16'h7), .eq(comparator_7_eq));  // open: gt, lt
  or or_12 (or_12_out, comparator_4_eq, comparator_5_eq);
  Pull_Resistor #(.pull(0)) pull_resistor_2 (.node(IRA));
  assign IRA = or_12_out ? ~CLK : 1'bz;  // Controlled_Inverter controlled_inverter_1
  Pull_Resistor #(.pull(0)) pull_resistor_3 (.node(IRB));
  assign IRB = comparator_6_eq ? ~CLK : 1'bz;  // Controlled_Inverter controlled_inverter_2
  Pull_Resistor #(.pull(0)) pull_resistor_4 (.node(IRC));
  assign IRC = comparator_7_eq ? ~CLK : 1'bz;  // Controlled_Inverter controlled_inverter_3
  sc_hard_wired_controller sc_hard_wired_controller_1 (
    .Func(IR[5:0]), .OP(IR[31:26]), .ALU_OP(AluOP), .MemToReg(MemToReg), .MemWrite(MemWrite),
    .ALU_SRC(AluSrcB), .RegWrite(RegWrite), .SysCALL(Syscall), .SignedExt(SignedExt), .RegDst(RegDst),
    .JR(JR), .JMP(JMP), .Beq(Beq), .JAL(JAL), .Bne(Bne), .Vshamt(Vshamt), .BLEZ(Blez), .HalfW(HalfW));
  syscall_process syscall_process_1 (
    .Syscall(Syscall), .CLK(CLK), .R2(MDin), .R1(R1), .Pause(Pause), .LedData(LedData));  // open: Get_KB_in, Screen_opt, Cycles, Get_Bitmap, CopyToRAM, FrameFlush

  // Other names for the same wires on the sheet: Func[5:0] = IR[5:0]; OP[5:0] = IR[31:26]; R2[31:0] = MDin

  // Notes on the sheet:
  //   中断源
  //   中断等待指示
  //   总复位信号应将除ROM以外所有存储组件全部清零
  //   控制位
  //   暂停节拍，不能为0
  //   用这个时钟源需要去掉电路中的其他时钟源
  //   数码管输出
  //   戳工具置1进入计数暂停模式，ctrl+k时钟自动运行到对应节拍暂停
  //   ctrl+k关闭时钟连续运行，将控制位置零，进入单步调试模式调试
  //   数码管输出应该用寄存器锁存，否则显示数据只能一闪而过
  //   指令存储器
  //   指令字
  //   contents of rom_1 (hex, n*v repeats v):
  //   201d07d0 20100001 109fc0 139fc3 8021 2012000c 24160008 26100001 3210000f 20080008 20090001 139900
  //   2709825 132020 20020022 c 1094022 1500fff9 22100001 2018000f 2188024 108700 20080008 20090001 139902
  //   2709825 132021 20020022 c 1094022 1500fff9 108702 2c9b022 12c00001 8000c07 4020 1084027 84400
  //   3508ffff 82021 20020022 c 8000c01 afa20000 23bd0004 afa40000 23bd0004 afb00000 23bd0004 afb30000
  //   23bd0004 afb40000 23bd0004 afb50000 23bd0004 afb60000 23bd0004 20160001 20140003 20150001 168020
  //   108100 2149825 132020 20020022 c 1600fffa 295a022 1680fff7 23bdfffc 8fb60000 23bdfffc 8fb50000
  //   23bdfffc 8fb40000 23bdfffc 8fb30000 23bdfffc 8fb00000 23bdfffc 8fa40000 23bdfffc 8fa20000 42000018
  //   afa20000 23bd0004 afa40000 23bd0004 afb00000 23bd0004 afb30000 23bd0004 afb40000 23bd0004 afb50000
  //   23bd0004 afb60000 23bd0004 20160002 20140003 20150001 168020 108100 2149825 132020 20020022 c
  //   1600fffa 295a022 1680fff7 23bdfffc 8fb60000 23bdfffc 8fb50000 23bdfffc 8fb40000 23bdfffc 8fb30000
  //   23bdfffc 8fb00000 23bdfffc 8fa40000 23bdfffc 8fa20000 42000018 afa20000 23bd0004 afa40000 23bd0004
  //   afb00000 23bd0004 afb30000 23bd0004 afb40000 23bd0004 afb50000 23bd0004 afb60000 23bd0004 20160003
  //   20140003 20150001 168020 108100 2149825 132020 20020022 c 1600fffa 295a022 1680fff7 23bdfffc
  //   8fb60000 23bdfffc 8fb50000 23bdfffc 8fb40000 23bdfffc 8fb30000 23bdfffc 8fb00000 23bdfffc 8fa40000
  //   23bdfffc 8fa20000 42000018
  //   可计数暂停的时钟源
  //   为方便自动评测，需要输出PC，IR，寄存器堆写如数据RDin
  //   RAM写使能MemWrite、RAM写入数据MDin等信号
  //   单级中断测试信号模拟器
endmodule

module multiple_stage_interruption_support (
  input  IR1,
  input  IR2,
  input  IR3,
  output RegWrite,
  output MemWrite,
  output [31:0] PC,
  output [31:0] IR,
  output [31:0] RDin,
  output [31:0] MDin,
  output [31:0] LedData
);

  wire AluSrcB, and_1_out, and_2_out, and_3_out, and_4_out, and_5_out, and_6_out, and_7_out, and_9_out, Beq,
       Blez, Bne, CLK, clock_2_out, comparator_2_eq, comparator_3_eq, comparator_4_eq, comparator_5_eq,
       comparator_7_eq, comparator_8_eq, comparator_9_eq, comparator_10_eq, comparator_11_eq,
       comparator_12_eq, comparator_12_lt, d_ff_1_q, d_ff_2_q, d_ff_3_q, d_ff_4_q, d_ff_5_qn, d_ff_6_q,
       d_ff_7_qn, d_ff_8_q, d_ff_9_qn, d_ff_10_q, d_ff_11_q, decoder_1_out0, decoder_1_out1, decoder_1_out2,
       Equal, ERET, Go, HalfW, IE, INIT, IR1_t, IR2_t, IR3_t, IRA, IRB, IRC, IRQ, JAL, JMP, JR, Less,
       MemToReg, MFC, MTC, nand_1_out, not_1_out, not_2_out, not_3_out, not_4_out, not_5_out, not_6_out,
       or_1_out, or_5_out, or_6_out, or_7_out, or_9_out, or_10_out, or_12_out, or_13_out, or_15_out,
       or_16_out, Pause, priority_encoder_1_gs, RegDst, SignedExt, Syscall, undriven, Vshamt, W1, W2, W3;
  wire [1:0] controlled_buffer_4_out, IRQ_Exe, IRQ_Number_Stack_data, IRQ_TODO;
  wire [2:0] multiplexer_1_out;
  wire [3:0] AluOP;
  wire [4:0] multiplexer_2_out, reg_choose_logic_1_r1adr, reg_choose_logic_1_r2adr, reg_choose_logic_1_shamt,
       reg_choose_logic_1_wadr;
  wire [12:0] CNT;
  wire [15:0] adder_3_out, controlled_buffer_6_out, controlled_buffer_8_out, register_2_q, subtractor_1_out,
       TotalCycles;
  wire [31:0] adder_1_out, adder_2_out, bit_extender_1_out, bit_extender_2_out, controlled_buffer_1_out, EPC,
       IRQ_Entry, mips_alu_1_result, mips_mem_1_memreaddata, multiplexer_3_out, multiplexer_5_out,
       multiplexer_6_out, PC_Next, R1;

  Clock #(.highDuration(1), .lowDuration(1)) clock_1 ();  // open: out
  Button _1 (.out(IRA));
  Button _2 (.out(IRB));
  Button _3 (.out(IRC));
  Button \u_继续运行  (.out(Go));
  LED #(.active("true")) IRQ_1 (.in(W1));
  LED #(.active("true")) IRQ_2 (.in(W2));
  LED #(.active("true")) IRQ_3 (.in(W3));
  Decoder #(.select(2), .tristate("false"), .disabled(0), .enable("true")) decoder_1 (
    .out0(decoder_1_out0), .out1(decoder_1_out1), .out2(decoder_1_out2), .sel(IRQ_Exe), .en(ERET));  // open: out3
  Multiplexer #(.select(2), .width(3), .disabled(0), .enable("false")) multiplexer_1 (
    .in0(3'b001), .in1(3'b011), .in2(3'b111), .in3(3'b000), .out(multiplexer_1_out), .sel(IRQ_Exe));
  Hex_Digit_Display hex_digit_display_1 (.value(LedData[31:28]));  // open: dp
  and and_1 (and_1_out, ~ERET, IRQ);  // AND_Gate
  or or_1 (or_1_out, ERET, IRQ);
  PC_update_logic pc_update_logic_1 (
    .Equal(Equal), .Beq(Beq), .Bne(Bne), .JAL(JAL), .JMP(JMP), .JR(JR), .BAddr(adder_2_out),
    .PC_plus_four(adder_1_out), .JAddr({PC[31:28], IR[25:0], 2'b00}), .JRAddr(R1), .PC_Next(PC_Next),
    .Blez(Blez), .Less(Less));  // open: Branched, BranchSig
  or or_2 (W1, d_ff_4_q, d_ff_1_q);
  or or_3 (W2, d_ff_6_q, d_ff_2_q);
  or or_4 (W3, d_ff_8_q, d_ff_3_q);
  Hex_Digit_Display hex_digit_display_2 (.value(LedData[27:24]));  // open: dp
  Hex_Digit_Display hex_digit_display_3 (.value(LedData[23:20]));  // open: dp
  assign controlled_buffer_1_out = ERET ? EPC : 32'bz;  // Controlled_Buffer controlled_buffer_1
  assign controlled_buffer_1_out = and_1_out ? IRQ_Entry : 32'bz;  // Controlled_Buffer controlled_buffer_2
  assign controlled_buffer_1_out = ~or_1_out ? PC_Next : 32'bz;  // Controlled_Buffer controlled_buffer_3
  D_Flip_Flop #(.trigger("rising"), .Pre_Clr_Positions("LEGACY"), .NegatePresetClear("false"), .enable("true"), .NewFFLayout("false")) d_ff_1 (
    .clk(IR1_t), .D(1'b1), .Q(d_ff_1_q), .reset(d_ff_4_q));  // open: Qn, preset, en
  D_Flip_Flop #(.trigger("rising"), .Pre_Clr_Positions("LEGACY"), .NegatePresetClear("false"), .enable("true"), .NewFFLayout("false")) d_ff_2 (
    .clk(IR2_t), .D(1'b1), .Q(d_ff_2_q), .reset(d_ff_6_q));  // open: Qn, preset, en
  D_Flip_Flop #(.trigger("rising"), .Pre_Clr_Positions("LEGACY"), .NegatePresetClear("false"), .enable("true"), .NewFFLayout("false")) d_ff_3 (
    .clk(IR3_t), .D(1'b1), .Q(d_ff_3_q), .reset(d_ff_8_q));  // open: Qn, preset, en
  Hex_Digit_Display hex_digit_display_4 (.value(LedData[19:16]));  // open: dp
  Hex_Digit_Display hex_digit_display_5 (.value(LedData[15:12]));  // open: dp
  Register #(.width(32), .trigger("rising"), .Select("low")) u_PC (
    .D(controlled_buffer_1_out), .Q(PC), .clk(CLK));  // open: en, clr
  or or_5 (or_5_out, d_ff_1_q, d_ff_4_q);
  or or_6 (or_6_out, d_ff_2_q, d_ff_6_q);
  or or_7 (or_7_out, d_ff_3_q, d_ff_8_q);
  Hex_Digit_Display hex_digit_display_6 (.value(LedData[11:8]));  // open: dp
  Hex_Digit_Display hex_digit_display_7 (.value(LedData[7:4]));  // open: dp
  Adder #(.width(32)) adder_1 (.a(PC), .b(32'h4), .out(adder_1_out));  // open: cin, cout
  and and_2 (and_2_out, or_5_out, ~decoder_1_out0);  // AND_Gate
  not not_1 (not_1_out, multiplexer_1_out[0]);
  and and_3 (and_3_out, or_6_out, ~decoder_1_out1);  // AND_Gate
  and and_4 (and_4_out, or_7_out, ~decoder_1_out2);  // AND_Gate
  not not_2 (not_2_out, multiplexer_1_out[2]);
  Hex_Digit_Display hex_digit_display_8 (.value(LedData[3:0]));  // open: dp
  // Probe on TotalCycles
  ROM #(.addrWidth(10), .dataWidth(32), .Select("low")) IR_ROM (.addr(PC[11:2]), .data(IR));
  D_Flip_Flop #(.trigger("rising"), .Pre_Clr_Positions("LEGACY"), .NegatePresetClear("false"), .enable("false"), .NewFFLayout("false")) d_ff_4 (
    .clk(CLK), .D(and_2_out), .Q(d_ff_4_q));  // open: Qn, preset, reset
  D_Flip_Flop #(.trigger("rising"), .Pre_Clr_Positions("LEGACY"), .NegatePresetClear("false"), .enable("false"), .NewFFLayout("false")) d_ff_5 (
    .Qn(d_ff_5_qn), .preset(multiplexer_1_out[0]), .reset(not_1_out));  // open: clk, D, Q
  and and_5 (and_5_out, d_ff_4_q, d_ff_5_qn);
  D_Flip_Flop #(.trigger("rising"), .Pre_Clr_Positions("LEGACY"), .NegatePresetClear("false"), .enable("true"), .NewFFLayout("false")) d_ff_6 (
    .clk(CLK), .D(and_3_out), .Q(d_ff_6_q));  // open: Qn, preset, en, reset
  D_Flip_Flop #(.trigger("rising"), .Pre_Clr_Positions("LEGACY"), .NegatePresetClear("false"), .enable("false"), .NewFFLayout("false")) d_ff_7 (
    .Qn(d_ff_7_qn), .preset(multiplexer_1_out[1]), .reset(not_3_out));  // open: clk, D, Q
  and and_6 (and_6_out, d_ff_6_q, d_ff_7_qn);
  not not_3 (not_3_out, multiplexer_1_out[1]);
  D_Flip_Flop #(.trigger("rising"), .Pre_Clr_Positions("LEGACY"), .NegatePresetClear("false"), .enable("false"), .NewFFLayout("false")) d_ff_8 (
    .clk(CLK), .D(and_4_out), .Q(d_ff_8_q));  // open: Qn, preset, reset
  D_Flip_Flop #(.trigger("rising"), .Pre_Clr_Positions("LEGACY"), .NegatePresetClear("false"), .enable("false"), .NewFFLayout("false")) d_ff_9 (
    .clk(undriven), .Qn(d_ff_9_qn), .preset(multiplexer_1_out[2]), .reset(not_2_out));  // open: D, Q
  and and_7 (and_7_out, d_ff_8_q, d_ff_9_qn);
  or or_8 (IR1_t, IR1, IRA);
  assign bit_extender_1_out = {{16{1'b0}}, IR[15:0]};  // Bit_Extender bit_extender_1
  assign bit_extender_2_out = {{16{IR[15]}}, IR[15:0]};  // Bit_Extender bit_extender_2
  Priority_Encoder #(.select(2), .disabled(0)) priority_encoder_1 (
    .in0(and_5_out), .in1(and_6_out), .in2(and_7_out), .in3(1'b0), .out(IRQ_TODO), .gs(priority_encoder_1_gs));  // open: en_out, en_in
  D_Flip_Flop #(.trigger("rising"), .Pre_Clr_Positions("LEGACY"), .NegatePresetClear("false"), .enable("true"), .NewFFLayout("false")) u_IE (
    .clk(CLK), .D(MFC), .Q(IE), .preset(or_9_out), .en(or_10_out), .reset(d_ff_10_q));  // open: Qn
  or or_9 (or_9_out, ERET, INIT);
  or or_10 (or_10_out, MTC, ERET, MFC, IRQ);
  Comparator #(.width(16), .mode("twosComplement")) comparator_1 (
    .a({16{1'b0}}), .b(TotalCycles), .eq(INIT));  // open: gt, lt
  or or_11 (IR2_t, IR2, IRB);
  reg_choose_logic reg_choose_logic_1 (
    ._21_25(IR[25:21]), .Syscall(Syscall), .RegDst(RegDst), ._16_20(IR[20:16]), ._11_15(IR[15:11]),
    .JAL(JAL), .PC_plus_four(adder_1_out), .WriteBack_Data(multiplexer_6_out), ._6_10(IR[10:6]),
    .R1Adr(reg_choose_logic_1_r1adr), .R2Adr(reg_choose_logic_1_r2adr), .WAdr(reg_choose_logic_1_wadr),
    .RDin(RDin), .Shamt(reg_choose_logic_1_shamt));
  and and_8 (IRQ, priority_encoder_1_gs, IE);
  Comparator #(.width(8), .mode("twosComplement")) comparator_2 (
    .a({8{1'b0}}), .b(IR[10:3]), .eq(comparator_2_eq));  // open: gt, lt
  Comparator #(.width(6), .mode("twosComplement")) comparator_3 (
    .a(6'b010000), .b(IR[31:26]), .eq(comparator_3_eq));  // open: gt, lt
  Comparator #(.width(5), .mode("twosComplement")) comparator_4 (
    .a({5{1'b0}}), .b(IR[25:21]), .eq(comparator_4_eq));  // open: gt, lt
  Comparator #(.width(5), .mode("twosComplement")) comparator_5 (
    .a(5'b00100), .b(IR[25:21]), .eq(comparator_5_eq));  // open: gt, lt
  MIPS_Regifile mips_regifile_1 (
    .Din(RDin), .Clk(CLK), .R1(R1), .R2(MDin), .WE(RegWrite), .WAdr(reg_choose_logic_1_wadr),
    .R1Adr(reg_choose_logic_1_r1adr), .R2Adr(reg_choose_logic_1_r2adr));
  Multiplexer #(.select(1), .width(5), .disabled(0), .enable("false")) multiplexer_2 (
    .in0(reg_choose_logic_1_shamt), .in1(R1[4:0]), .out(multiplexer_2_out), .sel(Vshamt));
  Adder #(.width(32)) adder_2 (
    .a(adder_1_out), .b({bit_extender_2_out[29:0], 2'b00}), .out(adder_2_out));  // open: cin, cout
  Multiplexer #(.select(1), .width(32), .disabled(0), .enable("false")) multiplexer_3 (
    .in0(bit_extender_1_out), .in1(bit_extender_2_out), .out(multiplexer_3_out), .sel(SignedExt));
  assign controlled_buffer_4_out = ERET ? IRQ_Number_Stack_data : 2'bz;  // Controlled_Buffer controlled_buffer_4
  or or_12 (or_12_out, IRQ, ERET);
  assign controlled_buffer_4_out = IRQ ? IRQ_TODO : 2'bz;  // Controlled_Buffer controlled_buffer_5
  Multiplexer #(.select(2), .width(32), .disabled(0), .enable("false")) multiplexer_4 (
    .in0(32'h30ac), .in1(32'h3158), .in2(32'h3204), .out(IRQ_Entry), .sel(controlled_buffer_4_out));  // open: in3
  D_Flip_Flop #(.trigger("rising"), .Pre_Clr_Positions("LEGACY"), .NegatePresetClear("false"), .enable("true"), .NewFFLayout("false")) d_ff_10 (
    .clk(CLK), .D(or_13_out), .Q(d_ff_10_q), .en(not_4_out));  // open: Qn, preset, reset
  or or_13 (or_13_out, IRQ, MTC);
  not not_4 (not_4_out, ERET);
  and and_9 (and_9_out, comparator_2_eq, comparator_3_eq);
  or or_14 (IR3_t, IR3, IRC);
  Multiplexer #(.select(1), .width(32), .disabled(0), .enable("false")) multiplexer_5 (
    .in0(MDin), .in1(multiplexer_3_out), .out(multiplexer_5_out), .sel(AluSrcB));
  Register #(.width(2), .trigger("rising"), .Select("low")) register_1 (
    .D(controlled_buffer_4_out), .en(or_12_out), .Q(IRQ_Exe), .clk(CLK), .preset(INIT));  // open: clr, cs
  and and_10 (MFC, and_9_out, comparator_4_eq);
  and and_11 (MTC, and_9_out, comparator_5_eq);
  Comparator #(.width(32), .mode("twosComplement")) comparator_6 (.a(IR), .b(32'h42000018), .eq(ERET));  // open: gt, lt
  MIPS_ALU mips_alu_1 (
    .X(R1), .Y(multiplexer_5_out), .AluOP(AluOP), .Equal(Equal), .Result(mips_alu_1_result),
    .shamt(multiplexer_2_out), .Less(Less));  // open: Result_2
  Adder #(.width(16)) adder_3 (.a(controlled_buffer_8_out), .b(16'h1), .out(adder_3_out));  // open: cin, cout
  Subtractor #(.width(16)) subtractor_1 (.a(register_2_q), .b(16'h1), .out(subtractor_1_out));  // open: bin, bout
  assign controlled_buffer_6_out = IRQ ? adder_3_out : 16'bz;  // Controlled_Buffer controlled_buffer_6
  assign controlled_buffer_6_out = ERET ? subtractor_1_out : 16'bz;  // Controlled_Buffer controlled_buffer_7
  assign controlled_buffer_8_out = ~ERET ? register_2_q : 16'bz;  // Controlled_Buffer controlled_buffer_8
  Register #(.width(16), .trigger("rising"), .Select("low")) register_2 (
    .D(controlled_buffer_6_out), .Q(register_2_q), .clk(CLK));  // open: en, clr
  assign controlled_buffer_8_out = ERET ? controlled_buffer_6_out : 16'bz;  // Controlled_Buffer controlled_buffer_9
  MIPS_MEM mips_mem_1 (
    .AluResult(mips_alu_1_result), .HalfW(HalfW), .WriteData(MDin), .MemWrite(MemWrite), .CLK(CLK),
    .MemReadData(mips_mem_1_memreaddata));
  not not_5 (not_5_out, IRQ);
  not not_6 (not_6_out, IRQ);
  RAM #(.addrWidth(16), .dataWidth(2), .bus("separate"), .Select("low")) IRQ_Number_Stack (
    .addr(controlled_buffer_8_out), .din(IRQ_Exe), .data(IRQ_Number_Stack_data), .str(IRQ), .clk(CLK),
    .ld(not_5_out));  // open: sel, clr
  RAM #(.addrWidth(16), .dataWidth(32), .bus("separate"), .Select("low")) PC_Stack (
    .addr(controlled_buffer_8_out), .din(PC_Next), .data(EPC), .str(IRQ), .clk(CLK), .ld(not_6_out));  // open: sel, clr
  Multiplexer #(.select(1), .width(32), .disabled(0), .enable("false")) multiplexer_6 (
    .in0(mips_alu_1_result), .in1(mips_mem_1_memreaddata), .out(multiplexer_6_out), .sel(MemToReg));
  D_Flip_Flop #(.trigger("high"), .Pre_Clr_Positions("LEGACY"), .NegatePresetClear("false"), .enable("true"), .NewFFLayout("false")) d_ff_11 (
    .Q(d_ff_11_q), .preset(Pause), .reset(Go));  // open: clk, D, Qn, en
  // Probe on 13'hc
  Comparator #(.width(16), .mode("twosComplement")) comparator_7 (
    .a(16'h258), .b(TotalCycles), .eq(comparator_7_eq));  // open: gt, lt
  Comparator #(.width(16), .mode("twosComplement")) comparator_8 (
    .a(TotalCycles), .b(16'h1), .eq(comparator_8_eq));  // open: gt, lt
  Comparator #(.width(16), .mode("twosComplement")) comparator_9 (
    .a(TotalCycles), .b(16'h4), .eq(comparator_9_eq));  // open: gt, lt
  Comparator #(.width(16), .mode("twosComplement")) comparator_10 (
    .a(TotalCycles), .b(16'h7), .eq(comparator_10_eq));  // open: gt, lt
  Comparator #(.width(16), .mode("twosComplement")) comparator_11 (
    .a(TotalCycles), .b(16'h241), .eq(comparator_11_eq));  // open: gt, lt
  Clock #(.highDuration(1), .lowDuration(1)) clock_2 (.out(clock_2_out));
  sc_hard_wired_controller sc_hard_wired_controller_1 (
    .Func(IR[5:0]), .OP(IR[31:26]), .ALU_OP(AluOP), .MemToReg(MemToReg), .MemWrite(MemWrite),
    .ALU_SRC(AluSrcB), .RegWrite(RegWrite), .SysCALL(Syscall), .SignedExt(SignedExt), .RegDst(RegDst),
    .JR(JR), .JMP(JMP), .Beq(Beq), .JAL(JAL), .Bne(Bne), .Vshamt(Vshamt), .BLEZ(Blez), .HalfW(HalfW));
  syscall_process syscall_process_1 (
    .Syscall(Syscall), .CLK(CLK), .R2(MDin), .R1(R1), .Pause(Pause), .LedData(LedData));  // open: Get_KB_in, Screen_opt, Cycles, Get_Bitmap, CopyToRAM, FrameFlush
  or or_15 (or_15_out, comparator_7_eq, comparator_8_eq);
  assign IRA = or_15_out ? ~CLK : 1'bz;  // Controlled_Inverter controlled_inverter_1
  assign IRB = comparator_9_eq ? ~CLK : 1'bz;  // Controlled_Inverter controlled_inverter_2
  or or_16 (or_16_out, comparator_10_eq, comparator_11_eq);
  assign IRC = or_16_out ? ~CLK : 1'bz;  // Controlled_Inverter controlled_inverter_3
  Comparator #(.width(13), .mode("twosComplement")) comparator_12 (
    .a(CNT), .b(13'hc), .eq(comparator_12_eq), .lt(comparator_12_lt));  // open: gt
  nand nand_1 (nand_1_out, d_ff_11_q, comparator_12_eq);
  Counter #(.width(13), .max('h1fff), .ongoal("stay"), .trigger("rising"), .behavior("old")) counter_1 (
    .count(comparator_12_lt), .Q(CNT), .clk(clock_2_out));  // open: load, D, carry, clr, preset
  assign CLK = nand_1_out ? clock_2_out : 1'bz;  // Controlled_Buffer controlled_buffer_10
  Counter #(.width(16), .max('hffff), .ongoal("stay"), .trigger("rising"), .behavior("old")) counter_2 (
    .Q(TotalCycles), .clk(CLK));  // open: load, D, count, carry, clr, preset

  // Other names for the same wires on the sheet: Func[5:0] = IR[5:0]; OP[5:0] = IR[31:26]; R2[31:0] = MDin

  // Notes on the sheet:
  //   中断源
  //   中断等待指示
  //   总复位信号应将除ROM以外所有存储组件全部清零
  //   数码管输出
  //   数码管输出应该用寄存器锁存，否则显示数据只能一闪而过
  //   指令存储器
  //   指令字
  //   contents of IR_ROM (hex, n*v repeats v):
  //   201d07d0 20100001 109fc0 139fc3 8021 2012000c 24160008 26100001 3210000f 20080008 20090001 139900
  //   2709825 132020 20020022 c 1094022 1500fff9 22100001 2018000f 2188024 108700 20080008 20090001 139902
  //   2709825 132021 20020022 c 1094022 1500fff9 108702 2c9b022 12c00001 8000c07 4020 1084027 84400
  //   3508ffff 82021 20020022 c 8000c01 afa20000 23bd0004 afa40000 23bd0004 afb00000 23bd0004 afb30000
  //   23bd0004 afb40000 23bd0004 afb50000 23bd0004 afb60000 23bd0004 40000000 20160001 20140003 20150001
  //   168020 108100 2149825 132020 20020022 c 1600fffa 295a022 1680fff7 40800000 23bdfffc 8fb60000
  //   23bdfffc 8fb50000 23bdfffc 8fb40000 23bdfffc 8fb30000 23bdfffc 8fb00000 23bdfffc 8fa40000 23bdfffc
  //   8fa20000 42000018 afa20000 23bd0004 afa40000 23bd0004 afb00000 23bd0004 afb30000 23bd0004 afb40000
  //   23bd0004 afb50000 23bd0004 afb60000 23bd0004 40000000 20160002 20140003 20150001 168020 108100
  //   2149825 132020 20020022 c 1600fffa 295a022 1680fff7 40800000 23bdfffc 8fb60000 23bdfffc 8fb50000
  //   23bdfffc 8fb40000 23bdfffc 8fb30000 23bdfffc 8fb00000 23bdfffc 8fa40000 23bdfffc 8fa20000 42000018
  //   afa20000 23bd0004 afa40000 23bd0004 afb00000 23bd0004 afb30000 23bd0004 afb40000 23bd0004 afb50000
  //   23bd0004 afb60000 23bd0004 40000000 20160003 20140003 20150001 168020 108100 2149825 132020 20020022
  //   c 1600fffa 295a022 1680fff7 40800000 23bdfffc 8fb60000 23bdfffc 8fb50000 23bdfffc 8fb40000 23bdfffc
  //   8fb30000 23bdfffc 8fb00000 23bdfffc 8fa40000 23bdfffc 8fa20000 42000018
  //   为方便自动评测，需要输出PC，IR，寄存器堆写如数据RDin
  //   RAM写使能MemWrite、RAM写入数据MDin等信号
  //   控制位
  //   暂停节拍，不能为0
  //   多级中断测试信号模拟器
  //   戳工具置1进入计数暂停模式，ctrl+k时钟自动运行到对应节拍暂停
  //   ctrl+k关闭时钟连续运行，将控制位置零，进入单步调试模式调试
  //   用这个时钟源需要去掉电路中的其他时钟源
  //   可计数暂停的时钟源
endmodule

module ideal_pipeline (
  output RegWrite,
  output MemWrite,
  output [31:0] IF_PC,
  output [31:0] ID_PC,
  output [31:0] EX_PC,
  output [31:0] M_PC,
  output [31:0] WB_PC,
  output [31:0] RDin,
  output [31:0] MDin,
  output [31:0] LedData
);

  wire Beq, Blez, Bne, CLK, clock_1_out, clock_2_out, comparator_1_eq, comparator_1_lt, d_ff_1_q, Equal,
       ex_mem_1_halfw_out, ex_mem_1_jal_out, ex_mem_1_memtoreg_out, ex_mem_1_regwrite_out,
       ex_mem_1_syscall_out, Go, id_ex_1_alusrcb_out, id_ex_1_halfw_out, id_ex_1_memtoreg_out,
       id_ex_1_memwrite_out, id_ex_1_regwrite_out, id_ex_1_syscall_out, IR1, IR2, IR3, JAL, JAL_WB, JMP, JR,
       Less, mem_wb_1_p10, nand_1_out, Pause, RegDst, RST, SignedExt, Syscall, Vshamt, W1, W2, W3;
  wire [3:0] id_ex_1_aluop_out, sc_hard_wired_controller_1_alu_op;
  wire [4:0] ex_mem_1_wadr_out, id_ex_1_shamt_out, id_ex_1_wadr_out, mem_wb_1_p14, multiplexer_2_out,
       reg_choose_logic_1_r1adr, reg_choose_logic_1_r2adr, reg_choose_logic_1_shamt, reg_choose_logic_1_wadr;
  wire [5:0] Func, OP, sc_hard_wired_controller_1_jr;
  wire [8:0] sc_hard_wired_controller_1_memtoreg;
  wire [12:0] CNT_num;
  wire [15:0] \LoadUse次数 , \总周期数 , \插入气泡数 , \无条件分支数 , \条件分支成功数 ;
  wire [27:8] if_id_1_instr_out;
  wire [31:0] adder_1_out, adder_2_out, bit_extender_1_out, bit_extender_2_out, ex_mem_1_aluresult_out,
       ex_mem_1_r1_out, id_ex_1_extdata_out, id_ex_1_pc_plus_four_out, id_ex_1_r2_out,
       if_id_1_pc_plus_four_out, IR, mem_wb_1_p12, mem_wb_1_p13, mips_alu_1_result, mips_mem_1_memreaddata,
       mips_regifile_1_r1, mips_regifile_1_r2, multiplexer_1_out, multiplexer_3_out, multiplexer_4_out,
       pc_update_logic_1_pc_next, R1;

  Button \u_总复位  (.out(RST));
  Button _1 (.out(IR1));
  Button _2 (.out(IR2));
  Button _3 (.out(IR3));
  Button \u_继续运行  (.out(Go));
  LED #(.active("true")) led_1 (.in(W1));
  LED #(.active("true")) led_2 (.in(W2));
  LED #(.active("true")) led_3 (.in(W3));
  PC_update_logic pc_update_logic_1 (
    .Equal(Equal), .Beq(Beq), .Bne(Bne), .JAL(JAL), .JMP(JMP), .JR(JR), .BAddr(adder_2_out),
    .PC_plus_four(adder_1_out), .JAddr({ID_PC[31:28], if_id_1_instr_out, Func, 2'b00}), .JRAddr(R1),
    .PC_Next(pc_update_logic_1_pc_next), .Blez(Blez), .Less(Less));  // open: Branched, BranchSig
  Hex_Digit_Display hex_digit_display_1 (.value(LedData[31:28]));  // open: dp
  D_Flip_Flop #(.trigger("high"), .Pre_Clr_Positions("LEGACY"), .NegatePresetClear("false"), .enable("true"), .NewFFLayout("false")) d_ff_1 (
    .Q(d_ff_1_q), .preset(Pause), .reset(Go));  // open: clk, D, Qn, en
  // Probe on 13'hc
  Hex_Digit_Display hex_digit_display_2 (.value(LedData[27:24]));  // open: dp
  Hex_Digit_Display hex_digit_display_3 (.value(LedData[23:20]));  // open: dp
  Register #(.width(32), .trigger("rising"), .Select("low")) PC (
    .D(pc_update_logic_1_pc_next), .Q(IF_PC), .clk(CLK));  // open: en, clr
  Comparator #(.width(13), .mode("twosComplement")) comparator_1 (
    .a(CNT_num), .b(13'hc), .eq(comparator_1_eq), .lt(comparator_1_lt));  // open: gt
  Clock #(.highDuration(1), .lowDuration(1)) clock_1 (.out(clock_1_out));
  Hex_Digit_Display hex_digit_display_4 (.value(LedData[15:12]));  // open: dp
  Hex_Digit_Display hex_digit_display_5 (.value(LedData[19:16]));  // open: dp
  Adder #(.width(32)) adder_1 (.a(IF_PC), .b(32'h4), .out(adder_1_out));  // open: cin, cout
  nand nand_1 (nand_1_out, d_ff_1_q, comparator_1_eq);
  Counter #(.width(13), .max('h1fff), .ongoal("stay"), .trigger("rising"), .behavior("old")) counter_1 (
    .count(comparator_1_lt), .Q(CNT_num), .clk(clock_1_out));  // open: load, D, carry, clr, preset
  Hex_Digit_Display hex_digit_display_6 (.value(LedData[7:4]));  // open: dp
  Hex_Digit_Display hex_digit_display_7 (.value(LedData[11:8]));  // open: dp
  Clock #(.highDuration(1), .lowDuration(1)) clock_2 (.out(clock_2_out));
  ROM #(.addrWidth(10), .dataWidth(32), .Select("low")) rom_1 (.addr(IF_PC[11:2]), .data(IR));
  Hex_Digit_Display hex_digit_display_8 (.value(LedData[3:0]));  // open: dp
  // Mips_Probe mips_probe_1: pin names not known; wires that end beside it: IR
  assign CLK = nand_1_out ? clock_1_out : 1'bz;  // Controlled_Buffer controlled_buffer_1
  Pull_Resistor #(.pull(1)) pull_resistor_1 (.node(CLK));
  // Probe on \总周期数 
  IF_ID if_id_1 (
    .CLK(CLK), .Instr(IR), .Instr_Out({OP, if_id_1_instr_out, Func}), .PC_plus_four(adder_1_out),
    .PC_plus_four_Out(if_id_1_pc_plus_four_out), .PC(IF_PC), .PC_Out(ID_PC), .CLR(1'b0));  // open: Stall, PredictJump, PredictJump_Out
  // Probe on \总周期数 
  // Probe on \无条件分支数 
  // Probe on \条件分支成功数 
  // Probe on \插入气泡数 
  // Probe on \LoadUse次数 
  Counter #(.width(16), .max('hffff), .ongoal("wrap"), .trigger("rising"), .behavior("new")) counter_2 (
    .Q(\总周期数 ), .clk(CLK));  // open: load, D, count, carry, clr, preset, down
  // Probe on IF_PC[11:0]
  sc_hard_wired_controller sc_hard_wired_controller_1 (
    .Func(Func), .OP(OP), .ALU_OP(sc_hard_wired_controller_1_alu_op),
    .MemToReg(sc_hard_wired_controller_1_memtoreg[0]), .MemWrite(sc_hard_wired_controller_1_memtoreg[2]),
    .ALU_SRC(sc_hard_wired_controller_1_memtoreg[8]), .RegWrite(sc_hard_wired_controller_1_memtoreg[1]),
    .SysCALL(Syscall), .SignedExt(SignedExt), .RegDst(RegDst), .JR(sc_hard_wired_controller_1_jr[0]),
    .JMP(JMP), .Beq(sc_hard_wired_controller_1_jr[4]), .JAL(sc_hard_wired_controller_1_jr[2]),
    .Bne(sc_hard_wired_controller_1_jr[5]), .Vshamt(Vshamt), .BLEZ(sc_hard_wired_controller_1_jr[3]),
    .HalfW(sc_hard_wired_controller_1_memtoreg[3]));
  // Probe on EX_PC[11:0]
  // Probe on ID_PC[11:0]
  reg_choose_logic reg_choose_logic_1 (
    ._21_25(if_id_1_instr_out[27:23]), .Syscall(Syscall), .RegDst(RegDst), ._16_20(if_id_1_instr_out[22:18]),
    ._11_15(if_id_1_instr_out[17:13]), .JAL(JAL_WB), .PC_plus_four(if_id_1_pc_plus_four_out),
    .WriteBack_Data(multiplexer_4_out), ._6_10(if_id_1_instr_out[12:8]), .R1Adr(reg_choose_logic_1_r1adr),
    .R2Adr(reg_choose_logic_1_r2adr), .WAdr(reg_choose_logic_1_wadr), .RDin(RDin),
    .Shamt(reg_choose_logic_1_shamt));
  assign bit_extender_1_out = {{16{1'b0}}, {if_id_1_instr_out[17:8], Func}};  // Bit_Extender bit_extender_1
  assign bit_extender_2_out = {{16{if_id_1_instr_out[17]}}, {if_id_1_instr_out[17:8], Func}};  // Bit_Extender bit_extender_2
  // Probe on M_PC[11:0]
  Multiplexer #(.select(1), .width(32), .disabled("Z"), .enable("false")) multiplexer_1 (
    .in0(bit_extender_1_out), .in1(bit_extender_2_out), .out(multiplexer_1_out), .sel(SignedExt));
  // Probe on WB_PC[11:0]
  MIPS_Regifile mips_regifile_1 (
    .Din(RDin), .Clk(CLK), .R1(mips_regifile_1_r1), .R2(mips_regifile_1_r2), .WE(RegWrite),
    .WAdr(mem_wb_1_p14), .R1Adr(reg_choose_logic_1_r1adr), .R2Adr(reg_choose_logic_1_r2adr));
  Multiplexer #(.select(1), .width(5), .disabled("Z"), .enable("false")) multiplexer_2 (
    .in0(reg_choose_logic_1_shamt), .in1(R1[4:0]), .out(multiplexer_2_out), .sel(Vshamt));
  ID_EX id_ex_1 (
    .JR(sc_hard_wired_controller_1_jr[0]), .JMP(JMP), .JAL(sc_hard_wired_controller_1_jr[2]),
    .BLEZ(sc_hard_wired_controller_1_jr[3]), .BEQ(sc_hard_wired_controller_1_jr[4]),
    .BNE(sc_hard_wired_controller_1_jr[5]), .MemToReg(sc_hard_wired_controller_1_memtoreg[0]),
    .Shamt(multiplexer_2_out), .R1(mips_regifile_1_r1), .R2(mips_regifile_1_r2), .JR_Out(JR), .JAL_Out(JAL),
    .BLEZ_Out(Blez), .BEQ_Out(Beq), .BNE_Out(Bne), .MemToReg_Out(id_ex_1_memtoreg_out),
    .Shamt_Out(id_ex_1_shamt_out), .R1_Out(R1), .R2_Out(id_ex_1_r2_out), .CLK(CLK),
    .AluOp(sc_hard_wired_controller_1_alu_op), .AluOp_Out(id_ex_1_aluop_out), .ExtData(multiplexer_1_out),
    .WAdr(reg_choose_logic_1_wadr), .RegWrite(sc_hard_wired_controller_1_memtoreg[1]),
    .RegWrite_Out(id_ex_1_regwrite_out), .MemWrite_Out(id_ex_1_memwrite_out), .HalfW_Out(id_ex_1_halfw_out),
    .AluSrcB_Out(id_ex_1_alusrcb_out), .Syscall_Out(id_ex_1_syscall_out),
    .MemWrite(sc_hard_wired_controller_1_memtoreg[2]), .HalfW(sc_hard_wired_controller_1_memtoreg[3]),
    .AluSrcB(sc_hard_wired_controller_1_memtoreg[8]), .Syscall(Syscall), .ExtData_Out(id_ex_1_extdata_out),
    .WAdr_Out(id_ex_1_wadr_out), .PC(ID_PC), .PC_Out(EX_PC), .CLR(1'b0),
    .PC_plus_four(if_id_1_pc_plus_four_out), .PC_plus_four_Out(id_ex_1_pc_plus_four_out));  // open: JMP_Out, JAddr, JAddr_Out, R1_Forward, R1_Forward_Out, Instr, Instr_out, R2_Forward, R2_Forward_Out, PredictJump, PredictJump_Out, MTC, MFC, MTC_Out, MFC_Out, ERET, ERET_Out
  Multiplexer #(.select(1), .width(32), .disabled("Z"), .enable("false")) multiplexer_3 (
    .in0(id_ex_1_r2_out), .in1(id_ex_1_extdata_out), .out(multiplexer_3_out), .sel(id_ex_1_alusrcb_out));
  MIPS_ALU mips_alu_1 (
    .X(R1), .Y(multiplexer_3_out), .AluOP(id_ex_1_aluop_out), .Equal(Equal), .Result(mips_alu_1_result),
    .shamt(id_ex_1_shamt_out), .Less(Less));  // open: Result_2
  Adder #(.width(32)) adder_2 (
    .a(id_ex_1_pc_plus_four_out), .b({id_ex_1_extdata_out[29:0], 2'b00}), .out(adder_2_out));  // open: cin, cout
  EX_MEM ex_mem_1 (
    .MemToReg(id_ex_1_memtoreg_out), .RegWrite(id_ex_1_regwrite_out), .MemWrite(id_ex_1_memwrite_out),
    .HalfW(id_ex_1_halfw_out), .AluResult(mips_alu_1_result), .R2(id_ex_1_r2_out), .WAdr(id_ex_1_wadr_out),
    .CLK(CLK), .MemToReg_Out(ex_mem_1_memtoreg_out), .RegWrite_Out(ex_mem_1_regwrite_out),
    .MemWrite_Out(MemWrite), .HalfW_Out(ex_mem_1_halfw_out), .AluResult_Out(ex_mem_1_aluresult_out),
    .R2_Out(MDin), .WAdr_Out(ex_mem_1_wadr_out), .PC(EX_PC), .PC_Out(M_PC), .R1(R1),
    .R1_Out(ex_mem_1_r1_out), .Syscall(id_ex_1_syscall_out), .Syscall_Out(ex_mem_1_syscall_out), .CLR(1'b0),
    .JAL(JAL), .JAL_Out(ex_mem_1_jal_out));  // open: PC_plus_four, PC_plus_four_Out, Instr, Instr_out
  syscall_process syscall_process_1 (
    .Syscall(ex_mem_1_syscall_out), .CLK(CLK), .R2(MDin), .R1(ex_mem_1_r1_out), .Pause(Pause),
    .LedData(LedData));  // open: Get_KB_in, Screen_opt, Cycles, Get_Bitmap, CopyToRAM, FrameFlush
  MIPS_MEM mips_mem_1 (
    .AluResult(ex_mem_1_aluresult_out), .HalfW(ex_mem_1_halfw_out), .WriteData(MDin), .MemWrite(MemWrite),
    .CLK(CLK), .MemReadData(mips_mem_1_memreaddata));
  // MEM_WB mem_wb_1: pin names not known; wires that end beside it: ex_mem_1_jal_out, ex_mem_1_memtoreg_out, ex_mem_1_regwrite_out, ex_mem_1_aluresult_out, mips_mem_1_memreaddata, ex_mem_1_wadr_out, M_PC, CLK, JAL_WB, mem_wb_1_p10, RegWrite, mem_wb_1_p12, mem_wb_1_p13, mem_wb_1_p14, WB_PC
  Multiplexer #(.select(1), .width(32), .disabled("Z"), .enable("false")) multiplexer_4 (
    .in0(mem_wb_1_p12), .in1(mem_wb_1_p13), .out(multiplexer_4_out), .sel(mem_wb_1_p10));

  // Other names for the same wires on the sheet: MEM_PC[31:0] = M_PC

  // Notes on the sheet:
  //   中断源
  //   中断等待指示
  //   控制位
  //   戳工具置1进入计数暂停模式，ctrl+k时钟自动运行到对应节拍暂停
  //   ctrl+k关闭时钟连续运行，将控制位置零，进入单步调试模式调试
  //   用这个时钟源需要去掉电路中的其他时钟源
  //   数码管输出
  //   指令存储器
  //   contents of rom_1 (hex, n*v repeats v):
  //   20100000 20110000 20120000 20130000 36100000 36310001 36520002 36730003 ae100000 ae110004 ae120008
  //   ae13000c 2002000a 20110000 20120000 20130000 c
  //   可计数暂停的时钟源
  //   指令字
  //   JR
  //   JMP
  //   JAL
  //   BLEZ
  //   BEQ
  //   BNE
  //   MemToReg
  //   RegWrite
  //   MemWrite
  //   HalfW
  //   AluOp
  //   AluSrcB
  //   流水调试日志用
  //   为方便自动评测，需要输出流水线各段保存的PC值，注意是PC不是PC_plus_four，另外ID段寄存器写入信息，Mem段内存写入信息也要输出
endmodule

module bubble_pipeline (
  output RegWrite,
  output MemWrite,
  output [31:0] IF_PC,
  output [31:0] ID_PC,
  output [31:0] EX_PC,
  output [31:0] M_PC,
  output [31:0] WB_PC,
  output [31:0] RDin,
  output [31:0] MDin,
  output [31:0] LedData
);

  wire Beq, Blez, Bne, CLK, clock_1_out, clock_2_out, comparator_1_eq, comparator_1_lt, d_ff_1_q, Equal,
       ex_mem_1_halfw_out, ex_mem_1_jal_out, ex_mem_1_memtoreg_out, ex_mem_1_regwrite_out,
       ex_mem_1_syscall_out, Go, id_ex_1_p23, id_ex_1_p32, id_ex_1_p33, id_ex_1_p34, id_ex_1_p35,
       id_ex_1_p37, id_ex_1_p38, id_ex_1_p48, IR1, IR2, IR3, JAL, JAL_WB, JMP, JR, Less,
       mem_wb_1_memtoreg_out, MemEff, nand_1_out, not_1_out, or_1_out, or_2_out, Pause,
       pc_update_logic_1_branched, pipeline_conflict_deal_logic_1_stall_pc_id,
       pipeline_conflict_deal_logic_2_stall_pc_id, RegDst, RST, SignedExt, Syscall, Vshamt, W1, W2, W3;
  wire [3:0] id_ex_1_p36, sc_hard_wired_controller_1_alu_op;
  wire [4:0] ex_mem_1_wadr_out, id_ex_1_p42, id_ex_1_p43, mem_wb_1_wadr_out, multiplexer_3_out,
       reg_choose_logic_1_r1adr, reg_choose_logic_1_r2adr, reg_choose_logic_1_shamt, reg_choose_logic_1_wadr;
  wire [5:0] Func, sc_hard_wired_controller_1_jr;
  wire [8:0] sc_hard_wired_controller_1_memtoreg;
  wire [12:0] CNT_num;
  wire [15:0] \LoadUse次数 , \总周期数 , \插入气泡数 , \无条件分支数 , \条件分支成功数 ;
  wire [31:0] adder_1_out, adder_2_out, bit_extender_1_out, bit_extender_2_out, EX_IR,
       ex_mem_1_aluresult_out, ex_mem_1_pc_plus_four_out, ex_mem_1_r1_out, id_ex_1_p40, id_ex_1_p41,
       id_ex_1_p46, id_ex_1_p47, if_id_1_pc_plus_four_out, IF_IR, MEM_IR, mem_wb_1_aluresult_out,
       mem_wb_1_pc_plus_four_out, mem_wb_1_r2_out, mips_alu_1_result, mips_mem_1_memreaddata,
       mips_regifile_1_r1, mips_regifile_1_r2, multiplexer_1_out, multiplexer_4_out, multiplexer_5_out,
       pc_update_logic_1_pc_next, R1, WB_IR;
  wire [31:6] ID_IR;

  Button \u_总复位  (.out(RST));
  Button _1 (.out(IR1));
  Button _2 (.out(IR2));
  Button _3 (.out(IR3));
  // Probe on \总周期数 
  // Probe on \总周期数 
  Button \u_继续运行  (.out(Go));
  LED #(.active("true")) led_1 (.in(W1));
  LED #(.active("true")) led_2 (.in(W2));
  LED #(.active("true")) led_3 (.in(W3));
  PC_update_logic pc_update_logic_1 (
    .Equal(Equal), .Beq(Beq), .Bne(Bne), .JAL(JAL), .JMP(JMP), .JR(JR), .BAddr(adder_2_out),
    .PC_plus_four(adder_1_out), .JAddr(id_ex_1_p47), .JRAddr(R1), .PC_Next(pc_update_logic_1_pc_next),
    .Blez(Blez), .Less(Less), .Branched(pc_update_logic_1_branched));  // open: BranchSig
  Hex_Digit_Display hex_digit_display_1 (.value(LedData[31:28]));  // open: dp
  // Probe on IF_PC[19:0]
  // Mips_Probe mips_probe_1: pin names not known; wires that end beside it: IF_IR
  D_Flip_Flop #(.trigger("high"), .Pre_Clr_Positions("LEGACY"), .NegatePresetClear("false"), .enable("true"), .NewFFLayout("false")) d_ff_1 (
    .Q(d_ff_1_q), .preset(Pause), .reset(Go));  // open: clk, D, Qn, en
  // Probe on 13'h624
  Hex_Digit_Display hex_digit_display_2 (.value(LedData[27:24]));  // open: dp
  Hex_Digit_Display hex_digit_display_3 (.value(LedData[23:20]));  // open: dp
  // Probe on ID_PC[19:0]
  // Mips_Probe mips_probe_2: pin names not known; wires that end beside it: {ID_IR, Func}
  Register #(.width(32), .trigger("rising"), .Select("low")) PC (
    .D(pc_update_logic_1_pc_next), .en(not_1_out), .Q(IF_PC), .clk(CLK));  // open: clr
  Comparator #(.width(13), .mode("twosComplement")) comparator_1 (
    .a(CNT_num), .b(13'h624), .eq(comparator_1_eq), .lt(comparator_1_lt));  // open: gt
  Clock #(.highDuration(1), .lowDuration(1)) clock_1 (.out(clock_1_out));
  Hex_Digit_Display hex_digit_display_4 (.value(LedData[15:12]));  // open: dp
  Hex_Digit_Display hex_digit_display_5 (.value(LedData[19:16]));  // open: dp
  Adder #(.width(32)) adder_1 (.a(IF_PC), .b(32'h4), .out(adder_1_out));  // open: cin, cout
  nand nand_1 (nand_1_out, d_ff_1_q, comparator_1_eq);
  Counter #(.width(13), .max('h1fff), .ongoal("stay"), .trigger("rising"), .behavior("old")) counter_1 (
    .count(comparator_1_lt), .Q(CNT_num), .clk(clock_1_out));  // open: load, D, carry, clr, preset
  Hex_Digit_Display hex_digit_display_6 (.value(LedData[11:8]));  // open: dp
  Hex_Digit_Display hex_digit_display_7 (.value(LedData[7:4]));  // open: dp
  Clock #(.highDuration(1), .lowDuration(1)) clock_2 (.out(clock_2_out));
  // Probe on EX_PC[19:0]
  // Mips_Probe mips_probe_3: pin names not known; wires that end beside it: clock_2_out, EX_IR, CLK
  ROM #(.addrWidth(10), .dataWidth(32), .Select("low")) rom_1 (.addr(IF_PC[11:2]), .data(IF_IR));
  Hex_Digit_Display hex_digit_display_8 (.value(LedData[3:0]));  // open: dp
  // Mips_Probe mips_probe_4: pin names not known; wires that end beside it: IF_IR
  assign CLK = nand_1_out ? clock_1_out : 1'bz;  // Controlled_Buffer controlled_buffer_1
  Pull_Resistor #(.pull(1)) pull_resistor_1 (.node(CLK));
  // Probe on \总周期数 
  // Probe on M_PC[19:0]
  // Mips_Probe mips_probe_5: pin names not known; wires that end beside it: MEM_IR
  IF_ID if_id_1 (
    .CLK(CLK), .Instr(IF_IR), .Instr_Out({ID_IR, Func}), .PC_plus_four(adder_1_out),
    .PC_plus_four_Out(if_id_1_pc_plus_four_out), .PC(IF_PC), .PC_Out(ID_PC),
    .CLR(pc_update_logic_1_branched), .Stall(not_1_out));  // open: PredictJump, PredictJump_Out
  // Probe on \总周期数 
  // Probe on \无条件分支数 
  // Probe on \条件分支成功数 
  // Probe on \插入气泡数 
  // Probe on \LoadUse次数 
  Counter #(.width(16), .max('hffff), .ongoal("wrap"), .trigger("rising"), .behavior("new")) counter_2 (
    .Q(\总周期数 ), .clk(CLK));  // open: load, D, count, carry, clr, preset, down
  // Probe on IF_PC[11:0]
  // Probe on WB_PC[19:0]
  // Mips_Probe mips_probe_6: pin names not known; wires that end beside it: WB_IR
  sc_hard_wired_controller sc_hard_wired_controller_1 (
    .Func(Func), .OP(ID_IR[31:26]), .ALU_OP(sc_hard_wired_controller_1_alu_op),
    .MemToReg(sc_hard_wired_controller_1_memtoreg[0]), .MemWrite(sc_hard_wired_controller_1_memtoreg[2]),
    .ALU_SRC(sc_hard_wired_controller_1_memtoreg[8]), .RegWrite(sc_hard_wired_controller_1_memtoreg[1]),
    .SysCALL(Syscall), .SignedExt(SignedExt), .RegDst(RegDst), .JR(sc_hard_wired_controller_1_jr[0]),
    .JMP(sc_hard_wired_controller_1_jr[1]), .Beq(sc_hard_wired_controller_1_jr[4]),
    .JAL(sc_hard_wired_controller_1_jr[2]), .Bne(sc_hard_wired_controller_1_jr[5]), .Vshamt(Vshamt),
    .BLEZ(sc_hard_wired_controller_1_jr[3]), .HalfW(sc_hard_wired_controller_1_memtoreg[3]));
  // Probe on EX_PC[11:0]
  // Probe on ID_PC[11:0]
  reg_choose_logic reg_choose_logic_1 (
    ._21_25(ID_IR[25:21]), .Syscall(Syscall), .RegDst(RegDst), ._16_20(ID_IR[20:16]), ._11_15(ID_IR[15:11]),
    .JAL(sc_hard_wired_controller_1_jr[2]), ._6_10(ID_IR[10:6]), .R1Adr(reg_choose_logic_1_r1adr),
    .R2Adr(reg_choose_logic_1_r2adr), .WAdr(reg_choose_logic_1_wadr), .Shamt(reg_choose_logic_1_shamt));  // open: PC_plus_four, WriteBack_Data, RDin
  assign bit_extender_1_out = {{16{1'b0}}, {ID_IR[15:6], Func}};  // Bit_Extender bit_extender_1
  assign bit_extender_2_out = {{16{ID_IR[15]}}, {ID_IR[15:6], Func}};  // Bit_Extender bit_extender_2
  // Probe on M_PC[11:0]
  Multiplexer #(.select(1), .width(32), .disabled("Z"), .enable("false")) multiplexer_1 (
    .in0(bit_extender_1_out), .in1(bit_extender_2_out), .out(multiplexer_1_out), .sel(SignedExt));
  Multiplexer #(.select(1), .width(32), .disabled("Z"), .enable("false")) multiplexer_2 (
    .in0(multiplexer_5_out), .in1(mem_wb_1_pc_plus_four_out), .out(RDin), .sel(JAL_WB));
  // Probe on WB_PC[11:0]
  MIPS_Regifile mips_regifile_1 (
    .Din(RDin), .Clk(CLK), .R1(mips_regifile_1_r1), .R2(mips_regifile_1_r2), .WE(RegWrite),
    .WAdr(mem_wb_1_wadr_out), .R1Adr(reg_choose_logic_1_r1adr), .R2Adr(reg_choose_logic_1_r2adr));
  Multiplexer #(.select(1), .width(5), .disabled("Z"), .enable("false")) multiplexer_3 (
    .in0(reg_choose_logic_1_shamt), .in1(mips_regifile_1_r1[4:0]), .out(multiplexer_3_out), .sel(Vshamt));
  not not_1 (not_1_out, or_2_out);
  or or_1 (or_1_out, pc_update_logic_1_branched, or_2_out);
  // ID_EX id_ex_1: pin names not known; wires that end beside it: sc_hard_wired_controller_1_jr[0], sc_hard_wired_controller_1_jr[1], sc_hard_wired_controller_1_jr[2], sc_hard_wired_controller_1_jr[3], sc_hard_wired_controller_1_jr[4], sc_hard_wired_controller_1_jr[5], sc_hard_wired_controller_1_memtoreg[0], sc_hard_wired_controller_1_memtoreg[1], sc_hard_wired_controller_1_memtoreg[2], sc_hard_wired_controller_1_memtoreg[3], sc_hard_wired_controller_1_alu_op, sc_hard_wired_controller_1_memtoreg[8], Syscall, mips_regifile_1_r1, mips_regifile_1_r2, multiplexer_1_out, reg_choose_logic_1_wadr, multiplexer_3_out, ID_PC, {ID_IR, Func}, if_id_1_pc_plus_four_out, {ID_PC[31:28], ID_IR[25:6], Func, 2'b00}, id_ex_1_p23, or_1_out, CLK, JR, JMP, JAL, Blez, Beq, Bne, id_ex_1_p32, id_ex_1_p33, id_ex_1_p34, id_ex_1_p35, id_ex_1_p36, id_ex_1_p37, id_ex_1_p38, R1, id_ex_1_p40, id_ex_1_p41, id_ex_1_p42, id_ex_1_p43, EX_PC, EX_IR, id_ex_1_p46, id_ex_1_p47, id_ex_1_p48
  or or_2 (or_2_out, pipeline_conflict_deal_logic_2_stall_pc_id, pipeline_conflict_deal_logic_1_stall_pc_id);
  pipeline_conflict_deal_logic pipeline_conflict_deal_logic_1 (
    .R1Adr(reg_choose_logic_1_r1adr), .WAdr(id_ex_1_p42), .R2Adr(reg_choose_logic_1_r2adr),
    .CLR(pc_update_logic_1_branched), .RegWrite(id_ex_1_p33),
    .Stall_PC_ID(pipeline_conflict_deal_logic_1_stall_pc_id), .AluSrc(sc_hard_wired_controller_1_memtoreg[8]));  // open: R1_CF, R2_CF
  Multiplexer #(.select(1), .width(32), .disabled("Z"), .enable("false")) multiplexer_4 (
    .in0(id_ex_1_p40), .in1(id_ex_1_p41), .out(multiplexer_4_out), .sel(id_ex_1_p37));
  pipeline_conflict_deal_logic pipeline_conflict_deal_logic_2 (
    .R1Adr(reg_choose_logic_1_r1adr), .WAdr(ex_mem_1_wadr_out), .R2Adr(reg_choose_logic_1_r2adr),
    .CLR(pc_update_logic_1_branched), .RegWrite(ex_mem_1_regwrite_out),
    .Stall_PC_ID(pipeline_conflict_deal_logic_2_stall_pc_id), .AluSrc(sc_hard_wired_controller_1_memtoreg[8]));  // open: R1_CF, R2_CF
  MIPS_ALU mips_alu_1 (
    .X(R1), .Y(multiplexer_4_out), .AluOP(id_ex_1_p36), .Equal(Equal), .Result(mips_alu_1_result),
    .shamt(id_ex_1_p43), .Less(Less));  // open: Result_2
  Adder #(.width(32)) adder_2 (.a(id_ex_1_p46), .b({id_ex_1_p41[29:0], 2'b00}), .out(adder_2_out));  // open: cin, cout
  EX_MEM ex_mem_1 (
    .MemToReg(id_ex_1_p32), .RegWrite(id_ex_1_p33), .MemWrite(id_ex_1_p34), .HalfW(id_ex_1_p35),
    .AluResult(mips_alu_1_result), .R2(id_ex_1_p40), .WAdr(id_ex_1_p42), .CLK(CLK),
    .MemToReg_Out(ex_mem_1_memtoreg_out), .RegWrite_Out(ex_mem_1_regwrite_out), .MemWrite_Out(MemWrite),
    .HalfW_Out(ex_mem_1_halfw_out), .AluResult_Out(ex_mem_1_aluresult_out), .R2_Out(MDin),
    .WAdr_Out(ex_mem_1_wadr_out), .PC(EX_PC), .PC_Out(M_PC), .R1(R1), .R1_Out(ex_mem_1_r1_out),
    .Syscall(id_ex_1_p38), .Syscall_Out(ex_mem_1_syscall_out), .CLR(1'b0), .JAL(JAL),
    .JAL_Out(ex_mem_1_jal_out), .PC_plus_four(id_ex_1_p46), .PC_plus_four_Out(ex_mem_1_pc_plus_four_out),
    .Instr(EX_IR), .Instr_out(MEM_IR));
  syscall_process syscall_process_1 (
    .Syscall(ex_mem_1_syscall_out), .CLK(CLK), .R2(MDin), .R1(ex_mem_1_r1_out), .Pause(Pause),
    .LedData(LedData));  // open: Get_KB_in, Screen_opt, Cycles, Get_Bitmap, CopyToRAM, FrameFlush
  MIPS_MEM mips_mem_1 (
    .AluResult(ex_mem_1_aluresult_out), .HalfW(ex_mem_1_halfw_out), .WriteData(MDin), .MemWrite(MemWrite),
    .CLK(CLK), .MemReadData(mips_mem_1_memreaddata));
  MEM_WB mem_wb_1 (
    .MemToReg(ex_mem_1_memtoreg_out), .RegWrite(ex_mem_1_regwrite_out), .AluResult(ex_mem_1_aluresult_out),
    .R2(mips_mem_1_memreaddata), .WAdr(ex_mem_1_wadr_out), .CLK(CLK), .MemToReg_Out(mem_wb_1_memtoreg_out),
    .RegWrite_Out(RegWrite), .AluResult_Out(mem_wb_1_aluresult_out), .R2_Out(mem_wb_1_r2_out),
    .WAdr_Out(mem_wb_1_wadr_out), .PC(M_PC), .PC_Out(WB_PC), .JAL(ex_mem_1_jal_out), .JAL_Out(JAL_WB),
    .PC_plus_four(ex_mem_1_pc_plus_four_out), .PC_plus_four_Out(mem_wb_1_pc_plus_four_out), .Instr(MEM_IR),
    .Instr_out(WB_IR), .KB_HIT(MemEff));  // open: KB_HIT_2, R2_2, Screen_in, Screen_ins_opt, Screen_ins_opt_2, Cycles, Get_Cycles, Get_Bitmap, Get_Bitmap_2, CopyToRAM, CopyToRAM_2, FrameFlush, FrameFlush_2
  Multiplexer #(.select(1), .width(32), .disabled("Z"), .enable("false")) multiplexer_5 (
    .in0(mem_wb_1_aluresult_out), .in1(mem_wb_1_r2_out), .out(multiplexer_5_out), .sel(mem_wb_1_memtoreg_out));

  // Other names for the same wires on the sheet: ID_IR[5:0] = Func; OP[5:0] = ID_IR[31:26]; IR[31:0] = IF_IR;
  //   MEM_PC[31:0] = M_PC

  // Notes on the sheet:
  //   中断源
  //   时空图监测，可删除
  //   中断等待指示
  //   控制位
  //   戳工具置1进入计数暂停模式，ctrl+k时钟自动运行到对应节拍暂停
  //   ctrl+k关闭时钟连续运行，将控制位置零，进入单步调试模式调试
  //   用这个时钟源需要去掉电路中的其他时钟源
  //   数码管输出
  //   指令存储器
  //   contents of rom_1 (hex, n*v repeats v):
  //   20110001 8000c05 20110001 20120002 20130003 8000c09 20110001 20120002 20130003 8000c0d 20110001
  //   20120002 20130003 8000c11 20110001 20120002 20130003 c000cb8 20100001 20110001 118fc0 112020
  //   20020022 c 118882 12200001 8000c15 112020 20020022 c 20110001 118880 112020 20020022 c 12200001
  //   8000c1f 20110001 118fc0 112020 20020022 c 1188c3 112020 20020022 c 118903 112020 20020022 c 118903
  //   112020 20020022 c 118903 112020 20020022 c 118903 112020 20020022 c 118903 112020 20020022 c 118903
  //   112020 20020022 c 118903 112020 20020022 c 20100001 109fc0 139fc3 8021 2012000c 24160003 26100001
  //   3210000f 20080008 20090001 139900 2709825 132020 20020022 c 1094022 1500fff9 22100001 2018000f
  //   2188024 108700 20080008 20090001 139902 2709825 132021 20020022 c 1094022 1500fff9 108702 2c9b022
  //   12c00001 8000c50 4020 1084027 84400 3508ffff 82021 20020022 c 2010ffff 20110000 ae300000 22100001
  //   22310004 ae300000 22100001 22310004 ae300000 22100001 22310004 ae300000 22100001 22310004 ae300000
  //   22100001 22310004 ae300000 22100001 22310004 ae300000 22100001 22310004 ae300000 22100001 22310004
  //   ae300000 22100001 22310004 ae300000 22100001 22310004 ae300000 22100001 22310004 ae300000 22100001
  //   22310004 ae300000 22100001 22310004 ae300000 22100001 22310004 ae300000 22100001 22310004 ae300000
  //   22100001 22310004 22100001 8020 2011003c 8e130000 8e340000 274402a 11000002 ae330000 ae140000
  //   2231fffc 1611fff8 102020 20020022 c 22100004 2011003c 1611fff2 20020032 c 20100000 22100001 102020
  //   20020022 c 22100002 102020 20020022 c 22100003 102020 20020022 c 22100004 102020 20020022 c 22100005
  //   102020 20020022 c 22100006 102020 20020022 c 22100007 102020 20020022 c 22100008 102020 20020022
  //   20020022 c 3e00008
  //   可计数暂停的时钟源
  //   指令字
  //   IF/ID
  //   JR
  //   JMP
  //   JAL
  //   BLEZ
  //   BEQ
  //   BNE
  //   MemToReg
  //   RegWrite
  //   MemWrite
  //   HalfW
  //   AluOp
  //   AluSrcB
  //   流水调试日志用
  //   为方便自动评测，需要输出流水线各段保存的PC值，注意是PC不是PC_plus_four，另外ID段寄存器写入信息，Mem段内存写入信息也要输出
endmodule

module redirection_pipeline (
  output RegWrite,
  output MemWrite,
  output [31:0] IF_PC,
  output [31:0] ID_PC,
  output [31:0] EX_PC,
  output [31:0] M_PC,
  output [31:0] WB_PC,
  output [31:0] RDin,
  output [31:0] MDin,
  output [31:0] LedData
);

  wire Beq, Blez, Bne, CLK, clock_2_out, comparator_1_eq, comparator_1_lt, d_ff_1_q,
       data_bypass_controller_1_stall, Equal, ex_mem_1_halfw_out, ex_mem_1_jal_out, ex_mem_1_memtoreg_out,
       ex_mem_1_regwrite_out, ex_mem_1_syscall_out, Go, id_ex_1_p25, id_ex_1_p34, id_ex_1_p35, id_ex_1_p36,
       id_ex_1_p37, id_ex_1_p39, id_ex_1_p40, id_ex_1_p52, IRA, IRB, IRC, JAL, JAL_WB, JMP, JR, Less,
       mem_wb_1_memtoreg_out, MemEff, nand_1_out, not_1_out, or_1_out, Pause, pc_update_logic_1_branched,
       RegDst, SignedExt, Syscall, Vshamt, W1, W2, W3;
  wire [1:0] id_ex_1_p15, id_ex_1_p16, id_ex_1_p42, id_ex_1_p43;
  wire [3:0] id_ex_1_p38, sc_hard_wired_controller_1_alu_op;
  wire [4:0] ex_mem_1_wadr_out, id_ex_1_p46, id_ex_1_p47, mem_wb_1_wadr_out, multiplexer_3_out,
       reg_choose_logic_1_r1adr, reg_choose_logic_1_r2adr, reg_choose_logic_1_shamt, reg_choose_logic_1_wadr;
  wire [5:0] Func, sc_hard_wired_controller_1_jr;
  wire [8:0] sc_hard_wired_controller_1_memtoreg;
  wire [12:0] CNT;
  wire [15:0] \LoadUse次数 , TotalCycles, \总周期数 , \插入气泡数 , \无条件分支数 , \条件分支成功数 ;
  wire [31:0] adder_1_out, adder_2_out, bit_extender_1_out, bit_extender_2_out, EX_IR,
       ex_mem_1_aluresult_out, ex_mem_1_pc_plus_four_out, ex_mem_1_r1_out, id_ex_1_p41, id_ex_1_p44,
       id_ex_1_p45, id_ex_1_p50, id_ex_1_p51, if_id_1_pc_plus_four_out, IF_IR, MEM_IR,
       mem_wb_1_aluresult_out, mem_wb_1_pc_plus_four_out, mem_wb_1_r2_out, mips_alu_1_result,
       mips_mem_1_memreaddata, mips_regifile_1_r1, mips_regifile_1_r2, multiplexer_1_out, multiplexer_5_out,
       multiplexer_6_out, multiplexer_7_out, pc_update_logic_1_pc_next, R1, WB_IR;
  wire [31:6] ID_IR;

  Clock #(.highDuration(1), .lowDuration(1)) clock_1 ();  // open: out
  Button _1 (.out(IRA));
  Button _2 (.out(IRB));
  Button _3 (.out(IRC));
  Button button_1 (.out(Go));
  LED #(.active("true")) IRQ_1 (.in(W1));
  LED #(.active("true")) IRQ_2 (.in(W2));
  LED #(.active("true")) IRQ_3 (.in(W3));
  PC_update_logic pc_update_logic_1 (
    .Equal(Equal), .Beq(Beq), .Bne(Bne), .JAL(JAL), .JMP(JMP), .JR(JR), .BAddr(adder_2_out),
    .PC_plus_four(adder_1_out), .JAddr(id_ex_1_p51), .JRAddr(R1), .PC_Next(pc_update_logic_1_pc_next),
    .Blez(Blez), .Less(Less), .Branched(pc_update_logic_1_branched));  // open: BranchSig
  Hex_Digit_Display hex_digit_display_1 (.value(LedData[31:28]));  // open: dp
  D_Flip_Flop #(.trigger("high"), .Pre_Clr_Positions("LEGACY"), .NegatePresetClear("false"), .enable("true"), .NewFFLayout("false")) d_ff_1 (
    .Q(d_ff_1_q), .preset(Pause), .reset(Go));  // open: clk, D, Qn, en
  // Probe on 13'hc
  Hex_Digit_Display hex_digit_display_2 (.value(LedData[27:24]));  // open: dp
  Hex_Digit_Display hex_digit_display_3 (.value(LedData[23:20]));  // open: dp
  Register #(.width(32), .trigger("rising"), .Select("low")) PC (
    .D(pc_update_logic_1_pc_next), .en(not_1_out), .Q(IF_PC), .clk(CLK));  // open: clr
  Comparator #(.width(13), .mode("twosComplement")) comparator_1 (
    .a(CNT), .b(13'hc), .eq(comparator_1_eq), .lt(comparator_1_lt));  // open: gt
  Clock #(.highDuration(1), .lowDuration(1)) clock_2 (.out(clock_2_out));
  Hex_Digit_Display hex_digit_display_4 (.value(LedData[19:16]));  // open: dp
  Hex_Digit_Display hex_digit_display_5 (.value(LedData[15:12]));  // open: dp
  Adder #(.width(32)) adder_1 (.a(IF_PC), .b(32'h4), .out(adder_1_out));  // open: cin, cout
  nand nand_1 (nand_1_out, d_ff_1_q, comparator_1_eq);
  Counter #(.width(13), .max('h1fff), .ongoal("stay"), .trigger("rising"), .behavior("old")) counter_1 (
    .count(comparator_1_lt), .Q(CNT), .clk(clock_2_out));  // open: load, D, carry, clr, preset
  Hex_Digit_Display hex_digit_display_6 (.value(LedData[11:8]));  // open: dp
  Hex_Digit_Display hex_digit_display_7 (.value(LedData[7:4]));  // open: dp
  ROM #(.addrWidth(10), .dataWidth(32), .Select("low")) IR_ROM (.addr(IF_PC[11:2]), .data(IF_IR));
  assign CLK = nand_1_out ? clock_2_out : 1'bz;  // Controlled_Buffer controlled_buffer_1
  Hex_Digit_Display hex_digit_display_8 (.value(LedData[3:0]));  // open: dp
  // Probe on TotalCycles
  // Probe on \总周期数 
  not not_1 (not_1_out, data_bypass_controller_1_stall);
  IF_ID if_id_1 (
    .CLK(CLK), .Instr(IF_IR), .Instr_Out({ID_IR, Func}), .PC_plus_four(adder_1_out),
    .PC_plus_four_Out(if_id_1_pc_plus_four_out), .PC(IF_PC), .PC_Out(ID_PC),
    .CLR(pc_update_logic_1_branched), .Stall(not_1_out));  // open: PredictJump, PredictJump_Out
  // Probe on \总周期数 
  // Probe on \无条件分支数 
  // Probe on \条件分支成功数 
  // Probe on \插入气泡数 
  // Probe on \LoadUse次数 
  Counter #(.width(16), .max('hffff), .ongoal("wrap"), .trigger("rising"), .behavior("new")) counter_2 (
    .Q(TotalCycles), .clk(CLK));  // open: load, D, count, carry, clr, preset, down
  // Probe on IF_PC[11:0]
  sc_hard_wired_controller sc_hard_wired_controller_1 (
    .Func(Func), .OP(ID_IR[31:26]), .ALU_OP(sc_hard_wired_controller_1_alu_op),
    .MemToReg(sc_hard_wired_controller_1_memtoreg[0]), .MemWrite(sc_hard_wired_controller_1_memtoreg[2]),
    .ALU_SRC(sc_hard_wired_controller_1_memtoreg[8]), .RegWrite(sc_hard_wired_controller_1_memtoreg[1]),
    .SysCALL(Syscall), .SignedExt(SignedExt), .RegDst(RegDst), .JR(sc_hard_wired_controller_1_jr[0]),
    .JMP(sc_hard_wired_controller_1_jr[1]), .Beq(sc_hard_wired_controller_1_jr[4]),
    .JAL(sc_hard_wired_controller_1_jr[2]), .Bne(sc_hard_wired_controller_1_jr[5]), .Vshamt(Vshamt),
    .BLEZ(sc_hard_wired_controller_1_jr[3]), .HalfW(sc_hard_wired_controller_1_memtoreg[3]));
  // Probe on ID_PC[11:0]
  // Probe on EX_PC[11:0]
  reg_choose_logic reg_choose_logic_1 (
    ._21_25(ID_IR[25:21]), .Syscall(Syscall), .RegDst(RegDst), ._16_20(ID_IR[20:16]), ._11_15(ID_IR[15:11]),
    .JAL(sc_hard_wired_controller_1_jr[2]), ._6_10(ID_IR[10:6]), .R1Adr(reg_choose_logic_1_r1adr),
    .R2Adr(reg_choose_logic_1_r2adr), .WAdr(reg_choose_logic_1_wadr), .Shamt(reg_choose_logic_1_shamt));  // open: PC_plus_four, WriteBack_Data, RDin
  assign bit_extender_1_out = {{16{1'b0}}, {ID_IR[15:6], Func}};  // Bit_Extender bit_extender_1
  assign bit_extender_2_out = {{16{ID_IR[15]}}, {ID_IR[15:6], Func}};  // Bit_Extender bit_extender_2
  // Probe on M_PC[11:0]
  Multiplexer #(.select(1), .width(32), .disabled(0), .enable("false")) multiplexer_1 (
    .in0(bit_extender_1_out), .in1(bit_extender_2_out), .out(multiplexer_1_out), .sel(SignedExt));
  Multiplexer #(.select(1), .width(32), .disabled(0), .enable("false")) multiplexer_2 (
    .in0(multiplexer_7_out), .in1(mem_wb_1_pc_plus_four_out), .out(RDin), .sel(JAL_WB));
  // Probe on WB_PC[11:0]
  MIPS_Regifile mips_regifile_1 (
    .Din(RDin), .Clk(CLK), .R1(mips_regifile_1_r1), .R2(mips_regifile_1_r2), .WE(RegWrite),
    .WAdr(mem_wb_1_wadr_out), .R1Adr(reg_choose_logic_1_r1adr), .R2Adr(reg_choose_logic_1_r2adr));
  Multiplexer #(.select(1), .width(5), .disabled(0), .enable("false")) multiplexer_3 (
    .in0(reg_choose_logic_1_shamt), .in1(mips_regifile_1_r1[4:0]), .out(multiplexer_3_out), .sel(Vshamt));
  or or_1 (or_1_out, pc_update_logic_1_branched, data_bypass_controller_1_stall);
  // ID_EX id_ex_1: pin names not known; wires that end beside it: sc_hard_wired_controller_1_jr[0], sc_hard_wired_controller_1_jr[1], sc_hard_wired_controller_1_jr[2], sc_hard_wired_controller_1_jr[3], sc_hard_wired_controller_1_jr[4], sc_hard_wired_controller_1_jr[5], sc_hard_wired_controller_1_memtoreg[0], sc_hard_wired_controller_1_memtoreg[1], sc_hard_wired_controller_1_memtoreg[2], sc_hard_wired_controller_1_memtoreg[3], sc_hard_wired_controller_1_alu_op, sc_hard_wired_controller_1_memtoreg[8], Syscall, mips_regifile_1_r1, id_ex_1_p15, id_ex_1_p16, mips_regifile_1_r2, multiplexer_1_out, reg_choose_logic_1_wadr, multiplexer_3_out, ID_PC, {ID_IR, Func}, if_id_1_pc_plus_four_out, {ID_PC[31:28], ID_IR[25:6], Func, 2'b00}, id_ex_1_p25, or_1_out, CLK, JR, JMP, JAL, Blez, Beq, Bne, id_ex_1_p34, id_ex_1_p35, id_ex_1_p36, id_ex_1_p37, id_ex_1_p38, id_ex_1_p39, id_ex_1_p40, id_ex_1_p41, id_ex_1_p42, id_ex_1_p43, id_ex_1_p44, id_ex_1_p45, id_ex_1_p46, id_ex_1_p47, EX_PC, EX_IR, id_ex_1_p50, id_ex_1_p51, id_ex_1_p52
  Multiplexer #(.select(2), .width(32), .disabled(0), .enable("false")) multiplexer_4 (
    .in0(id_ex_1_p41), .in1(mem_wb_1_aluresult_out), .in2(mem_wb_1_r2_out), .in3(ex_mem_1_aluresult_out),
    .out(R1), .sel(id_ex_1_p42));
  Multiplexer #(.select(2), .width(32), .disabled(0), .enable("false")) multiplexer_5 (
    .in0(id_ex_1_p44), .in1(mem_wb_1_aluresult_out), .in2(mem_wb_1_r2_out), .in3(ex_mem_1_aluresult_out),
    .out(multiplexer_5_out), .sel(id_ex_1_p43));
  Adder #(.width(32)) adder_2 (.a(id_ex_1_p50), .b({id_ex_1_p45[29:0], 2'b00}), .out(adder_2_out));  // open: cin, cout
  data_bypass_controller data_bypass_controller_1 (
    .ID_AluSrc(sc_hard_wired_controller_1_memtoreg[8]), .BranchCLR(pc_update_logic_1_branched),
    .ID_R1Adr(reg_choose_logic_1_r1adr), .ID_R2Adr(reg_choose_logic_1_r2adr), .EX_WAdr(id_ex_1_p46),
    .MEM_WAdr(ex_mem_1_wadr_out), .EX_RegWrite(id_ex_1_p35), .MEM_RegWrite(ex_mem_1_regwrite_out),
    .MEM_MemToReg(ex_mem_1_memtoreg_out), .R1_Forward(id_ex_1_p15), .R2_Forward(id_ex_1_p16),
    .ID_IR({ID_IR, Func}), .EX_IR(EX_IR), .Stall(data_bypass_controller_1_stall));
  Multiplexer #(.select(1), .width(32), .disabled(0), .enable("false")) multiplexer_6 (
    .in0(multiplexer_5_out), .in1(id_ex_1_p45), .out(multiplexer_6_out), .sel(id_ex_1_p39));
  MIPS_ALU mips_alu_1 (
    .X(R1), .Y(multiplexer_6_out), .AluOP(id_ex_1_p38), .Equal(Equal), .Result(mips_alu_1_result),
    .shamt(id_ex_1_p47), .Less(Less));  // open: Result_2
  EX_MEM ex_mem_1 (
    .MemToReg(id_ex_1_p34), .RegWrite(id_ex_1_p35), .MemWrite(id_ex_1_p36), .HalfW(id_ex_1_p37),
    .AluResult(mips_alu_1_result), .R2(multiplexer_5_out), .WAdr(id_ex_1_p46), .CLK(CLK),
    .MemToReg_Out(ex_mem_1_memtoreg_out), .RegWrite_Out(ex_mem_1_regwrite_out), .MemWrite_Out(MemWrite),
    .HalfW_Out(ex_mem_1_halfw_out), .AluResult_Out(ex_mem_1_aluresult_out), .R2_Out(MDin),
    .WAdr_Out(ex_mem_1_wadr_out), .PC(EX_PC), .PC_Out(M_PC), .R1(R1), .R1_Out(ex_mem_1_r1_out),
    .Syscall(id_ex_1_p40), .Syscall_Out(ex_mem_1_syscall_out), .CLR(1'b0), .JAL(JAL),
    .JAL_Out(ex_mem_1_jal_out), .PC_plus_four(id_ex_1_p50), .PC_plus_four_Out(ex_mem_1_pc_plus_four_out),
    .Instr(EX_IR), .Instr_out(MEM_IR));
  syscall_process syscall_process_1 (
    .Syscall(ex_mem_1_syscall_out), .CLK(CLK), .R2(MDin), .R1(ex_mem_1_r1_out), .Pause(Pause),
    .LedData(LedData));  // open: Get_KB_in, Screen_opt, Cycles, Get_Bitmap, CopyToRAM, FrameFlush
  MIPS_MEM mips_mem_1 (
    .AluResult(ex_mem_1_aluresult_out), .HalfW(ex_mem_1_halfw_out), .WriteData(MDin), .MemWrite(MemWrite),
    .CLK(CLK), .MemReadData(mips_mem_1_memreaddata));
  Multiplexer #(.select(1), .width(32), .disabled(0), .enable("false")) multiplexer_7 (
    .in0(mem_wb_1_aluresult_out), .in1(mem_wb_1_r2_out), .out(multiplexer_7_out), .sel(mem_wb_1_memtoreg_out));
  MEM_WB mem_wb_1 (
    .MemToReg(ex_mem_1_memtoreg_out), .RegWrite(ex_mem_1_regwrite_out), .AluResult(ex_mem_1_aluresult_out),
    .R2(mips_mem_1_memreaddata), .WAdr(ex_mem_1_wadr_out), .CLK(CLK), .MemToReg_Out(mem_wb_1_memtoreg_out),
    .RegWrite_Out(RegWrite), .AluResult_Out(mem_wb_1_aluresult_out), .R2_Out(mem_wb_1_r2_out),
    .WAdr_Out(mem_wb_1_wadr_out), .PC(M_PC), .PC_Out(WB_PC), .JAL(ex_mem_1_jal_out), .JAL_Out(JAL_WB),
    .PC_plus_four(ex_mem_1_pc_plus_four_out), .PC_plus_four_Out(mem_wb_1_pc_plus_four_out), .Instr(MEM_IR),
    .Instr_out(WB_IR), .KB_HIT(MemEff));  // open: KB_HIT_2, R2_2, Screen_in, Screen_ins_opt, Screen_ins_opt_2, Cycles, Get_Cycles, Get_Bitmap, Get_Bitmap_2, CopyToRAM, CopyToRAM_2, FrameFlush, FrameFlush_2

  // Other names for the same wires on the sheet: ID_IR[5:0] = Func; OP[5:0] = ID_IR[31:26]; IR[31:0] = IF_IR;
  //   MEM_PC[31:0] = M_PC

  // Notes on the sheet:
  //   控制位
  //   暂停节拍，不能为0
  //   数码管输出
  //   指令存储器
  //   contents of IR_ROM (hex, n*v repeats v):
  //   20090000 200b0020 20110001 20120001 a5310000 112020 20020022 c 2328820 21290002 216bffff 1560fff8
  //   200b0010 20090000 8d310000 112020 20020022 c 21290004 216bffff 1560fff9 2002000a c 2011fff1 112020
  //   20020022 c 22310001 1a20fffb 2002000a c
  //   可计数暂停的时钟源
  //   指令字
  //   IF/ID
  //   JR
  //   JMP
  //   JAL
  //   BLEZ
  //   BEQ
  //   BNE
  //   MemToReg
  //   RegWrite
  //   MemWrite
  //   HalfW
  //   AluOp
  //   AluSrcB
  //   流水调试日志用
  //   为方便自动评测，需要输出流水线各段保存的PC值，注意是PC不是PC_plus_four，另外ID段寄存器写入信息，Mem段内存写入信息也要输出
endmodule

module redirection_pipeline_with_BTB (
  input  Go,
  output [7:0] Seg,
  output [7:0] NA
);

  wire and_1_out, Beq, Blez, Bne, btb_1_predictjump, CLK, clock_1_out, data_bypass_controller_1_stall, Equal,
       EX_Branched, EX_BranchSig, ex_mem_1_halfw_out, ex_mem_1_jal_out, ex_mem_1_memtoreg_out,
       ex_mem_1_regwrite_out, ex_mem_1_syscall_out, EX_PredictJump, id_ex_1_p26, id_ex_1_p35, id_ex_1_p36,
       id_ex_1_p37, id_ex_1_p38, id_ex_1_p40, id_ex_1_p41, id_ex_1_p54, if_id_1_predictjump_out, JAL, JAL_WB,
       JMP, JR, Less, mem_wb_1_memtoreg_out, MemEff, MemWrite, not_1_out, or_1_out, Pause, RegDst,
       register_1_q, RegWrite, SignedExt, Syscall, Vshamt, xor_1_out;
  wire [1:0] id_ex_1_p15, id_ex_1_p16, id_ex_1_p43, id_ex_1_p44;
  wire [3:0] id_ex_1_p39, sc_hard_wired_controller_1_alu_op;
  wire [4:0] ex_mem_1_wadr_out, id_ex_1_p47, id_ex_1_p48, mem_wb_1_wadr_out, mips_regifile_1_r1,
       multiplexer_6_out, reg_choose_logic_1_r1adr, reg_choose_logic_1_r2adr, reg_choose_logic_1_shamt,
       reg_choose_logic_1_wadr;
  wire [5:0] Func, sc_hard_wired_controller_1_jr;
  wire [8:0] sc_hard_wired_controller_1_memtoreg;
  wire [31:0] adder_1_out, adder_2_out, bit_extender_1_out, bit_extender_2_out, btb_1_jumpaddr, EX_IR,
       ex_mem_1_aluresult_out, ex_mem_1_pc_plus_four_out, ex_mem_1_r1_out, EX_PC, EX_PC_plus_four,
       id_ex_1_p42, id_ex_1_p45, id_ex_1_p46, id_ex_1_p53, ID_PC, if_id_1_pc_plus_four_out, IF_IR, IF_PC,
       MDin, MEM_IR, MEM_PC, mem_wb_1_aluresult_out, mem_wb_1_pc_plus_four_out, mem_wb_1_r2_out,
       mips_alu_1_result, mips_mem_1_memreaddata, mips_regifile_1_r2, multiplexer_1_out, multiplexer_2_out,
       multiplexer_3_out, multiplexer_5_out, multiplexer_8_out, multiplexer_9_out, multiplexer_10_out,
       pc_update_logic_1_pc_next, R1, RDin, syscall_process_1_leddata, WB_IR, WB_PC;
  wire [31:5] mips_regifile_1_r1_2;
  wire [31:6] ID_IR;

  PC_update_logic pc_update_logic_1 (
    .Equal(Equal), .Beq(Beq), .Bne(Bne), .JAL(JAL), .JMP(JMP), .JR(JR), .BAddr(adder_2_out),
    .PC_plus_four(adder_1_out), .JAddr(id_ex_1_p53), .JRAddr(R1), .PC_Next(pc_update_logic_1_pc_next),
    .Blez(Blez), .Less(Less), .Branched(EX_Branched), .BranchSig(EX_BranchSig));
  Register #(.width(1), .trigger("rising"), .Select("low")) register_1 (
    .Q(register_1_q), .clr(Go), .preset(Pause));  // open: D, en, clk, cs
  xor xor_1 (xor_1_out, EX_PredictJump, EX_Branched);
  and and_1 (and_1_out, xor_1_out, EX_BranchSig);
  Multiplexer #(.select(1), .width(32), .disabled(0), .enable("false")) multiplexer_1 (
    .in0(EX_PC_plus_four), .in1(pc_update_logic_1_pc_next), .out(multiplexer_1_out), .sel(EX_Branched));
  Register #(.width(32), .trigger("rising"), .Select("low")) PC (
    .D(multiplexer_2_out), .en(not_1_out), .Q(IF_PC), .clk(CLK));  // open: clr
  Multiplexer #(.select(1), .width(32), .disabled(0), .enable("false")) multiplexer_2 (
    .in0(multiplexer_3_out), .in1(multiplexer_1_out), .out(multiplexer_2_out), .sel(and_1_out));
  Multiplexer #(.select(1), .width(32), .disabled(0), .enable("false")) multiplexer_3 (
    .in0(adder_1_out), .in1(btb_1_jumpaddr), .out(multiplexer_3_out), .sel(btb_1_predictjump));
  Clock #(.highDuration(1), .lowDuration(1)) clock_1 (.out(clock_1_out));
  and and_2 (CLK, ~register_1_q, clock_1_out);  // AND_Gate
  Adder #(.width(32)) adder_1 (.a(IF_PC), .b(32'h4), .out(adder_1_out));  // open: cin, cout
  ROM #(.addrWidth(10), .dataWidth(32), .Select("low")) IR_ROM (.addr(IF_PC[11:2]), .data(IF_IR));
  BTB btb_1 (
    .IF_PC(IF_PC), .EX_PC(EX_PC), .BranchSig(EX_BranchSig), .Branched(EX_Branched),
    .BranchAddr(pc_update_logic_1_pc_next), .JumpAddr(btb_1_jumpaddr), .CLK(CLK),
    .PredictJump(btb_1_predictjump));
  not not_1 (not_1_out, data_bypass_controller_1_stall);
  IF_ID if_id_1 (
    .CLK(CLK), .Instr(IF_IR), .Instr_Out({ID_IR, Func}), .PC_plus_four(adder_1_out),
    .PC_plus_four_Out(if_id_1_pc_plus_four_out), .PC(IF_PC), .PC_Out(ID_PC), .CLR(and_1_out),
    .Stall(not_1_out), .PredictJump(btb_1_predictjump), .PredictJump_Out(if_id_1_predictjump_out));
  sc_hard_wired_controller sc_hard_wired_controller_1 (
    .Func(Func), .OP(ID_IR[31:26]), .ALU_OP(sc_hard_wired_controller_1_alu_op),
    .MemToReg(sc_hard_wired_controller_1_memtoreg[0]), .MemWrite(sc_hard_wired_controller_1_memtoreg[2]),
    .ALU_SRC(sc_hard_wired_controller_1_memtoreg[8]), .RegWrite(sc_hard_wired_controller_1_memtoreg[1]),
    .SysCALL(Syscall), .SignedExt(SignedExt), .RegDst(RegDst), .JR(sc_hard_wired_controller_1_jr[0]),
    .JMP(sc_hard_wired_controller_1_jr[1]), .Beq(sc_hard_wired_controller_1_jr[4]),
    .JAL(sc_hard_wired_controller_1_jr[2]), .Bne(sc_hard_wired_controller_1_jr[5]), .Vshamt(Vshamt),
    .BLEZ(sc_hard_wired_controller_1_jr[3]), .HalfW(sc_hard_wired_controller_1_memtoreg[3]));
  reg_choose_logic reg_choose_logic_1 (
    ._21_25(ID_IR[25:21]), .Syscall(Syscall), .RegDst(RegDst), ._16_20(ID_IR[20:16]), ._11_15(ID_IR[15:11]),
    .JAL(sc_hard_wired_controller_1_jr[2]), .PC_plus_four({32{1'b0}}), .WriteBack_Data({32{1'b0}}),
    ._6_10(ID_IR[10:6]), .R1Adr(reg_choose_logic_1_r1adr), .R2Adr(reg_choose_logic_1_r2adr),
    .WAdr(reg_choose_logic_1_wadr), .Shamt(reg_choose_logic_1_shamt));  // open: RDin
  assign bit_extender_1_out = {{16{1'b0}}, {ID_IR[15:6], Func}};  // Bit_Extender bit_extender_1
  assign bit_extender_2_out = {{16{ID_IR[15]}}, {ID_IR[15:6], Func}};  // Bit_Extender bit_extender_2
  Multiplexer #(.select(1), .width(32), .disabled(0), .enable("false")) multiplexer_4 (
    .in0(multiplexer_10_out), .in1(mem_wb_1_pc_plus_four_out), .out(RDin), .sel(JAL_WB));
  Multiplexer #(.select(1), .width(32), .disabled(0), .enable("false")) multiplexer_5 (
    .in0(bit_extender_1_out), .in1(bit_extender_2_out), .out(multiplexer_5_out), .sel(SignedExt));
  MIPS_Regifile mips_regifile_1 (
    .Din(RDin), .Clk(CLK), .R1({mips_regifile_1_r1_2, mips_regifile_1_r1}), .R2(mips_regifile_1_r2),
    .WE(RegWrite), .WAdr(mem_wb_1_wadr_out), .R1Adr(reg_choose_logic_1_r1adr),
    .R2Adr(reg_choose_logic_1_r2adr));
  Multiplexer #(.select(1), .width(5), .disabled(0), .enable("false")) multiplexer_6 (
    .in0(reg_choose_logic_1_shamt), .in1(mips_regifile_1_r1), .out(multiplexer_6_out), .sel(Vshamt));
  or or_1 (or_1_out, and_1_out, data_bypass_controller_1_stall);
  // ID_EX id_ex_1: pin names not known; wires that end beside it: sc_hard_wired_controller_1_jr[0], sc_hard_wired_controller_1_jr[1], sc_hard_wired_controller_1_jr[2], sc_hard_wired_controller_1_jr[3], sc_hard_wired_controller_1_jr[4], sc_hard_wired_controller_1_jr[5], sc_hard_wired_controller_1_memtoreg[0], sc_hard_wired_controller_1_memtoreg[1], sc_hard_wired_controller_1_memtoreg[2], sc_hard_wired_controller_1_memtoreg[3], sc_hard_wired_controller_1_alu_op, sc_hard_wired_controller_1_memtoreg[8], Syscall, {mips_regifile_1_r1_2, mips_regifile_1_r1}, id_ex_1_p15, id_ex_1_p16, mips_regifile_1_r2, multiplexer_5_out, reg_choose_logic_1_wadr, multiplexer_6_out, if_id_1_predictjump_out, ID_PC, {ID_IR, Func}, if_id_1_pc_plus_four_out, {ID_PC[31:28], ID_IR[25:6], Func, 2'b00}, id_ex_1_p26, or_1_out, CLK, JR, JMP, JAL, Blez, Beq, Bne, id_ex_1_p35, id_ex_1_p36, id_ex_1_p37, id_ex_1_p38, id_ex_1_p39, id_ex_1_p40, id_ex_1_p41, id_ex_1_p42, id_ex_1_p43, id_ex_1_p44, id_ex_1_p45, id_ex_1_p46, id_ex_1_p47, id_ex_1_p48, EX_PredictJump, EX_PC, EX_IR, EX_PC_plus_four, id_ex_1_p53, id_ex_1_p54
  Multiplexer #(.select(2), .width(32), .disabled(0), .enable("false")) multiplexer_7 (
    .in0(id_ex_1_p42), .in1(mem_wb_1_aluresult_out), .in2(mem_wb_1_r2_out), .in3(ex_mem_1_aluresult_out),
    .out(R1), .sel(id_ex_1_p43));
  Multiplexer #(.select(2), .width(32), .disabled(0), .enable("false")) multiplexer_8 (
    .in0(id_ex_1_p45), .in1(mem_wb_1_aluresult_out), .in2(mem_wb_1_r2_out), .in3(ex_mem_1_aluresult_out),
    .out(multiplexer_8_out), .sel(id_ex_1_p44));
  data_bypass_controller data_bypass_controller_1 (
    .ID_AluSrc(sc_hard_wired_controller_1_memtoreg[8]), .BranchCLR(and_1_out),
    .ID_R1Adr(reg_choose_logic_1_r1adr), .ID_R2Adr(reg_choose_logic_1_r2adr), .EX_WAdr(id_ex_1_p47),
    .MEM_WAdr(ex_mem_1_wadr_out), .EX_RegWrite(id_ex_1_p36), .MEM_RegWrite(ex_mem_1_regwrite_out),
    .MEM_MemToReg(ex_mem_1_memtoreg_out), .R1_Forward(id_ex_1_p15), .R2_Forward(id_ex_1_p16),
    .ID_IR({ID_IR, Func}), .EX_IR(EX_IR), .Stall(data_bypass_controller_1_stall));
  Multiplexer #(.select(1), .width(32), .disabled(0), .enable("false")) multiplexer_9 (
    .in0(multiplexer_8_out), .in1(id_ex_1_p46), .out(multiplexer_9_out), .sel(id_ex_1_p40));
  Adder #(.width(32)) adder_2 (
    .a(EX_PC_plus_four), .b({id_ex_1_p46[29:0], 2'b00}), .out(adder_2_out));  // open: cin, cout
  MIPS_ALU mips_alu_1 (
    .X(R1), .Y(multiplexer_9_out), .AluOP(id_ex_1_p39), .Equal(Equal), .Result(mips_alu_1_result),
    .shamt(id_ex_1_p48), .Less(Less));  // open: Result_2
  EX_MEM ex_mem_1 (
    .MemToReg(id_ex_1_p35), .RegWrite(id_ex_1_p36), .MemWrite(id_ex_1_p37), .HalfW(id_ex_1_p38),
    .AluResult(mips_alu_1_result), .R2(multiplexer_8_out), .WAdr(id_ex_1_p47), .CLK(CLK),
    .MemToReg_Out(ex_mem_1_memtoreg_out), .RegWrite_Out(ex_mem_1_regwrite_out), .MemWrite_Out(MemWrite),
    .HalfW_Out(ex_mem_1_halfw_out), .AluResult_Out(ex_mem_1_aluresult_out), .R2_Out(MDin),
    .WAdr_Out(ex_mem_1_wadr_out), .PC(EX_PC), .PC_Out(MEM_PC), .R1(R1), .R1_Out(ex_mem_1_r1_out),
    .Syscall(id_ex_1_p41), .Syscall_Out(ex_mem_1_syscall_out), .CLR(1'b0), .JAL(JAL),
    .JAL_Out(ex_mem_1_jal_out), .PC_plus_four(EX_PC_plus_four), .PC_plus_four_Out(ex_mem_1_pc_plus_four_out),
    .Instr(EX_IR), .Instr_out(MEM_IR));
  syscall_process syscall_process_1 (
    .Syscall(ex_mem_1_syscall_out), .CLK(CLK), .R2(MDin), .R1(ex_mem_1_r1_out), .Pause(Pause),
    .LedData(syscall_process_1_leddata));  // open: Get_KB_in, Screen_opt, Cycles, Get_Bitmap, CopyToRAM, FrameFlush
  MIPS_MEM mips_mem_1 (
    .AluResult(ex_mem_1_aluresult_out), .HalfW(ex_mem_1_halfw_out), .WriteData(MDin), .MemWrite(MemWrite),
    .CLK(CLK), .MemReadData(mips_mem_1_memreaddata));
  MEM_WB mem_wb_1 (
    .MemToReg(ex_mem_1_memtoreg_out), .RegWrite(ex_mem_1_regwrite_out), .AluResult(ex_mem_1_aluresult_out),
    .R2(mips_mem_1_memreaddata), .WAdr(ex_mem_1_wadr_out), .CLK(CLK), .MemToReg_Out(mem_wb_1_memtoreg_out),
    .RegWrite_Out(RegWrite), .AluResult_Out(mem_wb_1_aluresult_out), .R2_Out(mem_wb_1_r2_out),
    .WAdr_Out(mem_wb_1_wadr_out), .PC(MEM_PC), .PC_Out(WB_PC), .JAL(ex_mem_1_jal_out), .JAL_Out(JAL_WB),
    .PC_plus_four(ex_mem_1_pc_plus_four_out), .PC_plus_four_Out(mem_wb_1_pc_plus_four_out), .Instr(MEM_IR),
    .Instr_out(WB_IR), .KB_HIT(MemEff));  // open: KB_HIT_2, R2_2, Screen_in, Screen_ins_opt, Screen_ins_opt_2, Cycles, Get_Cycles, Get_Bitmap, Get_Bitmap_2, CopyToRAM, CopyToRAM_2, FrameFlush, FrameFlush_2
  Multiplexer #(.select(1), .width(32), .disabled(0), .enable("false")) multiplexer_10 (
    .in0(mem_wb_1_aluresult_out), .in1(mem_wb_1_r2_out), .out(multiplexer_10_out), .sel(mem_wb_1_memtoreg_out));

  // Other names for the same wires on the sheet: ID_IR[5:0] = Func; OP[5:0] = ID_IR[31:26]; IR[31:0] = IF_IR

  // Notes on the sheet:
  //   指令存储器
  //   contents of IR_ROM (hex, n*v repeats v):
  //   20090000 200b0020 20110001 20120001 a5310000 112020 20020022 c 2328820 21290002 216bffff 1560fff8
  //   200b0010 20090000 8d310000 112020 20020022 c 21290004 216bffff 1560fff9 2002000a c 2011fff1 112020
  //   20020022 c 22310001 1a20fffb 2002000a c
  //   IF/ID
  //   指令字
  //   JR
  //   JMP
  //   JAL
  //   BLEZ
  //   BEQ
  //   BNE
  //   MemToReg
  //   RegWrite
  //   MemWrite
  //   HalfW
  //   AluOp
  //   AluSrcB
endmodule
module redirection_pipeline_with_BTB_and_multistage_interruption_support (
  input  Go
);

  wire and_1_out, and_3_out, and_4_out, and_5_out, Beq, Bitmap_XY_Get, Blez, Bne, btb_1_predictjump, CLK,
       clock_1_out, comparator_1_eq, comparator_2_eq, comparator_3_eq, comparator_4_eq, comparator_5_gt,
       CopyToRAM, data_bypass_controller_1_stall, Equal, ERET, EX_Branched, EX_BranchSig, ex_mem_1_halfw_out,
       ex_mem_1_jal_out, ex_mem_1_memtoreg_out, ex_mem_1_regwrite_out, EX_PredictJump, EX_Syscall,
       FrameFlush, Get_Cycles, Get_KB_in, Hazard, id_ex_1_alusrcb_out, id_ex_1_halfw_out,
       id_ex_1_memtoreg_out, id_ex_1_memwrite_out, id_ex_1_regwrite_out, if_id_1_predictjump_out, INT_SIG,
       JAL, JAL_WB, JMP, JR, KB_EN, KB_IN, Less, MEM_Syscall, mem_wb_1_memtoreg_out, MemWrite, MFC0, MTC0,
       multiplexer_13_out, multistage_interruption_support_1_w1, multistage_interruption_support_1_w2,
       multistage_interruption_support_1_w3, not_1_out, not_2_out, or_1_out, or_3_out, or_4_out, or_5_out,
       Pause, RegDst, register_1_q, RegWrite, Screen_opt, SignedExt, Syscall, syscall_process_1_copytoram,
       syscall_process_1_cycles, syscall_process_1_frameflush, syscall_process_1_get_bitmap,
       syscall_process_1_screen_opt, undriven, undriven_2, undriven_3, Vshamt, xor_1_out;
  wire [1:0] data_bypass_controller_1_r1_forward, data_bypass_controller_1_r2_forward,
       id_ex_1_r1_forward_out, id_ex_1_r2_forward_out, INT_NUM;
  wire [3:0] id_ex_1_aluop_out, sc_hard_wired_controller_1_alu_op;
  wire [4:0] ex_mem_1_wadr_out, id_ex_1_shamt_out, id_ex_1_wadr_out, mem_wb_1_wadr_out, mips_regifile_1_r1,
       multiplexer_9_out, multiplexer_14_out, multiplexer_19_out, reg_choose_logic_1_r1adr,
       reg_choose_logic_1_r2adr, reg_choose_logic_1_shamt, reg_choose_logic_1_wadr, subtractor_1_out;
  wire [5:0] Func, sc_hard_wired_controller_1_jr;
  wire [6:0] KB_CH;
  wire [8:0] sc_hard_wired_controller_1_memtoreg;
  wire [31:0] adder_1_out, adder_2_out, bit_extender_1_out, bit_extender_2_out, bit_extender_3_out,
       bit_extender_4_out, Bitmap_Get, Bitmap_Out, BreakPoint, btb_1_jumpaddr, Cycles, EX_IR,
       ex_mem_1_aluresult_out, ex_mem_1_pc_plus_four_out, ex_mem_1_r1_out, EX_PC, EX_PC_plus_four,
       id_ex_1_extdata_out, id_ex_1_jaddr_out, id_ex_1_r1_out, id_ex_1_r2_out, ID_PC,
       if_id_1_pc_plus_four_out, IF_IR, IF_PC, incrementer_1_p2, led_driver_1_r0, led_driver_1_r1,
       led_driver_1_r2, led_driver_1_r3, led_driver_1_r4, led_driver_1_r5, led_driver_1_r6, led_driver_1_r7,
       led_driver_1_r8, led_driver_1_r9, led_driver_1_r10, led_driver_1_r11, led_driver_1_r12,
       led_driver_1_r13, led_driver_1_r14, led_driver_1_r15, LED_OUT, MDin, MEM_IR, MEM_PC,
       mem_wb_1_aluresult_out, mem_wb_1_pc_plus_four_out, mem_wb_1_r2_out, mips_alu_1_result,
       mips_mem_1_memreaddata, mips_regifile_1_r2, multiplexer_1_out, multiplexer_2_out, multiplexer_3_out,
       multiplexer_5_out, multiplexer_6_out, multiplexer_8_out, multiplexer_11_out, multiplexer_12_out,
       multiplexer_15_out, multiplexer_16_out, multiplexer_17_out, multiplexer_18_out, PC_save,
       pc_update_logic_1_pc_next, R1, RDin, WB_IR, WB_PC;
  wire [31:5] mips_regifile_1_r1_2;
  wire [31:6] ID_IR;

  Multiplexer #(.select(2), .width(32), .disabled("Z"), .enable("false")) multiplexer_1 (
    .out(multiplexer_1_out), .sel(INT_NUM));  // open: in0, in1, in2, in3
  PC_update_logic pc_update_logic_1 (
    .Equal(Equal), .Beq(Beq), .Bne(Bne), .JAL(JAL), .JMP(JMP), .JR(JR), .BAddr(adder_2_out),
    .PC_plus_four(adder_1_out), .JAddr(id_ex_1_jaddr_out), .JRAddr(R1), .PC_Next(pc_update_logic_1_pc_next),
    .Blez(Blez), .Less(Less), .Branched(EX_Branched), .BranchSig(EX_BranchSig));
  Multiplexer #(.select(1), .width(32), .disabled("Z"), .enable("false")) multiplexer_2 (
    .in0(multiplexer_3_out), .in1(multiplexer_1_out), .out(multiplexer_2_out), .sel(INT_SIG));
  Register #(.width(1), .trigger("rising"), .Select("low")) register_1 (
    .Q(register_1_q), .clr(Go), .preset(Pause));  // open: D, en, clk, cs
  xor xor_1 (xor_1_out, EX_PredictJump, EX_Branched);
  and and_1 (and_1_out, xor_1_out, EX_BranchSig);
  Multiplexer #(.select(1), .width(32), .disabled(0), .enable("false")) multiplexer_3 (
    .in0(multiplexer_6_out), .in1(PC_save), .out(multiplexer_3_out), .sel(and_1_out));
  Multiplexer #(.select(1), .width(32), .disabled(0), .enable("false")) multiplexer_4 (
    .in0(EX_PC_plus_four), .in1(pc_update_logic_1_pc_next), .out(PC_save), .sel(EX_Branched));
  Multiplexer #(.select(1), .width(32), .disabled("Z"), .enable("false")) multiplexer_5 (
    .in0(multiplexer_2_out), .in1(BreakPoint), .out(multiplexer_5_out), .sel(ERET));
  Register #(.width(32), .trigger("rising"), .Select("low")) PC (
    .D(multiplexer_5_out), .en(not_1_out), .Q(IF_PC), .clk(CLK));  // open: clr
  Multiplexer #(.select(1), .width(32), .disabled(0), .enable("false")) multiplexer_6 (
    .in0(adder_1_out), .in1(btb_1_jumpaddr), .out(multiplexer_6_out), .sel(btb_1_predictjump));
  Clock #(.highDuration(1), .lowDuration(1)) clock_1 (.out(clock_1_out));
  and and_2 (CLK, ~register_1_q, clock_1_out);  // AND_Gate
  Adder #(.width(32)) adder_1 (.a(IF_PC), .b(32'h4), .out(adder_1_out));  // open: cin, cout
  // Incrementer incrementer_1: pin names not known; wires that end beside it: Cycles, incrementer_1_p2
  Register #(.width(32), .trigger("rising"), .Select("low")) register_2 (
    .D(incrementer_1_p2), .Q(Cycles), .clk(CLK));  // open: en, clr
  or or_1 (or_1_out, ERET, INT_SIG);
  // Mips_Probe mips_probe_1: pin names not known; wires that end beside it: IF_IR
  ROM #(.addrWidth(10), .dataWidth(32), .Select("low")) IR_ROM (.addr(IF_PC[11:2]), .data(IF_IR));
  BTB btb_1 (
    .IF_PC(IF_PC), .EX_PC(EX_PC), .BranchSig(EX_BranchSig), .Branched(EX_Branched),
    .BranchAddr(pc_update_logic_1_pc_next), .JumpAddr(btb_1_jumpaddr), .CLK(CLK),
    .PredictJump(btb_1_predictjump));
  not not_1 (not_1_out, Hazard);
  or or_2 (Hazard, EX_Syscall, MEM_Syscall, data_bypass_controller_1_stall);
  or or_3 (or_3_out, or_1_out, and_1_out);
  IF_ID if_id_1 (
    .CLK(CLK), .Instr(IF_IR), .Instr_Out({ID_IR, Func}), .PC_plus_four(adder_1_out),
    .PC_plus_four_Out(if_id_1_pc_plus_four_out), .PC(IF_PC), .PC_Out(ID_PC), .CLR(or_3_out),
    .Stall(not_1_out), .PredictJump(btb_1_predictjump), .PredictJump_Out(if_id_1_predictjump_out));
  Comparator #(.width(6), .mode("unsigned")) comparator_1 (
    .a(6'b010000), .b(ID_IR[31:26]), .eq(comparator_1_eq));  // open: gt, lt
  Comparator #(.width(5), .mode("unsigned")) comparator_2 (
    .a(ID_IR[25:21]), .b(5'b00100), .eq(comparator_2_eq));  // open: gt, lt
  Comparator #(.width(5), .mode("unsigned")) comparator_3 (
    .a(ID_IR[25:21]), .b({5{1'b0}}), .eq(comparator_3_eq));  // open: gt, lt
  sc_hard_wired_controller sc_hard_wired_controller_1 (
    .Func(Func), .OP(ID_IR[31:26]), .ALU_OP(sc_hard_wired_controller_1_alu_op),
    .MemToReg(sc_hard_wired_controller_1_memtoreg[0]), .MemWrite(sc_hard_wired_controller_1_memtoreg[2]),
    .ALU_SRC(sc_hard_wired_controller_1_memtoreg[8]), .RegWrite(sc_hard_wired_controller_1_memtoreg[1]),
    .SysCALL(Syscall), .SignedExt(SignedExt), .RegDst(RegDst), .JR(sc_hard_wired_controller_1_jr[0]),
    .JMP(sc_hard_wired_controller_1_jr[1]), .Beq(sc_hard_wired_controller_1_jr[4]),
    .JAL(sc_hard_wired_controller_1_jr[2]), .Bne(sc_hard_wired_controller_1_jr[5]), .Vshamt(Vshamt),
    .BLEZ(sc_hard_wired_controller_1_jr[3]), .HalfW(sc_hard_wired_controller_1_memtoreg[3]));
  reg_choose_logic reg_choose_logic_1 (
    ._21_25(ID_IR[25:21]), .Syscall(Syscall), .RegDst(RegDst), ._16_20(ID_IR[20:16]), ._11_15(ID_IR[15:11]),
    .JAL(sc_hard_wired_controller_1_jr[2]), .PC_plus_four({32{1'b0}}), .WriteBack_Data({32{1'b0}}),
    ._6_10(ID_IR[10:6]), .R1Adr(reg_choose_logic_1_r1adr), .R2Adr(reg_choose_logic_1_r2adr),
    .WAdr(reg_choose_logic_1_wadr), .Shamt(reg_choose_logic_1_shamt));  // open: RDin
  assign bit_extender_1_out = {{16{1'b0}}, {ID_IR[15:6], Func}};  // Bit_Extender bit_extender_1
  assign bit_extender_2_out = {{16{ID_IR[15]}}, {ID_IR[15:6], Func}};  // Bit_Extender bit_extender_2
  and and_3 (and_3_out, comparator_1_eq, comparator_2_eq);
  and and_4 (and_4_out, comparator_1_eq, comparator_3_eq);
  Multiplexer #(.select(1), .width(32), .disabled(0), .enable("false")) multiplexer_7 (
    .in0(multiplexer_18_out), .in1(mem_wb_1_pc_plus_four_out), .out(RDin), .sel(JAL_WB));
  Multiplexer #(.select(1), .width(32), .disabled(0), .enable("false")) multiplexer_8 (
    .in0(bit_extender_1_out), .in1(bit_extender_2_out), .out(multiplexer_8_out), .sel(SignedExt));
  MIPS_Regifile mips_regifile_1 (
    .Din(RDin), .Clk(CLK), .R1({mips_regifile_1_r1_2, mips_regifile_1_r1}), .R2(mips_regifile_1_r2),
    .WE(RegWrite), .WAdr(mem_wb_1_wadr_out), .R1Adr(reg_choose_logic_1_r1adr),
    .R2Adr(reg_choose_logic_1_r2adr));
  Multiplexer #(.select(1), .width(5), .disabled(0), .enable("false")) multiplexer_9 (
    .in0(reg_choose_logic_1_shamt), .in1(mips_regifile_1_r1), .out(multiplexer_9_out), .sel(Vshamt));
  Keyboard #(.Char_bit_width(7), .buflen(32), .trigger("rising")) keyboard_1 (
    .clk(CLK), .re(KB_EN), .avail(KB_IN), .data(KB_CH));  // open: clr
  Comparator #(.width(32), .mode("twosComplement")) comparator_4 (
    .a(IF_IR), .b(32'h42000018), .eq(comparator_4_eq));  // open: gt, lt
  or or_4 (or_4_out, and_1_out, or_1_out, Hazard);
  ID_EX id_ex_1 (
    .JR(sc_hard_wired_controller_1_jr[0]), .JMP(sc_hard_wired_controller_1_jr[1]),
    .JAL(sc_hard_wired_controller_1_jr[2]), .BLEZ(sc_hard_wired_controller_1_jr[3]),
    .BEQ(sc_hard_wired_controller_1_jr[4]), .BNE(sc_hard_wired_controller_1_jr[5]),
    .MemToReg(sc_hard_wired_controller_1_memtoreg[0]), .Shamt(multiplexer_9_out),
    .R1({mips_regifile_1_r1_2, mips_regifile_1_r1}), .R2(mips_regifile_1_r2), .JR_Out(JR), .JMP_Out(JMP),
    .JAL_Out(JAL), .BLEZ_Out(Blez), .BEQ_Out(Beq), .BNE_Out(Bne), .MemToReg_Out(id_ex_1_memtoreg_out),
    .Shamt_Out(id_ex_1_shamt_out), .R1_Out(id_ex_1_r1_out), .R2_Out(id_ex_1_r2_out), .CLK(CLK),
    .AluOp(sc_hard_wired_controller_1_alu_op), .AluOp_Out(id_ex_1_aluop_out), .ExtData(multiplexer_8_out),
    .WAdr(reg_choose_logic_1_wadr), .RegWrite(sc_hard_wired_controller_1_memtoreg[1]),
    .RegWrite_Out(id_ex_1_regwrite_out), .MemWrite_Out(id_ex_1_memwrite_out), .HalfW_Out(id_ex_1_halfw_out),
    .AluSrcB_Out(id_ex_1_alusrcb_out), .Syscall_Out(EX_Syscall),
    .MemWrite(sc_hard_wired_controller_1_memtoreg[2]), .HalfW(sc_hard_wired_controller_1_memtoreg[3]),
    .AluSrcB(sc_hard_wired_controller_1_memtoreg[8]), .Syscall(Syscall), .ExtData_Out(id_ex_1_extdata_out),
    .WAdr_Out(id_ex_1_wadr_out), .PC(ID_PC), .PC_Out(EX_PC), .CLR(or_4_out),
    .JAddr({ID_PC[31:28], ID_IR[25:6], Func, 2'b00}), .JAddr_Out(id_ex_1_jaddr_out),
    .PC_plus_four(if_id_1_pc_plus_four_out), .PC_plus_four_Out(EX_PC_plus_four),
    .R1_Forward(data_bypass_controller_1_r1_forward), .R1_Forward_Out(id_ex_1_r1_forward_out),
    .Instr({ID_IR, Func}), .Instr_out(EX_IR), .R2_Forward(data_bypass_controller_1_r2_forward),
    .R2_Forward_Out(id_ex_1_r2_forward_out), .PredictJump(if_id_1_predictjump_out),
    .PredictJump_Out(EX_PredictJump), .MTC(and_3_out), .MFC(and_4_out), .MTC_Out(MTC0), .MFC_Out(MFC0),
    .ERET(comparator_4_eq), .ERET_Out(ERET));
  Multiplexer #(.select(2), .width(32), .disabled(0), .enable("false")) multiplexer_10 (
    .in0(id_ex_1_r1_out), .in1(mem_wb_1_aluresult_out), .in2(mem_wb_1_r2_out), .in3(ex_mem_1_aluresult_out),
    .out(R1), .sel(id_ex_1_r1_forward_out));
  Multiplexer #(.select(2), .width(32), .disabled(0), .enable("false")) multiplexer_11 (
    .in0(id_ex_1_r2_out), .in1(mem_wb_1_aluresult_out), .in2(mem_wb_1_r2_out), .in3(ex_mem_1_aluresult_out),
    .out(multiplexer_11_out), .sel(id_ex_1_r2_forward_out));
  multistage_interruption_support multistage_interruption_support_1 (
    .CLK(CLK), .RST(1'b0), .IR1(undriven), .IR2(undriven_2), .IR3(undriven_3), .MTC0(MTC0), .MFC0(MFC0),
    .ERET(ERET), .EX_IR(EX_IR), .PC_in(PC_save), .INT_SIG(INT_SIG),
    .W1(multistage_interruption_support_1_w1), .W2(multistage_interruption_support_1_w2),
    .W3(multistage_interruption_support_1_w3), .BreakPoint(BreakPoint), .INT_NUM(INT_NUM));
  data_bypass_controller data_bypass_controller_1 (
    .ID_AluSrc(sc_hard_wired_controller_1_memtoreg[8]), .BranchCLR(and_1_out),
    .ID_R1Adr(reg_choose_logic_1_r1adr), .ID_R2Adr(reg_choose_logic_1_r2adr), .EX_WAdr(id_ex_1_wadr_out),
    .MEM_WAdr(ex_mem_1_wadr_out), .EX_RegWrite(id_ex_1_regwrite_out), .MEM_RegWrite(ex_mem_1_regwrite_out),
    .MEM_MemToReg(ex_mem_1_memtoreg_out), .R1_Forward(data_bypass_controller_1_r1_forward),
    .R2_Forward(data_bypass_controller_1_r2_forward), .ID_IR({ID_IR, Func}), .EX_IR(EX_IR),
    .Stall(data_bypass_controller_1_stall));
  Multiplexer #(.select(1), .width(32), .disabled(0), .enable("false")) multiplexer_12 (
    .in0(multiplexer_11_out), .in1(id_ex_1_extdata_out), .out(multiplexer_12_out), .sel(id_ex_1_alusrcb_out));
  // Mips_Probe mips_probe_2: pin names not known; wires that end beside it: EX_IR, multiplexer_11_out
  Adder #(.width(32)) adder_2 (
    .a(EX_PC_plus_four), .b({id_ex_1_extdata_out[29:0], 2'b00}), .out(adder_2_out));  // open: cin, cout
  Hex_Digit_Display hex_digit_display_1 (.value(LED_OUT[7:4]));  // open: dp
  LED #(.active("true")) _1 (.in(multistage_interruption_support_1_w1));
  LED #(.active("true")) _2 (.in(multistage_interruption_support_1_w2));
  LED #(.active("true")) _3 (.in(multistage_interruption_support_1_w3));
  MIPS_ALU mips_alu_1 (
    .X(R1), .Y(multiplexer_12_out), .AluOP(id_ex_1_aluop_out), .Equal(Equal), .Result(mips_alu_1_result),
    .shamt(id_ex_1_shamt_out), .Less(Less));  // open: Result_2
  Hex_Digit_Display hex_digit_display_2 (.value(LED_OUT[3:0]));  // open: dp
  DotMatrix #(.inputtype("column"), .matrixcols(16), .matrixrows(32), .persist(0), .dotshape("square")) dotmatrix_1 (
    .col0(led_driver_1_r0), .col1(led_driver_1_r1), .col2(led_driver_1_r2), .col3(led_driver_1_r3),
    .col4(led_driver_1_r4), .col5(led_driver_1_r5), .col6(led_driver_1_r6), .col7(led_driver_1_r7),
    .col8(led_driver_1_r8), .col9(led_driver_1_r9), .col10(led_driver_1_r10), .col11(led_driver_1_r11),
    .col12(led_driver_1_r12), .col13(led_driver_1_r13), .col14(led_driver_1_r14), .col15(led_driver_1_r15));
  led_driver led_driver_1 (
    .X(Bitmap_Get[3:0]), .Y(Bitmap_Get[9:5]), .SET(Bitmap_Get[10]), .LineRst(Bitmap_Get[11]),
    .RST(Bitmap_Get[12]), .CLK(not_2_out), .EN(Screen_opt), .R0(led_driver_1_r0), .R8(led_driver_1_r8),
    .R1(led_driver_1_r1), .R9(led_driver_1_r9), .R2(led_driver_1_r2), .R10(led_driver_1_r10),
    .R3(led_driver_1_r3), .R11(led_driver_1_r11), .R4(led_driver_1_r4), .R12(led_driver_1_r12),
    .R5(led_driver_1_r5), .R13(led_driver_1_r13), .R6(led_driver_1_r6), .R14(led_driver_1_r14),
    .R7(led_driver_1_r7), .R15(led_driver_1_r15));
  EX_MEM ex_mem_1 (
    .MemToReg(id_ex_1_memtoreg_out), .RegWrite(id_ex_1_regwrite_out), .MemWrite(id_ex_1_memwrite_out),
    .HalfW(id_ex_1_halfw_out), .AluResult(mips_alu_1_result), .R2(multiplexer_11_out),
    .WAdr(id_ex_1_wadr_out), .CLK(CLK), .MemToReg_Out(ex_mem_1_memtoreg_out),
    .RegWrite_Out(ex_mem_1_regwrite_out), .MemWrite_Out(MemWrite), .HalfW_Out(ex_mem_1_halfw_out),
    .AluResult_Out(ex_mem_1_aluresult_out), .R2_Out(MDin), .WAdr_Out(ex_mem_1_wadr_out), .PC(EX_PC),
    .PC_Out(MEM_PC), .R1(R1), .R1_Out(ex_mem_1_r1_out), .Syscall(EX_Syscall), .Syscall_Out(MEM_Syscall),
    .CLR(1'b0), .JAL(JAL), .JAL_Out(ex_mem_1_jal_out), .PC_plus_four(EX_PC_plus_four),
    .PC_plus_four_Out(ex_mem_1_pc_plus_four_out), .Instr(EX_IR), .Instr_out(MEM_IR));
  not not_2 (not_2_out, CLK);
  vga_sec_ram vga_sec_ram_1 (
    .Write(CopyToRAM), .X(Bitmap_Get[3:0]), .CLK(CLK), .R0(led_driver_1_r0), .R1(led_driver_1_r1),
    .R2(led_driver_1_r2), .R3(led_driver_1_r3), .R4(led_driver_1_r4), .R5(led_driver_1_r5),
    .R6(led_driver_1_r6), .R7(led_driver_1_r7), .R8(led_driver_1_r8), .R9(led_driver_1_r9),
    .R10(led_driver_1_r10), .R11(led_driver_1_r11), .R12(led_driver_1_r12), .R13(led_driver_1_r13),
    .R14(led_driver_1_r14), .R15(led_driver_1_r15));  // open: Read, addr, bit_out
  syscall_process syscall_process_1 (
    .Syscall(MEM_Syscall), .CLK(CLK), .R2(MDin), .R1(ex_mem_1_r1_out), .Pause(Pause), .LedData(LED_OUT),
    .Get_KB_in(Get_KB_in), .Screen_opt(syscall_process_1_screen_opt), .Cycles(syscall_process_1_cycles),
    .Get_Bitmap(syscall_process_1_get_bitmap), .CopyToRAM(syscall_process_1_copytoram),
    .FrameFlush(syscall_process_1_frameflush));
  MIPS_MEM mips_mem_1 (
    .AluResult(ex_mem_1_aluresult_out), .HalfW(ex_mem_1_halfw_out), .WriteData(MDin), .MemWrite(MemWrite),
    .CLK(CLK), .MemReadData(mips_mem_1_memreaddata));
  or or_5 (or_5_out, syscall_process_1_cycles, syscall_process_1_get_bitmap, and_5_out);
  and and_5 (and_5_out, Get_KB_in, KB_IN);
  bitmap_get bitmap_get_1 (
    .X(Bitmap_Get[3:0]), .Y(Bitmap_Get[9:5]), .R0(led_driver_1_r0), .R8(led_driver_1_r8),
    .R1(led_driver_1_r1), .R9(led_driver_1_r9), .R2(led_driver_1_r2), .R10(led_driver_1_r10),
    .R3(led_driver_1_r3), .R11(led_driver_1_r11), .R4(led_driver_1_r4), .R12(led_driver_1_r12),
    .R5(led_driver_1_r5), .R13(led_driver_1_r13), .R6(led_driver_1_r6), .R14(led_driver_1_r14),
    .R7(led_driver_1_r7), .R15(led_driver_1_r15), .Control_Bit(Bitmap_Get[11:10]), .out_20(Bitmap_Out));
  Multiplexer #(.select(1), .width(1), .disabled("Z"), .enable("false")) multiplexer_13 (
    .in0(ex_mem_1_regwrite_out), .in1(1'b1), .out(multiplexer_13_out), .sel(or_5_out));
  MEM_WB mem_wb_1 (
    .MemToReg(ex_mem_1_memtoreg_out), .RegWrite(multiplexer_13_out), .AluResult(ex_mem_1_aluresult_out),
    .R2(mips_mem_1_memreaddata), .WAdr(multiplexer_14_out), .CLK(CLK), .MemToReg_Out(mem_wb_1_memtoreg_out),
    .RegWrite_Out(RegWrite), .AluResult_Out(mem_wb_1_aluresult_out), .R2_Out(mem_wb_1_r2_out),
    .WAdr_Out(mem_wb_1_wadr_out), .PC(MEM_PC), .PC_Out(WB_PC), .JAL(ex_mem_1_jal_out), .JAL_Out(JAL_WB),
    .PC_plus_four(ex_mem_1_pc_plus_four_out), .PC_plus_four_Out(mem_wb_1_pc_plus_four_out), .Instr(MEM_IR),
    .Instr_out(WB_IR), .KB_HIT(and_5_out), .KB_HIT_2(KB_EN), .R2_2(MDin), .Screen_in(Bitmap_Get),
    .Screen_ins_opt(syscall_process_1_screen_opt), .Screen_ins_opt_2(Screen_opt),
    .Cycles(syscall_process_1_cycles), .Get_Cycles(Get_Cycles), .Get_Bitmap(syscall_process_1_get_bitmap),
    .Get_Bitmap_2(Bitmap_XY_Get), .CopyToRAM(syscall_process_1_copytoram), .CopyToRAM_2(CopyToRAM),
    .FrameFlush(syscall_process_1_frameflush), .FrameFlush_2(FrameFlush));
  Multiplexer #(.select(1), .width(5), .disabled("Z"), .enable("false")) multiplexer_14 (
    .in0(ex_mem_1_wadr_out), .in1(5'b00100), .out(multiplexer_14_out), .sel(or_5_out));
  Multiplexer #(.select(1), .width(32), .disabled(0), .enable("false")) multiplexer_15 (
    .in0(mem_wb_1_aluresult_out), .in1(mem_wb_1_r2_out), .out(multiplexer_15_out), .sel(mem_wb_1_memtoreg_out));
  Multiplexer #(.select(1), .width(32), .disabled(0), .enable("false")) multiplexer_16 (
    .in0(multiplexer_15_out), .in1(Bitmap_Out), .out(multiplexer_16_out), .sel(Bitmap_XY_Get));
  Multiplexer #(.select(1), .width(32), .disabled(0), .enable("false")) multiplexer_17 (
    .in0(multiplexer_16_out), .in1(bit_extender_3_out), .out(multiplexer_17_out), .sel(KB_EN));
  Multiplexer #(.select(1), .width(32), .disabled(0), .enable("false")) multiplexer_18 (
    .in0(multiplexer_17_out), .in1(bit_extender_4_out), .out(multiplexer_18_out), .sel(Get_Cycles));
  assign bit_extender_3_out = {{25{1'b0}}, KB_CH};  // Bit_Extender bit_extender_3
  Comparator #(.width(5), .mode("unsigned")) comparator_5 (
    .a(Cycles[4:0]), .b(5'b10100), .gt(comparator_5_gt));  // open: eq, lt
  Subtractor #(.width(5)) subtractor_1 (.a(Cycles[4:0]), .b(5'b10100), .out(subtractor_1_out));  // open: bin, bout
  Multiplexer #(.select(1), .width(5), .disabled(0), .enable("false")) multiplexer_19 (
    .in0(Cycles[4:0]), .in1(subtractor_1_out), .out(multiplexer_19_out), .sel(comparator_5_gt));
  assign bit_extender_4_out = {{27{1'b0}}, multiplexer_19_out};  // Bit_Extender bit_extender_4

  // Other names for the same wires on the sheet: ID_IR[5:0] = Func; OP[5:0] = ID_IR[31:26]; IR[31:0] = IF_IR;
  //   Screen_opt_ins[31:0] = Bitmap_Get

  // Notes on the sheet:
  //   指令存储器
  //   contents of IR_ROM (hex, n*v repeats v):
  //   201d0400 20110007 2013001f 2014000f 20150080 20160090 c1000fe c1000e4 20050400 c1000b1 2820 c1000b1
  //   22520001 c100073 10800004 2252ffff 20050400 c1000b1 8100050 20050400 c1000b1 2020 20020010 c
  //   10800034 43020 2820 c1000b1 62020 20010057 14240019 2003020 20080008 208482a 20010001 10290006
  //   32090003 20010003 14290009 20010003 2018022 8100032 32090001 20010001 14290003 20010001 2018022
  //   8100032 22100001 8100032 c1000e4 c100073 10800018 c08020 c1000e4 810004d 20010041 14240005 2231ffff
  //   c100073 10800010 22310001 810004d 20010053 14240005 22520001 c100073 10800009 2252ffff 8100050
  //   20010044 14240005 22310001 c100073 10800002 2231ffff 810004d 20050400 c1000b1 810000a 20050400
  //   c1000b1 20020031 c 48020 c1000e4 9020 20110007 c10005f 2e02020 20020022 c 20050400 c1000b1 810000a
  //   20050400 20060800 2008001f 3409ffff 20020021 82140 852025 c 14890006 20020020 82140 862025 c
  //   22f70001 8100063 10800003 2108ffff 2001ffff 1428fff1 3e00008 20020021 200a001f 200c000f 2020
  //   8ea80000 8ec90000 1114020 1324820 10c5825 156c0032 12a5825 156a0030 94940 882025 892025 c 1480002b
  //   2020 8ea80004 8ec90004 1114020 1324820 10c5825 156c0024 12a5825 156a0022 94940 882025 892025 c
  //   1480001d 2020 8ea80008 8ec90008 1114020 1324820 10c5825 156c0016 12a5825 156a0014 94940 882025
  //   892025 c 1480000f 2020 8ea8000c 8ec9000c 1114020 1324820 10c5825 156c0008 12a5825 156a0006 94940
  //   882025 892025 c 14800001 3e00008 20040001 3e00008 20020020 a02020 8ea80000 8ec90000 1114020 1324820
  //   94940 882025 892025 c a02020 8ea80004 8ec90004 1114020 1324820 94940 882025 892025 c a02020 8ea80008
  //   8ec90008 1114020 1324820 94940 882025 892025 c a02020 8ea8000c 8ec9000c 1114020 1324820 94940 882025
  //   892025 c 20010400 14250008 20020023 20040010 2084ffff c 1480fffd 81000e0 20020024 c 3e00008 2084ffff
  //   1480fffe 3e00008 104080 8d080000 31090003 aea90000 84082 31090003 aec90000 84082 31090003 aea90004
  //   84082 31090003 aec90004 84082 31090003 aea90008 84082 31090003 aec90008 84082 31090003 aea9000c
  //   84082 31090003 aec9000c 3e00008 3408c840 ac080000 34083210 ac080004 34085410 ac080008 34085410
  //   ac08000c 34086510 ac080010 34088541 ac080014 34085421 ac080018 34089540 ac08001c 34086541 ac080020
  //   34089651 ac080024 34089654 ac080028 34089541 ac08002c 34086542 ac080030 3408a951 ac080034 34088654
  //   ac080038 34089510 ac08003c 34086540 ac080040 34089521 ac080044 3408a654 ac080048 34089851 ac08004c
  //   3e00008
  //   IF/ID
  //   指令字
  //   JR
  //   JMP
  //   JAL
  //   BLEZ
  //   BEQ
  //   BNE
  //   MemToReg
  //   RegWrite
  //   MemWrite
  //   HalfW
  //   AluOp
  //   AluSrcB
endmodule

module sc_hard_wired_controller (
  input  [5:0] OP,
  input  [5:0] Func,
  output [3:0] ALU_OP,
  output MemToReg,
  output MemWrite,
  output ALU_SRC,
  output RegWrite,
  output SysCALL,
  output SignedExt,
  output RegDst,
  output Beq,
  output Bne,
  output JR,
  output JMP,
  output JAL,
  output Vshamt,
  output BLEZ,
  output HalfW
);

  ALU_controller_autogen alu_controller_autogen_1 (
    .OP0(OP[0]), .OP1(OP[1]), .OP2(OP[2]), .OP3(OP[3]), .OP4(OP[4]), .OP5(OP[5]), .F0(Func[0]), .F1(Func[1]),
    .F2(Func[2]), .F3(Func[3]), .F4(Func[4]), .F5(Func[5]), .S0(ALU_OP[0]), .S1(ALU_OP[1]), .S2(ALU_OP[2]),
    .S3(ALU_OP[3]));
  ctrl_sig_autogen ctrl_sig_autogen_1 (
    .OP0(OP[0]), .MemToReg(MemToReg), .OP1(OP[1]), .OP2(OP[2]), .OP3(OP[3]), .OP4(OP[4]),
    .MemWrite(MemWrite), .OP5(OP[5]), .F0(Func[0]), .F1(Func[1]), .F2(Func[2]), .F3(Func[3]), .F4(Func[4]),
    .F5(Func[5]), .ALU_SRC(ALU_SRC), .RegWrite(RegWrite), .SysCALL(SysCALL), .SignedExt(SignedExt),
    .RegDst(RegDst), .BEQ(Beq), .BNE(Bne), .JR(JR), .JUMP(JMP), .JAL(JAL), .Vshamt(Vshamt), .BLEZ(BLEZ),
    .HalfW(HalfW));

  // Other names for the same wires on the sheet: OP_CODE[5:0] = OP

  // Notes on the sheet:
  //   运算器控制器，根据指令生成运算器功能选择信号
  //   控制信号生成，产生数据通路需要的其他控制信号
endmodule

module ALU_controller_autogen (
  input  OP0,
  input  OP1,
  input  OP2,
  input  OP3,
  input  OP4,
  input  OP5,
  input  F0,
  input  F1,
  input  F2,
  input  F3,
  input  F4,
  input  F5,
  output S0,
  output S1,
  output S2,
  output S3
);

  wire and_1_out, and_2_out, and_3_out, and_4_out, and_5_out, and_6_out, and_7_out, and_8_out, and_9_out,
       and_10_out, and_11_out, and_12_out, and_13_out, and_14_out, and_15_out, and_16_out, and_17_out,
       and_18_out, and_19_out, and_20_out, and_21_out, and_22_out, and_23_out, and_24_out, and_25_out,
       and_26_out, and_27_out, and_28_out, and_29_out, and_30_out, and_31_out, and_32_out, and_33_out,
       and_34_out, and_35_out, and_36_out, and_37_out, and_38_out, not_1_out, not_2_out, not_3_out,
       not_4_out, not_5_out, not_6_out, not_7_out, not_8_out, not_9_out, not_10_out, not_11_out, not_12_out,
       not_13_out, not_14_out, not_15_out, not_16_out, not_17_out, not_18_out, not_19_out, not_20_out,
       not_21_out, not_22_out, not_23_out, not_24_out, not_25_out, not_26_out, not_27_out, not_28_out,
       not_29_out, not_30_out, not_31_out, not_32_out, not_33_out, not_34_out, not_35_out, not_36_out,
       not_37_out, not_38_out, not_39_out, not_40_out, not_41_out, not_42_out, not_43_out, not_44_out,
       not_45_out, not_46_out, not_47_out, not_48_out, not_49_out, not_50_out, not_51_out, not_52_out,
       not_53_out, not_54_out, not_55_out, not_56_out, not_57_out, not_58_out, not_59_out, not_60_out,
       not_61_out, not_62_out, not_63_out, not_64_out, not_65_out, not_66_out, not_67_out, not_68_out,
       not_69_out, not_70_out, not_71_out, not_72_out, not_73_out, not_74_out, not_75_out, not_76_out,
       not_77_out, not_78_out, not_79_out, not_80_out, not_81_out, not_82_out, not_83_out, not_84_out,
       not_85_out, not_86_out, not_87_out, not_88_out, not_89_out, not_90_out, not_91_out, not_92_out,
       not_93_out, not_94_out, not_95_out, not_96_out, not_97_out, not_98_out, not_99_out, not_100_out,
       not_101_out, not_102_out, not_103_out, not_104_out, not_105_out, not_106_out, not_107_out,
       not_108_out, not_109_out, not_110_out, not_111_out, not_112_out, not_113_out, not_114_out,
       not_115_out, not_116_out, not_117_out, not_118_out, not_119_out, not_120_out, not_121_out,
       not_122_out, not_123_out, not_124_out, not_125_out, not_126_out, not_127_out, not_128_out,
       not_129_out, not_130_out, not_131_out, not_132_out, not_133_out, not_134_out, not_135_out,
       not_136_out, not_137_out, not_138_out, not_139_out, not_140_out, not_141_out, not_142_out,
       not_143_out, not_144_out, not_145_out, not_146_out, not_147_out, not_148_out, not_149_out,
       not_150_out, not_151_out, not_152_out, not_153_out, not_154_out, not_155_out, not_156_out,
       not_157_out, not_158_out, not_159_out, not_160_out, not_161_out, not_162_out, not_163_out,
       not_164_out, not_165_out, not_166_out, not_167_out, not_168_out, not_169_out, not_170_out,
       not_171_out, not_172_out, not_173_out, not_174_out, not_175_out, not_176_out, not_177_out,
       not_178_out, not_179_out, not_180_out, not_181_out, not_182_out, not_183_out, not_184_out,
       not_185_out, not_186_out, not_187_out, not_188_out, not_189_out, not_190_out, not_191_out,
       not_192_out, not_193_out, not_194_out, not_195_out, not_196_out, not_197_out, not_198_out,
       not_199_out, not_200_out, not_201_out, not_202_out, not_203_out, not_204_out, not_205_out,
       not_206_out, not_207_out, not_208_out, not_209_out, not_210_out, not_211_out, not_212_out,
       not_213_out, not_214_out, not_215_out, not_216_out, not_217_out, not_218_out, not_219_out,
       not_220_out, not_221_out, not_222_out, not_223_out, not_224_out, not_225_out, not_226_out,
       not_227_out, not_228_out, not_229_out, not_230_out, not_231_out, not_232_out, not_233_out,
       not_234_out, not_235_out, not_236_out, not_237_out, not_238_out, not_239_out, not_240_out,
       not_241_out, not_242_out, not_243_out, not_244_out, not_245_out, not_246_out, not_247_out, not_248_out;

  not not_1 (not_1_out, OP5);
  not not_2 (not_2_out, OP4);
  not not_3 (not_3_out, OP3);
  not not_4 (not_4_out, OP2);
  not not_5 (not_5_out, OP1);
  not not_6 (not_6_out, OP0);
  not not_7 (not_7_out, F5);
  not not_8 (not_8_out, F4);
  not not_9 (not_9_out, F3);
  not not_10 (not_10_out, F2);
  not not_11 (not_11_out, OP5);
  not not_12 (not_12_out, OP4);
  not not_13 (not_13_out, OP3);
  not not_14 (not_14_out, OP2);
  not not_15 (not_15_out, OP1);
  not not_16 (not_16_out, OP0);
  not not_17 (not_17_out, F4);
  not not_18 (not_18_out, F3);
  not not_19 (not_19_out, F2);
  not not_20 (not_20_out, F1);
  not not_21 (not_21_out, F0);
  not not_22 (not_22_out, OP5);
  not not_23 (not_23_out, OP4);
  not not_24 (not_24_out, OP3);
  not not_25 (not_25_out, OP2);
  not not_26 (not_26_out, OP1);
  not not_27 (not_27_out, OP0);
  not not_28 (not_28_out, F4);
  not not_29 (not_29_out, F3);
  not not_30 (not_30_out, F2);
  not not_31 (not_31_out, F1);
  not not_32 (not_32_out, OP5);
  not not_33 (not_33_out, OP4);
  not not_34 (not_34_out, OP3);
  not not_35 (not_35_out, OP2);
  not not_36 (not_36_out, OP1);
  not not_37 (not_37_out, OP0);
  not not_38 (not_38_out, F4);
  not not_39 (not_39_out, F3);
  not not_40 (not_40_out, F1);
  not not_41 (not_41_out, F0);
  not not_42 (not_42_out, OP5);
  not not_43 (not_43_out, OP4);
  not not_44 (not_44_out, OP3);
  not not_45 (not_45_out, OP2);
  not not_46 (not_46_out, OP1);
  not not_47 (not_47_out, OP0);
  not not_48 (not_48_out, F4);
  not not_49 (not_49_out, F2);
  not not_50 (not_50_out, F0);
  not not_51 (not_51_out, OP5);
  not not_52 (not_52_out, OP4);
  not not_53 (not_53_out, OP2);
  not not_54 (not_54_out, OP1);
  not not_55 (not_55_out, OP0);
  not not_56 (not_56_out, OP5);
  not not_57 (not_57_out, OP4);
  not not_58 (not_58_out, OP1);
  not not_59 (not_59_out, OP0);
  not not_60 (not_60_out, OP5);
  not not_61 (not_61_out, OP4);
  not not_62 (not_62_out, OP2);
  not not_63 (not_63_out, OP1);
  not not_64 (not_64_out, OP5);
  not not_65 (not_65_out, OP4);
  not not_66 (not_66_out, OP2);
  not not_67 (not_67_out, OP0);
  not not_68 (not_68_out, OP4);
  not not_69 (not_69_out, OP3);
  not not_70 (not_70_out, OP2);
  not not_71 (not_71_out, OP4);
  not not_72 (not_72_out, OP2);
  not not_73 (not_73_out, OP4);
  not not_74 (not_74_out, OP2);
  not not_75 (not_75_out, OP1);
  not not_76 (not_76_out, OP5);
  not not_77 (not_77_out, OP4);
  not not_78 (not_78_out, OP3);
  not not_79 (not_79_out, OP2);
  not not_80 (not_80_out, OP1);
  not not_81 (not_81_out, OP0);
  not not_82 (not_82_out, F5);
  not not_83 (not_83_out, F4);
  not not_84 (not_84_out, F3);
  not not_85 (not_85_out, F2);
  not not_86 (not_86_out, F0);
  not not_87 (not_87_out, OP5);
  not not_88 (not_88_out, OP4);
  not not_89 (not_89_out, OP3);
  not not_90 (not_90_out, OP2);
  not not_91 (not_91_out, OP1);
  not not_92 (not_92_out, OP0);
  not not_93 (not_93_out, F4);
  not not_94 (not_94_out, F3);
  not not_95 (not_95_out, F2);
  not not_96 (not_96_out, F0);
  not not_97 (not_97_out, OP5);
  not not_98 (not_98_out, OP4);
  not not_99 (not_99_out, OP3);
  not not_100 (not_100_out, OP2);
  not not_101 (not_101_out, OP1);
  not not_102 (not_102_out, OP0);
  not not_103 (not_103_out, F4);
  not not_104 (not_104_out, F3);
  not not_105 (not_105_out, F1);
  not not_106 (not_106_out, F0);
  not not_107 (not_107_out, OP5);
  not not_108 (not_108_out, OP4);
  not not_109 (not_109_out, OP3);
  not not_110 (not_110_out, OP2);
  not not_111 (not_111_out, OP1);
  not not_112 (not_112_out, OP0);
  not not_113 (not_113_out, F4);
  not not_114 (not_114_out, F3);
  not not_115 (not_115_out, OP5);
  not not_116 (not_116_out, OP4);
  not not_117 (not_117_out, OP3);
  not not_118 (not_118_out, OP2);
  not not_119 (not_119_out, OP1);
  not not_120 (not_120_out, OP0);
  not not_121 (not_121_out, F4);
  not not_122 (not_122_out, F2);
  not not_123 (not_123_out, F0);
  not not_124 (not_124_out, OP5);
  not not_125 (not_125_out, OP4);
  not not_126 (not_126_out, OP1);
  not not_127 (not_127_out, OP0);
  not not_128 (not_128_out, OP5);
  not not_129 (not_129_out, OP4);
  not not_130 (not_130_out, OP2);
  not not_131 (not_131_out, OP0);
  not not_132 (not_132_out, OP5);
  not not_133 (not_133_out, OP4);
  not not_134 (not_134_out, OP3);
  not not_135 (not_135_out, OP2);
  not not_136 (not_136_out, OP1);
  not not_137 (not_137_out, OP0);
  not not_138 (not_138_out, F4);
  not not_139 (not_139_out, F3);
  not not_140 (not_140_out, F2);
  not not_141 (not_141_out, F1);
  not not_142 (not_142_out, F0);
  not not_143 (not_143_out, OP5);
  not not_144 (not_144_out, OP4);
  not not_145 (not_145_out, OP3);
  not not_146 (not_146_out, OP2);
  not not_147 (not_147_out, OP1);
  not not_148 (not_148_out, OP0);
  not not_149 (not_149_out, F4);
  not not_150 (not_150_out, F3);
  not not_151 (not_151_out, F2);
  not not_152 (not_152_out, F1);
  not not_153 (not_153_out, OP5);
  not not_154 (not_154_out, OP4);
  not not_155 (not_155_out, OP3);
  not not_156 (not_156_out, OP2);
  not not_157 (not_157_out, OP1);
  not not_158 (not_158_out, OP0);
  not not_159 (not_159_out, F4);
  not not_160 (not_160_out, F3);
  not not_161 (not_161_out, F2);
  not not_162 (not_162_out, F0);
  not not_163 (not_163_out, OP5);
  not not_164 (not_164_out, OP4);
  not not_165 (not_165_out, OP3);
  not not_166 (not_166_out, OP2);
  not not_167 (not_167_out, OP1);
  not not_168 (not_168_out, OP0);
  not not_169 (not_169_out, F4);
  not not_170 (not_170_out, F3);
  not not_171 (not_171_out, F1);
  not not_172 (not_172_out, F0);
  not not_173 (not_173_out, OP5);
  not not_174 (not_174_out, OP4);
  not not_175 (not_175_out, OP3);
  not not_176 (not_176_out, OP2);
  not not_177 (not_177_out, OP1);
  not not_178 (not_178_out, OP0);
  not not_179 (not_179_out, F4);
  not not_180 (not_180_out, F2);
  not not_181 (not_181_out, OP5);
  not not_182 (not_182_out, OP4);
  not not_183 (not_183_out, OP2);
  not not_184 (not_184_out, OP1);
  not not_185 (not_185_out, OP0);
  not not_186 (not_186_out, OP5);
  not not_187 (not_187_out, OP4);
  not not_188 (not_188_out, OP1);
  not not_189 (not_189_out, OP0);
  not not_190 (not_190_out, OP5);
  not not_191 (not_191_out, OP4);
  not not_192 (not_192_out, OP2);
  not not_193 (not_193_out, OP1);
  not not_194 (not_194_out, OP4);
  not not_195 (not_195_out, OP3);
  not not_196 (not_196_out, OP2);
  not not_197 (not_197_out, OP4);
  not not_198 (not_198_out, OP2);
  not not_199 (not_199_out, OP5);
  not not_200 (not_200_out, OP4);
  not not_201 (not_201_out, OP2);
  not not_202 (not_202_out, OP4);
  not not_203 (not_203_out, OP2);
  not not_204 (not_204_out, OP1);
  not not_205 (not_205_out, OP5);
  not not_206 (not_206_out, OP4);
  not not_207 (not_207_out, OP3);
  not not_208 (not_208_out, OP2);
  not not_209 (not_209_out, OP1);
  not not_210 (not_210_out, OP0);
  not not_211 (not_211_out, F4);
  not not_212 (not_212_out, F3);
  not not_213 (not_213_out, F1);
  not not_214 (not_214_out, OP5);
  not not_215 (not_215_out, OP4);
  not not_216 (not_216_out, OP3);
  not not_217 (not_217_out, OP2);
  not not_218 (not_218_out, OP1);
  not not_219 (not_219_out, OP0);
  not not_220 (not_220_out, F4);
  not not_221 (not_221_out, F3);
  not not_222 (not_222_out, OP5);
  not not_223 (not_223_out, OP4);
  not not_224 (not_224_out, OP3);
  not not_225 (not_225_out, OP2);
  not not_226 (not_226_out, OP1);
  not not_227 (not_227_out, OP0);
  not not_228 (not_228_out, F4);
  not not_229 (not_229_out, F2);
  not not_230 (not_230_out, F0);
  not not_231 (not_231_out, OP5);
  not not_232 (not_232_out, OP4);
  not not_233 (not_233_out, OP3);
  not not_234 (not_234_out, OP2);
  not not_235 (not_235_out, OP1);
  not not_236 (not_236_out, OP0);
  not not_237 (not_237_out, F4);
  not not_238 (not_238_out, F2);
  not not_239 (not_239_out, OP5);
  not not_240 (not_240_out, OP4);
  not not_241 (not_241_out, OP2);
  not not_242 (not_242_out, OP0);
  not not_243 (not_243_out, OP5);
  not not_244 (not_244_out, OP4);
  not not_245 (not_245_out, OP1);
  not not_246 (not_246_out, OP5);
  not not_247 (not_247_out, OP4);
  not not_248 (not_248_out, OP2);
  and and_1 (and_1_out, not_1_out, not_2_out, not_3_out, not_4_out, not_5_out, not_6_out, not_7_out, not_8_out, not_9_out, not_10_out, F1, F0);
  and and_2 (and_2_out, not_11_out, not_12_out, not_13_out, not_14_out, not_15_out, not_16_out, F5, not_17_out, not_18_out, not_19_out, not_20_out, not_21_out);
  and and_3 (and_3_out, not_22_out, not_23_out, not_24_out, not_25_out, not_26_out, not_27_out, F5, not_28_out, not_29_out, not_30_out, not_31_out, F0);
  and and_4 (and_4_out, not_32_out, not_33_out, not_34_out, not_35_out, not_36_out, not_37_out, F5, not_38_out, not_39_out, F2, not_40_out, not_41_out);
  and and_5 (and_5_out, not_42_out, not_43_out, not_44_out, not_45_out, not_46_out, not_47_out, F5, not_48_out, F3, not_49_out, F1, not_50_out);
  and and_6 (and_6_out, not_51_out, not_52_out, OP3, not_53_out, not_54_out, not_55_out);
  and and_7 (and_7_out, not_56_out, not_57_out, OP3, OP2, not_58_out, not_59_out);
  and and_8 (and_8_out, not_60_out, not_61_out, OP3, not_62_out, not_63_out, OP0);
  and and_9 (and_9_out, not_64_out, not_65_out, OP3, not_66_out, OP1, not_67_out);
  and and_10 (and_10_out, OP5, not_68_out, not_69_out, not_70_out, OP1, OP0);
  and and_11 (and_11_out, OP5, not_71_out, OP3, not_72_out, OP1, OP0);
  and and_12 (and_12_out, OP5, not_73_out, OP3, not_74_out, not_75_out, OP0);
  and and_13 (and_13_out, not_76_out, not_77_out, not_78_out, not_79_out, not_80_out, not_81_out, not_82_out, not_83_out, not_84_out, not_85_out, F1, not_86_out);
  and and_14 (and_14_out, not_87_out, not_88_out, not_89_out, not_90_out, not_91_out, not_92_out, F5, not_93_out, not_94_out, not_95_out, F1, not_96_out);
  and and_15 (and_15_out, not_97_out, not_98_out, not_99_out, not_100_out, not_101_out, not_102_out, F5, not_103_out, not_104_out, F2, not_105_out, not_106_out);
  and and_16 (and_16_out, not_107_out, not_108_out, not_109_out, not_110_out, not_111_out, not_112_out, F5, not_113_out, not_114_out, F2, F1, F0);
  and and_17 (and_17_out, not_115_out, not_116_out, not_117_out, not_118_out, not_119_out, not_120_out, F5, not_121_out, F3, not_122_out, F1, not_123_out);
  and and_18 (and_18_out, not_124_out, not_125_out, OP3, OP2, not_126_out, not_127_out);
  and and_19 (and_19_out, not_128_out, not_129_out, OP3, not_130_out, OP1, not_131_out);
  and and_20 (and_20_out, not_132_out, not_133_out, not_134_out, not_135_out, not_136_out, not_137_out, F5, not_138_out, not_139_out, not_140_out, not_141_out, not_142_out);
  and and_21 (and_21_out, not_143_out, not_144_out, not_145_out, not_146_out, not_147_out, not_148_out, F5, not_149_out, not_150_out, not_151_out, not_152_out, F0);
  and and_22 (and_22_out, not_153_out, not_154_out, not_155_out, not_156_out, not_157_out, not_158_out, F5, not_159_out, not_160_out, not_161_out, F1, not_162_out);
  and and_23 (and_23_out, not_163_out, not_164_out, not_165_out, not_166_out, not_167_out, not_168_out, F5, not_169_out, not_170_out, F2, not_171_out, not_172_out);
  and and_24 (and_24_out, not_173_out, not_174_out, not_175_out, not_176_out, not_177_out, not_178_out, F5, not_179_out, F3, not_180_out, F1, F0);
  and and_25 (and_25_out, not_181_out, not_182_out, OP3, not_183_out, not_184_out, not_185_out);
  and and_26 (and_26_out, not_186_out, not_187_out, OP3, OP2, not_188_out, not_189_out);
  and and_27 (and_27_out, not_190_out, not_191_out, OP3, not_192_out, not_193_out, OP0);
  and and_28 (and_28_out, OP5, not_194_out, not_195_out, not_196_out, OP1, OP0);
  and and_29 (and_29_out, OP5, not_197_out, OP3, not_198_out, OP1, OP0);
  and and_30 (and_30_out, not_199_out, not_200_out, OP3, not_201_out, OP1, OP0);
  and and_31 (and_31_out, OP5, not_202_out, OP3, not_203_out, not_204_out, OP0);
  and and_32 (and_32_out, not_205_out, not_206_out, not_207_out, not_208_out, not_209_out, not_210_out, F5, not_211_out, not_212_out, F2, not_213_out, F0);
  and and_33 (and_33_out, not_214_out, not_215_out, not_216_out, not_217_out, not_218_out, not_219_out, F5, not_220_out, not_221_out, F2, F1, F0);
  and and_34 (and_34_out, not_222_out, not_223_out, not_224_out, not_225_out, not_226_out, not_227_out, F5, not_228_out, F3, not_229_out, F1, not_230_out);
  and and_35 (and_35_out, not_231_out, not_232_out, not_233_out, not_234_out, not_235_out, not_236_out, F5, not_237_out, F3, not_238_out, F1, F0);
  and and_36 (and_36_out, not_239_out, not_240_out, OP3, not_241_out, OP1, not_242_out);
  and and_37 (and_37_out, not_243_out, not_244_out, OP3, OP2, not_245_out, OP0);
  and and_38 (and_38_out, not_246_out, not_247_out, OP3, not_248_out, OP1, OP0);
  or or_1 (S1, and_13_out, and_14_out, and_15_out, and_16_out, and_17_out, and_18_out, and_19_out);
  or or_2 (S3, and_32_out, and_33_out, and_34_out, and_35_out, and_36_out, and_37_out, and_38_out);
  or or_3 (S0, and_1_out, and_2_out, and_3_out, and_4_out, and_5_out, and_6_out, and_7_out, and_8_out, and_9_out, and_10_out, and_11_out, and_12_out);
  or or_4 (S2, and_20_out, and_21_out, and_22_out, and_23_out, and_24_out, and_25_out, and_26_out, and_27_out, and_28_out, and_29_out, and_30_out, and_31_out);
endmodule

module ctrl_sig_autogen (
  input  OP0,
  input  OP1,
  input  OP2,
  input  OP3,
  input  OP4,
  input  OP5,
  input  F0,
  input  F1,
  input  F2,
  input  F3,
  input  F4,
  input  F5,
  output MemToReg,
  output MemWrite,
  output ALU_SRC,
  output RegWrite,
  output SysCALL,
  output SignedExt,
  output RegDst,
  output BEQ,
  output BNE,
  output JR,
  output JUMP,
  output JAL,
  output Vshamt,
  output BLEZ,
  output HalfW
);

  wire and_2_out, and_3_out, and_4_out, and_5_out, and_6_out, and_7_out, and_8_out, and_9_out, and_10_out,
       and_11_out, and_12_out, and_13_out, and_14_out, and_15_out, and_16_out, and_17_out, and_18_out,
       and_19_out, and_20_out, and_21_out, and_22_out, and_23_out, and_24_out, and_25_out, and_26_out,
       and_27_out, and_28_out, and_29_out, and_30_out, and_31_out, and_32_out, and_34_out, and_35_out,
       and_36_out, and_37_out, and_38_out, and_39_out, and_40_out, and_41_out, and_42_out, and_43_out,
       and_44_out, and_45_out, and_46_out, and_47_out, and_48_out, and_49_out, and_50_out, and_51_out,
       and_52_out, and_53_out, and_54_out, and_55_out, not_1_out, not_2_out, not_3_out, not_4_out, not_5_out,
       not_6_out, not_7_out, not_8_out, not_9_out, not_10_out, not_11_out, not_12_out, not_13_out,
       not_14_out, not_15_out, not_16_out, not_17_out, not_18_out, not_19_out, not_20_out, not_21_out,
       not_22_out, not_23_out, not_24_out, not_25_out, not_26_out, not_27_out, not_28_out, not_29_out,
       not_30_out, not_31_out, not_32_out, not_33_out, not_34_out, not_35_out, not_36_out, not_37_out,
       not_38_out, not_39_out, not_40_out, not_41_out, not_42_out, not_43_out, not_44_out, not_45_out,
       not_46_out, not_47_out, not_48_out, not_49_out, not_50_out, not_51_out, not_52_out, not_53_out,
       not_54_out, not_55_out, not_56_out, not_57_out, not_58_out, not_59_out, not_60_out, not_61_out,
       not_62_out, not_63_out, not_64_out, not_65_out, not_66_out, not_67_out, not_68_out, not_69_out,
       not_70_out, not_71_out, not_72_out, not_73_out, not_74_out, not_75_out, not_76_out, not_77_out,
       not_78_out, not_79_out, not_80_out, not_81_out, not_82_out, not_83_out, not_84_out, not_85_out,
       not_86_out, not_87_out, not_88_out, not_89_out, not_90_out, not_91_out, not_92_out, not_93_out,
       not_94_out, not_95_out, not_96_out, not_97_out, not_98_out, not_99_out, not_100_out, not_101_out,
       not_102_out, not_103_out, not_104_out, not_105_out, not_106_out, not_107_out, not_108_out,
       not_109_out, not_110_out, not_111_out, not_112_out, not_113_out, not_114_out, not_115_out,
       not_116_out, not_117_out, not_118_out, not_119_out, not_120_out, not_121_out, not_122_out,
       not_123_out, not_124_out, not_125_out, not_126_out, not_127_out, not_128_out, not_129_out,
       not_130_out, not_131_out, not_132_out, not_133_out, not_134_out, not_135_out, not_136_out,
       not_137_out, not_138_out, not_139_out, not_140_out, not_141_out, not_142_out, not_143_out,
       not_144_out, not_145_out, not_146_out, not_147_out, not_148_out, not_149_out, not_150_out,
       not_151_out, not_152_out, not_153_out, not_154_out, not_155_out, not_156_out, not_157_out,
       not_158_out, not_159_out, not_160_out, not_161_out, not_162_out, not_163_out, not_164_out,
       not_165_out, not_166_out, not_167_out, not_168_out, not_169_out, not_170_out, not_171_out,
       not_172_out, not_173_out, not_174_out, not_175_out, not_176_out, not_177_out, not_178_out,
       not_179_out, not_180_out, not_181_out, not_182_out, not_183_out, not_184_out, not_185_out,
       not_186_out, not_187_out, not_188_out, not_189_out, not_190_out, not_191_out, not_192_out,
       not_193_out, not_194_out, not_195_out, not_196_out, not_197_out, not_198_out, not_199_out,
       not_200_out, not_201_out, not_202_out, not_203_out, not_204_out, not_205_out, not_206_out,
       not_207_out, not_208_out, not_209_out, not_210_out, not_211_out, not_212_out, not_213_out,
       not_214_out, not_215_out, not_216_out, not_217_out, not_218_out, not_219_out, not_220_out,
       not_221_out, not_222_out, not_223_out, not_224_out, not_225_out, not_226_out, not_227_out,
       not_228_out, not_229_out, not_230_out, not_231_out, not_232_out, not_233_out, not_234_out,
       not_235_out, not_236_out, not_237_out, not_238_out, not_239_out, not_240_out, not_241_out,
       not_242_out, not_243_out, not_244_out, not_245_out, not_246_out, not_247_out, not_248_out,
       not_249_out, not_250_out, not_251_out, not_252_out, not_253_out, not_254_out, not_255_out,
       not_256_out, not_257_out, not_258_out, not_259_out, not_260_out, not_261_out, not_262_out,
       not_263_out, not_264_out, not_265_out, not_266_out, not_267_out, not_268_out, not_269_out,
       not_270_out, not_271_out, not_272_out, not_273_out, not_274_out, not_275_out, not_276_out,
       not_277_out, not_278_out, not_279_out, not_280_out, not_281_out, not_282_out, not_283_out,
       not_284_out, not_285_out, not_286_out, not_287_out, not_288_out, not_289_out, not_290_out,
       not_291_out, not_292_out, not_293_out, not_294_out, not_295_out, not_296_out, not_297_out,
       not_298_out, not_299_out, not_300_out, not_301_out, not_302_out, not_303_out, not_304_out,
       not_305_out, not_306_out, not_307_out, not_308_out, not_309_out, not_310_out, not_311_out,
       not_312_out, not_313_out, not_314_out, not_315_out, not_316_out, not_317_out, not_318_out,
       not_319_out, not_320_out, not_321_out, not_322_out, not_323_out, not_324_out, not_325_out,
       not_326_out, not_327_out, not_328_out, not_329_out, not_330_out, not_331_out, not_332_out,
       not_333_out, not_334_out, not_335_out, not_336_out, not_337_out, not_338_out, not_339_out,
       not_340_out, not_341_out, not_342_out, not_343_out, not_344_out, not_345_out, not_346_out,
       not_347_out, not_348_out, not_349_out, not_350_out, not_351_out, not_352_out, not_353_out,
       not_354_out, not_355_out, not_356_out, not_357_out, not_358_out, not_359_out, not_360_out,
       not_361_out, not_362_out, not_363_out, not_364_out, not_365_out, not_366_out, not_367_out,
       not_368_out, not_369_out, not_370_out, not_371_out, not_372_out, not_373_out, not_374_out,
       not_375_out, not_376_out, not_377_out, not_378_out, not_379_out, not_380_out, not_381_out,
       not_382_out, not_383_out, not_384_out, not_385_out, not_386_out, not_387_out, not_388_out,
       not_389_out, not_390_out, not_391_out, not_392_out, not_393_out, not_394_out, not_395_out,
       not_396_out, not_397_out, not_398_out, not_399_out, not_400_out, not_401_out;

  not not_1 (not_1_out, OP4);
  not not_2 (not_2_out, OP3);
  not not_3 (not_3_out, OP2);
  not not_4 (not_4_out, OP4);
  not not_5 (not_5_out, OP2);
  not not_6 (not_6_out, OP4);
  not not_7 (not_7_out, OP2);
  not not_8 (not_8_out, OP1);
  not not_9 (not_9_out, OP5);
  not not_10 (not_10_out, OP4);
  not not_11 (not_11_out, OP2);
  not not_12 (not_12_out, OP1);
  not not_13 (not_13_out, OP0);
  not not_14 (not_14_out, OP5);
  not not_15 (not_15_out, OP4);
  not not_16 (not_16_out, OP1);
  not not_17 (not_17_out, OP0);
  not not_18 (not_18_out, OP5);
  not not_19 (not_19_out, OP4);
  not not_20 (not_20_out, OP2);
  not not_21 (not_21_out, OP1);
  not not_22 (not_22_out, OP5);
  not not_23 (not_23_out, OP4);
  not not_24 (not_24_out, OP2);
  not not_25 (not_25_out, OP0);
  not not_26 (not_26_out, OP5);
  not not_27 (not_27_out, OP4);
  not not_28 (not_28_out, OP1);
  not not_29 (not_29_out, OP4);
  not not_30 (not_30_out, OP3);
  not not_31 (not_31_out, OP2);
  not not_32 (not_32_out, OP4);
  not not_33 (not_33_out, OP2);
  not not_34 (not_34_out, OP5);
  not not_35 (not_35_out, OP4);
  not not_36 (not_36_out, OP2);
  not not_37 (not_37_out, OP4);
  not not_38 (not_38_out, OP2);
  not not_39 (not_39_out, OP1);
  not not_40 (not_40_out, OP5);
  not not_41 (not_41_out, OP4);
  not not_42 (not_42_out, OP3);
  not not_43 (not_43_out, OP2);
  not not_44 (not_44_out, OP1);
  not not_45 (not_45_out, OP0);
  not not_46 (not_46_out, F5);
  not not_47 (not_47_out, F4);
  not not_48 (not_48_out, F3);
  not not_49 (not_49_out, F2);
  not not_50 (not_50_out, F1);
  not not_51 (not_51_out, F0);
  not not_52 (not_52_out, OP5);
  not not_53 (not_53_out, OP4);
  not not_54 (not_54_out, OP3);
  not not_55 (not_55_out, OP2);
  not not_56 (not_56_out, OP1);
  not not_57 (not_57_out, OP0);
  not not_58 (not_58_out, F5);
  not not_59 (not_59_out, F4);
  not not_60 (not_60_out, F3);
  not not_61 (not_61_out, F2);
  not not_62 (not_62_out, OP5);
  not not_63 (not_63_out, OP4);
  not not_64 (not_64_out, OP3);
  not not_65 (not_65_out, OP2);
  not not_66 (not_66_out, OP1);
  not not_67 (not_67_out, OP0);
  not not_68 (not_68_out, F5);
  not not_69 (not_69_out, F4);
  not not_70 (not_70_out, F3);
  not not_71 (not_71_out, F2);
  not not_72 (not_72_out, F0);
  not not_73 (not_73_out, OP5);
  not not_74 (not_74_out, OP4);
  not not_75 (not_75_out, OP3);
  not not_76 (not_76_out, OP2);
  not not_77 (not_77_out, OP1);
  not not_78 (not_78_out, OP0);
  not not_79 (not_79_out, F4);
  not not_80 (not_80_out, F3);
  not not_81 (not_81_out, F2);
  not not_82 (not_82_out, F1);
  not not_83 (not_83_out, F0);
  not not_84 (not_84_out, OP5);
  not not_85 (not_85_out, OP4);
  not not_86 (not_86_out, OP3);
  not not_87 (not_87_out, OP2);
  not not_88 (not_88_out, OP1);
  not not_89 (not_89_out, OP0);
  not not_90 (not_90_out, F4);
  not not_91 (not_91_out, F3);
  not not_92 (not_92_out, F2);
  not not_93 (not_93_out, F1);
  not not_94 (not_94_out, OP5);
  not not_95 (not_95_out, OP4);
  not not_96 (not_96_out, OP3);
  not not_97 (not_97_out, OP2);
  not not_98 (not_98_out, OP1);
  not not_99 (not_99_out, OP0);
  not not_100 (not_100_out, F4);
  not not_101 (not_101_out, F3);
  not not_102 (not_102_out, F2);
  not not_103 (not_103_out, F0);
  not not_104 (not_104_out, OP5);
  not not_105 (not_105_out, OP4);
  not not_106 (not_106_out, OP3);
  not not_107 (not_107_out, OP2);
  not not_108 (not_108_out, OP1);
  not not_109 (not_109_out, OP0);
  not not_110 (not_110_out, F4);
  not not_111 (not_111_out, F3);
  not not_112 (not_112_out, F1);
  not not_113 (not_113_out, F0);
  not not_114 (not_114_out, OP5);
  not not_115 (not_115_out, OP4);
  not not_116 (not_116_out, OP3);
  not not_117 (not_117_out, OP2);
  not not_118 (not_118_out, OP1);
  not not_119 (not_119_out, OP0);
  not not_120 (not_120_out, F4);
  not not_121 (not_121_out, F3);
  not not_122 (not_122_out, F1);
  not not_123 (not_123_out, OP5);
  not not_124 (not_124_out, OP4);
  not not_125 (not_125_out, OP3);
  not not_126 (not_126_out, OP2);
  not not_127 (not_127_out, OP1);
  not not_128 (not_128_out, OP0);
  not not_129 (not_129_out, F4);
  not not_130 (not_130_out, F3);
  not not_131 (not_131_out, OP5);
  not not_132 (not_132_out, OP4);
  not not_133 (not_133_out, OP3);
  not not_134 (not_134_out, OP2);
  not not_135 (not_135_out, OP1);
  not not_136 (not_136_out, OP0);
  not not_137 (not_137_out, F4);
  not not_138 (not_138_out, F2);
  not not_139 (not_139_out, F0);
  not not_140 (not_140_out, OP5);
  not not_141 (not_141_out, OP4);
  not not_142 (not_142_out, OP3);
  not not_143 (not_143_out, OP2);
  not not_144 (not_144_out, OP1);
  not not_145 (not_145_out, OP0);
  not not_146 (not_146_out, F4);
  not not_147 (not_147_out, F2);
  not not_148 (not_148_out, OP5);
  not not_149 (not_149_out, OP4);
  not not_150 (not_150_out, OP3);
  not not_151 (not_151_out, OP2);
  not not_152 (not_152_out, OP5);
  not not_153 (not_153_out, OP4);
  not not_154 (not_154_out, OP2);
  not not_155 (not_155_out, OP1);
  not not_156 (not_156_out, OP0);
  not not_157 (not_157_out, OP5);
  not not_158 (not_158_out, OP4);
  not not_159 (not_159_out, OP1);
  not not_160 (not_160_out, OP0);
  not not_161 (not_161_out, OP5);
  not not_162 (not_162_out, OP4);
  not not_163 (not_163_out, OP2);
  not not_164 (not_164_out, OP1);
  not not_165 (not_165_out, OP5);
  not not_166 (not_166_out, OP4);
  not not_167 (not_167_out, OP2);
  not not_168 (not_168_out, OP0);
  not not_169 (not_169_out, OP5);
  not not_170 (not_170_out, OP4);
  not not_171 (not_171_out, OP1);
  not not_172 (not_172_out, OP4);
  not not_173 (not_173_out, OP3);
  not not_174 (not_174_out, OP2);
  not not_175 (not_175_out, OP5);
  not not_176 (not_176_out, OP4);
  not not_177 (not_177_out, OP3);
  not not_178 (not_178_out, OP2);
  not not_179 (not_179_out, OP1);
  not not_180 (not_180_out, OP0);
  not not_181 (not_181_out, F5);
  not not_182 (not_182_out, F4);
  not not_183 (not_183_out, F3);
  not not_184 (not_184_out, F1);
  not not_185 (not_185_out, F0);
  not not_186 (not_186_out, OP5);
  not not_187 (not_187_out, OP4);
  not not_188 (not_188_out, OP2);
  not not_189 (not_189_out, OP5);
  not not_190 (not_190_out, OP4);
  not not_191 (not_191_out, OP3);
  not not_192 (not_192_out, OP2);
  not not_193 (not_193_out, OP1);
  not not_194 (not_194_out, OP0);
  not not_195 (not_195_out, F5);
  not not_196 (not_196_out, F4);
  not not_197 (not_197_out, F1);
  not not_198 (not_198_out, F0);
  not not_199 (not_199_out, OP5);
  not not_200 (not_200_out, OP4);
  not not_201 (not_201_out, OP3);
  not not_202 (not_202_out, OP1);
  not not_203 (not_203_out, OP0);
  not not_204 (not_204_out, OP5);
  not not_205 (not_205_out, OP4);
  not not_206 (not_206_out, OP3);
  not not_207 (not_207_out, OP1);
  not not_208 (not_208_out, OP5);
  not not_209 (not_209_out, OP4);
  not not_210 (not_210_out, OP2);
  not not_211 (not_211_out, OP1);
  not not_212 (not_212_out, OP0);
  not not_213 (not_213_out, OP5);
  not not_214 (not_214_out, OP4);
  not not_215 (not_215_out, OP2);
  not not_216 (not_216_out, OP1);
  not not_217 (not_217_out, OP5);
  not not_218 (not_218_out, OP4);
  not not_219 (not_219_out, OP2);
  not not_220 (not_220_out, OP0);
  not not_221 (not_221_out, OP4);
  not not_222 (not_222_out, OP3);
  not not_223 (not_223_out, OP2);
  not not_224 (not_224_out, OP4);
  not not_225 (not_225_out, OP2);
  not not_226 (not_226_out, OP5);
  not not_227 (not_227_out, OP4);
  not not_228 (not_228_out, OP2);
  not not_229 (not_229_out, OP4);
  not not_230 (not_230_out, OP2);
  not not_231 (not_231_out, OP1);
  not not_232 (not_232_out, OP5);
  not not_233 (not_233_out, OP4);
  not not_234 (not_234_out, OP3);
  not not_235 (not_235_out, OP0);
  not not_236 (not_236_out, OP5);
  not not_237 (not_237_out, OP4);
  not not_238 (not_238_out, OP3);
  not not_239 (not_239_out, OP2);
  not not_240 (not_240_out, OP1);
  not not_241 (not_241_out, OP0);
  not not_242 (not_242_out, F5);
  not not_243 (not_243_out, F4);
  not not_244 (not_244_out, F3);
  not not_245 (not_245_out, F2);
  not not_246 (not_246_out, F1);
  not not_247 (not_247_out, F0);
  not not_248 (not_248_out, OP5);
  not not_249 (not_249_out, OP4);
  not not_250 (not_250_out, OP3);
  not not_251 (not_251_out, OP2);
  not not_252 (not_252_out, OP1);
  not not_253 (not_253_out, OP0);
  not not_254 (not_254_out, F5);
  not not_255 (not_255_out, F4);
  not not_256 (not_256_out, F3);
  not not_257 (not_257_out, F2);
  not not_258 (not_258_out, OP5);
  not not_259 (not_259_out, OP4);
  not not_260 (not_260_out, OP3);
  not not_261 (not_261_out, OP2);
  not not_262 (not_262_out, OP1);
  not not_263 (not_263_out, OP0);
  not not_264 (not_264_out, F5);
  not not_265 (not_265_out, F4);
  not not_266 (not_266_out, F3);
  not not_267 (not_267_out, F2);
  not not_268 (not_268_out, F0);
  not not_269 (not_269_out, OP5);
  not not_270 (not_270_out, OP4);
  not not_271 (not_271_out, OP3);
  not not_272 (not_272_out, OP2);
  not not_273 (not_273_out, OP1);
  not not_274 (not_274_out, OP0);
  not not_275 (not_275_out, F4);
  not not_276 (not_276_out, F3);
  not not_277 (not_277_out, F2);
  not not_278 (not_278_out, F1);
  not not_279 (not_279_out, F0);
  not not_280 (not_280_out, OP5);
  not not_281 (not_281_out, OP4);
  not not_282 (not_282_out, OP3);
  not not_283 (not_283_out, OP2);
  not not_284 (not_284_out, OP1);
  not not_285 (not_285_out, OP0);
  not not_286 (not_286_out, F4);
  not not_287 (not_287_out, F3);
  not not_288 (not_288_out, F2);
  not not_289 (not_289_out, F1);
  not not_290 (not_290_out, OP5);
  not not_291 (not_291_out, OP4);
  not not_292 (not_292_out, OP3);
  not not_293 (not_293_out, OP2);
  not not_294 (not_294_out, OP1);
  not not_295 (not_295_out, OP0);
  not not_296 (not_296_out, F4);
  not not_297 (not_297_out, F3);
  not not_298 (not_298_out, F2);
  not not_299 (not_299_out, F0);
  not not_300 (not_300_out, OP5);
  not not_301 (not_301_out, OP4);
  not not_302 (not_302_out, OP3);
  not not_303 (not_303_out, OP2);
  not not_304 (not_304_out, OP1);
  not not_305 (not_305_out, OP0);
  not not_306 (not_306_out, F4);
  not not_307 (not_307_out, F3);
  not not_308 (not_308_out, F1);
  not not_309 (not_309_out, F0);
  not not_310 (not_310_out, OP5);
  not not_311 (not_311_out, OP4);
  not not_312 (not_312_out, OP3);
  not not_313 (not_313_out, OP2);
  not not_314 (not_314_out, OP1);
  not not_315 (not_315_out, OP0);
  not not_316 (not_316_out, F4);
  not not_317 (not_317_out, F3);
  not not_318 (not_318_out, F1);
  not not_319 (not_319_out, OP5);
  not not_320 (not_320_out, OP4);
  not not_321 (not_321_out, OP3);
  not not_322 (not_322_out, OP2);
  not not_323 (not_323_out, OP1);
  not not_324 (not_324_out, OP0);
  not not_325 (not_325_out, F4);
  not not_326 (not_326_out, F3);
  not not_327 (not_327_out, OP5);
  not not_328 (not_328_out, OP4);
  not not_329 (not_329_out, OP3);
  not not_330 (not_330_out, OP2);
  not not_331 (not_331_out, OP1);
  not not_332 (not_332_out, OP0);
  not not_333 (not_333_out, F4);
  not not_334 (not_334_out, F2);
  not not_335 (not_335_out, F0);
  not not_336 (not_336_out, OP5);
  not not_337 (not_337_out, OP4);
  not not_338 (not_338_out, OP3);
  not not_339 (not_339_out, OP2);
  not not_340 (not_340_out, OP1);
  not not_341 (not_341_out, OP0);
  not not_342 (not_342_out, F4);
  not not_343 (not_343_out, F2);
  not not_344 (not_344_out, OP5);
  not not_345 (not_345_out, OP4);
  not not_346 (not_346_out, OP3);
  not not_347 (not_347_out, OP2);
  not not_348 (not_348_out, OP1);
  not not_349 (not_349_out, OP0);
  not not_350 (not_350_out, F5);
  not not_351 (not_351_out, F4);
  not not_352 (not_352_out, F3);
  not not_353 (not_353_out, F1);
  not not_354 (not_354_out, F0);
  not not_355 (not_355_out, OP5);
  not not_356 (not_356_out, OP4);
  not not_357 (not_357_out, OP3);
  not not_358 (not_358_out, OP1);
  not not_359 (not_359_out, OP0);
  not not_360 (not_360_out, OP5);
  not not_361 (not_361_out, OP4);
  not not_362 (not_362_out, OP3);
  not not_363 (not_363_out, OP1);
  not not_364 (not_364_out, OP5);
  not not_365 (not_365_out, OP4);
  not not_366 (not_366_out, OP3);
  not not_367 (not_367_out, OP2);
  not not_368 (not_368_out, OP1);
  not not_369 (not_369_out, OP0);
  not not_370 (not_370_out, F5);
  not not_371 (not_371_out, F4);
  not not_372 (not_372_out, F2);
  not not_373 (not_373_out, F1);
  not not_374 (not_374_out, F0);
  not not_375 (not_375_out, OP5);
  not not_376 (not_376_out, OP4);
  not not_377 (not_377_out, OP3);
  not not_378 (not_378_out, OP2);
  not not_379 (not_379_out, OP0);
  not not_380 (not_380_out, OP5);
  not not_381 (not_381_out, OP4);
  not not_382 (not_382_out, OP3);
  not not_383 (not_383_out, OP2);
  not not_384 (not_384_out, OP5);
  not not_385 (not_385_out, OP4);
  not not_386 (not_386_out, OP3);
  not not_387 (not_387_out, OP2);
  not not_388 (not_388_out, OP1);
  not not_389 (not_389_out, OP0);
  not not_390 (not_390_out, F5);
  not not_391 (not_391_out, F4);
  not not_392 (not_392_out, F3);
  not not_393 (not_393_out, F1);
  not not_394 (not_394_out, F0);
  not not_395 (not_395_out, OP0);
  not not_396 (not_396_out, OP3);
  not not_397 (not_397_out, OP4);
  not not_398 (not_398_out, OP5);
  not not_399 (not_399_out, OP1);
  not not_400 (not_400_out, OP2);
  not not_401 (not_401_out, OP4);
  and and_1 (MemToReg, OP5, not_1_out, not_2_out, not_3_out, OP1, OP0);
  and and_2 (and_2_out, OP5, not_4_out, OP3, not_5_out, OP1, OP0);
  and and_3 (and_3_out, OP5, not_6_out, OP3, not_7_out, not_8_out, OP0);
  and and_4 (and_4_out, not_9_out, not_10_out, OP3, not_11_out, not_12_out, not_13_out);
  and and_5 (and_5_out, not_14_out, not_15_out, OP3, OP2, not_16_out, not_17_out);
  and and_6 (and_6_out, not_18_out, not_19_out, OP3, not_20_out, not_21_out, OP0);
  and and_7 (and_7_out, not_22_out, not_23_out, OP3, not_24_out, OP1, not_25_out);
  and and_8 (and_8_out, not_26_out, not_27_out, OP3, OP2, not_28_out, OP0);
  and and_9 (and_9_out, OP5, not_29_out, not_30_out, not_31_out, OP1, OP0);
  and and_10 (and_10_out, OP5, not_32_out, OP3, not_33_out, OP1, OP0);
  and and_11 (and_11_out, not_34_out, not_35_out, OP3, not_36_out, OP1, OP0);
  and and_12 (and_12_out, OP5, not_37_out, OP3, not_38_out, not_39_out, OP0);
  and and_13 (and_13_out, not_40_out, not_41_out, not_42_out, not_43_out, not_44_out, not_45_out, not_46_out, not_47_out, not_48_out, not_49_out, not_50_out, not_51_out);
  and and_14 (and_14_out, not_52_out, not_53_out, not_54_out, not_55_out, not_56_out, not_57_out, not_58_out, not_59_out, not_60_out, not_61_out, F1, F0);
  and and_15 (and_15_out, not_62_out, not_63_out, not_64_out, not_65_out, not_66_out, not_67_out, not_68_out, not_69_out, not_70_out, not_71_out, F1, not_72_out);
  and and_16 (and_16_out, not_73_out, not_74_out, not_75_out, not_76_out, not_77_out, not_78_out, F5, not_79_out, not_80_out, not_81_out, not_82_out, not_83_out);
  and and_17 (and_17_out, not_84_out, not_85_out, not_86_out, not_87_out, not_88_out, not_89_out, F5, not_90_out, not_91_out, not_92_out, not_93_out, F0);
  and and_18 (and_18_out, not_94_out, not_95_out, not_96_out, not_97_out, not_98_out, not_99_out, F5, not_100_out, not_101_out, not_102_out, F1, not_103_out);
  and and_19 (and_19_out, not_104_out, not_105_out, not_106_out, not_107_out, not_108_out, not_109_out, F5, not_110_out, not_111_out, F2, not_112_out, not_113_out);
  and and_20 (and_20_out, not_114_out, not_115_out, not_116_out, not_117_out, not_118_out, not_119_out, F5, not_120_out, not_121_out, F2, not_122_out, F0);
  and and_21 (and_21_out, not_123_out, not_124_out, not_125_out, not_126_out, not_127_out, not_128_out, F5, not_129_out, not_130_out, F2, F1, F0);
  and and_22 (and_22_out, not_131_out, not_132_out, not_133_out, not_134_out, not_135_out, not_136_out, F5, not_137_out, F3, not_138_out, F1, not_139_out);
  and and_23 (and_23_out, not_140_out, not_141_out, not_142_out, not_143_out, not_144_out, not_145_out, F5, not_146_out, F3, not_147_out, F1, F0);
  and and_24 (and_24_out, not_148_out, not_149_out, not_150_out, not_151_out, OP1, OP0);
  and and_25 (and_25_out, not_152_out, not_153_out, OP3, not_154_out, not_155_out, not_156_out);
  and and_26 (and_26_out, not_157_out, not_158_out, OP3, OP2, not_159_out, not_160_out);
  and and_27 (and_27_out, not_161_out, not_162_out, OP3, not_163_out, not_164_out, OP0);
  and and_28 (and_28_out, not_165_out, not_166_out, OP3, not_167_out, OP1, not_168_out);
  and and_29 (and_29_out, not_169_out, not_170_out, OP3, OP2, not_171_out, OP0);
  and and_30 (and_30_out, OP5, not_172_out, not_173_out, not_174_out, OP1, OP0);
  and and_31 (and_31_out, not_175_out, not_176_out, not_177_out, not_178_out, not_179_out, not_180_out, not_181_out, not_182_out, not_183_out, F2, not_184_out, not_185_out);
  and and_32 (and_32_out, not_186_out, not_187_out, OP3, not_188_out, OP1, OP0);
  and and_33 (SysCALL, not_189_out, not_190_out, not_191_out, not_192_out, not_193_out, not_194_out, not_195_out, not_196_out, F3, F2, not_197_out, not_198_out);
  and and_34 (and_34_out, not_199_out, not_200_out, not_201_out, OP2, not_202_out, not_203_out);
  and and_35 (and_35_out, not_204_out, not_205_out, not_206_out, OP2, not_207_out, OP0);
  and and_36 (and_36_out, not_208_out, not_209_out, OP3, not_210_out, not_211_out, not_212_out);
  and and_37 (and_37_out, not_213_out, not_214_out, OP3, not_215_out, not_216_out, OP0);
  and and_38 (and_38_out, not_217_out, not_218_out, OP3, not_219_out, OP1, not_220_out);
  and and_39 (and_39_out, OP5, not_221_out, not_222_out, not_223_out, OP1, OP0);
  and and_40 (and_40_out, OP5, not_224_out, OP3, not_225_out, OP1, OP0);
  and and_41 (and_41_out, not_226_out, not_227_out, OP3, not_228_out, OP1, OP0);
  and and_42 (and_42_out, OP5, not_229_out, OP3, not_230_out, not_231_out, OP0);
  and and_43 (and_43_out, not_232_out, not_233_out, not_234_out, OP2, OP1, not_235_out);
  and and_44 (and_44_out, not_236_out, not_237_out, not_238_out, not_239_out, not_240_out, not_241_out, not_242_out, not_243_out, not_244_out, not_245_out, not_246_out, not_247_out);
  and and_45 (and_45_out, not_248_out, not_249_out, not_250_out, not_251_out, not_252_out, not_253_out, not_254_out, not_255_out, not_256_out, not_257_out, F1, F0);
  and and_46 (and_46_out, not_258_out, not_259_out, not_260_out, not_261_out, not_262_out, not_263_out, not_264_out, not_265_out, not_266_out, not_267_out, F1, not_268_out);
  and and_47 (and_47_out, not_269_out, not_270_out, not_271_out, not_272_out, not_273_out, not_274_out, F5, not_275_out, not_276_out, not_277_out, not_278_out, not_279_out);
  and and_48 (and_48_out, not_280_out, not_281_out, not_282_out, not_283_out, not_284_out, not_285_out, F5, not_286_out, not_287_out, not_288_out, not_289_out, F0);
  and and_49 (and_49_out, not_290_out, not_291_out, not_292_out, not_293_out, not_294_out, not_295_out, F5, not_296_out, not_297_out, not_298_out, F1, not_299_out);
  and and_50 (and_50_out, not_300_out, not_301_out, not_302_out, not_303_out, not_304_out, not_305_out, F5, not_306_out, not_307_out, F2, not_308_out, not_309_out);
  and and_51 (and_51_out, not_310_out, not_311_out, not_312_out, not_313_out, not_314_out, not_315_out, F5, not_316_out, not_317_out, F2, not_318_out, F0);
  and and_52 (and_52_out, not_319_out, not_320_out, not_321_out, not_322_out, not_323_out, not_324_out, F5, not_325_out, not_326_out, F2, F1, F0);
  and and_53 (and_53_out, not_327_out, not_328_out, not_329_out, not_330_out, not_331_out, not_332_out, F5, not_333_out, F3, not_334_out, F1, not_335_out);
  and and_54 (and_54_out, not_336_out, not_337_out, not_338_out, not_339_out, not_340_out, not_341_out, F5, not_342_out, F3, not_343_out, F1, F0);
  and and_55 (and_55_out, not_344_out, not_345_out, not_346_out, not_347_out, not_348_out, not_349_out, not_350_out, not_351_out, not_352_out, F2, not_353_out, not_354_out);
  and and_56 (BEQ, not_355_out, not_356_out, not_357_out, OP2, not_358_out, not_359_out);
  and and_57 (BNE, not_360_out, not_361_out, not_362_out, OP2, not_363_out, OP0);
  and and_58 (JR, not_364_out, not_365_out, not_366_out, not_367_out, not_368_out, not_369_out, not_370_out, not_371_out, F3, not_372_out, not_373_out, not_374_out);
  and and_59 (JUMP, not_375_out, not_376_out, not_377_out, not_378_out, OP1, not_379_out);
  and and_60 (JAL, not_380_out, not_381_out, not_382_out, not_383_out, OP1, OP0);
  and and_61 (Vshamt, not_384_out, not_385_out, not_386_out, not_387_out, not_388_out, not_389_out, not_390_out, not_391_out, not_392_out, F2, not_393_out, not_394_out);
  and and_62 (BLEZ, not_395_out, OP1, OP2, not_396_out, not_397_out, not_398_out);
  and and_63 (HalfW, OP0, not_399_out, not_400_out, OP3, not_401_out, OP5);
  or or_1 (MemWrite, and_2_out, and_3_out);
  or or_2 (ALU_SRC, and_4_out, and_5_out, and_6_out, and_7_out, and_8_out, and_9_out, and_10_out, and_11_out, and_12_out);
  or or_3 (SignedExt, and_34_out, and_35_out, and_36_out, and_37_out, and_38_out, and_39_out, and_40_out, and_41_out, and_42_out, and_43_out);
  or or_4 (RegWrite, and_13_out, and_14_out, and_15_out, and_16_out, and_17_out, and_18_out, and_19_out, and_20_out, and_21_out, and_22_out, and_23_out, and_24_out, and_25_out, and_26_out, and_27_out, and_28_out, and_29_out, and_30_out, and_31_out, and_32_out);
  or or_5 (RegDst, and_44_out, and_45_out, and_46_out, and_47_out, and_48_out, and_49_out, and_50_out, and_51_out, and_52_out, and_53_out, and_54_out, and_55_out);
endmodule

// ALU
module MIPS_ALU (
  input  [4:0] shamt,
  input  [31:0] X,
  input  [31:0] Y,
  input  [3:0] AluOP,
  output Equal,
  output [31:0] Result,
  output [31:0] Result_2,
  output Less
);

  wire [0:0] comparator_1_lt, comparator_2_lt;
  wire [31:0] adder_1_out, AND_out, divider_1_out, divider_1_rem, multiplier_1_cout, multiplier_1_out,
       NOR_out, OR_out, shifter_1_out, shifter_2_out, shifter_3_out, subtractor_1_out, XOR_out;

  assign AND_out = X & Y;  // AND_Gate AND, 32 bits wide
  assign OR_out = X | Y;  // OR_Gate OR, 32 bits wide
  Shifter #(.width(32), .shift("ll")) shifter_1 (.in(Y), .\dist (shamt), .out(shifter_1_out));
  Shifter #(.width(32), .shift("ar")) shifter_2 (.in(Y), .\dist (shamt), .out(shifter_2_out));
  Shifter #(.width(32), .shift("lr")) shifter_3 (.in(Y), .\dist (shamt), .out(shifter_3_out));
  Multiplier #(.width(32)) multiplier_1 (.a(X), .b(Y), .out(multiplier_1_out), .cout(multiplier_1_cout));  // open: cin
  Divider #(.width(32)) divider_1 (.a(X), .b(Y), .out(divider_1_out), .rem(divider_1_rem));  // open: upper
  Adder #(.width(32)) adder_1 (.a(X), .b(Y), .out(adder_1_out));  // open: cin, cout
  Subtractor #(.width(32)) subtractor_1 (.a(X), .b(Y), .out(subtractor_1_out));  // open: bin, bout
  assign XOR_out = X ^ Y;  // XOR_Gate XOR, 32 bits wide
  assign NOR_out = ~(X | Y);  // NOR_Gate NOR, 32 bits wide
  Comparator #(.width(32), .mode("twosComplement")) comparator_1 (
    .a(X), .b(Y), .eq(Equal), .lt(comparator_1_lt[0]));  // open: gt
  Comparator #(.width(32), .mode("unsigned")) comparator_2 (.a(X), .b(Y), .lt(comparator_2_lt[0]));  // open: gt, eq
  Comparator #(.width(32), .mode("twosComplement")) comparator_3 (.a(X), .b(Y), .lt(Less));  // open: gt, eq
  Multiplexer #(.select(4), .width(32), .disabled(0), .enable("false")) multiplexer_1 (
    .in0(shifter_1_out), .in1(shifter_2_out), .in2(shifter_3_out), .in3(multiplier_1_out),
    .in4(divider_1_out), .in5(adder_1_out), .in6(subtractor_1_out), .in7(AND_out), .in8(OR_out),
    .in9(XOR_out), .in10(NOR_out), .in11({{31{1'b0}}, comparator_1_lt[0]}),
    .in12({{31{1'b0}}, comparator_2_lt[0]}), .in13({32{1'b0}}), .in14({32{1'b0}}), .in15({32{1'b0}}),
    .out(Result), .sel(AluOP));
  Multiplexer #(.select(4), .width(32), .disabled(0), .enable("false")) multiplexer_2 (
    .in0({32{1'b0}}), .in1({32{1'b0}}), .in2({32{1'b0}}), .in3(multiplier_1_cout), .in4(divider_1_rem),
    .in5({32{1'b0}}), .in6({32{1'b0}}), .in7({32{1'b0}}), .in8({32{1'b0}}), .in9({32{1'b0}}),
    .in10({32{1'b0}}), .in11({32{1'b0}}), .in12({32{1'b0}}), .in13({32{1'b0}}), .in14({32{1'b0}}),
    .in15({32{1'b0}}), .out(Result_2), .sel(AluOP));

  // Other names for the same wires on the sheet: Result2[31:0] = Result_2; S[3:0] = AluOP

  // Notes on the sheet:
  //   不要改变此引脚区域内容，也不要改变ALU封装形式
  //   输入引脚
  //   输出引脚
endmodule

module MIPS_Regifile (
  input  [31:0] Din,
  input  Clk,
  input  WE,
  input  [4:0] R1Adr,
  input  [4:0] WAdr,
  input  [4:0] R2Adr,
  output [31:0] R1,
  output [31:0] R2
);

  // RegisterFile registerfile_1: pin names not known; wires that end beside it: Din, Clk, WE, WAdr, R1Adr, R2Adr, R1, R2
endmodule

module syscall_process (
  input  Syscall,
  input  CLK,
  input  [31:0] R2,
  input  [31:0] R1,
  output Pause,
  output [31:0] LedData,
  output Get_KB_in,
  output Screen_opt,
  output Cycles,
  output Get_Bitmap,
  output CopyToRAM,
  output FrameFlush
);

  wire and_1_out, and_2_out, comparator_1_eq, comparator_2_eq, comparator_3_eq, comparator_4_eq,
       comparator_5_eq, comparator_6_eq, comparator_7_eq, comparator_8_eq;

  Comparator #(.width(32), .mode("twosComplement")) comparator_1 (
    .a(32'h32), .b(R1), .eq(comparator_1_eq));  // open: gt, lt
  Comparator #(.width(32), .mode("twosComplement")) comparator_2 (
    .a(R1), .b(32'h22), .eq(comparator_2_eq));  // open: gt, lt
  Comparator #(.width(32), .mode("twosComplement")) comparator_3 (
    .a(R1), .b(32'h10), .eq(comparator_3_eq));  // open: gt, lt
  Comparator #(.width(32), .mode("twosComplement")) comparator_4 (
    .a(R1), .b(32'h20), .eq(comparator_4_eq));  // open: gt, lt
  Comparator #(.width(32), .mode("twosComplement")) comparator_5 (
    .a(R1), .b(32'h31), .eq(comparator_5_eq));  // open: gt, lt
  Comparator #(.width(32), .mode("twosComplement")) comparator_6 (
    .a(R1), .b(32'h21), .eq(comparator_6_eq));  // open: gt, lt
  Comparator #(.width(32), .mode("twosComplement")) comparator_7 (
    .a(R1), .b(32'h23), .eq(comparator_7_eq));  // open: gt, lt
  Comparator #(.width(32), .mode("twosComplement")) comparator_8 (
    .a(R1), .b(32'h24), .eq(comparator_8_eq));  // open: gt, lt
  and and_1 (and_1_out, Syscall, comparator_1_eq);
  and and_2 (and_2_out, Syscall, comparator_2_eq);
  and and_3 (Get_KB_in, Syscall, comparator_3_eq);
  and and_4 (Screen_opt, Syscall, comparator_4_eq);
  and and_5 (Cycles, Syscall, comparator_5_eq);
  and and_6 (Get_Bitmap, Syscall, comparator_6_eq);
  and and_7 (CopyToRAM, Syscall, comparator_7_eq);
  and and_8 (FrameFlush, Syscall, comparator_8_eq);
  Register #(.width(1), .trigger("rising"), .Select("low")) register_1 (
    .D(and_1_out), .Q(Pause), .clk(CLK));  // open: en, clr
  Register #(.width(32), .trigger("rising"), .Select("low")) register_2 (
    .D(R2), .en(and_2_out), .Q(LedData), .clk(CLK));  // open: clr
endmodule

module reg_choose_logic (
  input  [4:0] _21_25,
  input  Syscall,
  input  RegDst,
  input  [4:0] _16_20,
  input  [4:0] _11_15,
  input  JAL,
  input  [31:0] WriteBack_Data,
  input  [31:0] PC_plus_four,
  input  [4:0] _6_10,
  output [4:0] R1Adr,
  output [4:0] R2Adr,
  output [4:0] WAdr,
  output [31:0] RDin,
  output [4:0] Shamt
);

  wire [4:0] multiplexer_1_out;

  Multiplexer #(.select(1), .width(5), .disabled(0), .enable("false")) multiplexer_1 (
    .in0(_16_20), .in1(_11_15), .out(multiplexer_1_out), .sel(RegDst));
  Multiplexer #(.select(1), .width(5), .disabled(0), .enable("false")) multiplexer_2 (
    .in0(_21_25), .in1(5'b00010), .out(R1Adr), .sel(Syscall));
  Multiplexer #(.select(1), .width(5), .disabled(0), .enable("false")) multiplexer_3 (
    .in0(_16_20), .in1(5'b00100), .out(R2Adr), .sel(Syscall));
  Multiplexer #(.select(1), .width(5), .disabled(0), .enable("false")) multiplexer_4 (
    .in0(multiplexer_1_out), .in1({5{1'b1}}), .out(WAdr), .sel(JAL));
  Multiplexer #(.select(1), .width(32), .disabled(0), .enable("false")) multiplexer_5 (
    .in0(WriteBack_Data), .in1(PC_plus_four), .out(RDin), .sel(JAL));

  assign Shamt = _6_10;
endmodule

module PC_update_logic (
  input  Blez,
  input  Less,
  input  Equal,
  input  Beq,
  input  Bne,
  input  JAL,
  input  JMP,
  input  JR,
  input  [31:0] BAddr,
  input  [31:0] PC_plus_four,
  input  [31:0] JAddr,
  input  [31:0] JRAddr,
  output BranchSig,
  output Branched,
  output [31:0] PC_Next
);

  wire and_1_out, and_2_out, and_3_out, nor_1_out, or_1_out, or_2_out, or_4_out;
  wire [1:0] priority_encoder_1_out;

  or or_1 (or_1_out, Less, Equal);
  and and_1 (and_1_out, Equal, Beq);
  and and_2 (and_2_out, ~Equal, Bne);  // AND_Gate
  or or_2 (or_2_out, JAL, JMP);
  or or_3 (BranchSig, Blez, Beq, Bne, JAL, JMP, JR);
  and and_3 (and_3_out, Blez, or_1_out);
  or or_4 (or_4_out, and_3_out, and_1_out, and_2_out);
  nor nor_1 (nor_1_out, and_3_out, and_1_out, and_2_out, JR, or_2_out);
  or or_5 (Branched, or_4_out, or_2_out, JR);
  Priority_Encoder #(.select(2), .disabled(0)) priority_encoder_1 (
    .in0(nor_1_out), .in1(or_4_out), .in2(or_2_out), .in3(JR), .out(priority_encoder_1_out));  // open: gs, en_out, en_in
  Multiplexer #(.select(2), .width(32), .disabled(0), .enable("false")) multiplexer_1 (
    .in0(PC_plus_four), .in1(BAddr), .in2(JAddr), .in3(JRAddr), .out(PC_Next), .sel(priority_encoder_1_out));
endmodule

module IF_ID (
  input  [31:0] Instr,
  input  PredictJump,
  input  [31:0] PC,
  input  [31:0] PC_plus_four,
  input  CLK,
  input  CLR,
  input  Stall,
  output [31:0] Instr_Out,
  output PredictJump_Out,
  output [31:0] PC_Out,
  output [31:0] PC_plus_four_Out
);

  wire multiplexer_2_out;
  wire [31:0] multiplexer_1_out, multiplexer_3_out, multiplexer_4_out;

  Multiplexer #(.select(1), .width(32), .disabled(0), .enable("false")) multiplexer_1 (
    .in0(Instr), .in1({32{1'b0}}), .out(multiplexer_1_out), .sel(CLR));
  Multiplexer #(.select(1), .width(1), .disabled(0), .enable("false")) multiplexer_2 (
    .in0(PredictJump), .in1(1'b0), .out(multiplexer_2_out), .sel(CLR));
  Multiplexer #(.select(1), .width(32), .disabled(0), .enable("false")) multiplexer_3 (
    .in0(PC), .in1({32{1'b0}}), .out(multiplexer_3_out), .sel(CLR));
  Multiplexer #(.select(1), .width(32), .disabled(0), .enable("false")) multiplexer_4 (
    .in0(PC_plus_four), .in1({32{1'b0}}), .out(multiplexer_4_out), .sel(CLR));
  Register #(.width(32), .trigger("rising"), .Select("low")) register_1 (
    .D(multiplexer_1_out), .en(Stall), .Q(Instr_Out), .clk(CLK));  // open: clr
  Register #(.width(1), .trigger("rising"), .Select("low")) register_2 (
    .D(multiplexer_2_out), .en(Stall), .Q(PredictJump_Out), .clk(CLK));  // open: clr
  Register #(.width(32), .trigger("rising"), .Select("low")) register_3 (
    .D(multiplexer_3_out), .en(Stall), .Q(PC_Out), .clk(CLK));  // open: clr
  Register #(.width(32), .trigger("rising"), .Select("low")) register_4 (
    .D(multiplexer_4_out), .en(Stall), .Q(PC_plus_four_Out), .clk(CLK));  // open: clr
endmodule

module ID_EX (
  input  ERET,
  input  JR,
  input  JMP,
  input  JAL,
  input  BLEZ,
  input  BEQ,
  input  BNE,
  input  MemToReg,
  input  RegWrite,
  input  MemWrite,
  input  HalfW,
  input  AluSrcB,
  input  Syscall,
  input  MTC,
  input  MFC,
  input  [4:0] Shamt,
  input  [31:0] R1,
  input  [1:0] R1_Forward,
  input  [1:0] R2_Forward,
  input  [31:0] R2,
  input  [3:0] AluOp,
  input  [31:0] ExtData,
  input  [4:0] WAdr,
  input  PredictJump,
  input  [31:0] PC,
  input  [31:0] Instr,
  input  [31:0] PC_plus_four,
  input  [31:0] JAddr,
  input  CLK,
  input  CLR,
  output ERET_Out,
  output JR_Out,
  output JMP_Out,
  output JAL_Out,
  output BLEZ_Out,
  output BEQ_Out,
  output BNE_Out,
  output MemToReg_Out,
  output RegWrite_Out,
  output MemWrite_Out,
  output HalfW_Out,
  output AluSrcB_Out,
  output Syscall_Out,
  output MTC_Out,
  output MFC_Out,
  output [4:0] Shamt_Out,
  output [31:0] R1_Out,
  output [1:0] R1_Forward_Out,
  output [1:0] R2_Forward_Out,
  output [31:0] R2_Out,
  output [3:0] AluOp_Out,
  output [31:0] ExtData_Out,
  output [4:0] WAdr_Out,
  output PredictJump_Out,
  output [31:0] PC_Out,
  output [31:0] Instr_out,
  output [31:0] PC_plus_four_Out,
  output [31:0] JAddr_Out
);

  wire multiplexer_10_out;
  wire [1:0] multiplexer_4_out, multiplexer_5_out;
  wire [3:0] multiplexer_7_out;
  wire [4:0] multiplexer_2_out, multiplexer_9_out;
  wire [14:0] multiplexer_1_out;
  wire [31:0] multiplexer_3_out, multiplexer_6_out, multiplexer_8_out, multiplexer_11_out,
       multiplexer_12_out, multiplexer_13_out, multiplexer_14_out;

  Multiplexer #(.select(1), .width(15), .disabled(0), .enable("false")) multiplexer_1 (
    .in0({MFC, MTC, Syscall, AluSrcB, HalfW, MemWrite, RegWrite, MemToReg, BNE, BEQ, BLEZ, JAL, JMP, JR, ERET}),
    .in1({15{1'b0}}), .out(multiplexer_1_out), .sel(CLR));
  Multiplexer #(.select(1), .width(5), .disabled(0), .enable("false")) multiplexer_2 (
    .in0(Shamt), .in1({5{1'b0}}), .out(multiplexer_2_out), .sel(CLR));
  Multiplexer #(.select(1), .width(32), .disabled(0), .enable("false")) multiplexer_3 (
    .in0(R1), .in1({32{1'b0}}), .out(multiplexer_3_out), .sel(CLR));
  Multiplexer #(.select(1), .width(2), .disabled(0), .enable("false")) multiplexer_4 (
    .in0(R1_Forward), .in1(2'b00), .out(multiplexer_4_out), .sel(CLR));
  Multiplexer #(.select(1), .width(2), .disabled(0), .enable("false")) multiplexer_5 (
    .in0(R2_Forward), .in1(2'b00), .out(multiplexer_5_out), .sel(CLR));
  Multiplexer #(.select(1), .width(32), .disabled(0), .enable("false")) multiplexer_6 (
    .in0(R2), .in1({32{1'b0}}), .out(multiplexer_6_out), .sel(CLR));
  Multiplexer #(.select(1), .width(4), .disabled(0), .enable("false")) multiplexer_7 (
    .in0(AluOp), .in1(4'b0000), .out(multiplexer_7_out), .sel(CLR));
  Multiplexer #(.select(1), .width(32), .disabled(0), .enable("false")) multiplexer_8 (
    .in0(ExtData), .in1({32{1'b0}}), .out(multiplexer_8_out), .sel(CLR));
  Multiplexer #(.select(1), .width(5), .disabled(0), .enable("false")) multiplexer_9 (
    .in0(WAdr), .in1({5{1'b0}}), .out(multiplexer_9_out), .sel(CLR));
  Multiplexer #(.select(1), .width(1), .disabled(0), .enable("false")) multiplexer_10 (
    .in0(PredictJump), .in1(1'b0), .out(multiplexer_10_out), .sel(CLR));
  Multiplexer #(.select(1), .width(32), .disabled(0), .enable("false")) multiplexer_11 (
    .in0(PC), .in1({32{1'b0}}), .out(multiplexer_11_out), .sel(CLR));
  Multiplexer #(.select(1), .width(32), .disabled(0), .enable("false")) multiplexer_12 (
    .in0(Instr), .in1({32{1'b0}}), .out(multiplexer_12_out), .sel(CLR));
  Multiplexer #(.select(1), .width(32), .disabled(0), .enable("false")) multiplexer_13 (
    .in0(PC_plus_four), .in1({32{1'b0}}), .out(multiplexer_13_out), .sel(CLR));
  Multiplexer #(.select(1), .width(32), .disabled(0), .enable("false")) multiplexer_14 (
    .in0(JAddr), .in1({32{1'b0}}), .out(multiplexer_14_out), .sel(CLR));
  Register #(.width(15), .trigger("rising"), .Select("low")) register_1 (
    .D(multiplexer_1_out),
    .Q({MFC_Out, MTC_Out, Syscall_Out, AluSrcB_Out, HalfW_Out, MemWrite_Out, RegWrite_Out, MemToReg_Out, BNE_Out, BEQ_Out, BLEZ_Out, JAL_Out, JMP_Out, JR_Out, ERET_Out}),
    .clk(CLK));  // open: en, clr
  Register #(.width(5), .trigger("rising"), .Select("low")) register_2 (
    .D(multiplexer_2_out), .Q(Shamt_Out), .clk(CLK));  // open: en, clr
  Register #(.width(32), .trigger("rising"), .Select("low")) register_3 (
    .D(multiplexer_3_out), .Q(R1_Out), .clk(CLK));  // open: en, clr
  Register #(.width(2), .trigger("rising"), .Select("low")) register_4 (
    .D(multiplexer_4_out), .Q(R1_Forward_Out), .clk(CLK));  // open: en, clr
  Register #(.width(2), .trigger("rising"), .Select("low")) register_5 (
    .D(multiplexer_5_out), .Q(R2_Forward_Out), .clk(CLK));  // open: en, clr
  Register #(.width(32), .trigger("rising"), .Select("low")) register_6 (
    .D(multiplexer_6_out), .Q(R2_Out), .clk(CLK));  // open: en, clr
  Register #(.width(4), .trigger("rising"), .Select("low")) register_7 (
    .D(multiplexer_7_out), .Q(AluOp_Out), .clk(CLK));  // open: en, clr
  Register #(.width(32), .trigger("rising"), .Select("low")) register_8 (
    .D(multiplexer_8_out), .Q(ExtData_Out), .clk(CLK));  // open: en, clr
  Register #(.width(5), .trigger("rising"), .Select("low")) register_9 (
    .D(multiplexer_9_out), .Q(WAdr_Out), .clk(CLK));  // open: en, clr
  Register #(.width(1), .trigger("rising"), .Select("low")) register_10 (
    .D(multiplexer_10_out), .Q(PredictJump_Out), .clk(CLK));  // open: en, clr
  Register #(.width(32), .trigger("rising"), .Select("low")) register_11 (
    .D(multiplexer_11_out), .Q(PC_Out), .clk(CLK));  // open: en, clr
  Register #(.width(32), .trigger("rising"), .Select("low")) register_12 (
    .D(multiplexer_12_out), .Q(Instr_out), .clk(CLK));  // open: en, clr
  Register #(.width(32), .trigger("rising"), .Select("low")) register_13 (
    .D(multiplexer_13_out), .Q(PC_plus_four_Out), .clk(CLK));  // open: en, clr
  Register #(.width(32), .trigger("rising"), .Select("low")) register_14 (
    .D(multiplexer_14_out), .Q(JAddr_Out), .clk(CLK));  // open: en, clr
endmodule

module EX_MEM (
  input  JAL,
  input  MemToReg,
  input  RegWrite,
  input  MemWrite,
  input  HalfW,
  input  Syscall,
  input  [31:0] AluResult,
  input  [31:0] R1,
  input  [31:0] R2,
  input  [31:0] PC,
  input  [31:0] Instr,
  input  [31:0] PC_plus_four,
  input  [4:0] WAdr,
  input  CLR,
  input  CLK,
  output JAL_Out,
  output MemToReg_Out,
  output RegWrite_Out,
  output MemWrite_Out,
  output HalfW_Out,
  output Syscall_Out,
  output [31:0] AluResult_Out,
  output [31:0] R1_Out,
  output [31:0] R2_Out,
  output [31:0] PC_Out,
  output [31:0] Instr_out,
  output [31:0] PC_plus_four_Out,
  output [4:0] WAdr_Out
);

  wire [4:0] multiplexer_8_out;
  wire [5:0] multiplexer_1_out;
  wire [31:0] multiplexer_2_out, multiplexer_3_out, multiplexer_4_out, multiplexer_5_out, multiplexer_6_out,
       multiplexer_7_out;

  Multiplexer #(.select(1), .width(6), .disabled(0), .enable("false")) multiplexer_1 (
    .in0({Syscall, HalfW, MemWrite, RegWrite, MemToReg, JAL}), .in1({6{1'b0}}), .out(multiplexer_1_out),
    .sel(CLR));
  Multiplexer #(.select(1), .width(32), .disabled(0), .enable("false")) multiplexer_2 (
    .in0(AluResult), .in1({32{1'b0}}), .out(multiplexer_2_out), .sel(CLR));
  Multiplexer #(.select(1), .width(32), .disabled(0), .enable("false")) multiplexer_3 (
    .in0(R1), .in1({32{1'b0}}), .out(multiplexer_3_out), .sel(CLR));
  Multiplexer #(.select(1), .width(32), .disabled(0), .enable("false")) multiplexer_4 (
    .in0(R2), .in1({32{1'b0}}), .out(multiplexer_4_out), .sel(CLR));
  Multiplexer #(.select(1), .width(32), .disabled(0), .enable("false")) multiplexer_5 (
    .in0(PC), .in1({32{1'b0}}), .out(multiplexer_5_out), .sel(CLR));
  Multiplexer #(.select(1), .width(32), .disabled(0), .enable("false")) multiplexer_6 (
    .in0(Instr), .in1({32{1'b0}}), .out(multiplexer_6_out), .sel(CLR));
  Multiplexer #(.select(1), .width(32), .disabled(0), .enable("false")) multiplexer_7 (
    .in0(PC_plus_four), .in1({32{1'b0}}), .out(multiplexer_7_out), .sel(CLR));
  Multiplexer #(.select(1), .width(5), .disabled(0), .enable("false")) multiplexer_8 (
    .in0(WAdr), .in1({5{1'b0}}), .out(multiplexer_8_out), .sel(CLR));
  Register #(.width(6), .trigger("rising"), .Select("low")) register_1 (
    .D(multiplexer_1_out), .Q({Syscall_Out, HalfW_Out, MemWrite_Out, RegWrite_Out, MemToReg_Out, JAL_Out}),
    .clk(CLK));  // open: en, clr
  Register #(.width(32), .trigger("rising"), .Select("low")) register_2 (
    .D(multiplexer_2_out), .Q(AluResult_Out), .clk(CLK));  // open: en, clr
  Register #(.width(32), .trigger("rising"), .Select("low")) register_3 (
    .D(multiplexer_3_out), .Q(R1_Out), .clk(CLK));  // open: en, clr
  Register #(.width(32), .trigger("rising"), .Select("low")) register_4 (
    .D(multiplexer_4_out), .Q(R2_Out), .clk(CLK));  // open: en, clr
  Register #(.width(32), .trigger("rising"), .Select("low")) register_5 (
    .D(multiplexer_5_out), .Q(PC_Out), .clk(CLK));  // open: en, clr
  Register #(.width(32), .trigger("rising"), .Select("low")) register_6 (
    .D(multiplexer_6_out), .Q(Instr_out), .clk(CLK));  // open: en, clr
  Register #(.width(32), .trigger("rising"), .Select("low")) register_7 (
    .D(multiplexer_7_out), .Q(PC_plus_four_Out), .clk(CLK));  // open: en, clr
  Register #(.width(5), .trigger("rising"), .Select("low")) register_8 (
    .D(multiplexer_8_out), .Q(WAdr_Out), .clk(CLK));  // open: en, clr
endmodule

module MEM_WB (
  input  CLK,
  input  JAL,
  input  MemToReg,
  input  RegWrite,
  input  [31:0] AluResult,
  input  [31:0] R2,
  input  [31:0] PC,
  input  [31:0] Instr,
  input  [31:0] PC_plus_four,
  input  [4:0] WAdr,
  input  KB_HIT,
  input  Screen_ins_opt,
  input  Cycles,
  input  Get_Bitmap,
  input  CopyToRAM,
  input  FrameFlush,
  input  [31:0] R2_2,
  output JAL_Out,
  output MemToReg_Out,
  output RegWrite_Out,
  output [31:0] AluResult_Out,
  output [31:0] R2_Out,
  output [31:0] PC_Out,
  output [31:0] Instr_out,
  output [31:0] PC_plus_four_Out,
  output [4:0] WAdr_Out,
  output KB_HIT_2,
  output Screen_ins_opt_2,
  output Get_Cycles,
  output Get_Bitmap_2,
  output CopyToRAM_2,
  output FrameFlush_2,
  output [31:0] Screen_in
);

  Register #(.width(3), .trigger("rising"), .Select("low")) register_1 (
    .D({RegWrite, MemToReg, JAL}), .Q({RegWrite_Out, MemToReg_Out, JAL_Out}), .clk(CLK));  // open: en, clr
  Register #(.width(32), .trigger("rising"), .Select("low")) register_2 (
    .D(AluResult), .Q(AluResult_Out), .clk(CLK));  // open: en, clr
  Register #(.width(32), .trigger("rising"), .Select("low")) register_3 (
    .D(R2), .Q(R2_Out), .clk(CLK));  // open: en, clr
  Register #(.width(32), .trigger("rising"), .Select("low")) register_4 (
    .D(PC), .Q(PC_Out), .clk(CLK));  // open: en, clr
  Register #(.width(32), .trigger("rising"), .Select("low")) register_5 (
    .D(Instr), .Q(Instr_out), .clk(CLK));  // open: en, clr
  Register #(.width(32), .trigger("rising"), .Select("low")) register_6 (
    .D(PC_plus_four), .Q(PC_plus_four_Out), .clk(CLK));  // open: en, clr
  Register #(.width(5), .trigger("rising"), .Select("low")) register_7 (
    .D(WAdr), .Q(WAdr_Out), .clk(CLK));  // open: en, clr
  Register #(.width(1), .trigger("rising"), .Select("low")) register_8 (
    .D(KB_HIT), .Q(KB_HIT_2), .clk(CLK));  // open: en, clr
  Register #(.width(1), .trigger("rising"), .Select("low")) register_9 (
    .D(Screen_ins_opt), .Q(Screen_ins_opt_2), .clk(CLK));  // open: en, clr
  Register #(.width(1), .trigger("rising"), .Select("low")) register_10 (
    .D(Cycles), .Q(Get_Cycles), .clk(CLK));  // open: en, clr
  Register #(.width(1), .trigger("rising"), .Select("low")) register_11 (
    .D(Get_Bitmap), .Q(Get_Bitmap_2), .clk(CLK));  // open: en, clr
  Register #(.width(1), .trigger("rising"), .Select("low")) register_12 (
    .D(CopyToRAM), .Q(CopyToRAM_2), .clk(CLK));  // open: en, clr
  Register #(.width(1), .trigger("rising"), .Select("low")) register_13 (
    .D(FrameFlush), .Q(FrameFlush_2), .clk(CLK));  // open: en, clr
  Register #(.width(32), .trigger("rising"), .Select("low")) register_14 (
    .D(R2_2), .Q(Screen_in), .clk(CLK));  // open: en, clr
endmodule

module MIPS_MEM (
  input  [31:0] AluResult,
  input  HalfW,
  input  [31:0] WriteData,
  input  MemWrite,
  input  CLK,
  output [31:0] MemReadData
);

  wire decoder_1_out0, decoder_1_out1, multiplexer_3_out, multiplexer_4_out, not_1_out, not_2_out;
  wire [15:0] demultiplexer_1_out0, demultiplexer_1_out1, multiplexer_1_out, multiplexer_2_out;

  Demultiplexer #(.select(1), .width(16), .tristate("false"), .disabled(0), .enable("false")) demultiplexer_1 (
    .out0(demultiplexer_1_out0), .out1(demultiplexer_1_out1), .in(WriteData[15:0]), .sel(AluResult[1]));
  Decoder #(.select(1), .tristate("false"), .disabled(0), .enable("false")) decoder_1 (
    .out0(decoder_1_out0), .out1(decoder_1_out1), .sel(AluResult[1]));
  not not_1 (not_1_out, decoder_1_out0);
  not not_2 (not_2_out, decoder_1_out1);
  Multiplexer #(.select(1), .width(16), .disabled(0), .enable("false")) multiplexer_1 (
    .in0(WriteData[15:0]), .in1(demultiplexer_1_out0), .out(multiplexer_1_out), .sel(HalfW));
  Multiplexer #(.select(1), .width(16), .disabled(0), .enable("false")) multiplexer_2 (
    .in0(WriteData[31:16]), .in1(demultiplexer_1_out1), .out(multiplexer_2_out), .sel(HalfW));
  Multiplexer #(.select(1), .width(1), .disabled(0), .enable("false")) multiplexer_3 (
    .in0(1'b1), .in1(not_2_out), .out(multiplexer_3_out), .sel(HalfW));
  Multiplexer #(.select(1), .width(1), .disabled(0), .enable("false")) multiplexer_4 (
    .in0(1'b1), .in1(not_1_out), .out(multiplexer_4_out), .sel(HalfW));
  RAM #(.addrWidth(10), .dataWidth(16), .bus("separate"), .Select("high")) lower_byte_RAM (
    .addr(AluResult[11:2]), .din(multiplexer_1_out), .data(MemReadData[15:0]), .str(MemWrite),
    .sel(multiplexer_3_out), .clk(CLK));  // open: ld, clr
  RAM #(.addrWidth(10), .dataWidth(16), .bus("separate"), .Select("high")) upper_byte_RAM (
    .addr(AluResult[11:2]), .din(multiplexer_2_out), .data(MemReadData[31:16]), .str(MemWrite),
    .sel(multiplexer_4_out), .clk(CLK));  // open: ld, clr
endmodule

module pipeline_conflict_deal_logic (
  input  [4:0] R1Adr,
  input  [4:0] WAdr,
  input  [4:0] R2Adr,
  input  CLR,
  input  RegWrite,
  input  AluSrc,
  output R1_CF,
  output Stall_PC_ID,
  output R2_CF
);

  wire comparator_1_eq, comparator_2_eq, comparator_3_eq, comparator_4_eq, or_1_out;

  Comparator #(.width(5), .mode("twosComplement")) comparator_1 (
    .a({5{1'b0}}), .b(R1Adr), .eq(comparator_1_eq));  // open: gt, lt
  Comparator #(.width(5), .mode("twosComplement")) comparator_2 (
    .a(WAdr), .b(R1Adr), .eq(comparator_2_eq));  // open: gt, lt
  Comparator #(.width(5), .mode("twosComplement")) comparator_3 (
    .a(WAdr), .b(R2Adr), .eq(comparator_3_eq));  // open: gt, lt
  Comparator #(.width(5), .mode("twosComplement")) comparator_4 (
    .a(R2Adr), .b({5{1'b0}}), .eq(comparator_4_eq));  // open: gt, lt
  and and_1 (R1_CF, ~comparator_1_eq, comparator_2_eq);  // AND_Gate
  or or_1 (or_1_out, R1_CF, R2_CF);
  and and_2 (R2_CF, comparator_3_eq, ~AluSrc, ~comparator_4_eq);  // AND_Gate
  and and_3 (Stall_PC_ID, or_1_out, ~CLR, RegWrite);  // AND_Gate
endmodule

module data_bypass_controller (
  input  [31:0] EX_IR,
  input  [31:0] ID_IR,
  input  ID_AluSrc,
  input  BranchCLR,
  input  [4:0] ID_R1Adr,
  input  [4:0] ID_R2Adr,
  input  [4:0] EX_WAdr,
  input  [4:0] MEM_WAdr,
  input  EX_RegWrite,
  input  MEM_RegWrite,
  input  MEM_MemToReg,
  output Stall,
  output [1:0] R1_Forward,
  output [1:0] R2_Forward
);

  wire and_1_out, and_2_out, and_4_out, and_5_out, and_6_out, and_7_out, and_8_out, and_9_out, and_10_out,
       and_11_out, comparator_1_eq, comparator_2_eq, comparator_3_eq, comparator_4_eq, comparator_5_eq,
       or_1_out, or_2_out, pipeline_conflict_deal_logic_1_r1_cf, pipeline_conflict_deal_logic_1_r2_cf,
       pipeline_conflict_deal_logic_1_stall_pc_id, pipeline_conflict_deal_logic_2_r1_cf,
       pipeline_conflict_deal_logic_2_r2_cf, pipeline_conflict_deal_logic_2_stall_pc_id;

  Comparator #(.width(6), .mode("twosComplement")) comparator_1 (
    .a(6'b100011), .b(EX_IR[31:26]), .eq(comparator_1_eq));  // open: gt, lt
  Comparator #(.width(5), .mode("twosComplement")) comparator_2 (
    .a(EX_IR[20:16]), .b(ID_IR[25:21]), .eq(comparator_2_eq));  // open: gt, lt
  Comparator #(.width(5), .mode("twosComplement")) comparator_3 (
    .a(EX_IR[20:16]), .b(ID_IR[20:16]), .eq(comparator_3_eq));  // open: gt, lt
  Comparator #(.width(6), .mode("twosComplement")) comparator_4 (
    .a(6'b100011), .b(ID_IR[31:26]), .eq(comparator_4_eq));  // open: gt, lt
  Comparator #(.width(6), .mode("twosComplement")) comparator_5 (
    .a(ID_IR[31:26]), .b(6'b101011), .eq(comparator_5_eq));  // open: gt, lt
  or or_1 (or_1_out, comparator_2_eq, and_1_out);
  and and_1 (and_1_out, comparator_3_eq, ~ID_AluSrc);  // AND_Gate
  or or_2 (or_2_out, comparator_4_eq, comparator_5_eq);
  and and_2 (and_2_out, ~or_2_out, ID_AluSrc);  // AND_Gate
  and and_3 (Stall, comparator_1_eq, or_1_out);
  and and_4 (and_4_out, pipeline_conflict_deal_logic_1_r1_cf, pipeline_conflict_deal_logic_1_stall_pc_id);
  and and_5 (and_5_out, pipeline_conflict_deal_logic_1_stall_pc_id, pipeline_conflict_deal_logic_1_r2_cf);
  pipeline_conflict_deal_logic pipeline_conflict_deal_logic_1 (
    .R1Adr(ID_R1Adr), .WAdr(EX_WAdr), .R2Adr(ID_R2Adr), .CLR(BranchCLR), .RegWrite(EX_RegWrite),
    .Stall_PC_ID(pipeline_conflict_deal_logic_1_stall_pc_id), .AluSrc(and_2_out),
    .R1_CF(pipeline_conflict_deal_logic_1_r1_cf), .R2_CF(pipeline_conflict_deal_logic_1_r2_cf));
  and and_6 (and_6_out, ~MEM_MemToReg, and_8_out);  // AND_Gate
  and and_7 (and_7_out, MEM_MemToReg, and_8_out);
  and and_8 (and_8_out, pipeline_conflict_deal_logic_2_r1_cf, pipeline_conflict_deal_logic_2_stall_pc_id);
  and and_9 (and_9_out, pipeline_conflict_deal_logic_2_stall_pc_id, pipeline_conflict_deal_logic_2_r2_cf);
  pipeline_conflict_deal_logic pipeline_conflict_deal_logic_2 (
    .R1Adr(ID_R1Adr), .WAdr(MEM_WAdr), .R2Adr(ID_R2Adr), .CLR(BranchCLR), .RegWrite(MEM_RegWrite),
    .Stall_PC_ID(pipeline_conflict_deal_logic_2_stall_pc_id), .AluSrc(and_2_out),
    .R1_CF(pipeline_conflict_deal_logic_2_r1_cf), .R2_CF(pipeline_conflict_deal_logic_2_r2_cf));
  Priority_Encoder #(.select(2), .disabled(0)) priority_encoder_1 (
    .in0(1'b1), .in1(and_6_out), .in2(and_7_out), .in3(and_4_out), .out(R1_Forward));  // open: gs, en_out, en_in
  and and_10 (and_10_out, ~MEM_MemToReg, and_9_out);  // AND_Gate
  and and_11 (and_11_out, MEM_MemToReg, and_9_out);
  Priority_Encoder #(.select(2), .disabled(0)) priority_encoder_2 (
    .in0(1'b1), .in1(and_10_out), .in2(and_11_out), .in3(and_5_out), .out(R2_Forward));  // open: gs, en_out, en_in
endmodule

module dual_bit_predction_with_state_shifting_logic (
  input  Success,
  input  Preset,
  input  CLK,
  input  EX_Hit,
  input  Hit,
  output JumpPredict
);

  wire and_1_out, and_2_out, and_3_out, and_4_out, and_5_out, not_1_out, not_2_out, not_3_out, not_4_out,
       not_5_out, or_3_out;
  wire [1:0] multiplexer_1_out, or_2_out, register_1_q;

  not not_1 (not_1_out, register_1_q[0]);
  not not_2 (not_2_out, register_1_q[1]);
  not not_3 (not_3_out, register_1_q[0]);
  not not_4 (not_4_out, register_1_q[0]);
  not not_5 (not_5_out, Success);
  and and_1 (and_1_out, register_1_q[0], Success);
  and and_2 (and_2_out, register_1_q[1], not_1_out);
  and and_3 (and_3_out, not_2_out, not_3_out, Success);
  and and_4 (and_4_out, register_1_q[1], not_4_out, not_5_out);
  or or_1 (or_2_out[1], and_1_out, and_2_out);
  or or_2 (or_2_out[0], and_3_out, and_4_out);
  Multiplexer #(.select(1), .width(2), .disabled(0), .enable("false")) multiplexer_1 (
    .in0(or_2_out), .in1(2'b11), .out(multiplexer_1_out), .sel(Preset));
  or or_3 (or_3_out, Preset, EX_Hit);
  Register #(.width(2), .trigger("rising"), .Select("low")) register_1 (
    .D(multiplexer_1_out), .en(or_3_out), .Q(register_1_q), .clk(CLK));  // open: clr
  and and_5 (and_5_out, register_1_q[1], Hit);
  Register #(.width(1), .trigger("high"), .Select("low")) register_2 (
    .D(and_5_out), .en(1'b1), .Q(JumpPredict), .clk(CLK));  // open: clr
endmodule
module BTB (
  input  BranchSig,
  input  [31:0] EX_PC,
  input  [31:0] IF_PC,
  input  [31:0] BranchAddr,
  input  Branched,
  input  CLK,
  output PredictJump,
  output [31:0] JumpAddr
);

  wire and_1_out, and_2_out, and_3_out, and_4_out, and_5_out, and_6_out, and_7_out, and_8_out, and_9_out,
       and_10_out, and_11_out, and_12_out, and_13_out, and_14_out, and_15_out, and_16_out, and_17_out,
       comparator_1_eq, comparator_2_eq, comparator_3_eq, comparator_4_eq, comparator_5_eq, comparator_6_eq,
       comparator_7_eq, comparator_8_eq, comparator_9_eq, comparator_10_eq, comparator_11_eq,
       comparator_12_eq, comparator_13_eq, comparator_14_eq, comparator_15_eq, comparator_16_eq,
       comparator_17_eq, comparator_18_eq, comparator_19_eq, comparator_20_eq, comparator_21_eq,
       comparator_22_eq, comparator_23_eq, comparator_24_eq, decoder_1_out0, decoder_1_out1, decoder_1_out2,
       decoder_1_out3, decoder_1_out4, decoder_1_out5, decoder_1_out6, decoder_1_out7, decoder_2_out0,
       decoder_2_out1, decoder_2_out2, decoder_2_out3, decoder_2_out4, decoder_2_out5, decoder_2_out6,
       decoder_2_out7, dual_bit_predction_with_state_shifting_logic_1_jumppredict,
       dual_bit_predction_with_state_shifting_logic_2_jumppredict,
       dual_bit_predction_with_state_shifting_logic_3_jumppredict,
       dual_bit_predction_with_state_shifting_logic_4_jumppredict,
       dual_bit_predction_with_state_shifting_logic_5_jumppredict,
       dual_bit_predction_with_state_shifting_logic_6_jumppredict,
       dual_bit_predction_with_state_shifting_logic_7_jumppredict,
       dual_bit_predction_with_state_shifting_logic_8_jumppredict, EX_L1, EX_L2, EX_L3, EX_L4, EX_L5, EX_L6,
       EX_L7, EX_L8, EX_Miss, Hit, L1, L2, L3, L4, L5, L6, L7, L8, multiplexer_1_out, multiplexer_2_out,
       multiplexer_3_out, multiplexer_4_out, multiplexer_5_out, multiplexer_6_out, multiplexer_7_out,
       multiplexer_8_out, not_1_out, not_2_out, not_3_out, not_4_out, not_5_out, not_6_out, not_7_out,
       not_8_out, or_2_out, or_3_out, or_4_out, or_5_out, or_6_out, or_7_out, or_8_out, or_9_out, or_10_out,
       or_11_out, priority_encoder_1_gs, V1, V2, V3, V4, V5, V6, V7, V8;
  wire [2:0] max3_1_max_number, max3_2_max_number, max3_3_max_number, max3_4_max_number, max3_5_max_number,
       max3_6_max_number, priority_encoder_1_out, priority_encoder_2_out, ReWriteAddr;
  wire [15:0] counter_1_q, counter_2_q, counter_3_q, counter_4_q, counter_5_q, counter_6_q, counter_7_q,
       counter_8_q, max3_1_max, max3_2_max, max3_3_max, max3_4_max, max3_5_max, max3_6_max,
       multiplexer_9_out, multiplexer_10_out, multiplexer_11_out, multiplexer_12_out, multiplexer_13_out,
       multiplexer_14_out, multiplexer_15_out, multiplexer_16_out;
  wire [31:0] register_9_q, register_10_q, register_11_q, register_12_q, register_13_q, register_14_q,
       register_15_q, register_16_q, register_17_q, register_18_q, register_19_q, register_20_q,
       register_21_q, register_22_q, register_23_q, register_24_q;

  or or_1 (Hit, L1, L2, L3, L4, L5, L6, L7, L8);
  nor nor_1 (EX_Miss, EX_L1, EX_L2, EX_L3, EX_L4, EX_L5, EX_L6, EX_L7, EX_L8);
  not not_1 (not_1_out, V8);
  not not_2 (not_2_out, V7);
  not not_3 (not_3_out, V6);
  not not_4 (not_4_out, V5);
  not not_5 (not_5_out, V4);
  not not_6 (not_6_out, V3);
  not not_7 (not_7_out, V2);
  not not_8 (not_8_out, V1);
  Priority_Encoder #(.select(3), .disabled(0)) priority_encoder_1 (
    .in0(not_1_out), .in1(not_2_out), .in2(not_3_out), .in3(not_4_out), .in4(not_5_out), .in5(not_6_out),
    .in6(not_7_out), .in7(not_8_out), .out(priority_encoder_1_out), .gs(priority_encoder_1_gs), .en_in(1'b1));  // open: en_out
  Decoder #(.select(3), .tristate("false"), .disabled(0), .enable("false")) decoder_1 (
    .out0(decoder_1_out0), .out1(decoder_1_out1), .out2(decoder_1_out2), .out3(decoder_1_out3),
    .out4(decoder_1_out4), .out5(decoder_1_out5), .out6(decoder_1_out6), .out7(decoder_1_out7),
    .sel(ReWriteAddr));
  Decoder #(.select(3), .tristate("false"), .disabled(0), .enable("false")) decoder_2 (
    .out0(decoder_2_out0), .out1(decoder_2_out1), .out2(decoder_2_out2), .out3(decoder_2_out3),
    .out4(decoder_2_out4), .out5(decoder_2_out5), .out6(decoder_2_out6), .out7(decoder_2_out7),
    .sel(priority_encoder_1_out));
  and and_1 (and_1_out, BranchSig, Branched);
  Multiplexer #(.select(1), .width(1), .disabled(0), .enable("false")) multiplexer_1 (
    .in0(decoder_1_out0), .in1(decoder_2_out7), .out(multiplexer_1_out), .sel(priority_encoder_1_gs));
  Multiplexer #(.select(1), .width(1), .disabled(0), .enable("false")) multiplexer_2 (
    .in0(decoder_1_out1), .in1(decoder_2_out6), .out(multiplexer_2_out), .sel(priority_encoder_1_gs));
  Multiplexer #(.select(1), .width(1), .disabled(0), .enable("false")) multiplexer_3 (
    .in0(decoder_1_out2), .in1(decoder_2_out5), .out(multiplexer_3_out), .sel(priority_encoder_1_gs));
  Multiplexer #(.select(1), .width(1), .disabled(0), .enable("false")) multiplexer_4 (
    .in0(decoder_1_out3), .in1(decoder_2_out4), .out(multiplexer_4_out), .sel(priority_encoder_1_gs));
  Multiplexer #(.select(1), .width(1), .disabled(0), .enable("false")) multiplexer_5 (
    .in0(decoder_1_out4), .in1(decoder_2_out3), .out(multiplexer_5_out), .sel(priority_encoder_1_gs));
  Multiplexer #(.select(1), .width(1), .disabled(0), .enable("false")) multiplexer_6 (
    .in0(decoder_1_out5), .in1(decoder_2_out2), .out(multiplexer_6_out), .sel(priority_encoder_1_gs));
  Multiplexer #(.select(1), .width(1), .disabled(0), .enable("false")) multiplexer_7 (
    .in0(decoder_1_out6), .in1(decoder_2_out1), .out(multiplexer_7_out), .sel(priority_encoder_1_gs));
  Multiplexer #(.select(1), .width(1), .disabled(0), .enable("false")) multiplexer_8 (
    .in0(decoder_1_out7), .in1(decoder_2_out0), .out(multiplexer_8_out), .sel(priority_encoder_1_gs));
  and and_2 (and_2_out, EX_Miss, and_1_out, multiplexer_1_out);
  and and_3 (and_3_out, EX_Miss, and_1_out, multiplexer_2_out);
  and and_4 (and_4_out, EX_Miss, and_1_out, multiplexer_3_out);
  and and_5 (and_5_out, EX_Miss, and_1_out, multiplexer_4_out);
  and and_6 (and_6_out, EX_Miss, and_1_out, multiplexer_5_out);
  and and_7 (and_7_out, EX_Miss, and_1_out, multiplexer_6_out);
  and and_8 (and_8_out, EX_Miss, and_1_out, multiplexer_7_out);
  and and_9 (and_9_out, EX_Miss, and_1_out, multiplexer_8_out);
  and and_10 (and_10_out, Hit, L1);
  or or_2 (or_2_out, and_10_out, and_2_out);
  and and_11 (and_11_out, Hit, L2);
  or or_3 (or_3_out, and_11_out, and_3_out);
  and and_12 (and_12_out, Hit, L3);
  or or_4 (or_4_out, and_12_out, and_4_out);
  and and_13 (and_13_out, Hit, L4);
  or or_5 (or_5_out, and_13_out, and_5_out);
  and and_14 (and_14_out, Hit, L5);
  or or_6 (or_6_out, and_14_out, and_6_out);
  and and_15 (and_15_out, Hit, L6);
  or or_7 (or_7_out, and_15_out, and_7_out);
  and and_16 (and_16_out, Hit, L7);
  or or_8 (or_8_out, and_16_out, and_8_out);
  and and_17 (and_17_out, Hit, L8);
  or or_9 (or_9_out, and_17_out, and_9_out);
  Multiplexer #(.select(1), .width(16), .disabled(0), .enable("false")) multiplexer_9 (
    .in0(counter_1_q), .in1({16{1'b0}}), .out(multiplexer_9_out), .sel(or_2_out));
  Counter #(.width(16), .max('hffff), .ongoal("wrap"), .trigger("rising"), .behavior("new")) counter_1 (
    .load(or_2_out), .D(multiplexer_9_out), .Q(counter_1_q), .clk(CLK));  // open: count, carry, clr, preset, down
  Multiplexer #(.select(1), .width(16), .disabled(0), .enable("false")) multiplexer_10 (
    .in0(counter_2_q), .in1({16{1'b0}}), .out(multiplexer_10_out), .sel(or_3_out));
  Counter #(.width(16), .max('hffff), .ongoal("wrap"), .trigger("rising"), .behavior("new")) counter_2 (
    .load(or_3_out), .D(multiplexer_10_out), .Q(counter_2_q), .clk(CLK));  // open: count, carry, clr, preset, down
  Multiplexer #(.select(1), .width(16), .disabled(0), .enable("false")) multiplexer_11 (
    .in0(counter_3_q), .in1({16{1'b0}}), .out(multiplexer_11_out), .sel(or_4_out));
  Counter #(.width(16), .max('hffff), .ongoal("wrap"), .trigger("rising"), .behavior("new")) counter_3 (
    .load(or_4_out), .D(multiplexer_11_out), .Q(counter_3_q), .clk(CLK));  // open: count, carry, clr, preset, down
  Multiplexer #(.select(1), .width(16), .disabled(0), .enable("false")) multiplexer_12 (
    .in0(counter_4_q), .in1({16{1'b0}}), .out(multiplexer_12_out), .sel(or_5_out));
  Counter #(.width(16), .max('hffff), .ongoal("wrap"), .trigger("rising"), .behavior("new")) counter_4 (
    .load(or_5_out), .D(multiplexer_12_out), .Q(counter_4_q), .clk(CLK));  // open: count, carry, clr, preset, down
  Multiplexer #(.select(1), .width(16), .disabled(0), .enable("false")) multiplexer_13 (
    .in0(counter_5_q), .in1({16{1'b0}}), .out(multiplexer_13_out), .sel(or_6_out));
  Counter #(.width(16), .max('hffff), .ongoal("wrap"), .trigger("rising"), .behavior("new")) counter_5 (
    .load(or_6_out), .D(multiplexer_13_out), .Q(counter_5_q), .clk(CLK));  // open: count, carry, clr, preset, down
  Multiplexer #(.select(1), .width(16), .disabled(0), .enable("false")) multiplexer_14 (
    .in0(counter_6_q), .in1({16{1'b0}}), .out(multiplexer_14_out), .sel(or_7_out));
  Counter #(.width(16), .max('hffff), .ongoal("wrap"), .trigger("rising"), .behavior("new")) counter_6 (
    .load(or_7_out), .D(multiplexer_14_out), .Q(counter_6_q), .clk(CLK));  // open: count, carry, clr, preset, down
  Multiplexer #(.select(1), .width(16), .disabled(0), .enable("false")) multiplexer_15 (
    .in0(counter_7_q), .in1({16{1'b0}}), .out(multiplexer_15_out), .sel(or_8_out));
  Counter #(.width(16), .max('hffff), .ongoal("wrap"), .trigger("rising"), .behavior("new")) counter_7 (
    .load(or_8_out), .D(multiplexer_15_out), .Q(counter_7_q), .clk(CLK));  // open: count, carry, clr, preset, down
  Multiplexer #(.select(1), .width(16), .disabled(0), .enable("false")) multiplexer_16 (
    .in0(counter_8_q), .in1({16{1'b0}}), .out(multiplexer_16_out), .sel(or_9_out));
  Counter #(.width(16), .max('hffff), .ongoal("wrap"), .trigger("rising"), .behavior("new")) counter_8 (
    .load(or_9_out), .D(multiplexer_16_out), .Q(counter_8_q), .clk(CLK));  // open: count, carry, clr, preset, down
  MAX3 max3_1 (
    .Y(counter_2_q), .X(counter_1_q), .Y_Number(3'b001), .X_Number(3'b000), .MAX(max3_1_max),
    .Max_Number(max3_1_max_number));
  MAX3 max3_2 (
    .Y(counter_4_q), .X(counter_3_q), .Y_Number(3'b011), .X_Number(3'b010), .MAX(max3_2_max),
    .Max_Number(max3_2_max_number));
  MAX3 max3_3 (
    .Y(counter_6_q), .X(counter_5_q), .Y_Number(3'b101), .X_Number(3'b100), .MAX(max3_3_max),
    .Max_Number(max3_3_max_number));
  MAX3 max3_4 (
    .Y(counter_8_q), .X(counter_7_q), .Y_Number(3'b111), .X_Number(3'b110), .MAX(max3_4_max),
    .Max_Number(max3_4_max_number));
  MAX3 max3_5 (
    .Y(max3_2_max), .X(max3_1_max), .Y_Number(max3_2_max_number), .X_Number(max3_1_max_number),
    .MAX(max3_5_max), .Max_Number(max3_5_max_number));
  MAX3 max3_6 (
    .Y(max3_4_max), .X(max3_3_max), .Y_Number(max3_4_max_number), .X_Number(max3_3_max_number),
    .MAX(max3_6_max), .Max_Number(max3_6_max_number));
  MAX3 max3_7 (
    .Y(max3_6_max), .X(max3_5_max), .Y_Number(max3_6_max_number), .X_Number(max3_5_max_number),
    .Max_Number(ReWriteAddr));  // open: MAX
  Register #(.width(1), .trigger("rising"), .Select("low")) register_1 (
    .D(and_2_out), .en(and_2_out), .Q(V1), .clk(CLK));  // open: clr
  Register #(.width(1), .trigger("rising"), .Select("low")) register_2 (
    .D(and_3_out), .en(and_3_out), .Q(V2), .clk(CLK));  // open: clr
  Register #(.width(1), .trigger("rising"), .Select("low")) register_3 (
    .D(and_4_out), .en(and_4_out), .Q(V3), .clk(CLK));  // open: clr
  Register #(.width(1), .trigger("rising"), .Select("low")) register_4 (
    .D(and_5_out), .en(and_5_out), .Q(V4), .clk(CLK));  // open: clr
  Register #(.width(1), .trigger("rising"), .Select("low")) register_5 (
    .D(and_6_out), .en(and_6_out), .Q(V5), .clk(CLK));  // open: clr
  Register #(.width(1), .trigger("rising"), .Select("low")) register_6 (
    .D(and_7_out), .en(and_7_out), .Q(V6), .clk(CLK));  // open: clr
  Register #(.width(1), .trigger("rising"), .Select("low")) register_7 (
    .D(and_8_out), .en(and_8_out), .Q(V7), .clk(CLK));  // open: clr
  Register #(.width(1), .trigger("rising"), .Select("low")) register_8 (
    .D(and_9_out), .en(and_9_out), .Q(V8), .clk(CLK));  // open: clr
  Register #(.width(32), .trigger("rising"), .Select("low")) register_9 (
    .D(EX_PC), .en(and_2_out), .Q(register_9_q), .clk(CLK));  // open: clr
  Register #(.width(32), .trigger("rising"), .Select("low")) register_10 (
    .D(EX_PC), .en(and_3_out), .Q(register_10_q), .clk(CLK));  // open: clr
  Register #(.width(32), .trigger("rising"), .Select("low")) register_11 (
    .D(EX_PC), .en(and_4_out), .Q(register_11_q), .clk(CLK));  // open: clr
  Register #(.width(32), .trigger("rising"), .Select("low")) register_12 (
    .D(EX_PC), .en(and_5_out), .Q(register_12_q), .clk(CLK));  // open: clr
  Register #(.width(32), .trigger("rising"), .Select("low")) register_13 (
    .D(EX_PC), .en(and_6_out), .Q(register_13_q), .clk(CLK));  // open: clr
  Register #(.width(32), .trigger("rising"), .Select("low")) register_14 (
    .D(EX_PC), .en(and_7_out), .Q(register_14_q), .clk(CLK));  // open: clr
  Register #(.width(32), .trigger("rising"), .Select("low")) register_15 (
    .D(EX_PC), .en(and_8_out), .Q(register_15_q), .clk(CLK));  // open: clr
  Register #(.width(32), .trigger("rising"), .Select("low")) register_16 (
    .D(EX_PC), .en(and_9_out), .Q(register_16_q), .clk(CLK));  // open: clr
  Comparator #(.width(32), .mode("twosComplement")) comparator_1 (
    .a(register_9_q), .b(IF_PC), .eq(comparator_1_eq));  // open: gt, lt
  Comparator #(.width(32), .mode("twosComplement")) comparator_2 (
    .a(register_10_q), .b(IF_PC), .eq(comparator_2_eq));  // open: gt, lt
  Comparator #(.width(32), .mode("twosComplement")) comparator_3 (
    .a(register_11_q), .b(IF_PC), .eq(comparator_3_eq));  // open: gt, lt
  Comparator #(.width(32), .mode("twosComplement")) comparator_4 (
    .a(register_12_q), .b(IF_PC), .eq(comparator_4_eq));  // open: gt, lt
  Comparator #(.width(32), .mode("twosComplement")) comparator_5 (
    .a(register_13_q), .b(IF_PC), .eq(comparator_5_eq));  // open: gt, lt
  Comparator #(.width(32), .mode("twosComplement")) comparator_6 (
    .a(register_14_q), .b(IF_PC), .eq(comparator_6_eq));  // open: gt, lt
  Comparator #(.width(32), .mode("twosComplement")) comparator_7 (
    .a(register_15_q), .b(IF_PC), .eq(comparator_7_eq));  // open: gt, lt
  Comparator #(.width(32), .mode("twosComplement")) comparator_8 (
    .a(register_16_q), .b(IF_PC), .eq(comparator_8_eq));  // open: gt, lt
  and and_18 (L1, V1, comparator_1_eq);
  and and_19 (L2, V2, comparator_2_eq);
  and and_20 (L3, V3, comparator_3_eq);
  and and_21 (L4, V4, comparator_4_eq);
  and and_22 (L5, V5, comparator_5_eq);
  and and_23 (L6, V6, comparator_6_eq);
  and and_24 (L7, V7, comparator_7_eq);
  and and_25 (L8, V8, comparator_8_eq);
  Comparator #(.width(32), .mode("twosComplement")) comparator_9 (
    .a(EX_PC), .b(register_9_q), .eq(comparator_9_eq));  // open: gt, lt
  Comparator #(.width(32), .mode("twosComplement")) comparator_10 (
    .a(EX_PC), .b(register_10_q), .eq(comparator_10_eq));  // open: gt, lt
  Comparator #(.width(32), .mode("twosComplement")) comparator_11 (
    .a(EX_PC), .b(register_11_q), .eq(comparator_11_eq));  // open: gt, lt
  Comparator #(.width(32), .mode("twosComplement")) comparator_12 (
    .a(EX_PC), .b(register_12_q), .eq(comparator_12_eq));  // open: gt, lt
  Comparator #(.width(32), .mode("twosComplement")) comparator_13 (
    .a(EX_PC), .b(register_13_q), .eq(comparator_13_eq));  // open: gt, lt
  Comparator #(.width(32), .mode("twosComplement")) comparator_14 (
    .a(EX_PC), .b(register_14_q), .eq(comparator_14_eq));  // open: gt, lt
  Comparator #(.width(32), .mode("twosComplement")) comparator_15 (
    .a(EX_PC), .b(register_15_q), .eq(comparator_15_eq));  // open: gt, lt
  Comparator #(.width(32), .mode("twosComplement")) comparator_16 (
    .a(EX_PC), .b(register_16_q), .eq(comparator_16_eq));  // open: gt, lt
  and and_26 (EX_L1, V1, comparator_9_eq);
  and and_27 (EX_L2, V2, comparator_10_eq);
  and and_28 (EX_L3, V3, comparator_11_eq);
  and and_29 (EX_L4, V4, comparator_12_eq);
  and and_30 (EX_L5, V5, comparator_13_eq);
  and and_31 (EX_L6, V6, comparator_14_eq);
  and and_32 (EX_L7, V7, comparator_15_eq);
  and and_33 (EX_L8, V8, comparator_16_eq);
  dual_bit_predction_with_state_shifting_logic dual_bit_predction_with_state_shifting_logic_1 (
    .Success(comparator_17_eq), .Preset(and_2_out), .CLK(CLK),
    .JumpPredict(dual_bit_predction_with_state_shifting_logic_1_jumppredict), .EX_Hit(EX_L1), .Hit(L1));
  dual_bit_predction_with_state_shifting_logic dual_bit_predction_with_state_shifting_logic_2 (
    .Success(comparator_18_eq), .Preset(and_3_out), .CLK(CLK),
    .JumpPredict(dual_bit_predction_with_state_shifting_logic_2_jumppredict), .EX_Hit(EX_L2), .Hit(L2));
  dual_bit_predction_with_state_shifting_logic dual_bit_predction_with_state_shifting_logic_3 (
    .Success(comparator_19_eq), .Preset(and_4_out), .CLK(CLK),
    .JumpPredict(dual_bit_predction_with_state_shifting_logic_3_jumppredict), .EX_Hit(EX_L3), .Hit(L3));
  dual_bit_predction_with_state_shifting_logic dual_bit_predction_with_state_shifting_logic_4 (
    .Success(comparator_20_eq), .Preset(and_5_out), .CLK(CLK),
    .JumpPredict(dual_bit_predction_with_state_shifting_logic_4_jumppredict), .EX_Hit(EX_L4), .Hit(L4));
  dual_bit_predction_with_state_shifting_logic dual_bit_predction_with_state_shifting_logic_5 (
    .Success(comparator_21_eq), .Preset(and_6_out), .CLK(CLK),
    .JumpPredict(dual_bit_predction_with_state_shifting_logic_5_jumppredict), .EX_Hit(EX_L5), .Hit(L5));
  dual_bit_predction_with_state_shifting_logic dual_bit_predction_with_state_shifting_logic_6 (
    .Success(comparator_22_eq), .Preset(and_7_out), .CLK(CLK),
    .JumpPredict(dual_bit_predction_with_state_shifting_logic_6_jumppredict), .EX_Hit(EX_L6), .Hit(L6));
  dual_bit_predction_with_state_shifting_logic dual_bit_predction_with_state_shifting_logic_7 (
    .Success(comparator_23_eq), .Preset(and_8_out), .CLK(CLK),
    .JumpPredict(dual_bit_predction_with_state_shifting_logic_7_jumppredict), .EX_Hit(EX_L7), .Hit(L7));
  dual_bit_predction_with_state_shifting_logic dual_bit_predction_with_state_shifting_logic_8 (
    .Success(comparator_24_eq), .Preset(and_9_out), .CLK(CLK),
    .JumpPredict(dual_bit_predction_with_state_shifting_logic_8_jumppredict), .EX_Hit(EX_L8), .Hit(L8));
  or or_10 (or_10_out, dual_bit_predction_with_state_shifting_logic_1_jumppredict, dual_bit_predction_with_state_shifting_logic_2_jumppredict, dual_bit_predction_with_state_shifting_logic_3_jumppredict, dual_bit_predction_with_state_shifting_logic_4_jumppredict);
  or or_11 (or_11_out, dual_bit_predction_with_state_shifting_logic_5_jumppredict, dual_bit_predction_with_state_shifting_logic_6_jumppredict, dual_bit_predction_with_state_shifting_logic_7_jumppredict, dual_bit_predction_with_state_shifting_logic_8_jumppredict);
  or or_12 (PredictJump, or_10_out, or_11_out);
  Register #(.width(32), .trigger("rising"), .Select("low")) register_17 (
    .D(BranchAddr), .en(and_2_out), .Q(register_17_q), .clk(CLK));  // open: clr
  Register #(.width(32), .trigger("rising"), .Select("low")) register_18 (
    .D(BranchAddr), .en(and_3_out), .Q(register_18_q), .clk(CLK));  // open: clr
  Register #(.width(32), .trigger("rising"), .Select("low")) register_19 (
    .D(BranchAddr), .en(and_4_out), .Q(register_19_q), .clk(CLK));  // open: clr
  Register #(.width(32), .trigger("rising"), .Select("low")) register_20 (
    .D(BranchAddr), .en(and_5_out), .Q(register_20_q), .clk(CLK));  // open: clr
  Register #(.width(32), .trigger("rising"), .Select("low")) register_21 (
    .D(BranchAddr), .en(and_6_out), .Q(register_21_q), .clk(CLK));  // open: clr
  Register #(.width(32), .trigger("rising"), .Select("low")) register_22 (
    .D(BranchAddr), .en(and_7_out), .Q(register_22_q), .clk(CLK));  // open: clr
  Register #(.width(32), .trigger("rising"), .Select("low")) register_23 (
    .D(BranchAddr), .en(and_8_out), .Q(register_23_q), .clk(CLK));  // open: clr
  Register #(.width(32), .trigger("rising"), .Select("low")) register_24 (
    .D(BranchAddr), .en(and_9_out), .Q(register_24_q), .clk(CLK));  // open: clr
  Comparator #(.width(32), .mode("twosComplement")) comparator_17 (
    .a(BranchAddr), .b(register_17_q), .eq(comparator_17_eq));  // open: gt, lt
  Comparator #(.width(32), .mode("twosComplement")) comparator_18 (
    .a(BranchAddr), .b(register_18_q), .eq(comparator_18_eq));  // open: gt, lt
  Comparator #(.width(32), .mode("twosComplement")) comparator_19 (
    .a(BranchAddr), .b(register_19_q), .eq(comparator_19_eq));  // open: gt, lt
  Comparator #(.width(32), .mode("twosComplement")) comparator_20 (
    .a(BranchAddr), .b(register_20_q), .eq(comparator_20_eq));  // open: gt, lt
  Comparator #(.width(32), .mode("twosComplement")) comparator_21 (
    .a(BranchAddr), .b(register_21_q), .eq(comparator_21_eq));  // open: gt, lt
  Comparator #(.width(32), .mode("twosComplement")) comparator_22 (
    .a(BranchAddr), .b(register_22_q), .eq(comparator_22_eq));  // open: gt, lt
  Comparator #(.width(32), .mode("twosComplement")) comparator_23 (
    .a(BranchAddr), .b(register_23_q), .eq(comparator_23_eq));  // open: gt, lt
  Comparator #(.width(32), .mode("twosComplement")) comparator_24 (
    .a(BranchAddr), .b(register_24_q), .eq(comparator_24_eq));  // open: gt, lt
  Priority_Encoder #(.select(3), .disabled(0)) priority_encoder_2 (
    .in0(L1), .in1(L2), .in2(L3), .in3(L4), .in4(L5), .in5(L6), .in6(L7), .in7(L8),
    .out(priority_encoder_2_out));  // open: gs, en_out, en_in
  Multiplexer #(.select(3), .width(32), .disabled(0), .enable("false")) multiplexer_17 (
    .in0(register_17_q), .in1(register_18_q), .in2(register_19_q), .in3(register_20_q), .in4(register_21_q),
    .in5(register_22_q), .in6(register_23_q), .in7(register_24_q), .out(JumpAddr),
    .sel(priority_encoder_2_out));
endmodule

module MAX3 (
  input  [15:0] Y,
  input  [15:0] X,
  input  [2:0] Y_Number,
  input  [2:0] X_Number,
  output [15:0] MAX,
  output [2:0] Max_Number
);

  wire comparator_1_eq, comparator_1_gt, or_1_out;

  Multiplexer #(.select(1), .width(16), .disabled(0), .enable("false")) multiplexer_1 (
    .in0(Y), .in1(X), .out(MAX), .sel(or_1_out));
  Comparator #(.width(16), .mode("unsigned")) comparator_1 (
    .a(X), .b(Y), .gt(comparator_1_gt), .eq(comparator_1_eq));  // open: lt
  or or_1 (or_1_out, comparator_1_gt, comparator_1_eq);
  Multiplexer #(.select(1), .width(3), .disabled(0), .enable("false")) multiplexer_2 (
    .in0(Y_Number), .in1(X_Number), .out(Max_Number), .sel(or_1_out));
endmodule

module display_decoder (
  input  [3:0] hex_digit,
  output [7:0] DP_SegCtrl
);

  wire and_1_out, and_2_out, and_3_out, and_4_out, and_5_out, and_6_out, and_7_out, and_8_out, and_9_out,
       and_10_out, and_11_out, and_12_out, and_13_out, and_14_out, and_15_out, and_16_out, and_17_out,
       and_18_out, and_19_out, and_20_out, and_21_out, and_22_out, and_23_out, and_24_out, and_25_out,
       and_26_out, and_27_out, and_28_out, and_29_out, and_30_out, and_31_out, and_32_out, and_33_out,
       and_34_out, and_35_out, not_1_out, not_2_out, not_3_out, not_4_out, not_5_out, not_6_out, not_7_out,
       not_8_out, not_9_out, not_10_out, not_11_out, not_12_out, not_13_out, not_14_out, not_15_out,
       not_16_out, not_17_out, not_18_out, not_19_out, not_20_out, not_21_out, not_22_out, not_23_out,
       not_24_out, not_25_out, not_26_out, not_27_out, not_28_out, not_29_out, not_30_out, not_31_out,
       not_32_out, not_33_out, not_34_out, not_35_out, not_36_out, not_37_out, not_38_out, not_39_out,
       not_40_out, not_41_out, not_42_out, not_43_out;

  not not_1 (not_1_out, hex_digit[2]);
  and and_1 (and_1_out, not_1_out, not_2_out);
  not not_2 (not_2_out, hex_digit[0]);
  not not_3 (not_3_out, hex_digit[3]);
  and and_2 (and_2_out, not_3_out, hex_digit[1]);
  not not_4 (not_4_out, hex_digit[3]);
  and and_3 (and_3_out, not_4_out, hex_digit[2], hex_digit[0]);
  and and_4 (and_4_out, hex_digit[2], hex_digit[1]);
  and and_5 (and_5_out, hex_digit[3], not_5_out, not_6_out);
  not not_5 (not_5_out, hex_digit[2]);
  not not_6 (not_6_out, hex_digit[1]);
  and and_6 (and_6_out, hex_digit[3], not_7_out);
  not not_7 (not_7_out, hex_digit[0]);
  not not_8 (not_8_out, hex_digit[3]);
  and and_7 (and_7_out, not_8_out, not_9_out);
  not not_9 (not_9_out, hex_digit[2]);
  not not_10 (not_10_out, hex_digit[3]);
  not not_11 (not_11_out, hex_digit[1]);
  and and_8 (and_8_out, not_10_out, not_11_out, not_12_out);
  not not_12 (not_12_out, hex_digit[0]);
  not not_13 (not_13_out, hex_digit[2]);
  and and_9 (and_9_out, not_13_out, not_14_out);
  not not_14 (not_14_out, hex_digit[0]);
  not not_15 (not_15_out, hex_digit[3]);
  and and_10 (and_10_out, not_15_out, hex_digit[1], hex_digit[0]);
  not not_16 (not_16_out, hex_digit[1]);
  and and_11 (and_11_out, hex_digit[3], not_16_out, hex_digit[0]);
  not not_17 (not_17_out, hex_digit[3]);
  and and_12 (and_12_out, not_17_out, not_18_out);
  not not_18 (not_18_out, hex_digit[1]);
  not not_19 (not_19_out, hex_digit[3]);
  and and_13 (and_13_out, not_19_out, hex_digit[0]);
  not not_20 (not_20_out, hex_digit[1]);
  and and_14 (and_14_out, not_20_out, hex_digit[0]);
  not not_21 (not_21_out, hex_digit[3]);
  and and_15 (and_15_out, not_21_out, hex_digit[2]);
  and and_16 (and_16_out, hex_digit[3], not_22_out);
  not not_22 (not_22_out, hex_digit[2]);
  not not_23 (not_23_out, hex_digit[3]);
  not not_24 (not_24_out, hex_digit[2]);
  and and_17 (and_17_out, not_23_out, not_24_out, not_25_out);
  not not_25 (not_25_out, hex_digit[0]);
  not not_26 (not_26_out, hex_digit[2]);
  and and_18 (and_18_out, not_26_out, hex_digit[1], hex_digit[0]);
  and and_19 (and_19_out, hex_digit[2], not_27_out, hex_digit[0]);
  not not_27 (not_27_out, hex_digit[1]);
  and and_20 (and_20_out, hex_digit[2], hex_digit[1], not_28_out);
  not not_28 (not_28_out, hex_digit[0]);
  and and_21 (and_21_out, hex_digit[3], not_29_out);
  not not_29 (not_29_out, hex_digit[1]);
  not not_30 (not_30_out, hex_digit[2]);
  and and_22 (and_22_out, not_30_out, not_31_out);
  not not_31 (not_31_out, hex_digit[0]);
  and and_23 (and_23_out, hex_digit[1], not_32_out);
  not not_32 (not_32_out, hex_digit[0]);
  and and_24 (and_24_out, hex_digit[3], hex_digit[1]);
  and and_25 (and_25_out, hex_digit[3], hex_digit[2]);
  not not_33 (not_33_out, hex_digit[1]);
  and and_26 (and_26_out, not_33_out, not_34_out);
  not not_34 (not_34_out, hex_digit[0]);
  not not_35 (not_35_out, hex_digit[3]);
  and and_27 (and_27_out, not_35_out, hex_digit[2], not_36_out);
  not not_36 (not_36_out, hex_digit[1]);
  and and_28 (and_28_out, hex_digit[2], not_37_out);
  not not_37 (not_37_out, hex_digit[0]);
  and and_29 (and_29_out, hex_digit[3], not_38_out);
  not not_38 (not_38_out, hex_digit[2]);
  and and_30 (and_30_out, hex_digit[3], hex_digit[1]);
  not not_39 (not_39_out, hex_digit[2]);
  and and_31 (and_31_out, not_39_out, hex_digit[1]);
  and and_32 (and_32_out, hex_digit[1], not_40_out);
  not not_40 (not_40_out, hex_digit[0]);
  not not_41 (not_41_out, hex_digit[3]);
  and and_33 (and_33_out, not_41_out, hex_digit[2], not_42_out);
  not not_42 (not_42_out, hex_digit[1]);
  and and_34 (and_34_out, hex_digit[3], not_43_out);
  not not_43 (not_43_out, hex_digit[2]);
  and and_35 (and_35_out, hex_digit[3], hex_digit[0]);
  or or_1 (DP_SegCtrl[1], and_7_out, and_8_out, and_9_out, and_10_out, and_11_out);
  or or_2 (DP_SegCtrl[2], and_12_out, and_13_out, and_14_out, and_15_out, and_16_out);
  or or_3 (DP_SegCtrl[3], and_17_out, and_18_out, and_19_out, and_20_out, and_21_out);
  or or_4 (DP_SegCtrl[4], and_22_out, and_23_out, and_24_out, and_25_out);
  or or_5 (DP_SegCtrl[5], and_26_out, and_27_out, and_28_out, and_29_out, and_30_out);
  or or_6 (DP_SegCtrl[6], and_31_out, and_32_out, and_33_out, and_34_out, and_35_out);
  or or_7 (DP_SegCtrl[0], and_1_out, and_2_out, and_3_out, and_4_out, and_5_out, and_6_out);

  assign DP_SegCtrl[7] = 1'b0;
endmodule

// interruption
module multistage_interruption_support (
  input  CLK,
  input  RST,
  input  IR1,
  input  IR2,
  input  IR3,
  input  MTC0,
  input  MFC0,
  input  ERET,
  input  [31:0] EX_IR,
  input  [31:0] PC_in,
  output INT_SIG,
  output W1,
  output W2,
  output W3,
  output [31:0] BreakPoint,
  output [1:0] INT_NUM
);

  wire and_1_out, and_2_out, and_3_out, comparator_1_eq, IE, multiplexer_1_out, multiplexer_2_out, not_2_out,
       or_4_out, or_5_out, or_6_out, or_7_out, or_8_out, or_9_out, or_10_out, or_11_out,
       priority_encoder_1_en_out, register_1_q, register_2_q, register_3_q, register_4_q;
  wire [1:0] INT_TOP, multiplexer_3_out, multiplexer_4_out, multiplexer_6_out, register_8_q, register_9_q;
  wire [2:0] and_4_out, and_5_out, decoder_1_out1, INM, INM_q, multiplexer_5_out, multiplexer_8_out,
       multiplexer_10_out, multiplexer_12_out, register_5_q, register_11_q, register_13_q;
  wire [31:0] multiplexer_7_out, multiplexer_9_out, multiplexer_11_out, register_10_q, register_12_q;

  or or_1 (W1, register_5_q[0], register_1_q);
  or or_2 (W2, register_5_q[1], register_2_q);
  or or_3 (W3, register_5_q[2], register_3_q);
  Register #(.width(1), .trigger("rising"), .Select("low")) register_1 (
    .D(1'b1), .Q(register_1_q), .clk(IR1), .clr(register_5_q[0]));  // open: en
  Register #(.width(1), .trigger("rising"), .Select("low")) register_2 (
    .D(1'b1), .Q(register_2_q), .clk(IR2), .clr(register_5_q[1]));  // open: en
  Register #(.width(1), .trigger("rising"), .Select("low")) register_3 (
    .D(1'b1), .Q(register_3_q), .clk(IR3), .clr(register_5_q[2]));  // open: en
  or or_4 (or_4_out, MTC0, INT_SIG);
  Multiplexer #(.select(1), .width(1), .disabled("Z"), .enable("false")) multiplexer_1 (
    .in0(register_4_q), .in1(1'b1), .out(multiplexer_1_out), .sel(or_4_out));
  or or_5 (or_5_out, register_1_q, register_5_q[0]);
  or or_6 (or_6_out, register_2_q, register_5_q[1]);
  or or_7 (or_7_out, register_3_q, register_5_q[2]);
  Comparator #(.width(32), .mode("twosComplement")) comparator_1 (
    .a(EX_IR), .b({32{1'b0}}), .eq(comparator_1_eq));  // open: gt, lt
  Multiplexer #(.select(1), .width(1), .disabled("Z"), .enable("false")) multiplexer_2 (
    .in0(multiplexer_1_out), .in1(1'b0), .out(multiplexer_2_out), .sel(MFC0));
  and and_1 (and_1_out, or_5_out, ~and_5_out[0]);  // AND_Gate
  and and_2 (and_2_out, or_6_out, ~and_5_out[1]);  // AND_Gate
  and and_3 (and_3_out, or_7_out, ~and_5_out[2]);  // AND_Gate
  Register #(.width(1), .trigger("rising"), .Select("low")) register_4 (
    .D(multiplexer_2_out), .Q(register_4_q), .clk(CLK), .clr(or_8_out));  // open: en
  or or_8 (or_8_out, RST, ERET);
  not not_1 (IE, register_4_q);
  Register #(.width(1), .trigger("rising"), .Select("low")) register_5 (
    .D(and_1_out), .Q(register_5_q[0]), .clk(CLK), .clr(RST));  // open: en
  assign and_4_out = register_5_q & INM;  // AND_Gate and_4, 3 bits wide
  Register #(.width(1), .trigger("rising"), .Select("low")) register_6 (
    .D(and_2_out), .Q(register_5_q[1]), .clk(CLK), .clr(RST));  // open: en
  Register #(.width(1), .trigger("rising"), .Select("low")) register_7 (
    .D(and_3_out), .Q(register_5_q[2]), .clk(CLK), .clr(RST));  // open: en
  assign and_5_out = decoder_1_out1 & {3{ERET}};  // AND_Gate and_5, 3 bits wide
  not not_2 (not_2_out, comparator_1_eq);
  and and_6 (INT_SIG, IE, not_2_out, ~priority_encoder_1_en_out);  // AND_Gate
  Priority_Encoder #(.select(2), .disabled("Z")) priority_encoder_1 (
    .in1(and_4_out[0]), .in2(and_4_out[1]), .in3(and_4_out[2]), .out(INT_NUM),
    .en_out(priority_encoder_1_en_out));  // open: in0, gs, en_in
  Decoder #(.select(2), .tristate("false"), .disabled("Z"), .enable("false")) decoder_1 (
    .out1(decoder_1_out1[0]), .out2(decoder_1_out1[1]), .out3(decoder_1_out1[2]), .sel(INT_TOP));  // open: out0
  or or_9 (or_9_out, INT_SIG, ERET);
  Multiplexer #(.select(1), .width(2), .disabled("Z"), .enable("false")) multiplexer_3 (
    .in0(INT_NUM), .in1(register_8_q), .out(multiplexer_3_out), .sel(ERET));
  Register #(.width(2), .trigger("rising"), .Select("low")) INT (
    .D(multiplexer_3_out), .en(or_9_out), .Q(INT_TOP), .clk(CLK), .clr(RST));
  Multiplexer #(.select(1), .width(2), .disabled("Z"), .enable("false")) multiplexer_4 (
    .in0(INT_TOP), .in1(register_9_q), .out(multiplexer_4_out), .sel(ERET));
  Register #(.width(2), .trigger("rising"), .Select("low")) register_8 (
    .D(multiplexer_4_out), .en(or_9_out), .Q(register_8_q), .clk(CLK), .clr(RST));
  Multiplexer #(.select(2), .width(3), .disabled("Z"), .enable("false")) multiplexer_5 (
    .in0(3'b000), .in1(3'b001), .in2(3'b011), .in3(3'b111), .out(multiplexer_5_out), .sel(INT_NUM));
  Multiplexer #(.select(1), .width(2), .disabled("Z"), .enable("false")) multiplexer_6 (
    .in0(register_8_q), .in1(2'b00), .out(multiplexer_6_out), .sel(ERET));
  Register #(.width(2), .trigger("rising"), .Select("low")) register_9 (
    .D(multiplexer_6_out), .en(or_9_out), .Q(register_9_q), .clk(CLK), .clr(RST));
  Multiplexer #(.select(1), .width(32), .disabled("Z"), .enable("false")) multiplexer_7 (
    .in0(PC_in), .in1(register_10_q), .out(multiplexer_7_out), .sel(ERET));
  or or_10 (or_10_out, INT_SIG, ERET);
  Multiplexer #(.select(1), .width(3), .disabled("Z"), .enable("false")) multiplexer_8 (
    .in0(multiplexer_5_out), .in1(register_11_q), .out(multiplexer_8_out), .sel(ERET));
  or or_11 (or_11_out, INT_SIG, ERET);
  Register #(.width(32), .trigger("rising"), .Select("low")) EPC_Top (
    .D(multiplexer_7_out), .en(or_10_out), .Q(BreakPoint), .clk(CLK), .clr(RST));
  assign INM = ~INM_q;  // NOT_Gate not_3, 3 bits wide
  Register #(.width(3), .trigger("rising"), .Select("low")) u_INM (
    .D(multiplexer_8_out), .en(or_11_out), .Q(INM_q), .clk(CLK), .clr(RST));
  Multiplexer #(.select(1), .width(32), .disabled("Z"), .enable("false")) multiplexer_9 (
    .in0(BreakPoint), .in1(register_12_q), .out(multiplexer_9_out), .sel(ERET));
  Register #(.width(32), .trigger("rising"), .Select("low")) register_10 (
    .D(multiplexer_9_out), .en(or_10_out), .Q(register_10_q), .clk(CLK), .clr(RST));
  Register #(.width(3), .trigger("rising"), .Select("low")) register_11 (
    .D(multiplexer_10_out), .en(or_11_out), .Q(register_11_q), .clk(CLK), .clr(RST));
  Multiplexer #(.select(1), .width(3), .disabled("Z"), .enable("false")) multiplexer_10 (
    .in0(INM_q), .in1(register_13_q), .out(multiplexer_10_out), .sel(ERET));
  Multiplexer #(.select(1), .width(32), .disabled("Z"), .enable("false")) multiplexer_11 (
    .in0(register_10_q), .in1({32{1'b0}}), .out(multiplexer_11_out), .sel(ERET));
  Multiplexer #(.select(1), .width(3), .disabled("Z"), .enable("false")) multiplexer_12 (
    .in0(register_11_q), .in1(3'b000), .out(multiplexer_12_out), .sel(ERET));
  Register #(.width(32), .trigger("rising"), .Select("low")) register_12 (
    .D(multiplexer_11_out), .en(or_10_out), .Q(register_12_q), .clk(CLK), .clr(RST));
  Register #(.width(3), .trigger("rising"), .Select("low")) register_13 (
    .D(multiplexer_12_out), .en(or_11_out), .Q(register_13_q), .clk(CLK), .clr(RST));

  // Other names for the same wires on the sheet: INT[1:0] = INT_NUM; RecoverPC[31:0] = PC_in

  // Notes on the sheet:
  //   Reset 
  //   使用ERET指令来反向MUX
endmodule

module led_driver (
  input  [3:0] X,
  input  [4:0] Y,
  input  SET,
  input  LineRst,
  input  RST,
  input  CLK,
  input  EN,
  output [31:0] R0,
  output [31:0] R8,
  output [31:0] R1,
  output [31:0] R9,
  output [31:0] R2,
  output [31:0] R10,
  output [31:0] R3,
  output [31:0] R11,
  output [31:0] R4,
  output [31:0] R12,
  output [31:0] R5,
  output [31:0] R13,
  output [31:0] R6,
  output [31:0] R14,
  output [31:0] R7,
  output [31:0] R15
);

  wire S0, S1, S2, S3, S4, S5, S6, S7, S8, S9, S10, S11, S12, S13, S14, S15;
  wire [4:0] subtractor_2_out, Y_t;
  wire [31:0] mask, YS;

  Subtractor #(.width(5)) subtractor_1 (.a({5{1'b1}}), .b(Y), .out(Y_t));  // open: bin, bout
  Decoder #(.select(4), .tristate("false"), .disabled("Z"), .enable("false")) decoder_1 (
    .out0(S0), .out1(S1), .out2(S2), .out3(S3), .out4(S4), .out5(S5), .out6(S6), .out7(S7), .out8(S8),
    .out9(S9), .out10(S10), .out11(S11), .out12(S12), .out13(S13), .out14(S14), .out15(S15), .sel(X));
  Shifter #(.width(32), .shift("ll")) shifter_1 (.in(32'h1), .\dist (Y_t), .out(mask));
  led_driver_unit led_driver_unit_1 (
    .mask(mask), .YS(YS), .SET(SET), .LineRst(LineRst), .RST(RST), .CLK(CLK), .EN(EN), .Select(S0), .R1(R0));
  led_driver_unit led_driver_unit_2 (
    .mask(mask), .YS(YS), .SET(SET), .LineRst(LineRst), .RST(RST), .CLK(CLK), .EN(EN), .Select(S1), .R1(R1));
  led_driver_unit led_driver_unit_3 (
    .mask(mask), .YS(YS), .SET(SET), .LineRst(LineRst), .RST(RST), .CLK(CLK), .EN(EN), .Select(S2), .R1(R2));
  led_driver_unit led_driver_unit_4 (
    .mask(mask), .YS(YS), .SET(SET), .LineRst(LineRst), .RST(RST), .CLK(CLK), .EN(EN), .Select(S3), .R1(R3));
  led_driver_unit led_driver_unit_5 (
    .mask(mask), .YS(YS), .SET(SET), .LineRst(LineRst), .RST(RST), .CLK(CLK), .EN(EN), .Select(S4), .R1(R4));
  led_driver_unit led_driver_unit_6 (
    .mask(mask), .YS(YS), .SET(SET), .LineRst(LineRst), .RST(RST), .CLK(CLK), .EN(EN), .Select(S5), .R1(R5));
  led_driver_unit led_driver_unit_7 (
    .mask(mask), .YS(YS), .SET(SET), .LineRst(LineRst), .RST(RST), .CLK(CLK), .EN(EN), .Select(S6), .R1(R6));
  led_driver_unit led_driver_unit_8 (
    .mask(mask), .YS(YS), .SET(SET), .LineRst(LineRst), .RST(RST), .CLK(CLK), .EN(EN), .Select(S7), .R1(R7));
  Subtractor #(.width(5)) subtractor_2 (.a({5{1'b1}}), .b(Y_t), .out(subtractor_2_out));  // open: bin, bout
  Shifter #(.width(32), .shift("ar")) shifter_2 (.in(32'h80000000), .\dist (subtractor_2_out), .out(YS));
  led_driver_unit led_driver_unit_9 (
    .mask(mask), .YS(YS), .SET(SET), .LineRst(LineRst), .RST(RST), .CLK(CLK), .EN(EN), .Select(S8), .R1(R8));
  led_driver_unit led_driver_unit_10 (
    .mask(mask), .YS(YS), .SET(SET), .LineRst(LineRst), .RST(RST), .CLK(CLK), .EN(EN), .Select(S9), .R1(R9));
  led_driver_unit led_driver_unit_11 (
    .mask(mask), .YS(YS), .SET(SET), .LineRst(LineRst), .RST(RST), .CLK(CLK), .EN(EN), .Select(S10), .R1(R10));
  led_driver_unit led_driver_unit_12 (
    .mask(mask), .YS(YS), .SET(SET), .LineRst(LineRst), .RST(RST), .CLK(CLK), .EN(EN), .Select(S11), .R1(R11));
  led_driver_unit led_driver_unit_13 (
    .mask(mask), .YS(YS), .SET(SET), .LineRst(LineRst), .RST(RST), .CLK(CLK), .EN(EN), .Select(S12), .R1(R12));
  led_driver_unit led_driver_unit_14 (
    .mask(mask), .YS(YS), .SET(SET), .LineRst(LineRst), .RST(RST), .CLK(CLK), .EN(EN), .Select(S13), .R1(R13));
  led_driver_unit led_driver_unit_15 (
    .mask(mask), .YS(YS), .SET(SET), .LineRst(LineRst), .RST(RST), .CLK(CLK), .EN(EN), .Select(S14), .R1(R14));
  led_driver_unit led_driver_unit_16 (
    .mask(mask), .YS(YS), .SET(SET), .LineRst(LineRst), .RST(RST), .CLK(CLK), .EN(EN), .Select(S15), .R1(R15));
endmodule

module led_driver_unit (
  input  [31:0] mask,
  input  [31:0] YS,
  input  SET,
  input  LineRst,
  input  RST,
  input  CLK,
  input  EN,
  input  Select,
  output [31:0] R1
);

  wire [0:0] and_4_out_2;
  wire [30:0] and_4_out;
  wire [31:0] and_1_out, and_2_out, and_3_out, multiplexer_1_out, multiplexer_2_out, multiplexer_3_out,
       multiplexer_4_out, not_1_out, not_2_out, or_1_out, or_2_out;

  assign or_1_out = and_3_out | and_1_out;  // OR_Gate or_1, 32 bits wide
  Multiplexer #(.select(1), .width(32), .disabled("Z"), .enable("false")) multiplexer_1 (
    .in0(R1), .in1(multiplexer_2_out), .out(multiplexer_1_out), .sel(Select));
  assign and_1_out = {1'b0, and_4_out} & YS;  // AND_Gate and_1, 32 bits wide
  Multiplexer #(.select(1), .width(32), .disabled("Z"), .enable("false")) multiplexer_2 (
    .in0(and_2_out), .in1(or_2_out), .out(multiplexer_2_out), .sel(SET));
  Multiplexer #(.select(1), .width(32), .disabled("Z"), .enable("false")) multiplexer_3 (
    .in0(multiplexer_1_out), .in1(or_1_out), .out(multiplexer_3_out), .sel(LineRst));
  assign and_2_out = not_2_out & R1;  // AND_Gate and_2, 32 bits wide
  assign or_2_out = mask | R1;  // OR_Gate or_2, 32 bits wide
  Multiplexer #(.select(1), .width(32), .disabled("Z"), .enable("false")) multiplexer_4 (
    .in0(multiplexer_3_out), .in1({32{1'b0}}), .out(multiplexer_4_out), .sel(RST));
  assign not_1_out = ~YS;  // NOT_Gate not_1, 32 bits wide
  assign and_3_out = not_1_out & R1;  // AND_Gate and_3, 32 bits wide
  assign {and_4_out, and_4_out_2[0]} = YS & R1;  // AND_Gate and_4, 32 bits wide
  assign not_2_out = ~mask;  // NOT_Gate not_2, 32 bits wide
  Register #(.width(32), .trigger("rising"), .Select("low")) register_1 (
    .D(multiplexer_4_out), .en(EN), .Q(R1), .clk(CLK));  // open: clr
endmodule

module bitmap_get (
  input  [3:0] X,
  input  [4:0] Y,
  input  [31:0] R0,
  input  [31:0] R8,
  input  [31:0] R1,
  input  [31:0] R9,
  input  [31:0] R2,
  input  [31:0] R10,
  input  [31:0] R3,
  input  [31:0] R11,
  input  [1:0] Control_Bit,
  input  [31:0] R4,
  input  [31:0] R12,
  input  [31:0] R5,
  input  [31:0] R13,
  input  [31:0] R6,
  input  [31:0] R14,
  input  [31:0] R7,
  input  [31:0] R15,
  output [31:0] out_20
);

  wire [0:0] bitselector_17_out;
  wire [4:0] Y_t;
  wire [15:0] bitselector_1_out;
  wire [31:0] multiplexer_1_out;

  Subtractor #(.width(5)) subtractor_1 (.a({5{1'b1}}), .b(Y), .out(Y_t));  // open: bin, bout
  BitSelector #(.width(32), .group(1)) bitselector_1 (.in(R0), .out(bitselector_1_out[0]), .sel(Y_t));
  BitSelector #(.width(32), .group(1)) bitselector_2 (.in(R1), .out(bitselector_1_out[1]), .sel(Y_t));
  BitSelector #(.width(32), .group(1)) bitselector_3 (.in(R2), .out(bitselector_1_out[2]), .sel(Y_t));
  BitSelector #(.width(32), .group(1)) bitselector_4 (.in(R3), .out(bitselector_1_out[3]), .sel(Y_t));
  BitSelector #(.width(32), .group(1)) bitselector_5 (.in(R4), .out(bitselector_1_out[4]), .sel(Y_t));
  BitSelector #(.width(32), .group(1)) bitselector_6 (.in(R5), .out(bitselector_1_out[5]), .sel(Y_t));
  BitSelector #(.width(32), .group(1)) bitselector_7 (.in(R6), .out(bitselector_1_out[6]), .sel(Y_t));
  BitSelector #(.width(32), .group(1)) bitselector_8 (.in(R7), .out(bitselector_1_out[7]), .sel(Y_t));
  BitSelector #(.width(32), .group(1)) bitselector_9 (.in(R8), .out(bitselector_1_out[8]), .sel(Y_t));
  BitSelector #(.width(32), .group(1)) bitselector_10 (.in(R9), .out(bitselector_1_out[9]), .sel(Y_t));
  BitSelector #(.width(32), .group(1)) bitselector_11 (.in(R10), .out(bitselector_1_out[10]), .sel(Y_t));
  BitSelector #(.width(32), .group(1)) bitselector_12 (.in(R11), .out(bitselector_1_out[11]), .sel(Y_t));
  BitSelector #(.width(32), .group(1)) bitselector_13 (.in(R12), .out(bitselector_1_out[12]), .sel(Y_t));
  BitSelector #(.width(32), .group(1)) bitselector_14 (.in(R13), .out(bitselector_1_out[13]), .sel(Y_t));
  BitSelector #(.width(32), .group(1)) bitselector_15 (.in(R14), .out(bitselector_1_out[14]), .sel(Y_t));
  BitSelector #(.width(32), .group(1)) bitselector_16 (.in(R15), .out(bitselector_1_out[15]), .sel(Y_t));
  Multiplexer #(.select(4), .width(32), .disabled("Z"), .enable("false")) multiplexer_1 (
    .in0(R0), .in1(R1), .in2(R2), .in3(R3), .in4(R4), .in5(R5), .in6(R6), .in7(R7), .in8(R8), .in9(R9),
    .in10(R10), .in11(R11), .in12(R12), .in13(R13), .in14(R14), .in15(R15), .out(multiplexer_1_out), .sel(X));
  BitSelector #(.width(16), .group(1)) bitselector_17 (.in(bitselector_1_out), .out(bitselector_17_out[0]), .sel(X));
  Multiplexer #(.select(2), .width(32), .disabled("Z"), .enable("false")) multiplexer_2 (
    .in0({{31{1'b0}}, bitselector_17_out[0]}), .in1({{16{1'b0}}, bitselector_1_out}),
    .in2(multiplexer_1_out), .out(out_20), .sel(Control_Bit));  // open: in3
endmodule

module vga_sec_ram (
  input  Read,
  input  Write,
  input  [3:0] X,
  input  CLK,
  input  [8:0] addr,
  input  [31:0] R0,
  input  [31:0] R1,
  input  [31:0] R2,
  input  [31:0] R3,
  input  [31:0] R4,
  input  [31:0] R5,
  input  [31:0] R6,
  input  [31:0] R7,
  input  [31:0] R8,
  input  [31:0] R9,
  input  [31:0] R10,
  input  [31:0] R11,
  input  [31:0] R12,
  input  [31:0] R13,
  input  [31:0] R14,
  input  [31:0] R15,
  output bit_out
);

  wire ram_1_data, ram_2_data, ram_3_data, ram_4_data, ram_5_data, ram_6_data, ram_7_data, ram_8_data,
       ram_9_data, ram_10_data, ram_11_data, ram_12_data, ram_13_data, ram_14_data, ram_15_data, ram_16_data,
       ram_17_data, ram_18_data, ram_19_data, ram_20_data, ram_21_data, ram_22_data, ram_23_data,
       ram_24_data, ram_25_data, ram_26_data, ram_27_data, ram_28_data, ram_29_data, ram_30_data,
       ram_31_data, ram_32_data;
  wire [3:0] multiplexer_2_out, multiplexer_3_out, multiplexer_4_out, multiplexer_5_out, multiplexer_6_out,
       multiplexer_7_out, multiplexer_8_out, multiplexer_9_out, multiplexer_10_out, multiplexer_11_out,
       multiplexer_12_out, multiplexer_13_out, multiplexer_14_out, multiplexer_15_out, multiplexer_16_out,
       multiplexer_17_out, multiplexer_18_out, multiplexer_19_out, multiplexer_20_out, multiplexer_21_out,
       multiplexer_22_out, multiplexer_23_out, multiplexer_24_out, multiplexer_25_out, multiplexer_26_out,
       multiplexer_27_out, multiplexer_28_out, multiplexer_29_out, multiplexer_30_out, multiplexer_31_out,
       multiplexer_32_out, multiplexer_33_out;
  wire [31:0] multiplexer_1_out;

  Multiplexer #(.select(4), .width(32), .disabled("Z"), .enable("false")) multiplexer_1 (
    .in0(R0), .in1(R1), .in2(R2), .in3(R3), .in4(R4), .in5(R5), .in6(R6), .in7(R7), .in8(R8), .in9(R9),
    .in10(R10), .in11(R11), .in12(R12), .in13(R13), .in14(R14), .in15(R15), .out(multiplexer_1_out), .sel(X));
  Multiplexer #(.select(1), .width(4), .disabled("Z"), .enable("false")) multiplexer_2 (
    .in0(addr[3:0]), .in1(X), .out(multiplexer_2_out), .sel(Write));
  Multiplexer #(.select(1), .width(4), .disabled("Z"), .enable("false")) multiplexer_3 (
    .in0(addr[3:0]), .in1(X), .out(multiplexer_3_out), .sel(Write));
  Multiplexer #(.select(1), .width(4), .disabled("Z"), .enable("false")) multiplexer_4 (
    .in0(addr[3:0]), .in1(X), .out(multiplexer_4_out), .sel(Write));
  Multiplexer #(.select(1), .width(4), .disabled("Z"), .enable("false")) multiplexer_5 (
    .in0(addr[3:0]), .in1(X), .out(multiplexer_5_out), .sel(Write));
  RAM #(.addrWidth(4), .dataWidth(1), .bus("separate"), .Select("low")) ram_1 (
    .addr(multiplexer_2_out), .din(multiplexer_1_out[31]), .data(ram_1_data), .str(Write), .clk(CLK),
    .ld(Read));  // open: sel, clr
  RAM #(.addrWidth(4), .dataWidth(1), .bus("separate"), .Select("low")) ram_2 (
    .addr(multiplexer_3_out), .din(multiplexer_1_out[23]), .data(ram_2_data), .str(Write), .clk(CLK),
    .ld(Read));  // open: sel, clr
  RAM #(.addrWidth(4), .dataWidth(1), .bus("separate"), .Select("low")) ram_3 (
    .addr(multiplexer_4_out), .din(multiplexer_1_out[15]), .data(ram_3_data), .str(Write), .clk(CLK),
    .ld(Read));  // open: sel, clr
  RAM #(.addrWidth(4), .dataWidth(1), .bus("separate"), .Select("low")) ram_4 (
    .addr(multiplexer_5_out), .din(multiplexer_1_out[7]), .data(ram_4_data), .str(Write), .clk(CLK), .ld(Read));  // open: sel, clr
  Multiplexer #(.select(1), .width(4), .disabled("Z"), .enable("false")) multiplexer_6 (
    .in0(addr[3:0]), .in1(X), .out(multiplexer_6_out), .sel(Write));
  Multiplexer #(.select(1), .width(4), .disabled("Z"), .enable("false")) multiplexer_7 (
    .in0(addr[3:0]), .in1(X), .out(multiplexer_7_out), .sel(Write));
  Multiplexer #(.select(1), .width(4), .disabled("Z"), .enable("false")) multiplexer_8 (
    .in0(addr[3:0]), .in1(X), .out(multiplexer_8_out), .sel(Write));
  Multiplexer #(.select(1), .width(4), .disabled("Z"), .enable("false")) multiplexer_9 (
    .in0(addr[3:0]), .in1(X), .out(multiplexer_9_out), .sel(Write));
  RAM #(.addrWidth(4), .dataWidth(1), .bus("separate"), .Select("low")) ram_5 (
    .addr(multiplexer_6_out), .din(multiplexer_1_out[30]), .data(ram_5_data), .str(Write), .clk(CLK),
    .ld(Read));  // open: sel, clr
  RAM #(.addrWidth(4), .dataWidth(1), .bus("separate"), .Select("low")) ram_6 (
    .addr(multiplexer_7_out), .din(multiplexer_1_out[22]), .data(ram_6_data), .str(Write), .clk(CLK),
    .ld(Read));  // open: sel, clr
  RAM #(.addrWidth(4), .dataWidth(1), .bus("separate"), .Select("low")) ram_7 (
    .addr(multiplexer_8_out), .din(multiplexer_1_out[14]), .data(ram_7_data), .str(Write), .clk(CLK),
    .ld(Read));  // open: sel, clr
  RAM #(.addrWidth(4), .dataWidth(1), .bus("separate"), .Select("low")) ram_8 (
    .addr(multiplexer_9_out), .din(multiplexer_1_out[6]), .data(ram_8_data), .str(Write), .clk(CLK), .ld(Read));  // open: sel, clr
  Multiplexer #(.select(1), .width(4), .disabled("Z"), .enable("false")) multiplexer_10 (
    .in0(addr[3:0]), .in1(X), .out(multiplexer_10_out), .sel(Write));
  Multiplexer #(.select(1), .width(4), .disabled("Z"), .enable("false")) multiplexer_11 (
    .in0(addr[3:0]), .in1(X), .out(multiplexer_11_out), .sel(Write));
  Multiplexer #(.select(1), .width(4), .disabled("Z"), .enable("false")) multiplexer_12 (
    .in0(addr[3:0]), .in1(X), .out(multiplexer_12_out), .sel(Write));
  Multiplexer #(.select(1), .width(4), .disabled("Z"), .enable("false")) multiplexer_13 (
    .in0(addr[3:0]), .in1(X), .out(multiplexer_13_out), .sel(Write));
  RAM #(.addrWidth(4), .dataWidth(1), .bus("separate"), .Select("low")) ram_9 (
    .addr(multiplexer_10_out), .din(multiplexer_1_out[29]), .data(ram_9_data), .str(Write), .clk(CLK),
    .ld(Read));  // open: sel, clr
  RAM #(.addrWidth(4), .dataWidth(1), .bus("separate"), .Select("low")) ram_10 (
    .addr(multiplexer_11_out), .din(multiplexer_1_out[21]), .data(ram_10_data), .str(Write), .clk(CLK),
    .ld(Read));  // open: sel, clr
  RAM #(.addrWidth(4), .dataWidth(1), .bus("separate"), .Select("low")) ram_11 (
    .addr(multiplexer_12_out), .din(multiplexer_1_out[13]), .data(ram_11_data), .str(Write), .clk(CLK),
    .ld(Read));  // open: sel, clr
  RAM #(.addrWidth(4), .dataWidth(1), .bus("separate"), .Select("low")) ram_12 (
    .addr(multiplexer_13_out), .din(multiplexer_1_out[5]), .data(ram_12_data), .str(Write), .clk(CLK),
    .ld(Read));  // open: sel, clr
  Multiplexer #(.select(1), .width(4), .disabled("Z"), .enable("false")) multiplexer_14 (
    .in0(addr[3:0]), .in1(X), .out(multiplexer_14_out), .sel(Write));
  Multiplexer #(.select(1), .width(4), .disabled("Z"), .enable("false")) multiplexer_15 (
    .in0(addr[3:0]), .in1(X), .out(multiplexer_15_out), .sel(Write));
  Multiplexer #(.select(1), .width(4), .disabled("Z"), .enable("false")) multiplexer_16 (
    .in0(addr[3:0]), .in1(X), .out(multiplexer_16_out), .sel(Write));
  Multiplexer #(.select(1), .width(4), .disabled("Z"), .enable("false")) multiplexer_17 (
    .in0(addr[3:0]), .in1(X), .out(multiplexer_17_out), .sel(Write));
  RAM #(.addrWidth(4), .dataWidth(1), .bus("separate"), .Select("low")) ram_13 (
    .addr(multiplexer_14_out), .din(multiplexer_1_out[28]), .data(ram_13_data), .str(Write), .clk(CLK),
    .ld(Read));  // open: sel, clr
  RAM #(.addrWidth(4), .dataWidth(1), .bus("separate"), .Select("low")) ram_14 (
    .addr(multiplexer_15_out), .din(multiplexer_1_out[20]), .data(ram_14_data), .str(Write), .clk(CLK),
    .ld(Read));  // open: sel, clr
  RAM #(.addrWidth(4), .dataWidth(1), .bus("separate"), .Select("low")) ram_15 (
    .addr(multiplexer_16_out), .din(multiplexer_1_out[12]), .data(ram_15_data), .str(Write), .clk(CLK),
    .ld(Read));  // open: sel, clr
  RAM #(.addrWidth(4), .dataWidth(1), .bus("separate"), .Select("low")) ram_16 (
    .addr(multiplexer_17_out), .din(multiplexer_1_out[4]), .data(ram_16_data), .str(Write), .clk(CLK),
    .ld(Read));  // open: sel, clr
  Multiplexer #(.select(1), .width(4), .disabled("Z"), .enable("false")) multiplexer_18 (
    .in0(addr[3:0]), .in1(X), .out(multiplexer_18_out), .sel(Write));
  Multiplexer #(.select(1), .width(4), .disabled("Z"), .enable("false")) multiplexer_19 (
    .in0(addr[3:0]), .in1(X), .out(multiplexer_19_out), .sel(Write));
  Multiplexer #(.select(1), .width(4), .disabled("Z"), .enable("false")) multiplexer_20 (
    .in0(addr[3:0]), .in1(X), .out(multiplexer_20_out), .sel(Write));
  Multiplexer #(.select(1), .width(4), .disabled("Z"), .enable("false")) multiplexer_21 (
    .in0(addr[3:0]), .in1(X), .out(multiplexer_21_out), .sel(Write));
  RAM #(.addrWidth(4), .dataWidth(1), .bus("separate"), .Select("low")) ram_17 (
    .addr(multiplexer_18_out), .din(multiplexer_1_out[27]), .data(ram_17_data), .str(Write), .clk(CLK),
    .ld(Read));  // open: sel, clr
  RAM #(.addrWidth(4), .dataWidth(1), .bus("separate"), .Select("low")) ram_18 (
    .addr(multiplexer_19_out), .din(multiplexer_1_out[19]), .data(ram_18_data), .str(Write), .clk(CLK),
    .ld(Read));  // open: sel, clr
  RAM #(.addrWidth(4), .dataWidth(1), .bus("separate"), .Select("low")) ram_19 (
    .addr(multiplexer_20_out), .din(multiplexer_1_out[11]), .data(ram_19_data), .str(Write), .clk(CLK),
    .ld(Read));  // open: sel, clr
  RAM #(.addrWidth(4), .dataWidth(1), .bus("separate"), .Select("low")) ram_20 (
    .addr(multiplexer_21_out), .din(multiplexer_1_out[3]), .data(ram_20_data), .str(Write), .clk(CLK),
    .ld(Read));  // open: sel, clr
  Multiplexer #(.select(1), .width(4), .disabled("Z"), .enable("false")) multiplexer_22 (
    .in0(addr[3:0]), .in1(X), .out(multiplexer_22_out), .sel(Write));
  Multiplexer #(.select(1), .width(4), .disabled("Z"), .enable("false")) multiplexer_23 (
    .in0(addr[3:0]), .in1(X), .out(multiplexer_23_out), .sel(Write));
  Multiplexer #(.select(1), .width(4), .disabled("Z"), .enable("false")) multiplexer_24 (
    .in0(addr[3:0]), .in1(X), .out(multiplexer_24_out), .sel(Write));
  Multiplexer #(.select(1), .width(4), .disabled("Z"), .enable("false")) multiplexer_25 (
    .in0(addr[3:0]), .in1(X), .out(multiplexer_25_out), .sel(Write));
  RAM #(.addrWidth(4), .dataWidth(1), .bus("separate"), .Select("low")) ram_21 (
    .addr(multiplexer_22_out), .din(multiplexer_1_out[26]), .data(ram_21_data), .str(Write), .clk(CLK),
    .ld(Read));  // open: sel, clr
  RAM #(.addrWidth(4), .dataWidth(1), .bus("separate"), .Select("low")) ram_22 (
    .addr(multiplexer_23_out), .din(multiplexer_1_out[18]), .data(ram_22_data), .str(Write), .clk(CLK),
    .ld(Read));  // open: sel, clr
  RAM #(.addrWidth(4), .dataWidth(1), .bus("separate"), .Select("low")) ram_23 (
    .addr(multiplexer_24_out), .din(multiplexer_1_out[10]), .data(ram_23_data), .str(Write), .clk(CLK),
    .ld(Read));  // open: sel, clr
  RAM #(.addrWidth(4), .dataWidth(1), .bus("separate"), .Select("low")) ram_24 (
    .addr(multiplexer_25_out), .din(multiplexer_1_out[2]), .data(ram_24_data), .str(Write), .clk(CLK),
    .ld(Read));  // open: sel, clr
  Multiplexer #(.select(1), .width(4), .disabled("Z"), .enable("false")) multiplexer_26 (
    .in0(addr[3:0]), .in1(X), .out(multiplexer_26_out), .sel(Write));
  Multiplexer #(.select(1), .width(4), .disabled("Z"), .enable("false")) multiplexer_27 (
    .in0(addr[3:0]), .in1(X), .out(multiplexer_27_out), .sel(Write));
  Multiplexer #(.select(1), .width(4), .disabled("Z"), .enable("false")) multiplexer_28 (
    .in0(addr[3:0]), .in1(X), .out(multiplexer_28_out), .sel(Write));
  Multiplexer #(.select(1), .width(4), .disabled("Z"), .enable("false")) multiplexer_29 (
    .in0(addr[3:0]), .in1(X), .out(multiplexer_29_out), .sel(Write));
  RAM #(.addrWidth(4), .dataWidth(1), .bus("separate"), .Select("low")) ram_25 (
    .addr(multiplexer_26_out), .din(multiplexer_1_out[25]), .data(ram_25_data), .str(Write), .clk(CLK),
    .ld(Read));  // open: sel, clr
  RAM #(.addrWidth(4), .dataWidth(1), .bus("separate"), .Select("low")) ram_26 (
    .addr(multiplexer_27_out), .din(multiplexer_1_out[17]), .data(ram_26_data), .str(Write), .clk(CLK),
    .ld(Read));  // open: sel, clr
  RAM #(.addrWidth(4), .dataWidth(1), .bus("separate"), .Select("low")) ram_27 (
    .addr(multiplexer_28_out), .din(multiplexer_1_out[9]), .data(ram_27_data), .str(Write), .clk(CLK),
    .ld(Read));  // open: sel, clr
  RAM #(.addrWidth(4), .dataWidth(1), .bus("separate"), .Select("low")) ram_28 (
    .addr(multiplexer_29_out), .din(multiplexer_1_out[1]), .data(ram_28_data), .str(Write), .clk(CLK),
    .ld(Read));  // open: sel, clr
  Multiplexer #(.select(1), .width(4), .disabled("Z"), .enable("false")) multiplexer_30 (
    .in0(addr[3:0]), .in1(X), .out(multiplexer_30_out), .sel(Write));
  Multiplexer #(.select(1), .width(4), .disabled("Z"), .enable("false")) multiplexer_31 (
    .in0(addr[3:0]), .in1(X), .out(multiplexer_31_out), .sel(Write));
  Multiplexer #(.select(1), .width(4), .disabled("Z"), .enable("false")) multiplexer_32 (
    .in0(addr[3:0]), .in1(X), .out(multiplexer_32_out), .sel(Write));
  Multiplexer #(.select(1), .width(4), .disabled("Z"), .enable("false")) multiplexer_33 (
    .in0(addr[3:0]), .in1(X), .out(multiplexer_33_out), .sel(Write));
  RAM #(.addrWidth(4), .dataWidth(1), .bus("separate"), .Select("low")) ram_29 (
    .addr(multiplexer_30_out), .din(multiplexer_1_out[24]), .data(ram_29_data), .str(Write), .clk(CLK),
    .ld(Read));  // open: sel, clr
  RAM #(.addrWidth(4), .dataWidth(1), .bus("separate"), .Select("low")) ram_30 (
    .addr(multiplexer_31_out), .din(multiplexer_1_out[16]), .data(ram_30_data), .str(Write), .clk(CLK),
    .ld(Read));  // open: sel, clr
  RAM #(.addrWidth(4), .dataWidth(1), .bus("separate"), .Select("low")) ram_31 (
    .addr(multiplexer_32_out), .din(multiplexer_1_out[8]), .data(ram_31_data), .str(Write), .clk(CLK),
    .ld(Read));  // open: sel, clr
  RAM #(.addrWidth(4), .dataWidth(1), .bus("separate"), .Select("low")) ram_32 (
    .addr(multiplexer_33_out), .din(multiplexer_1_out[0]), .data(ram_32_data), .str(Write), .clk(CLK),
    .ld(Read));  // open: sel, clr
  Multiplexer #(.select(5), .width(1), .disabled("Z"), .enable("false")) multiplexer_34 (
    .in0(ram_1_data), .in1(ram_5_data), .in2(ram_9_data), .in3(ram_13_data), .in4(ram_17_data),
    .in5(ram_21_data), .in6(ram_25_data), .in7(ram_29_data), .in8(ram_2_data), .in9(ram_6_data),
    .in10(ram_10_data), .in11(ram_14_data), .in12(ram_18_data), .in13(ram_22_data), .in14(ram_26_data),
    .in15(ram_30_data), .in16(ram_3_data), .in17(ram_7_data), .in18(ram_11_data), .in19(ram_15_data),
    .in20(ram_19_data), .in21(ram_23_data), .in22(ram_27_data), .in23(ram_31_data), .in24(ram_4_data),
    .in25(ram_8_data), .in26(ram_12_data), .in27(ram_16_data), .in28(ram_20_data), .in29(ram_24_data),
    .in30(ram_28_data), .in31(ram_32_data), .out(bit_out), .sel(addr[8:4]));

  // Other names for the same wires on the sheet: inner_off[3:0] = addr[3:0]; select[4:0] = addr[8:4]
endmodule
